// Digital circuit 32-bit Binary to BCD.dig as structural Verilog
module _32_bit_Binary_to_BCD (
  input  [31:0] In,
  output [3:0] _1e10s,
  output [3:0] _1e9s,
  output [3:0] _1e8s,
  output [3:0] _1e7s,
  output [3:0] _1e6s,
  output [3:0] _1e5s,
  output [3:0] _1e4s,
  output [3:0] _1e3s,
  output [3:0] _1e2s,
  output [3:0] _10s,
  output [3:0] _1s
);

  cond__add_3 cond__add_3_1 ();
  cond__add_3 cond__add_3_2 ();
  cond__add_3 cond__add_3_3 ();
  cond__add_3 cond__add_3_4 ();
  cond__add_3 cond__add_3_5 ();
  cond__add_3 cond__add_3_6 ();
  cond__add_3 cond__add_3_7 ();
  cond__add_3 cond__add_3_8 ();
  cond__add_3 cond__add_3_9 ();
  cond__add_3 cond__add_3_10 ();
  cond__add_3 cond__add_3_11 ();
  cond__add_3 cond__add_3_12 ();
  cond__add_3 cond__add_3_13 ();
  cond__add_3 cond__add_3_14 ();
  cond__add_3 cond__add_3_15 ();
  cond__add_3 cond__add_3_16 ();
  cond__add_3 cond__add_3_17 ();
  cond__add_3 cond__add_3_18 ();
  cond__add_3 cond__add_3_19 ();
  cond__add_3 cond__add_3_20 ();
  cond__add_3 cond__add_3_21 ();
  cond__add_3 cond__add_3_22 ();
  cond__add_3 cond__add_3_23 ();
  cond__add_3 cond__add_3_24 ();
  cond__add_3 cond__add_3_25 ();
  cond__add_3 cond__add_3_26 ();
  cond__add_3 cond__add_3_27 ();
  cond__add_3 cond__add_3_28 ();
  cond__add_3 cond__add_3_29 ();
  cond__add_3 cond__add_3_30 ();
  cond__add_3 cond__add_3_31 ();
  cond__add_3 cond__add_3_32 ();
  cond__add_3 cond__add_3_33 ();
  cond__add_3 cond__add_3_34 ();
  cond__add_3 cond__add_3_35 ();
  cond__add_3 cond__add_3_36 ();
  cond__add_3 cond__add_3_37 ();
  cond__add_3 cond__add_3_38 ();
  cond__add_3 cond__add_3_39 ();
  cond__add_3 cond__add_3_40 ();
  cond__add_3 cond__add_3_41 ();
  cond__add_3 cond__add_3_42 ();
  cond__add_3 cond__add_3_43 ();
  cond__add_3 cond__add_3_44 ();
  cond__add_3 cond__add_3_45 ();
  cond__add_3 cond__add_3_46 ();
  cond__add_3 cond__add_3_47 ();
  cond__add_3 cond__add_3_48 ();
  cond__add_3 cond__add_3_49 ();
  cond__add_3 cond__add_3_50 ();
  cond__add_3 cond__add_3_51 ();
  cond__add_3 cond__add_3_52 ();
  cond__add_3 cond__add_3_53 ();
  cond__add_3 cond__add_3_54 ();
  cond__add_3 cond__add_3_55 ();
  cond__add_3 cond__add_3_56 ();
  cond__add_3 cond__add_3_57 ();
  cond__add_3 cond__add_3_58 ();
  cond__add_3 cond__add_3_59 ();
  cond__add_3 cond__add_3_60 ();
  cond__add_3 cond__add_3_61 ();
  cond__add_3 cond__add_3_62 ();
  cond__add_3 cond__add_3_63 ();
  cond__add_3 cond__add_3_64 ();
  cond__add_3 cond__add_3_65 ();
  cond__add_3 cond__add_3_66 ();
  cond__add_3 cond__add_3_67 ();
  cond__add_3 cond__add_3_68 ();
  cond__add_3 cond__add_3_69 ();
  cond__add_3 cond__add_3_70 ();
  cond__add_3 cond__add_3_71 ();
  cond__add_3 cond__add_3_72 ();
  cond__add_3 cond__add_3_73 ();
  cond__add_3 cond__add_3_74 ();
  cond__add_3 cond__add_3_75 ();
  cond__add_3 cond__add_3_76 ();
  cond__add_3 cond__add_3_77 ();
  cond__add_3 cond__add_3_78 ();
  cond__add_3 cond__add_3_79 ();
  cond__add_3 cond__add_3_80 ();
  cond__add_3 cond__add_3_81 ();
  cond__add_3 cond__add_3_82 ();
  cond__add_3 cond__add_3_83 ();
  cond__add_3 cond__add_3_84 ();
  cond__add_3 cond__add_3_85 ();
  cond__add_3 cond__add_3_86 ();
  cond__add_3 cond__add_3_87 ();
  cond__add_3 cond__add_3_88 ();
  cond__add_3 cond__add_3_89 ();
  cond__add_3 cond__add_3_90 ();
  cond__add_3 cond__add_3_91 ();
  cond__add_3 cond__add_3_92 ();
  cond__add_3 cond__add_3_93 ();
  cond__add_3 cond__add_3_94 ();
  cond__add_3 cond__add_3_95 ();
  cond__add_3 cond__add_3_96 ();
  cond__add_3 cond__add_3_97 ();
  cond__add_3 cond__add_3_98 ();
  cond__add_3 cond__add_3_99 ();
  cond__add_3 cond__add_3_100 ();
  cond__add_3 cond__add_3_101 ();
  cond__add_3 cond__add_3_102 ();
  cond__add_3 cond__add_3_103 ();
  cond__add_3 cond__add_3_104 ();
  cond__add_3 cond__add_3_105 ();
  cond__add_3 cond__add_3_106 ();
  cond__add_3 cond__add_3_107 ();
  cond__add_3 cond__add_3_108 ();
  cond__add_3 cond__add_3_109 ();
  cond__add_3 cond__add_3_110 ();
  cond__add_3 cond__add_3_111 ();
  cond__add_3 cond__add_3_112 ();
  cond__add_3 cond__add_3_113 ();
  cond__add_3 cond__add_3_114 ();
  cond__add_3 cond__add_3_115 ();
  cond__add_3 cond__add_3_116 ();
  cond__add_3 cond__add_3_117 ();
  cond__add_3 cond__add_3_118 ();
  cond__add_3 cond__add_3_119 ();
  cond__add_3 cond__add_3_120 ();
  cond__add_3 cond__add_3_121 ();
  cond__add_3 cond__add_3_122 ();
  cond__add_3 cond__add_3_123 ();
  cond__add_3 cond__add_3_124 ();
  cond__add_3 cond__add_3_125 ();
  cond__add_3 cond__add_3_126 ();
  cond__add_3 cond__add_3_127 ();
  cond__add_3 cond__add_3_128 ();
  cond__add_3 cond__add_3_129 ();
  cond__add_3 cond__add_3_130 ();
  cond__add_3 cond__add_3_131 ();
  cond__add_3 cond__add_3_132 ();
  cond__add_3 cond__add_3_133 ();
  cond__add_3 cond__add_3_134 ();
  cond__add_3 cond__add_3_135 ();
  cond__add_3 cond__add_3_136 ();
  cond__add_3 cond__add_3_137 ();
  cond__add_3 cond__add_3_138 ();
  cond__add_3 cond__add_3_139 ();
  cond__add_3 cond__add_3_140 ();
  cond__add_3 cond__add_3_141 ();
  cond__add_3 cond__add_3_142 ();
  cond__add_3 cond__add_3_143 ();
  cond__add_3 cond__add_3_144 ();
  cond__add_3 cond__add_3_145 ();
  cond__add_3 cond__add_3_146 ();
  cond__add_3 cond__add_3_147 ();
  cond__add_3 cond__add_3_148 ();
  cond__add_3 cond__add_3_149 ();
  cond__add_3 cond__add_3_150 ();
  cond__add_3 cond__add_3_151 ();
  cond__add_3 cond__add_3_152 ();
  cond__add_3 cond__add_3_153 ();
  cond__add_3 cond__add_3_154 ();

  assign _1e10s[3:1] = 3'b000;
  assign _1s[0] = In[0];
endmodule
