// Digital circuit Binary to BCD.dig as structural Verilog
module Binary_to_BCD (
  input  [7:0] In,
  output [3:0] _100s,
  output [3:0] _10s,
  output [3:0] _1s
);

  cond__add_3 cond__add_3_1 ();
  cond__add_3 cond__add_3_2 ();
  cond__add_3 cond__add_3_3 ();
  cond__add_3 cond__add_3_4 ();
  cond__add_3 cond__add_3_5 ();
  cond__add_3 cond__add_3_6 ();
  cond__add_3 cond__add_3_7 ();

  assign _1s[0] = In[0];
  assign _100s[3:2] = 2'b00;
endmodule
