// Digital circuit cond. add 3.dig as structural Verilog
module cond__add_3 (
  input  A3,
  input  A2,
  input  A1,
  input  A0,
  output Q0,
  output Q1,
  output Q2,
  output Q3
);

  wire comparator_1_gt;
  wire [3:0] add_1_s;

  Comparator #(.Bits(4)) comparator_1 (.a({A3, A2, A1, A0}), .b(4'b0100), .gt(comparator_1_gt));  // open: eq, lt
  Add #(.Bits(4)) add_1 (.a({A3, A2, A1, A0}), .b(4'b0011), .c_i(1'b0), .s(add_1_s));  // open: c_o
  Multiplexer #(.Bits(4)) multiplexer_1 (
    .sel(comparator_1_gt), .in_0({A3, A2, A1, A0}), .in_1(add_1_s), .out({Q3, Q2, Q1, Q0}));
endmodule
