// Digital circuit eater_8bit_digital.dig as structural Verilog
module eater_8bit_digital (
  input  clk,
  input  HALT,
  input  in_3,
  input  clk_2,
  input  clk_3,
  input  in_6,
  input  clk_4,
  input  MANUAL,
  input  [7:0] in_9,
  input  Manual_Load_BUS,
  input  in_11
);

  wire add_1_c_o, AI, and_1_out, and_2_out, AO, BI, CE, CLOCK, CO, EO, FI, HALT_t, II, IO, J, MI, nCLOCK, OI,
       or_1_out, or_3_out, or_4_out, or_5_out, or_6_out, relaydt_1_p7, relaydt_1_p8, relaydt_2_p2, RI, RO,
       rs_ff_1_nq, rs_ff_1_q, STEP_out, SU, sub_1_c_o;
  wire [1:0] FLAGS, multiplexer_5_out;
  wire [2:0] counterpreset_1_out;
  wire [3:0] binary_to_bcd_1__1s, binary_to_bcd_1__10s, binary_to_bcd_1__100s, counterpreset_2_out,
       Inst_Register_q, INSTRUCTION, Mem_Address_Register_q, multiplexer_6_out;
  wire [7:0] A_Register_q, add_1_s, B_Register_q, BUS, multiplexer_1_out, multiplexer_2_out,
       multiplexer_3_out, multiplexer_4_out, Output_Register_q, sub_1_s;
  wire [15:0] R2_d;

  LED u_MI (.in(MI));
  LED HT (.in(HALT_t));
  CounterPreset #(.maxValue(4), .Bits(3)) counterpreset_1 (
    .en(1'b1), .C(nCLOCK), .dir(1'b0), .in(3'b000), .ld(1'b0), .clr(in_11), .out(counterpreset_1_out));  // open: ovf
  LED u_RO (.in(RO));
  LED u_RI (.in(RI));
  // RelayDT #(.poles(2)) relaydt_1: pin names not known; wires that end beside it: in_6, clk_3, clk_2, clk, clk_4, 1'b0, relaydt_1_p7, relaydt_1_p8, in_3, relaydt_1_p7, relaydt_1_p8
  or or_1 (or_1_out, HALT, HALT_t);
  LED led_1 (.in(counterpreset_1_out[0]));
  LED led_2 (.in(counterpreset_1_out[2]));
  LED led_3 (.in(counterpreset_1_out[1]));
  LED u_IO (.in(IO));
  LED u_II (.in(II));
  // RelayDT relaydt_2: pin names not known; wires that end beside it: 1'b0, relaydt_2_p2
  EEPROMDualPort #(.AddrBits(9), .isProgramMemory("true"), .Bits(16)) R1 (
    .A({FLAGS, INSTRUCTION, counterpreset_1_out}), .Din({16{1'b0}}), .str(1'b0), .C(CLOCK), .ld(1'b1),
    .D({HALT_t, MI, RI, RO, IO, II, AI, AO, EO, SU, BI, OI, CE, CO, J, FI}));
  LED u_AI (.in(AI));
  LED u_AO (.in(AO));
  Button STEP (.out(STEP_out));
  and and_1 (and_1_out, STEP_out, MANUAL, ~or_1_out);  // And
  RS_FF rs_ff_1 (.S(and_2_out), .C(relaydt_2_p2), .R(~and_2_out), .Q(rs_ff_1_q), .nQ(rs_ff_1_nq));
  LED u_SU (.in(SU));
  LED E0 (.in(EO));
  and and_2 (and_2_out, ~MANUAL, ~or_1_out, rs_ff_1_nq);  // And
  CounterPreset #(.Bits(4)) counterpreset_2 (
    .en(CE), .C(CLOCK), .dir(1'b0), .in(BUS[3:0]), .ld(J), .clr(in_11), .out(counterpreset_2_out));  // open: ovf
  LED led_4 (.in(counterpreset_2_out[3]));
  LED u_OI (.in(OI));
  LED u_BI (.in(BI));
  or or_2 (CLOCK, and_1_out, rs_ff_1_q);
  LED led_5 (.in(counterpreset_2_out[0]));
  LED led_6 (.in(counterpreset_2_out[2]));
  LED led_7 (.in(counterpreset_2_out[1]));
  LED u_CE (.in(CE));
  LED u_CO (.in(CO));
  not not_1 (nCLOCK, CLOCK);
  assign BUS = CO ? {4'b0000, counterpreset_2_out} : 8'bz;  // Driver driver_1
  LED u_J (.in(J));
  LED u_FI (.in(FI));
  LED led_8 (.in(CLOCK));
  LED led_9 (.in(nCLOCK));
  LED led_10 (.in(BUS[7]));
  LED led_11 (.in(BUS[5]));
  LED led_12 (.in(BUS[6]));
  Multiplexer #(.Bits(8)) multiplexer_1 (.sel(in_11), .in_0(BUS), .in_1({8{1'b0}}), .out(multiplexer_1_out));
  or or_3 (or_3_out, in_11, II);
  LED led_13 (.in(BUS[3]));
  LED led_14 (.in(BUS[4]));
  Multiplexer #(.Bits(8)) multiplexer_2 (.sel(in_11), .in_0(BUS), .in_1({8{1'b0}}), .out(multiplexer_2_out));
  or or_4 (or_4_out, in_11, AI);
  Multiplexer #(.Bits(8)) multiplexer_3 (.sel(in_11), .in_0(BUS), .in_1({8{1'b0}}), .out(multiplexer_3_out));
  or or_5 (or_5_out, in_11, BI);
  LED led_15 (.in(INSTRUCTION[2]));
  LED led_16 (.in(INSTRUCTION[3]));
  assign BUS = Manual_Load_BUS ? in_9 : 8'bz;  // Driver driver_2
  LED led_17 (.in(BUS[1]));
  LED led_18 (.in(BUS[2]));
  Register #(.Bits(8)) A_Register (.D(multiplexer_2_out), .C(CLOCK), .en(or_4_out), .Q(A_Register_q));
  LED led_19 (.in(A_Register_q[7]));
  LED led_20 (.in(A_Register_q[6]));
  LED led_21 (.in(A_Register_q[5]));
  LED led_22 (.in(A_Register_q[4]));
  Register #(.Bits(8)) B_Register (.D(multiplexer_3_out), .C(CLOCK), .en(or_5_out), .Q(B_Register_q));
  LED led_23 (.in(B_Register_q[7]));
  LED led_24 (.in(B_Register_q[6]));
  LED led_25 (.in(B_Register_q[5]));
  LED led_26 (.in(B_Register_q[4]));
  Register #(.Bits(8)) Inst_Register (
    .D(multiplexer_1_out), .C(CLOCK), .en(or_3_out), .Q({INSTRUCTION, Inst_Register_q}));
  LED led_27 (.in(Inst_Register_q[3]));
  LED led_28 (.in(Inst_Register_q[2]));
  LED led_29 (.in(INSTRUCTION[0]));
  LED led_30 (.in(INSTRUCTION[1]));
  LED led_31 (.in(BUS[0]));
  LED led_32 (.in(A_Register_q[3]));
  LED led_33 (.in(A_Register_q[2]));
  LED led_34 (.in(A_Register_q[1]));
  LED led_35 (.in(A_Register_q[0]));
  LED led_36 (.in(B_Register_q[3]));
  LED led_37 (.in(B_Register_q[2]));
  LED led_38 (.in(B_Register_q[1]));
  LED led_39 (.in(B_Register_q[0]));
  assign BUS = IO ? {INSTRUCTION, Inst_Register_q} : 8'bz;  // Driver driver_3
  LED led_40 (.in(Inst_Register_q[0]));
  LED led_41 (.in(Inst_Register_q[1]));
  assign BUS = AO ? A_Register_q : 8'bz;  // Driver driver_4
  Register #(.Bits(8)) Output_Register (.D(BUS), .C(CLOCK), .en(OI), .Q(Output_Register_q));
  Binary_to_BCD binary_to_bcd_1 (
    .In(Output_Register_q), ._100s(binary_to_bcd_1__100s), ._10s(binary_to_bcd_1__10s),
    ._1s(binary_to_bcd_1__1s));
  Add #(.Bits(8)) add_1 (.a(A_Register_q), .b(B_Register_q), .c_i(1'b0), .s(add_1_s), .c_o(add_1_c_o));
  Sub #(.Bits(8)) sub_1 (.a(A_Register_q), .b(B_Register_q), .c_i(1'b0), .s(sub_1_s), .c_o(sub_1_c_o));
  Seven_Seg_Hex seven_seg_hex_1 (.d(binary_to_bcd_1__100s), .dp(1'b0));
  Multiplexer #(.Bits(8)) multiplexer_4 (.sel(SU), .in_0(add_1_s), .in_1(sub_1_s), .out(multiplexer_4_out));
  Multiplexer multiplexer_5 (.sel(SU), .in_0(add_1_c_o), .in_1(sub_1_c_o), .out(multiplexer_5_out[0]));
  Multiplexer #(.Bits(4)) multiplexer_6 (.sel(in_11), .in_0(BUS[3:0]), .in_1(4'b0000), .out(multiplexer_6_out));
  or or_6 (or_6_out, in_11, MI);
  Seven_Seg_Hex seven_seg_hex_2 (.d(binary_to_bcd_1__10s), .dp(1'b0));
  Seven_Seg_Hex seven_seg_hex_3 (.d(binary_to_bcd_1__1s), .dp(1'b0));
  assign BUS = EO ? multiplexer_4_out : 8'bz;  // Driver driver_5
  Comparator #(.Bits(8)) comparator_1 (
    .a(multiplexer_4_out), .b({8{1'b0}}), .eq(multiplexer_5_out[1]));  // open: gt, lt
  Register #(.Bits(4)) Mem_Address_Register (
    .D(multiplexer_6_out), .C(CLOCK), .en(or_6_out), .Q(Mem_Address_Register_q));
  Register #(.Bits(2)) Flag_Register (.D(multiplexer_5_out), .C(CLOCK), .en(FI), .Q(FLAGS));
  LED led_42 (.in(R2_d[7]));
  LED led_43 (.in(FLAGS[0]));
  LED led_44 (.in(FLAGS[1]));
  RAMDualPort #(.AddrBits(4), .isProgramMemory("true"), .Bits(16)) R2 (
    .A(Mem_Address_Register_q), .Din({{8{1'b0}}, BUS}), .str(RI), .C(CLOCK), .ld(1'b1), .D(R2_d));
  LED led_45 (.in(R2_d[3]));
  LED led_46 (.in(R2_d[4]));
  LED led_47 (.in(R2_d[5]));
  LED led_48 (.in(R2_d[6]));
  LED led_49 (.in(R2_d[0]));
  LED led_50 (.in(R2_d[1]));
  LED led_51 (.in(R2_d[2]));
  assign BUS = RO ? R2_d[7:0] : 8'bz;  // Driver driver_6

  // Other names for the same wires on the sheet: RESET = in_11

  // Notes on the sheet:
  //   clk: Hz: 8
  //   clk_2: Hz: 16
  //   clk_3: Hz: 64
  //   clk_4: Hz: 2
  //   MANUAL: default 1
  //   CLOCK
  //   contents of R1 (hex, n*v repeats v):
  //   4004,1408,6*0,4004,1408,4800,1200,4*0,4004,1408,4800,1020,281
  //   ,0,0,0,4004,1408,4800,1020,2c1,0,0,0,4004,1408,4800,2100,4*0,4004
  //   ,1408,a00,5*0,4004,1408,802,5*0,4004,1408,6*0,4004,1408,46*0,4004
  //   ,1408,110,5*0,4004,1408,8000,5*0,4004,1408,6*0,4004,1408,4800
  //   ,1200,4*0,4004,1408,4800,1020,281,0,0,0,4004,1408,4800,1020,2c1
  //   ,0,0,0,4004,1408,4800,2100,4*0,4004,1408,a00,5*0,4004,1408,802
  //   ,5*0,4004,1408,802,5*0,4004,1408,46*0,4004,1408,110,5*0,4004,1408
  //   ,8000,5*0,4004,1408,6*0,4004,1408,4800,1200,4*0,4004,1408,4800
  //   ,1020,281,0,0,0,4004,1408,4800,1020,2c1,0,0,0,4004,1408,4800,2100
  //   ,4*0,4004,1408,a00,5*0,4004,1408,802,5*0,4004,1408,6*0,4004,1408
  //   ,802,45*0,4004,1408,110,5*0,4004,1408,8000,5*0,4004,1408,6*0,4004
  //   ,1408,4800,1200,4*0,4004,1408,4800,1020,281,0,0,0,4004,1408,4800
  //   ,1020,2c1,0,0,0,4004,1408,4800,2100,4*0,4004,1408,a00,5*0,4004
  //   ,1408,802,5*0,4004,1408,802,5*0,4004,1408,802,45*0,4004,1408,110
  //   ,5*0,4004,1408,8000
  //   ALU
endmodule
