// Digital circuit eater_8bit_ic.dig as structural Verilog
module eater_8bit_ic (
  input  _5_Hz,
  input  On__eq__Clock,
  input  ENABLE,
  input  in_4,
  input  in_5,
  input  in_6,
  input  in_7,
  input  PROGRAM,
  input  in_9,
  input  in_10,
  input  in_11,
  input  in_12,
  input  in_13,
  input  in_14,
  input  in_15,
  input  in_16,
  input  in_17,
  input  ENABLE_2,
  input  in_19,
  input  _50_Hz
);

  wire _7404_1_pin2, _7404_1_pin6, _7408_1_pin4, _7408_1_pin5, _7408_1_pin6, _7408_1_pin8, _7408_1_pin9,
       _7408_1_pin10, _7408_2_pin3, _7408_2_pin5, _7408_2_pin11, _74138_1_pin10, _74138_1_pin11,
       _74138_1_pin12, _74138_1_pin13, _74138_1_pin14, _74138_1_pin15, _74157_1_pin1, _74157_4_pin2,
       _74157_4_pin3, _74161_1_pin1, _74161_1_pin2, _74161_2_pin1, _74161_2_pin9, _74173_1_pin7,
       _74173_6_pin9, _74173_8_pin9, _74189_1_pin3, _74245_4_pin11, _74245_4_pin12, _74245_4_pin13,
       _74245_4_pin14, _74245_4_pin15, _74245_4_pin16, _74245_4_pin17, _74245_4_pin18, _74245_4_pin19,
       _74245_5_pin11, _74245_5_pin12, _74245_5_pin13, _74245_5_pin14, _74245_5_pin15, _74245_5_pin16,
       _74245_5_pin17, _74245_5_pin18, _74245_5_pin19, _74245_6_pin19, _74245_7_pin19, _74245_8_pin19,
       _74273_1_pin1, _74273_1_pin11, _74283_1_pin2, _74283_1_pin6, _74283_1_pin9, _74283_1_pin11,
       _74283_1_pin15, _74283_2_pin2, _74283_2_pin6, _74283_2_pin11, _74283_2_pin15, AI, AO, BI, CE, CO, CY,
       EO, FI, HALT, II, IO, J, MI, not_1_out, not_2_out, not_3_out, not_4_out, not_5_out, not_6_out, OI,
       RESET, RI, RO, SET_out, SU, switchdt_1_p3, Z;
  wire [1:0] _7404_2_pin2, _7404_2_pin12, _7404_3_pin2, _7404_3_pin12, _74157_1_pin3, _74157_1_pin10,
       _74173_5_pin3, _74173_5_pin5, _74189_1_pin4, _74189_1_pin5, _74189_1_pin11, _74189_1_pin12,
       _74189_2_pin4, _74189_2_pin5, _74189_2_pin11, _74189_2_pin12, _74283_1_pin5, _74283_1_pin14,
       _74283_2_pin5, _74283_2_pin14;
  wire [3:0] _74173_1_pin14, _74173_2_pin3, _74173_4_pin14, _74173_6_pin3, _74189_1_pin1, _74245_6_pin2,
       _74245_6_pin6, _74245_7_pin2, _74245_7_pin6, _74273_1_pin2, _74273_1_pin19, _74283_1_pin10,
       _74283_2_pin13, binary_to_bcd_1__1s, binary_to_bcd_1__10s, binary_to_bcd_1__100s;
  wire [8:0] _74161_1_pin13;

  not not_1 (not_1_out, EO);
  _7408 _7408_1 (
    .pin1(1'b0), .pin2(1'b0), .pin4(_7408_1_pin4), .pin5(_7408_1_pin5), .pin6(_7408_1_pin6), .pin7(1'b0),
    .pin8(_7408_1_pin8), .pin9(_7408_1_pin9), .pin10(_7408_1_pin10), .pin11(Z), .pin12(_7408_1_pin6),
    .pin13(_7408_1_pin8), .pin14(1'b1));  // open: pin3
  _74283 _74283_1 (
    .pin1(_74283_1_pin10[1]), .pin2(_74283_1_pin2), .pin3(_74283_1_pin5[1]), .pin4(_74283_1_pin10[0]),
    .pin5(_74283_1_pin5[0]), .pin6(_74283_1_pin6), .pin7(SU), .pin8(1'b0), .pin9(_74283_1_pin9),
    .pin10(_74283_1_pin10[3]), .pin11(_74283_1_pin11), .pin12(_74283_1_pin14[1]), .pin13(_74283_1_pin10[2]),
    .pin14(_74283_1_pin14[0]), .pin15(_74283_1_pin15), .pin16(1'b1));
  _74283 _74283_2 (
    .pin1(_74283_2_pin13[1]), .pin2(_74283_2_pin2), .pin3(_74283_2_pin5[1]), .pin4(_74283_2_pin13[0]),
    .pin5(_74283_2_pin5[0]), .pin6(_74283_2_pin6), .pin7(_74283_1_pin9), .pin8(1'b0), .pin9(CY),
    .pin10(_74283_2_pin13[3]), .pin11(_74283_2_pin11), .pin12(_74283_2_pin14[1]), .pin13(_74283_2_pin13[2]),
    .pin14(_74283_2_pin14[0]), .pin15(_74283_2_pin15), .pin16(1'b1));
  _7402 _7402_1 (
    .pin1(_7408_1_pin5), .pin2(_74283_1_pin10[0]), .pin3(_74283_1_pin10[1]), .pin4(_7408_1_pin4),
    .pin5(_74283_1_pin10[2]), .pin6(_74283_1_pin10[3]), .pin7(1'b0), .pin8(_74283_2_pin13[0]),
    .pin9(_74283_2_pin13[1]), .pin10(_7408_1_pin10), .pin11(_74283_2_pin13[2]), .pin12(_74283_2_pin13[3]),
    .pin13(_7408_1_pin9), .pin14(1'b1));
  not not_2 (not_2_out, AI);
  not not_3 (not_3_out, AO);
  not not_4 (not_4_out, BI);
  not not_5 (not_5_out, in_17);
  _74161 _74161_1 (
    .pin1(_74161_1_pin1), .pin2(_74161_1_pin2), .pin3(1'b0), .pin4(1'b0), .pin5(1'b0), .pin6(1'b0),
    .pin7(1'b1), .pin8(1'b0), .pin9(1'b1), .pin10(1'b1), .pin12(_74161_1_pin13[2]),
    .pin13(_74161_1_pin13[1]), .pin14(_74161_1_pin13[0]), .pin16(1'b1));  // open: pin11, pin15
  LED led_1 (.in(HALT));
  LED led_2 (.in(MI));
  LED led_3 (.in(RI));
  // SwitchDT switchdt_1: pin names not known; wires that end beside it: _5_Hz, _50_Hz, switchdt_1_p3
  _74173 _74173_1 (
    .pin1(1'b0), .pin2(1'b0), .pin3(_74283_1_pin5[0]), .pin4(_74283_1_pin5[1]), .pin5(_74283_1_pin14[0]),
    .pin6(_74283_1_pin14[1]), .pin7(_74173_1_pin7), .pin8(1'b0), .pin9(not_2_out), .pin10(not_2_out),
    .pin11(_74173_1_pin14[3]), .pin12(_74173_1_pin14[2]), .pin13(_74173_1_pin14[1]),
    .pin14(_74173_1_pin14[0]), .pin15(RESET), .pin16(1'b1));
  _74173 _74173_2 (
    .pin1(1'b0), .pin2(1'b0), .pin3(_74173_2_pin3[0]), .pin4(_74173_2_pin3[1]), .pin5(_74173_2_pin3[2]),
    .pin6(_74173_2_pin3[3]), .pin7(_74173_1_pin7), .pin8(1'b0), .pin9(not_4_out), .pin10(not_4_out),
    .pin11(_74173_1_pin14[3]), .pin12(_74173_1_pin14[2]), .pin13(_74173_1_pin14[1]),
    .pin14(_74173_1_pin14[0]), .pin15(RESET), .pin16(1'b1));
  and and_1 (_74161_1_pin1, ~RESET, _74138_1_pin10);  // And
  LED led_4 (.in(RO));
  _7404 _7404_1 (
    .pin1(On__eq__Clock), .pin2(_7404_1_pin2), .pin3(_74173_1_pin7), .pin4(_74161_1_pin2), .pin5(HALT),
    .pin6(_7404_1_pin6), .pin7(1'b0), .pin9(1'b0), .pin11(1'b0), .pin13(1'b0), .pin14(1'b1));  // open: pin8, pin10, pin12
  _7486 _7486_1 (
    .pin1(SU), .pin2(_74173_2_pin3[0]), .pin3(_74283_1_pin6), .pin4(SU), .pin5(_74173_2_pin3[1]),
    .pin6(_74283_1_pin2), .pin7(1'b0), .pin8(_74283_1_pin15), .pin9(SU), .pin10(_74173_2_pin3[2]),
    .pin11(_74283_1_pin11), .pin12(SU), .pin13(_74173_2_pin3[3]), .pin14(1'b1));
  not not_6 (not_6_out, FI);
  LED led_5 (.in(IO));
  _74173 _74173_3 (
    .pin1(1'b0), .pin2(1'b0), .pin3(_74161_1_pin13[7]), .pin4(_74161_1_pin13[8]), .pin7(_74173_1_pin7),
    .pin8(1'b0), .pin9(not_6_out), .pin10(not_6_out), .pin11(1'b0), .pin12(1'b0), .pin13(Z), .pin14(CY),
    .pin15(RESET), .pin16(1'b1));  // open: pin5, pin6
  EEPROMDualPort #(.AddrBits(9), .isProgramMemory("true"), .Bits(8)) PC1 (
    .A({_74161_1_pin13[8:7], _74173_6_pin3, _74161_1_pin13[2:0]}), .Din({8{1'b0}}), .str(1'b0),
    .C(_74161_1_pin2), .ld(1'b1), .D({HALT, MI, RI, RO, IO, II, AI, AO}));
  LED led_6 (.in(II));
  LED led_7 (.in(AI));
  LED led_8 (.in(_74138_1_pin15));
  _74138 _74138_1 (
    .pin1(_74161_1_pin13[0]), .pin2(_74161_1_pin13[1]), .pin3(_74161_1_pin13[2]), .pin4(1'b0), .pin5(1'b0),
    .pin6(1'b1), .pin8(1'b0), .pin10(_74138_1_pin10), .pin11(_74138_1_pin11), .pin12(_74138_1_pin12),
    .pin13(_74138_1_pin13), .pin14(_74138_1_pin14), .pin15(_74138_1_pin15), .pin16(1'b1));  // open: pin7, pin9
  LED led_9 (.in(AO));
  _74173 _74173_4 (
    .pin1(1'b0), .pin2(1'b0), .pin3(_74283_2_pin5[0]), .pin4(_74283_2_pin5[1]), .pin5(_74283_2_pin14[0]),
    .pin6(_74283_2_pin14[1]), .pin7(_74173_1_pin7), .pin8(1'b0), .pin9(not_2_out), .pin10(not_2_out),
    .pin11(_74173_4_pin14[3]), .pin12(_74173_4_pin14[2]), .pin13(_74173_4_pin14[1]),
    .pin14(_74173_4_pin14[0]), .pin15(RESET), .pin16(1'b1));
  _74173 _74173_5 (
    .pin1(1'b0), .pin2(1'b0), .pin3(_74173_5_pin3[0]), .pin4(_74173_5_pin3[1]), .pin5(_74173_5_pin5[0]),
    .pin6(_74173_5_pin5[1]), .pin7(_74173_1_pin7), .pin8(1'b0), .pin9(not_4_out), .pin10(not_4_out),
    .pin11(_74173_4_pin14[3]), .pin12(_74173_4_pin14[2]), .pin13(_74173_4_pin14[1]),
    .pin14(_74173_4_pin14[0]), .pin15(RESET), .pin16(1'b1));
  LED led_10 (.in(_74138_1_pin14));
  LED led_11 (.in(_74138_1_pin13));
  EEPROMDualPort #(.AddrBits(9), .isProgramMemory("true"), .Bits(8)) PC2 (
    .A({_74161_1_pin13[8:7], _74173_6_pin3, _74161_1_pin13[2:0]}), .Din({8{1'b0}}), .str(1'b0),
    .C(_74161_1_pin2), .ld(1'b1), .D({EO, SU, BI, OI, CE, CO, J, FI}));
  LED led_12 (.in(EO));
  _7408 _7408_2 (
    .pin1(_7404_1_pin2), .pin2(in_19), .pin3(_7408_2_pin3), .pin4(_7404_1_pin6), .pin5(_7408_2_pin5),
    .pin6(_74173_1_pin7), .pin7(1'b0), .pin9(1'b0), .pin10(1'b0), .pin11(_7408_2_pin11),
    .pin12(switchdt_1_p3), .pin13(On__eq__Clock), .pin14(1'b1));  // open: pin8
  _7486 _7486_2 (
    .pin1(SU), .pin2(_74173_5_pin3[0]), .pin3(_74283_2_pin6), .pin4(SU), .pin5(_74173_5_pin3[1]),
    .pin6(_74283_2_pin2), .pin7(1'b0), .pin8(_74283_2_pin15), .pin9(SU), .pin10(_74173_5_pin5[0]),
    .pin11(_74283_2_pin11), .pin12(SU), .pin13(_74173_5_pin5[1]), .pin14(1'b1));
  LED led_13 (.in(_74138_1_pin12));
  LED led_14 (.in(_74138_1_pin11));
  LED led_15 (.in(BI));
  LED led_16 (.in(SU));
  LED led_17 (.in(OI));
  LED led_18 (.in(CE));
  LED led_19 (.in(CO));
  LED led_20 (.in(J));
  _7432 _7432_1 (
    .pin1(1'b0), .pin2(1'b0), .pin4(1'b0), .pin5(1'b0), .pin7(1'b0), .pin9(1'b0), .pin10(1'b0),
    .pin11(_7408_2_pin5), .pin12(_7408_2_pin3), .pin13(_7408_2_pin11), .pin14(1'b1));  // open: pin3, pin6, pin8
  _74245 _74245_1 (
    .pin1(1'b1), .pin2(_74283_1_pin5[0]), .pin3(_74283_1_pin5[1]), .pin4(_74283_1_pin14[0]),
    .pin5(_74283_1_pin14[1]), .pin6(_74283_2_pin5[0]), .pin7(_74283_2_pin5[1]), .pin8(_74283_2_pin14[0]),
    .pin9(_74283_2_pin14[1]), .pin10(1'b0), .pin11(_74173_4_pin14[3]), .pin12(_74173_4_pin14[2]),
    .pin13(_74173_4_pin14[1]), .pin14(_74173_4_pin14[0]), .pin15(_74173_1_pin14[3]),
    .pin16(_74173_1_pin14[2]), .pin17(_74173_1_pin14[1]), .pin18(_74173_1_pin14[0]), .pin19(not_3_out),
    .pin20(1'b1));
  _74245 _74245_2 (
    .pin1(1'b1), .pin2(_74283_1_pin10[0]), .pin3(_74283_1_pin10[1]), .pin4(_74283_1_pin10[2]),
    .pin5(_74283_1_pin10[3]), .pin6(_74283_2_pin13[0]), .pin7(_74283_2_pin13[1]), .pin8(_74283_2_pin13[2]),
    .pin9(_74283_2_pin13[3]), .pin10(1'b0), .pin11(_74173_4_pin14[3]), .pin12(_74173_4_pin14[2]),
    .pin13(_74173_4_pin14[1]), .pin14(_74173_4_pin14[0]), .pin15(_74173_1_pin14[3]),
    .pin16(_74173_1_pin14[2]), .pin17(_74173_1_pin14[1]), .pin18(_74173_1_pin14[0]), .pin19(not_1_out),
    .pin20(1'b1));
  _74245 _74245_3 (
    .pin1(1'b1), .pin2(_74173_2_pin3[0]), .pin3(_74173_2_pin3[1]), .pin4(_74173_2_pin3[2]),
    .pin5(_74173_2_pin3[3]), .pin6(_74173_5_pin3[0]), .pin7(_74173_5_pin3[1]), .pin8(_74173_5_pin5[0]),
    .pin9(_74173_5_pin5[1]), .pin10(1'b0), .pin11(_74173_4_pin14[3]), .pin12(_74173_4_pin14[2]),
    .pin13(_74173_4_pin14[1]), .pin14(_74173_4_pin14[0]), .pin15(_74173_1_pin14[3]),
    .pin16(_74173_1_pin14[2]), .pin17(_74173_1_pin14[1]), .pin18(_74173_1_pin14[0]), .pin19(not_5_out),
    .pin20(1'b1));
  LED led_21 (.in(FI));
  Button u_RESET (.out(RESET));
  LED led_22 (.in(in_17));
  LED Clock_High (.in(_74173_1_pin7));
  LED Clock_Low (.in(_74161_1_pin2));
  LED led_23 (.in(_74161_1_pin13[8]));
  LED led_24 (.in(_74161_1_pin13[7]));
  LED led_25 (.in(_74283_2_pin14[1]));
  LED led_26 (.in(_74283_2_pin14[0]));
  LED led_27 (.in(_74283_2_pin5[1]));
  LED led_28 (.in(_74283_2_pin5[0]));
  LED led_29 (.in(_74283_1_pin14[1]));
  LED led_30 (.in(_74283_1_pin14[0]));
  LED led_31 (.in(_74283_1_pin5[1]));
  LED led_32 (.in(_74283_1_pin5[0]));
  LED led_33 (.in(_74283_2_pin13[3]));
  LED led_34 (.in(_74283_2_pin13[2]));
  LED led_35 (.in(_74283_2_pin13[1]));
  LED led_36 (.in(_74283_2_pin13[0]));
  LED led_37 (.in(_74283_1_pin10[3]));
  LED led_38 (.in(_74283_1_pin10[2]));
  LED led_39 (.in(_74283_1_pin10[1]));
  LED led_40 (.in(_74283_1_pin10[0]));
  LED led_41 (.in(_74173_5_pin5[1]));
  LED led_42 (.in(_74173_5_pin5[0]));
  LED led_43 (.in(_74173_5_pin3[1]));
  LED led_44 (.in(_74173_5_pin3[0]));
  LED led_45 (.in(_74173_2_pin3[3]));
  LED led_46 (.in(_74173_2_pin3[2]));
  LED led_47 (.in(_74173_2_pin3[1]));
  LED led_48 (.in(_74173_2_pin3[0]));
  _74245 _74245_4 (
    .pin1(1'b0), .pin2(_74173_4_pin14[3]), .pin3(_74173_4_pin14[2]), .pin4(_74173_4_pin14[1]),
    .pin5(_74173_4_pin14[0]), .pin6(_74173_1_pin14[3]), .pin7(_74173_1_pin14[2]), .pin8(_74173_1_pin14[1]),
    .pin9(_74173_1_pin14[0]), .pin10(1'b0), .pin11(_74245_4_pin11), .pin12(_74245_4_pin12),
    .pin13(_74245_4_pin13), .pin14(_74245_4_pin14), .pin15(_74245_4_pin15), .pin16(_74245_4_pin16),
    .pin17(_74245_4_pin17), .pin18(_74245_4_pin18), .pin19(_74245_4_pin19), .pin20(1'b1));
  _74245 _74245_5 (
    .pin1(1'b0), .pin2(_74173_4_pin14[3]), .pin3(_74173_4_pin14[2]), .pin4(_74173_4_pin14[1]),
    .pin5(_74173_4_pin14[0]), .pin6(_74173_1_pin14[3]), .pin7(_74173_1_pin14[2]), .pin8(_74173_1_pin14[1]),
    .pin9(_74173_1_pin14[0]), .pin10(1'b0), .pin11(_74245_5_pin11), .pin12(_74245_5_pin12),
    .pin13(_74245_5_pin13), .pin14(_74245_5_pin14), .pin15(_74245_5_pin15), .pin16(_74245_5_pin16),
    .pin17(_74245_5_pin17), .pin18(_74245_5_pin18), .pin19(_74245_5_pin19), .pin20(1'b1));
  not not_7 (_74245_4_pin19, ENABLE);
  DipSwitch dipswitch_1 (.out(_74245_4_pin18));
  LED led_49 (.in(_74173_4_pin14[3]));
  LED led_50 (.in(_74173_4_pin14[3]));
  not not_8 (_74245_5_pin19, ENABLE_2);
  DipSwitch dipswitch_2 (.out(_74245_5_pin18));
  DipSwitch dipswitch_3 (.out(_74245_4_pin17));
  DipSwitch dipswitch_4 (.out(_74245_4_pin16));
  LED led_51 (.in(_74173_4_pin14[2]));
  LED led_52 (.in(_74173_4_pin14[1]));
  LED led_53 (.in(_74173_4_pin14[0]));
  LED led_54 (.in(_74173_1_pin14[3]));
  LED led_55 (.in(_74173_4_pin14[2]));
  LED led_56 (.in(_74173_4_pin14[1]));
  LED led_57 (.in(_74173_4_pin14[0]));
  LED led_58 (.in(_74173_1_pin14[3]));
  DipSwitch dipswitch_5 (.out(_74245_5_pin17));
  DipSwitch dipswitch_6 (.out(_74245_5_pin16));
  DipSwitch dipswitch_7 (.out(_74245_4_pin15));
  DipSwitch dipswitch_8 (.out(_74245_4_pin14));
  LED led_59 (.in(_74173_1_pin14[2]));
  LED led_60 (.in(_74173_1_pin14[1]));
  LED led_61 (.in(_74173_1_pin14[0]));
  LED led_62 (.in(_74173_1_pin14[2]));
  LED led_63 (.in(_74173_1_pin14[1]));
  LED led_64 (.in(_74173_1_pin14[0]));
  DipSwitch dipswitch_9 (.out(_74245_5_pin15));
  DipSwitch dipswitch_10 (.out(_74245_5_pin14));
  DipSwitch dipswitch_11 (.out(_74245_4_pin13));
  DipSwitch dipswitch_12 (.out(_74245_4_pin12));
  DipSwitch dipswitch_13 (.out(_74245_5_pin13));
  DipSwitch dipswitch_14 (.out(_74245_5_pin12));
  DipSwitch dipswitch_15 (.out(_74245_4_pin11));
  DipSwitch dipswitch_16 (.out(_74245_5_pin11));
  LED led_65 (.in(_74245_6_pin2[3]));
  LED led_66 (.in(_74245_6_pin2[2]));
  LED led_67 (.in(_74245_6_pin2[1]));
  LED led_68 (.in(_74245_6_pin2[0]));
  LED led_69 (.in(_74173_6_pin3[3]));
  LED led_70 (.in(_74173_6_pin3[2]));
  LED led_71 (.in(_74173_6_pin3[1]));
  LED led_72 (.in(_74173_6_pin3[0]));
  LED led_73 (.in(_74245_7_pin2[3]));
  LED led_74 (.in(_74245_7_pin2[2]));
  LED led_75 (.in(_74245_7_pin2[1]));
  LED led_76 (.in(_74245_7_pin2[0]));
  LED led_77 (.in(_74189_1_pin1[3]));
  LED led_78 (.in(_74189_1_pin1[2]));
  LED led_79 (.in(_74189_1_pin1[1]));
  LED led_80 (.in(_74189_1_pin1[0]));
  LED led_81 (.in(_7404_3_pin12[1]));
  LED led_82 (.in(_7404_3_pin12[0]));
  LED led_83 (.in(_7404_3_pin2[1]));
  LED led_84 (.in(_7404_3_pin2[0]));
  LED led_85 (.in(_7404_2_pin12[1]));
  LED led_86 (.in(_7404_2_pin12[0]));
  LED led_87 (.in(_7404_2_pin2[1]));
  LED led_88 (.in(_7404_2_pin2[0]));
  _74245 _74245_6 (
    .pin1(1'b1), .pin2(_74245_6_pin2[0]), .pin3(_74245_6_pin2[1]), .pin4(_74245_6_pin2[2]),
    .pin5(_74245_6_pin2[3]), .pin6(_74245_6_pin6[0]), .pin7(_74245_6_pin6[1]), .pin8(_74245_6_pin6[2]),
    .pin9(_74245_6_pin6[3]), .pin10(1'b0), .pin11(_74173_4_pin14[3]), .pin12(_74173_4_pin14[2]),
    .pin13(_74173_4_pin14[1]), .pin14(_74173_4_pin14[0]), .pin15(_74173_1_pin14[3]),
    .pin16(_74173_1_pin14[2]), .pin17(_74173_1_pin14[1]), .pin18(_74173_1_pin14[0]), .pin19(_74245_6_pin19),
    .pin20(1'b1));
  _74245 _74245_7 (
    .pin1(1'b1), .pin2(_74245_7_pin2[0]), .pin3(_74245_7_pin2[1]), .pin4(_74245_7_pin2[2]),
    .pin5(_74245_7_pin2[3]), .pin6(_74245_7_pin6[0]), .pin7(_74245_7_pin6[1]), .pin8(_74245_7_pin6[2]),
    .pin9(_74245_7_pin6[3]), .pin10(1'b0), .pin11(_74173_4_pin14[3]), .pin12(_74173_4_pin14[2]),
    .pin13(_74173_4_pin14[1]), .pin14(_74173_4_pin14[0]), .pin15(_74173_1_pin14[3]),
    .pin16(_74173_1_pin14[2]), .pin17(_74173_1_pin14[1]), .pin18(_74173_1_pin14[0]), .pin19(_74245_7_pin19),
    .pin20(1'b1));
  _74189 _74189_1 (
    .pin1(_74189_1_pin1[0]), .pin2(1'b0), .pin3(_74189_1_pin3), .pin4(_74189_1_pin4[0]),
    .pin5(_74189_1_pin5[0]), .pin6(_74189_1_pin4[1]), .pin7(_74189_1_pin5[1]), .pin8(1'b0),
    .pin9(_74189_1_pin11[0]), .pin10(_74189_1_pin12[0]), .pin11(_74189_1_pin11[1]),
    .pin12(_74189_1_pin12[1]), .pin13(_74189_1_pin1[3]), .pin14(_74189_1_pin1[2]), .pin15(_74189_1_pin1[1]),
    .pin16(1'b1));
  _74273 _74273_1 (
    .pin1(_74273_1_pin1), .pin2(_74273_1_pin2[0]), .pin3(_74173_1_pin14[0]), .pin4(_74173_1_pin14[1]),
    .pin5(_74273_1_pin2[1]), .pin6(_74273_1_pin2[2]), .pin7(_74173_1_pin14[2]), .pin8(_74173_1_pin14[3]),
    .pin9(_74273_1_pin2[3]), .pin10(1'b0), .pin11(_74273_1_pin11), .pin12(_74273_1_pin19[0]),
    .pin13(_74173_4_pin14[0]), .pin14(_74173_4_pin14[1]), .pin15(_74273_1_pin19[1]),
    .pin16(_74273_1_pin19[2]), .pin17(_74173_4_pin14[2]), .pin18(_74173_4_pin14[3]),
    .pin19(_74273_1_pin19[3]), .pin20(1'b1));
  _74189 _74189_2 (
    .pin1(_74189_1_pin1[0]), .pin2(1'b0), .pin3(_74189_1_pin3), .pin4(_74189_2_pin4[0]),
    .pin5(_74189_2_pin5[0]), .pin6(_74189_2_pin4[1]), .pin7(_74189_2_pin5[1]), .pin8(1'b0),
    .pin9(_74189_2_pin11[0]), .pin10(_74189_2_pin12[0]), .pin11(_74189_2_pin11[1]),
    .pin12(_74189_2_pin12[1]), .pin13(_74189_1_pin1[3]), .pin14(_74189_1_pin1[2]), .pin15(_74189_1_pin1[1]),
    .pin16(1'b1));
  _74157 _74157_1 (
    .pin1(_74157_1_pin1), .pin2(in_4), .pin3(_74157_1_pin3[0]), .pin4(_74189_1_pin1[0]), .pin5(in_5),
    .pin6(_74157_1_pin3[1]), .pin7(_74189_1_pin1[1]), .pin8(1'b0), .pin9(_74189_1_pin1[2]),
    .pin10(_74157_1_pin10[0]), .pin11(in_6), .pin12(_74189_1_pin1[3]), .pin13(_74157_1_pin10[1]),
    .pin14(in_7), .pin15(1'b0), .pin16(1'b1));
  _74157 _74157_2 (
    .pin1(_74157_1_pin1), .pin2(in_9), .pin3(_74173_1_pin14[0]), .pin4(_74189_1_pin4[0]), .pin5(in_10),
    .pin6(_74173_1_pin14[1]), .pin7(_74189_1_pin4[1]), .pin8(1'b0), .pin9(_74189_1_pin12[0]),
    .pin10(_74173_1_pin14[2]), .pin11(in_11), .pin12(_74189_1_pin12[1]), .pin13(_74173_1_pin14[3]),
    .pin14(in_12), .pin15(1'b0), .pin16(1'b1));
  _74161 _74161_2 (
    .pin1(_74161_2_pin1), .pin2(_74173_1_pin7), .pin3(_74173_1_pin14[0]), .pin4(_74173_1_pin14[1]),
    .pin5(_74173_1_pin14[2]), .pin6(_74173_1_pin14[3]), .pin7(CE), .pin8(1'b0), .pin9(_74161_2_pin9),
    .pin10(CE), .pin11(_74245_6_pin2[3]), .pin12(_74245_6_pin2[2]), .pin13(_74245_6_pin2[1]),
    .pin14(_74245_6_pin2[0]), .pin16(1'b1));  // open: pin15
  _74173 _74173_6 (
    .pin1(1'b0), .pin2(1'b0), .pin3(_74173_6_pin3[0]), .pin4(_74173_6_pin3[1]), .pin5(_74173_6_pin3[2]),
    .pin6(_74173_6_pin3[3]), .pin7(_74173_1_pin7), .pin8(1'b0), .pin9(_74173_6_pin9), .pin10(_74173_6_pin9),
    .pin11(_74173_4_pin14[3]), .pin12(_74173_4_pin14[2]), .pin13(_74173_4_pin14[1]),
    .pin14(_74173_4_pin14[0]), .pin15(RESET), .pin16(1'b1));
  Seven_Seg_Hex seven_seg_hex_1 (.d(binary_to_bcd_1__100s), .dp(1'b0));
  Binary_to_BCD binary_to_bcd_1 (
    .In({_74273_1_pin19, _74273_1_pin2}), ._100s(binary_to_bcd_1__100s), ._10s(binary_to_bcd_1__10s),
    ._1s(binary_to_bcd_1__1s));
  Seven_Seg_Hex seven_seg_hex_2 (.d(binary_to_bcd_1__10s), .dp(1'b0));
  Seven_Seg_Hex seven_seg_hex_3 (.d(binary_to_bcd_1__1s), .dp(1'b0));
  _7404 _7404_2 (
    .pin1(_74189_1_pin5[0]), .pin2(_7404_2_pin2[0]), .pin3(_74189_1_pin5[1]), .pin4(_7404_2_pin2[1]),
    .pin5(1'b0), .pin7(1'b0), .pin9(1'b0), .pin10(_7404_2_pin12[0]), .pin11(_74189_1_pin11[0]),
    .pin12(_7404_2_pin12[1]), .pin13(_74189_1_pin11[1]), .pin14(1'b1));  // open: pin6, pin8
  _74173 _74173_7 (
    .pin1(1'b0), .pin2(1'b0), .pin3(_74245_7_pin2[0]), .pin4(_74245_7_pin2[1]), .pin5(_74245_7_pin2[2]),
    .pin6(_74245_7_pin2[3]), .pin7(_74173_1_pin7), .pin8(1'b0), .pin9(_74173_6_pin9), .pin10(_74173_6_pin9),
    .pin11(_74173_1_pin14[3]), .pin12(_74173_1_pin14[2]), .pin13(_74173_1_pin14[1]),
    .pin14(_74173_1_pin14[0]), .pin15(RESET), .pin16(1'b1));
  _74173 _74173_8 (
    .pin1(1'b0), .pin2(1'b0), .pin3(_74157_1_pin3[0]), .pin4(_74157_1_pin3[1]), .pin5(_74157_1_pin10[0]),
    .pin6(_74157_1_pin10[1]), .pin7(_74173_1_pin7), .pin8(1'b0), .pin9(_74173_8_pin9), .pin10(_74173_8_pin9),
    .pin11(_74173_1_pin14[3]), .pin12(_74173_1_pin14[2]), .pin13(_74173_1_pin14[1]),
    .pin14(_74173_1_pin14[0]), .pin15(RESET), .pin16(1'b1));
  _74157 _74157_3 (
    .pin1(_74157_1_pin1), .pin2(in_13), .pin3(_74173_4_pin14[0]), .pin4(_74189_2_pin4[0]), .pin5(in_14),
    .pin6(_74173_4_pin14[1]), .pin7(_74189_2_pin4[1]), .pin8(1'b0), .pin9(_74189_2_pin12[0]),
    .pin10(_74173_4_pin14[2]), .pin11(in_15), .pin12(_74189_2_pin12[1]), .pin13(_74173_4_pin14[3]),
    .pin14(in_16), .pin15(1'b0), .pin16(1'b1));
  _7408 _7408_3 (
    .pin1(1'b0), .pin2(1'b0), .pin4(1'b0), .pin5(1'b0), .pin7(1'b0), .pin9(1'b0), .pin10(1'b0),
    .pin11(_74273_1_pin11), .pin12(OI), .pin13(_74173_1_pin7), .pin14(1'b1));  // open: pin3, pin6, pin8
  _7404 _7404_3 (
    .pin1(_74189_2_pin5[0]), .pin2(_7404_3_pin2[0]), .pin3(_74189_2_pin5[1]), .pin4(_7404_3_pin2[1]),
    .pin5(1'b0), .pin7(1'b0), .pin9(1'b0), .pin10(_7404_3_pin12[0]), .pin11(_74189_2_pin11[0]),
    .pin12(_7404_3_pin12[1]), .pin13(_74189_2_pin11[1]), .pin14(1'b1));  // open: pin6, pin8
  not not_9 (_74161_2_pin9, J);
  not not_10 (_74173_8_pin9, MI);
  not not_11 (_74157_1_pin1, PROGRAM);
  not not_12 (_74161_2_pin1, RESET);
  not not_13 (_74245_6_pin19, CO);
  not not_14 (_74173_6_pin9, II);
  not not_15 (_74245_7_pin19, IO);
  not not_16 (_74273_1_pin1, RESET);
  _74245 _74245_8 (
    .pin1(1'b1), .pin2(_7404_2_pin2[0]), .pin3(_7404_2_pin2[1]), .pin4(_7404_2_pin12[0]),
    .pin5(_7404_2_pin12[1]), .pin6(_7404_3_pin2[0]), .pin7(_7404_3_pin2[1]), .pin8(_7404_3_pin12[0]),
    .pin9(_7404_3_pin12[1]), .pin10(1'b0), .pin11(_74173_4_pin14[3]), .pin12(_74173_4_pin14[2]),
    .pin13(_74173_4_pin14[1]), .pin14(_74173_4_pin14[0]), .pin15(_74173_1_pin14[3]),
    .pin16(_74173_1_pin14[2]), .pin17(_74173_1_pin14[1]), .pin18(_74173_1_pin14[0]), .pin19(_74245_8_pin19),
    .pin20(1'b1));
  _74157 _74157_4 (
    .pin1(_74157_1_pin1), .pin2(_74157_4_pin2), .pin3(_74157_4_pin3), .pin4(_74189_1_pin3), .pin5(1'b0),
    .pin6(1'b0), .pin8(1'b0), .pin10(1'b0), .pin11(1'b0), .pin13(1'b0), .pin14(1'b0), .pin15(1'b0),
    .pin16(1'b1));  // open: pin7, pin9, pin12
  not not_17 (_74157_4_pin2, SET_out);
  Button SET (.out(SET_out));
  _7400 _7400_1 (
    .pin1(1'b0), .pin2(1'b0), .pin4(1'b0), .pin5(1'b0), .pin7(1'b0), .pin9(1'b0), .pin10(1'b0),
    .pin11(_74157_4_pin3), .pin12(RI), .pin13(_74173_1_pin7), .pin14(1'b1));  // open: pin3, pin6, pin8
  not not_18 (_74245_8_pin19, RO);
  // also tied to GND on the sheet: {_74245_6_pin6[0], _74245_6_pin6[1], _74245_6_pin6[2], _74245_6_pin6[3], _74245_7_pin6[0], _74245_7_pin6[1], _74245_7_pin6[2], _74245_7_pin6[3]}

  // Other names for the same wires on the sheet: BO = in_17

  // Notes on the sheet:
  //   _5_Hz: Hz: 5
  //   _50_Hz: Hz: 50
  //   ALU
  //   Flag Register
  //   Clock
  //   A REG
  //   B REG
  //   contents of PC1 (hex, n*v repeats v):
  //   40,14,6*0,40,14,48,12,4*0,40,14,48,10,2,0,0,0,40,14,48,10,2,0,0,0
  //   ,40,14,48,21,4*0,40,14,a,5*0,40,14,8,5*0,40,14,6*0,40,14,46*0
  //   ,40,14,1,5*0,40,14,80,5*0,40,14,6*0,40,14,48,12,4*0,40,14,48,10
  //   ,2,0,0,0,40,14,48,10,2,0,0,0,40,14,48,21,4*0,40,14,a,5*0,40,14
  //   ,8,5*0,40,14,8,5*0,40,14,46*0,40,14,1,5*0,40,14,80,5*0,40,14,6*0
  //   ,40,14,48,12,4*0,40,14,48,10,2,0,0,0,40,14,48,10,2,0,0,0,40,14
  //   ,48,21,4*0,40,14,a,5*0,40,14,8,5*0,40,14,6*0,40,14,8,45*0,40,14
  //   ,1,5*0,40,14,80,5*0,40,14,6*0,40,14,48,12,4*0,40,14,48,10,2,0,0,0
  //   ,40,14,48,10,2,0,0,0,40,14,48,21,4*0,40,14,a,5*0,40,14,8,5*0,40
  //   ,14,8,5*0,40,14,8,45*0,40,14,1,5*0,40,14,80
  //   contents of PC2 (hex, n*v repeats v):
  //   4,8,6*0,4,8,6*0,4,8,0,20,81,0,0,0,4,8,0,20,c1,0,0,0,4,8,6*0,4
  //   ,8,6*0,4,8,2,5*0,4,8,6*0,4,8,46*0,4,8,10,5*0,4,8,6*0,4,8,6*0,4
  //   ,8,6*0,4,8,0,20,81,0,0,0,4,8,0,20,c1,0,0,0,4,8,6*0,4,8,6*0,4,8
  //   ,2,5*0,4,8,2,5*0,4,8,46*0,4,8,10,5*0,4,8,6*0,4,8,6*0,4,8,6*0,4
  //   ,8,0,20,81,0,0,0,4,8,0,20,c1,0,0,0,4,8,6*0,4,8,6*0,4,8,2,5*0,4
  //   ,8,6*0,4,8,2,45*0,4,8,10,5*0,4,8,6*0,4,8,6*0,4,8,6*0,4,8,0,20
  //   ,81,0,0,0,4,8,0,20,c1,0,0,0,4,8,6*0,4,8,6*0,4,8,2,5*0,4,8,2,5*0
  //   ,4,8,2,45*0,4,8,10,5*0,4,8
  //   BUS
  //   CLOCK
  //   Bus
  //   D7-D0
  //   Program Counter
  //   Inst REG
  //   Programming
  //   16B RAM
  //   Output Register
  //   ADDRESS
  //   PROGRAM
  //   A0-A3
  //   PROGRAM
  //   D0-D7
endmodule
