// Digital circuit eater_8bit_relay.dig as structural Verilog
module eater_8bit_relay (
  input  clk,
  input  in_2,
  input  clk_2,
  input  clk_3,
  input  in_5,
  input  clk_4,
  input  MANUAL,
  input  in_8,
  input  in_9,
  input  in_10,
  input  in_11,
  input  in_12,
  input  in_13,
  input  in_14,
  input  in_15,
  input  SELECT,
  input  in_17,
  input  [7:0] _1,
  input  [2:0] in_19,
  input  [3:0] _1_2,
  input  in_21,
  input  [2:0] _1_3
);

  wire and_1_out, and_2_out, and_3_out, AND_E, B_SIGN, CARRY, CE, CLOCK, CO, HALT, INCB_E, J, LRAM, nCLOCK,
       NOTB_E, or_2_out, or_3_out, or_4_out, or_5_out, or_6_out, or_7_out, or_8_out, or_10_out, or_11_out,
       OR_E, relay_2_p2, relay_3_p2, relay_4_p2, relay_5_p2, relay_6_p2, relay_7_p2, relay_8_p2, relay_9_p2,
       relay_10_p2, relay_11_p2, relay_12_p2, relay_13_p3, relay_14_p2, relay_15_p2, relay_16_p2,
       relay_17_p2, relay_18_p2, relay_19_p4, relay_20_p2, relay_21_p4, relay_22_p4, relay_23_p4,
       relay_24_p4, relay_25_p4, relay_26_p4, relay_27_p4, relay_28_p4, relay_29_p4, relay_30_p4,
       relay_31_p4, relay_32_p4, relay_33_p4, relay_34_p4, relay_35_p4, relay_36_p4, relay_37_p4,
       relay_38_p4, relay_39_p4, relay_40_p4, relay_41_p4, relay_42_p4, relay_43_p4, relay_44_p4,
       relay_45_p4, relay_46_p4, relay_47_p4, relay_48_p4, relay_49_p4, relay_50_p4, relay_52_p4,
       relay_53_p4, relay_54_p4, relay_55_p4, relay_56_p4, relay_57_p4, relay_58_p4, relay_63_p3,
       relay_63_p4, relay_65_p2, relay_66_p4, relay_67_p3, relay_68_p2, relay_69_p4, relay_70_p4,
       relay_71_p4, relay_73_p2, relay_75_p4, relay_80_p4, relay_81_p4, relaydt_1_p7, relaydt_1_p8,
       relaydt_2_p2, relaydt_3_p8, relaydt_4_p8, relaydt_5_p8, relaydt_6_p8, relaydt_8_p8, relaydt_10_p3,
       relaydt_10_p5, relaydt_11_p1, relaydt_11_p4, relaydt_11_p5, relaydt_11_p7, relaydt_11_p8,
       relaydt_11_p10, relaydt_12_p5, relaydt_12_p6, relaydt_14_p4, relaydt_14_p5, relaydt_16_p4,
       relaydt_16_p5, relaydt_18_p4, relaydt_18_p5, relaydt_20_p3, relaydt_20_p5, relaydt_20_p6,
       relaydt_21_p4, relaydt_21_p5, relaydt_23_p2, relaydt_23_p3, relaydt_24_p8, relaydt_33_p1,
       relaydt_33_p2, relaydt_40_p4, relaydt_40_p6, relaydt_41_p1, relaydt_41_p4, relaydt_41_p5,
       relaydt_41_p7, relaydt_41_p8, relaydt_41_p10, relaydt_49_p1, relaydt_49_p2, relaydt_53_p4,
       relaydt_53_p6, relaydt_59_p1, relaydt_59_p5, relaydt_59_p6, relaydt_59_p8, relaydt_62_p1,
       relaydt_62_p2, relaydt_68_p4, relaydt_68_p5, relaydt_69_p2, relaydt_89_p1, relaydt_89_p4,
       relaydt_89_p6, relaydt_91_p1, relaydt_91_p4, relaydt_91_p6, relaydt_92_p3, relaydt_92_p6,
       relaydt_92_p9, relaydt_92_p12, relaydt_92_p17, relaydt_94_p1, relaydt_94_p4, relaydt_94_p5,
       relaydt_94_p7, relaydt_94_p8, relaydt_94_p10, relaydt_95_p1, relaydt_95_p4, relaydt_95_p5,
       relaydt_95_p7, relaydt_95_p8, relaydt_95_p10, relaydt_96_p4, relaydt_96_p6, relaydt_96_p7,
       relaydt_101_p3, relaydt_101_p5, relaydt_102_p1, relaydt_102_p2, relaydt_103_p1, relaydt_103_p2,
       relaydt_104_p1, relaydt_104_p4, relaydt_104_p5, relaydt_104_p7, relaydt_104_p8, relaydt_104_p10,
       relaydt_105_p3, relaydt_105_p6, relaydt_105_p9, relaydt_105_p14, relaydt_108_p4, relaydt_108_p6,
       relaydt_110_p4, relaydt_110_p6, relaydt_113_p1, relaydt_113_p4, relaydt_113_p5, relaydt_113_p7,
       relaydt_113_p8, relaydt_113_p10, relaydt_114_p1, relaydt_114_p4, relaydt_114_p5, relaydt_114_p7,
       relaydt_114_p8, relaydt_114_p10, relaydt_116_p4, relaydt_116_p6, relaydt_117_p1, relaydt_117_p2,
       relaydt_118_p1, relaydt_118_p4, relaydt_118_p5, relaydt_118_p7, relaydt_118_p8, relaydt_118_p10,
       relaydt_119_p3, relaydt_119_p6, relaydt_119_p9, relaydt_119_p14, relaydt_122_p4, relaydt_122_p6,
       relaydt_123_p1, relaydt_123_p2, relaydt_125_p4, relaydt_125_p6, relaydt_126_p1, relaydt_126_p2,
       relaydt_128_p4, relaydt_128_p6, relaydt_128_p7, relaydt_129_p1, relaydt_129_p4, relaydt_129_p5,
       relaydt_129_p7, relaydt_129_p8, relaydt_129_p10, relaydt_130_p1, relaydt_130_p4, relaydt_130_p5,
       relaydt_130_p7, relaydt_130_p8, relaydt_130_p10, relaydt_133_p1, relaydt_133_p2, relaydt_136_p4,
       relaydt_136_p6, relaydt_137_p3, relaydt_137_p6, relaydt_137_p9, relaydt_137_p14, relaydt_139_p1,
       relaydt_139_p2, relaydt_140_p1, relaydt_140_p2, relaydt_141_p6, relaydt_142_p1, relaydt_142_p4,
       relaydt_142_p5, relaydt_142_p7, relaydt_142_p8, relaydt_142_p10, relaydt_144_p4, relaydt_144_p6,
       relaydt_146_p4, relaydt_146_p6, relaydt_147_p6, relaydt_150_p1, relaydt_150_p4, relaydt_150_p5,
       relaydt_150_p7, relaydt_150_p8, relaydt_150_p10, relaydt_151_p1, relaydt_151_p4, relaydt_151_p5,
       relaydt_151_p7, relaydt_151_p8, relaydt_151_p10, relaydt_152_p6, relaydt_154_p1, relaydt_154_p2,
       relaydt_155_p3, relaydt_155_p6, relaydt_155_p9, relaydt_155_p14, relaydt_160_p4, relaydt_160_p6,
       relaydt_161_p1, relaydt_161_p2, relaydt_162_p1, relaydt_162_p2, relaydt_163_p6, relaydt_165_p1,
       relaydt_165_p5, relaydt_165_p6, relaydt_165_p8, relaydt_167_p4, relaydt_167_p6, relaydt_169_p4,
       relaydt_169_p6, relaydt_170_p6, relaydt_171_p3, relaydt_171_p6, relaydt_171_p9, relaydt_171_p14,
       relaydt_173_p1, relaydt_173_p4, relaydt_173_p5, relaydt_173_p7, relaydt_173_p8, relaydt_173_p10,
       relaydt_174_p1, relaydt_174_p4, relaydt_174_p5, relaydt_174_p7, relaydt_174_p8, relaydt_174_p10,
       relaydt_175_p6, relaydt_178_p1, relaydt_178_p2, relaydt_178_p15, relaydt_179_p11, relaydt_179_p12,
       relaydt_179_p13, relaydt_179_p14, relaydt_180_p6, relaydt_182_p5, relaydt_183_p1, relaydt_183_p2,
       relaydt_184_p1, relaydt_184_p2, relaydt_186_p3, relaydt_186_p4, relaydt_187_p3, relaydt_187_p6,
       relaydt_187_p9, relaydt_187_p14, relaydt_190_p4, relaydt_190_p6, relaydt_192_p4, relaydt_192_p6,
       relaydt_196_p1, relaydt_196_p4, relaydt_196_p5, relaydt_196_p7, relaydt_196_p8, relaydt_196_p10,
       relaydt_197_p1, relaydt_197_p4, relaydt_197_p5, relaydt_197_p7, relaydt_197_p8, relaydt_197_p10,
       relaydt_198_p11, relaydt_198_p12, relaydt_198_p13, relaydt_198_p14, relaydt_200_p5, relaydt_201_p3,
       relaydt_201_p6, relaydt_201_p9, relaydt_204_p4, relaydt_204_p6, relaydt_205_p1, relaydt_205_p2,
       relaydt_207_p4, relaydt_207_p6, relaydt_208_p1, relaydt_208_p2, relaydt_209_p1, relaydt_209_p4,
       relaydt_209_p5, relaydt_209_p7, relaydt_209_p8, relaydt_209_p10, relaydt_210_p1, relaydt_210_p4,
       relaydt_210_p5, relaydt_210_p7, relaydt_210_p8, relaydt_210_p10, relaydt_211_p11, relaydt_211_p12,
       relaydt_211_p13, relaydt_211_p14, relaydt_212_p5, relaydt_214_p1, relaydt_214_p2, relaydt_215_p1,
       relaydt_215_p2, relaydt_217_p4, relaydt_217_p6, relaydt_219_p4, relaydt_219_p6, relaydt_221_p1,
       relaydt_221_p5, relaydt_221_p6, relaydt_221_p8, relaydt_222_p1, relaydt_222_p5, relaydt_222_p6,
       relaydt_222_p8, relaydt_223_p1, relaydt_223_p2, relaydt_224_p1, relaydt_224_p2, relaydt_225_p11,
       relaydt_225_p12, relaydt_225_p13, relaydt_225_p14, relaydt_227_p1, relaydt_227_p5, relaydt_227_p9,
       relaydt_227_p13, relaydt_227_p19, relaydt_227_p23, relaydt_227_p24, relaydt_227_p25, RLA, RLB, RLC,
       RLI, RML, ROL, rs_ff_1_nq, rs_ff_1_q, RSA, RSB, RSI, SCZL, SHLB_E, SRAM, STEP_out, SUM_E, XOR_E, ZERO;
  wire [0:0] relay_25_p5, relaydt_44_p3, relaydt_50_p3, relaydt_54_p3, relaydt_58_p3, relaydt_60_p3,
       relaydt_62_p11, relaydt_63_p3, relaydt_66_p3, relaydt_67_p3, relaydt_70_p3, relaydt_73_p3,
       relaydt_74_p3, relaydt_76_p3, relaydt_79_p3, relaydt_80_p3, relaydt_82_p3, relaydt_85_p3,
       relaydt_86_p3, relaydt_106_p14, relaydt_120_p3, relaydt_120_p6, relaydt_120_p9, relaydt_120_p14,
       relaydt_134_p1, relaydt_138_p3, relaydt_138_p6, relaydt_138_p9, relaydt_138_p14, relaydt_139_p11,
       relaydt_140_p11, relaydt_154_p11, relaydt_156_p3, relaydt_156_p6, relaydt_156_p9, relaydt_156_p14,
       relaydt_157_p1, relaydt_161_p11, relaydt_162_p11, relaydt_164_p1, relaydt_172_p3, relaydt_172_p6,
       relaydt_172_p9, relaydt_172_p14, relaydt_176_p1, relaydt_178_p11, relaydt_181_p1, relaydt_183_p11,
       relaydt_184_p11, relaydt_185_p1, relaydt_188_p3, relaydt_188_p6, relaydt_188_p9, relaydt_188_p14,
       relaydt_202_p3, relaydt_202_p6, relaydt_202_p10, relaydt_205_p11, relaydt_208_p11, relaydt_214_p11,
       relaydt_215_p11, relaydt_223_p11, relaydt_224_p11;
  wire [1:0] ALU_F, relaydt_13_p2, relaydt_22_p2, relaydt_30_p2, relaydt_33_p11, relaydt_93_p3,
       relaydt_93_p6, relaydt_93_p9, relaydt_93_p12, relaydt_102_p11, relaydt_103_p11, relaydt_117_p11,
       relaydt_148_p1, RL_F, RS_F;
  wire [2:0] REG_uCOUNT, relaydt_24_p6, SCZ, uCIncrement;
  wire [3:0] binary_to_bcd_1__1s, binary_to_bcd_1__10s, binary_to_bcd_1__100s, CIncrement, INST, REG_COUNT,
       relaydt_112_p5;
  wire [6:0] REG_B;
  wire [7:0] BUS, REG_C, relaydt_3_p5, relaydt_4_p5, relaydt_5_p5, relaydt_6_p5, relaydt_7_p5, relaydt_8_p5,
       relaydt_97_p5;
  wire [15:0] R2_d;

  // RelayDT #(.poles(2)) relaydt_1: pin names not known; wires that end beside it: in_5, clk_3, clk_2, clk, clk_4, 1'b0, relaydt_1_p7, relaydt_1_p8, in_2, relaydt_1_p7, relaydt_1_p8
  // RelayDT relaydt_2: pin names not known; wires that end beside it: 1'b0, relaydt_2_p2
  Button STEP (.out(STEP_out));
  and and_1 (and_1_out, STEP_out, MANUAL, ~HALT);  // And
  RS_FF rs_ff_1 (.S(and_2_out), .C(relaydt_2_p2), .R(~and_2_out), .Q(rs_ff_1_q), .nQ(rs_ff_1_nq));
  or or_1 (CLOCK, and_1_out, rs_ff_1_q);
  and and_2 (and_2_out, ~MANUAL, ~HALT, rs_ff_1_nq);  // And
  LED led_1 (.in(BUS[7]));
  not not_1 (nCLOCK, CLOCK);
  LED led_2 (.in(BUS[6]));
  LED led_3 (.in(BUS[5]));
  LED led_4 (.in(BUS[4]));
  LED led_5 (.in(BUS[3]));
  LED led_6 (.in(CLOCK));
  LED led_7 (.in(nCLOCK));
  // Relay #(.Bits(8)) relay_1: pin names not known; wires that end beside it: SELECT, {in_15, in_14, in_13, in_12, in_11, in_10, in_9, in_8}, 1'b0
  LED led_8 (.in(BUS[2]));
  LED led_9 (.in(BUS[1]));
  LED led_10 (.in(BUS[0]));
  or or_2 (or_2_out, RLA, in_21);
  or or_3 (or_3_out, RLB, in_21);
  or or_4 (or_4_out, RLC, in_21);
  or or_5 (or_5_out, RLI, in_21);
  or or_6 (or_6_out, ROL, in_21);
  // Relay relay_2: pin names not known; wires that end beside it: or_2_out, relay_2_p2
  // RelayDT #(.Bits(8)) relaydt_3: pin names not known; wires that end beside it: in_21, {8{1'b0}}, BUS, 1'b0, relaydt_3_p5, CLOCK, 1'b0, relaydt_3_p8, 1'b0
  // Relay relay_3: pin names not known; wires that end beside it: or_3_out, relay_3_p2
  // RelayDT #(.Bits(8)) relaydt_4: pin names not known; wires that end beside it: in_21, {8{1'b0}}, BUS, 1'b0, relaydt_4_p5, CLOCK, 1'b0, relaydt_4_p8, 1'b0
  // Relay relay_4: pin names not known; wires that end beside it: or_4_out, relay_4_p2
  // RelayDT #(.Bits(8)) relaydt_5: pin names not known; wires that end beside it: in_21, {8{1'b0}}, BUS, 1'b0, relaydt_5_p5, CLOCK, 1'b0, relaydt_5_p8, 1'b0
  // Relay relay_5: pin names not known; wires that end beside it: or_5_out, relay_5_p2
  // RelayDT #(.Bits(8)) relaydt_6: pin names not known; wires that end beside it: in_21, {8{1'b0}}, BUS, 1'b0, relaydt_6_p5, CLOCK, 1'b0, relaydt_6_p8, 1'b0
  or or_7 (or_7_out, RML, in_21);
  // RelayDT #(.Bits(8)) relaydt_7: pin names not known; wires that end beside it: in_21, {8{1'b0}}, BUS, 1'b0, relaydt_7_p5, CLOCK, 1'b0
  // Relay relay_6: pin names not known; wires that end beside it: or_6_out, relay_6_p2
  // RelayDT #(.Bits(8)) relaydt_8: pin names not known; wires that end beside it: in_21, {8{1'b0}}, BUS, 1'b0, relaydt_8_p5, CLOCK, 1'b0, relaydt_8_p8, 1'b0
  or or_8 (or_8_out, in_21, and_3_out);
  // RelayDT relaydt_9: pin names not known; wires that end beside it: 1'b0, 1'b1, 1'b0
  // RelayDT relaydt_10: pin names not known; wires that end beside it: 1'b0, 1'b1, relaydt_10_p3, relaydt_10_p3, relaydt_10_p5
  // Relay relay_7: pin names not known; wires that end beside it: relaydt_3_p5[7], relay_7_p2
  // Relay relay_8: pin names not known; wires that end beside it: relaydt_4_p5[7], relay_8_p2
  // Relay relay_9: pin names not known; wires that end beside it: relaydt_5_p5[7], relay_9_p2
  // Relay relay_10: pin names not known; wires that end beside it: relaydt_6_p5[7], relay_10_p2
  // Relay relay_11: pin names not known; wires that end beside it: or_7_out, relay_11_p2
  // Relay relay_12: pin names not known; wires that end beside it: relaydt_8_p5[7], relay_12_p2
  and and_3 (and_3_out, ~uCIncrement[0], uCIncrement[1], uCIncrement[2]);  // And
  // RelayDT #(.poles(4)) relaydt_11: pin names not known; wires that end beside it: relaydt_11_p1, _1_3[2], relaydt_11_p1, relaydt_11_p4, relaydt_11_p5, 1'b0, relaydt_11_p7, relaydt_11_p8, relaydt_10_p5, relaydt_11_p10, relaydt_11_p10, relaydt_11_p7, relaydt_11_p8
  // RelayDT #(.poles(2)) relaydt_12: pin names not known; wires that end beside it: relay_2_p2, 1'b1, relay_7_p2, 1'b0, relaydt_12_p5, relaydt_12_p6, 1'b0, relaydt_12_p5, 1'b0
  // RelayDT #(.poles(2)) relaydt_13: pin names not known; wires that end beside it: relay_7_p2, relaydt_13_p2[1], 1'b0, relaydt_12_p6, 1'b1, 1'b0
  LED led_11 (.in(relaydt_13_p2[1]));
  // RelayDT #(.poles(2)) relaydt_14: pin names not known; wires that end beside it: relay_3_p2, 1'b1, relay_8_p2, relaydt_14_p4, relaydt_14_p5, 1'b0, relaydt_14_p4, 1'b0
  // RelayDT #(.poles(2)) relaydt_15: pin names not known; wires that end beside it: relay_8_p2, B_SIGN, 1'b0, relaydt_14_p5, 1'b1, 1'b0
  LED led_12 (.in(B_SIGN));
  // RelayDT #(.poles(2)) relaydt_16: pin names not known; wires that end beside it: relay_4_p2, 1'b1, relay_9_p2, relaydt_16_p4, relaydt_16_p5, 1'b0, relaydt_16_p4, 1'b0
  // RelayDT #(.poles(2)) relaydt_17: pin names not known; wires that end beside it: relay_9_p2, REG_C[7], 1'b0, relaydt_16_p5, 1'b1, 1'b0
  LED led_13 (.in(REG_C[7]));
  // RelayDT #(.poles(2)) relaydt_18: pin names not known; wires that end beside it: relay_5_p2, 1'b1, relay_10_p2, relaydt_18_p4, relaydt_18_p5, 1'b0, relaydt_18_p4, 1'b0
  // RelayDT #(.poles(2)) relaydt_19: pin names not known; wires that end beside it: relay_10_p2, INST[3], relaydt_18_p5, 1'b1, 1'b0
  LED led_14 (.in(INST[3]));
  // RelayDT #(.poles(2)) relaydt_20: pin names not known; wires that end beside it: relay_11_p2, 1'b1, relaydt_20_p3, 1'b0, relaydt_20_p5, relaydt_20_p6, 1'b0, relaydt_20_p5, 1'b0
  // Relay relay_13: pin names not known; wires that end beside it: relaydt_7_p5[3], 1'b0, relay_13_p3
  // RelayDT #(.poles(2)) relaydt_21: pin names not known; wires that end beside it: relay_6_p2, 1'b1, relay_12_p2, relaydt_21_p4, relaydt_21_p5, 1'b0, relaydt_21_p4, 1'b0
  // RelayDT #(.poles(2)) relaydt_22: pin names not known; wires that end beside it: relay_12_p2, relaydt_22_p2[1], relaydt_21_p5, 1'b1, 1'b0
  // RelayDT #(.poles(2)) relaydt_23: pin names not known; wires that end beside it: 1'b1, relaydt_23_p2, relaydt_23_p3, relaydt_23_p2, 1'b0
  // RelayDT #(.Bits(3)) relaydt_24: pin names not known; wires that end beside it: or_8_out, 3'b000, uCIncrement, nCLOCK, 1'b0, relaydt_24_p6, 1'b0, relaydt_24_p8, 1'b0
  // RelayDT relaydt_25: pin names not known; wires that end beside it: 1'b1, relaydt_3_p8, relaydt_3_p8, 1'b0
  // Relay relay_14: pin names not known; wires that end beside it: relaydt_3_p5[6], relay_14_p2
  // RelayDT relaydt_26: pin names not known; wires that end beside it: 1'b1, relaydt_4_p8, relaydt_4_p8, 1'b0
  // Relay relay_15: pin names not known; wires that end beside it: relaydt_4_p5[6], relay_15_p2
  // RelayDT relaydt_27: pin names not known; wires that end beside it: 1'b1, relaydt_5_p8, relaydt_5_p8, 1'b0
  // Relay relay_16: pin names not known; wires that end beside it: relaydt_5_p5[6], relay_16_p2
  // RelayDT relaydt_28: pin names not known; wires that end beside it: 1'b1, relaydt_6_p8, relaydt_6_p8, 1'b0
  // Relay relay_17: pin names not known; wires that end beside it: relaydt_6_p5[6], relay_17_p2
  // RelayDT relaydt_29: pin names not known; wires that end beside it: 1'b1, relay_13_p3, relaydt_20_p3, 1'b0
  // RelayDT #(.poles(2)) relaydt_30: pin names not known; wires that end beside it: relay_13_p3, relaydt_30_p2[1], relaydt_20_p6, 1'b1, 1'b0
  LED led_15 (.in(relaydt_30_p2[1]));
  // RelayDT relaydt_31: pin names not known; wires that end beside it: 1'b1, relaydt_8_p8, relaydt_8_p8, 1'b0
  // Relay relay_18: pin names not known; wires that end beside it: relaydt_8_p5[6], relay_18_p2
  // RelayDT relaydt_32: pin names not known; wires that end beside it: 1'b1, relaydt_24_p8
  // RelayDT #(.poles(4)) relaydt_33: pin names not known; wires that end beside it: relaydt_33_p1, relaydt_33_p2, relaydt_10_p5, relaydt_11_p10, relaydt_11_p8, relaydt_33_p1, relaydt_33_p1, relaydt_33_p2, 1'b0, relaydt_11_p4, relaydt_33_p11[1], 1'b1, relaydt_11_p5, REG_uCOUNT[2], 1'b0
  // RelayDT #(.poles(2)) relaydt_34: pin names not known; wires that end beside it: relay_14_p2, relay_14_p2, relaydt_13_p2[0], 1'b0, relaydt_12_p6, 1'b1, 1'b0
  LED led_16 (.in(relaydt_13_p2[0]));
  // RelayDT #(.poles(2)) relaydt_35: pin names not known; wires that end beside it: relay_15_p2, relay_15_p2, REG_B[6], 1'b0, relaydt_14_p5, 1'b1, 1'b0
  LED led_17 (.in(REG_B[6]));
  // RelayDT #(.poles(2)) relaydt_36: pin names not known; wires that end beside it: relay_16_p2, relay_16_p2, REG_C[6], 1'b0, relaydt_16_p5, 1'b1, 1'b0
  LED led_18 (.in(REG_C[6]));
  // RelayDT #(.poles(2)) relaydt_37: pin names not known; wires that end beside it: relay_17_p2, relay_17_p2, INST[2], 1'b0, relaydt_18_p5, 1'b1, 1'b0
  LED led_19 (.in(INST[2]));
  // RelayDT #(.poles(2)) relaydt_38: pin names not known; wires that end beside it: relay_18_p2, relay_18_p2, relaydt_22_p2[0], 1'b0, relaydt_21_p5, 1'b1, 1'b0
  // RelayDT relaydt_39: pin names not known; wires that end beside it: relaydt_11_p4, 1'b1, 1'b0
  // RelayDT relaydt_40: pin names not known; wires that end beside it: relaydt_11_p5, 1'b0, 1'b1, relaydt_40_p4, relaydt_40_p4, relaydt_40_p6
  LED led_20 (.in(relaydt_33_p11[1]));
  // Relay relay_19: pin names not known; wires that end beside it: relaydt_20_p3, relaydt_7_p5[2], 1'b0, relay_19_p4
  LED led_21 (.in(relaydt_30_p2[0]));
  // Relay relay_20: pin names not known; wires that end beside it: relaydt_24_p6[2], relay_20_p2
  LED led_22 (.in(REG_uCOUNT[2]));
  // RelayDT #(.poles(4)) relaydt_41: pin names not known; wires that end beside it: relaydt_41_p1, _1_3[1], relaydt_41_p1, relaydt_41_p4, relaydt_41_p5, 1'b0, relaydt_41_p7, relaydt_41_p8, relaydt_40_p6, relaydt_41_p10, relaydt_41_p10, relaydt_41_p7, relaydt_41_p8
  // Relay relay_21: pin names not known; wires that end beside it: relaydt_3_p8, relaydt_3_p5[5], 1'b0, relay_21_p4
  // Relay relay_22: pin names not known; wires that end beside it: relaydt_4_p8, relaydt_4_p5[5], 1'b0, relay_22_p4
  // Relay relay_23: pin names not known; wires that end beside it: relaydt_5_p8, relaydt_5_p5[5], 1'b0, relay_23_p4
  // Relay relay_24: pin names not known; wires that end beside it: relaydt_6_p8, relaydt_6_p5[5], 1'b0, relay_24_p4
  // RelayDT #(.poles(2)) relaydt_42: pin names not known; wires that end beside it: relay_19_p4, relay_19_p4, relaydt_30_p2[0], 1'b0, relaydt_20_p6, 1'b1, 1'b0
  // Relay relay_25: pin names not known; wires that end beside it: relaydt_8_p8, relaydt_8_p5[5], 1'b0, relay_25_p4, relay_25_p5[0]
  // RelayDT #(.poles(2)) relaydt_43: pin names not known; wires that end beside it: relay_20_p2, relay_20_p2, REG_uCOUNT[2], 1'b0, relaydt_23_p3, 1'b1, 1'b0
  // RelayDT #(.poles(2)) relaydt_44: pin names not known; wires that end beside it: relay_21_p4, relay_21_p4, relaydt_44_p3[0], 1'b0, relaydt_12_p6, 1'b1, 1'b0
  LED led_23 (.in(relaydt_44_p3[0]));
  // RelayDT #(.poles(2)) relaydt_45: pin names not known; wires that end beside it: relay_22_p4, relay_22_p4, REG_B[5], 1'b0, relaydt_14_p5, 1'b1, 1'b0
  LED led_24 (.in(REG_B[5]));
  // RelayDT #(.poles(2)) relaydt_46: pin names not known; wires that end beside it: relay_23_p4, relay_23_p4, REG_C[5], 1'b0, relaydt_16_p5, 1'b1, 1'b0
  LED led_25 (.in(REG_C[5]));
  // RelayDT #(.poles(2)) relaydt_47: pin names not known; wires that end beside it: relay_24_p4, relay_24_p4, INST[1], 1'b0, relaydt_18_p5, 1'b1, 1'b0
  LED led_26 (.in(INST[1]));
  // Relay relay_26: pin names not known; wires that end beside it: relaydt_20_p3, relaydt_7_p5[1], 1'b0, relay_26_p4
  // RelayDT #(.poles(2)) relaydt_48: pin names not known; wires that end beside it: relay_25_p4, relay_25_p4, relay_25_p5[0], 1'b0, relaydt_21_p5, 1'b1, 1'b0
  // Relay relay_27: pin names not known; wires that end beside it: relaydt_24_p8, relaydt_24_p6[1], 1'b0, relay_27_p4
  // RelayDT #(.poles(4)) relaydt_49: pin names not known; wires that end beside it: relaydt_49_p1, relaydt_49_p2, relaydt_40_p6, relaydt_41_p10, relaydt_41_p8, relaydt_49_p1, relaydt_49_p1, relaydt_49_p2, 1'b0, relaydt_41_p4, relaydt_33_p11[0], 1'b1, relaydt_41_p5, REG_uCOUNT[1], 1'b0
  LED led_27 (.in(relaydt_33_p11[0]));
  // Relay relay_28: pin names not known; wires that end beside it: relaydt_3_p8, relaydt_3_p5[4], 1'b0, relay_28_p4
  // Relay relay_29: pin names not known; wires that end beside it: relaydt_4_p8, relaydt_4_p5[4], 1'b0, relay_29_p4
  // Relay relay_30: pin names not known; wires that end beside it: relaydt_5_p8, relaydt_5_p5[4], 1'b0, relay_30_p4
  // Relay relay_31: pin names not known; wires that end beside it: relaydt_6_p8, relaydt_6_p5[4], 1'b0, relay_31_p4
  // RelayDT #(.poles(2)) relaydt_50: pin names not known; wires that end beside it: relay_26_p4, relay_26_p4, relaydt_50_p3[0], 1'b0, relaydt_20_p6, 1'b1, 1'b0
  LED led_28 (.in(relaydt_50_p3[0]));
  // Relay relay_32: pin names not known; wires that end beside it: relaydt_8_p8, relaydt_8_p5[4], 1'b0, relay_32_p4
  // RelayDT #(.poles(2)) relaydt_51: pin names not known; wires that end beside it: relay_27_p4, relay_27_p4, REG_uCOUNT[1], 1'b0, relaydt_23_p3, 1'b1, 1'b0
  LED led_29 (.in(REG_uCOUNT[1]));
  // RelayDT relaydt_52: pin names not known; wires that end beside it: relaydt_41_p4, 1'b1, 1'b0
  // RelayDT relaydt_53: pin names not known; wires that end beside it: relaydt_41_p5, 1'b0, 1'b1, relaydt_53_p4, relaydt_53_p4, relaydt_53_p6
  // RelayDT #(.poles(2)) relaydt_54: pin names not known; wires that end beside it: relay_28_p4, relay_28_p4, relaydt_54_p3[0], 1'b0, relaydt_12_p6, 1'b1, 1'b0
  LED led_30 (.in(relaydt_54_p3[0]));
  // RelayDT #(.poles(2)) relaydt_55: pin names not known; wires that end beside it: relay_29_p4, relay_29_p4, REG_B[4], 1'b0, relaydt_14_p5, 1'b1, 1'b0
  LED led_31 (.in(REG_B[4]));
  // RelayDT #(.poles(2)) relaydt_56: pin names not known; wires that end beside it: relay_30_p4, relay_30_p4, REG_C[4], 1'b0, relaydt_16_p5, 1'b1, 1'b0
  LED led_32 (.in(REG_C[4]));
  // RelayDT #(.poles(2)) relaydt_57: pin names not known; wires that end beside it: relay_31_p4, relay_31_p4, INST[0], 1'b0, relaydt_18_p5, 1'b1, 1'b0
  LED led_33 (.in(INST[0]));
  // RelayDT #(.poles(2)) relaydt_58: pin names not known; wires that end beside it: relay_32_p4, relay_32_p4, relaydt_58_p3[0], 1'b0, relaydt_21_p5, 1'b1, 1'b0
  // RelayDT #(.poles(4)) relaydt_59: pin names not known; wires that end beside it: relaydt_59_p1, _1_3[0], relaydt_59_p1, 1'b0, relaydt_59_p5, relaydt_59_p6, relaydt_53_p6, relaydt_59_p8, relaydt_59_p8, relaydt_59_p5, relaydt_59_p6
  // Relay relay_33: pin names not known; wires that end beside it: relaydt_20_p3, relaydt_7_p5[0], 1'b0, relay_33_p4
  LED led_34 (.in(relaydt_60_p3[0]));
  // Relay relay_34: pin names not known; wires that end beside it: relaydt_24_p8, relaydt_24_p6[0], 1'b0, relay_34_p4
  LED led_35 (.in(REG_uCOUNT[0]));
  // Relay relay_35: pin names not known; wires that end beside it: relaydt_3_p8, relaydt_3_p5[3], 1'b0, relay_35_p4
  // Relay relay_36: pin names not known; wires that end beside it: relaydt_4_p8, relaydt_4_p5[3], 1'b0, relay_36_p4
  // Relay relay_37: pin names not known; wires that end beside it: relaydt_5_p8, relaydt_5_p5[3], 1'b0, relay_37_p4
  // Relay relay_38: pin names not known; wires that end beside it: relaydt_6_p8, relaydt_6_p5[3], 1'b0, relay_38_p4
  // RelayDT #(.poles(2)) relaydt_60: pin names not known; wires that end beside it: relay_33_p4, relay_33_p4, relaydt_60_p3[0], 1'b0, relaydt_20_p6, 1'b1, 1'b0
  // Relay relay_39: pin names not known; wires that end beside it: relaydt_8_p8, relaydt_8_p5[3], 1'b0, relay_39_p4
  // RelayDT #(.poles(2)) relaydt_61: pin names not known; wires that end beside it: relay_34_p4, relay_34_p4, REG_uCOUNT[0], 1'b0, relaydt_23_p3, 1'b1, 1'b0
  // RelayDT #(.poles(4)) relaydt_62: pin names not known; wires that end beside it: relaydt_62_p1, relaydt_62_p2, relaydt_53_p6, relaydt_59_p8, relaydt_59_p6, relaydt_62_p1, relaydt_62_p1, relaydt_62_p2, 1'b0, 1'b1, relaydt_62_p11[0], 1'b1, 1'b0, REG_uCOUNT[0]
  LED led_36 (.in(relaydt_62_p11[0]));
  // RelayDT #(.poles(2)) relaydt_63: pin names not known; wires that end beside it: relay_35_p4, relay_35_p4, relaydt_63_p3[0], 1'b0, relaydt_12_p6, 1'b1, 1'b0
  LED led_37 (.in(relaydt_63_p3[0]));
  // RelayDT #(.poles(2)) relaydt_64: pin names not known; wires that end beside it: relay_36_p4, relay_36_p4, REG_B[3], 1'b0, relaydt_14_p5, 1'b1, 1'b0
  LED led_38 (.in(REG_B[3]));
  // RelayDT #(.poles(2)) relaydt_65: pin names not known; wires that end beside it: relay_37_p4, relay_37_p4, REG_C[3], 1'b0, relaydt_16_p5, 1'b1, 1'b0
  LED led_39 (.in(REG_C[3]));
  // RelayDT #(.poles(2)) relaydt_66: pin names not known; wires that end beside it: relay_38_p4, relay_38_p4, relaydt_66_p3[0], 1'b0, relaydt_18_p5, 1'b1, 1'b0
  LED led_40 (.in(relaydt_66_p3[0]));
  // RelayDT #(.poles(2)) relaydt_67: pin names not known; wires that end beside it: relay_39_p4, relay_39_p4, relaydt_67_p3[0], 1'b0, relaydt_21_p5, 1'b1, 1'b0
  // RelayDT #(.poles(2)) relaydt_68: pin names not known; wires that end beside it: CLOCK, 1'b1, 1'b0, relaydt_68_p4, relaydt_68_p5, relaydt_68_p4, 1'b0
  // Relay relay_40: pin names not known; wires that end beside it: relaydt_3_p8, relaydt_3_p5[2], 1'b0, relay_40_p4
  // Relay relay_41: pin names not known; wires that end beside it: relaydt_4_p8, relaydt_4_p5[2], 1'b0, relay_41_p4
  // Relay relay_42: pin names not known; wires that end beside it: relaydt_5_p8, relaydt_5_p5[2], 1'b0, relay_42_p4
  // Relay relay_43: pin names not known; wires that end beside it: relaydt_6_p8, relaydt_6_p5[2], 1'b0, relay_43_p4
  // Relay relay_44: pin names not known; wires that end beside it: relaydt_8_p8, relaydt_8_p5[2], 1'b0, relay_44_p4
  // RelayDT relaydt_69: pin names not known; wires that end beside it: 1'b1, relaydt_69_p2
  // RelayDT #(.poles(2)) relaydt_70: pin names not known; wires that end beside it: relay_40_p4, relay_40_p4, relaydt_70_p3[0], 1'b0, relaydt_12_p6, 1'b1, 1'b0
  LED led_41 (.in(relaydt_70_p3[0]));
  // RelayDT #(.poles(2)) relaydt_71: pin names not known; wires that end beside it: relay_41_p4, relay_41_p4, REG_B[2], 1'b0, relaydt_14_p5, 1'b1, 1'b0
  LED led_42 (.in(REG_B[2]));
  // RelayDT #(.poles(2)) relaydt_72: pin names not known; wires that end beside it: relay_42_p4, relay_42_p4, REG_C[2], 1'b0, relaydt_16_p5, 1'b1, 1'b0
  LED led_43 (.in(REG_C[2]));
  // RelayDT #(.poles(2)) relaydt_73: pin names not known; wires that end beside it: relay_43_p4, relay_43_p4, relaydt_73_p3[0], 1'b0, relaydt_18_p5, 1'b1, 1'b0
  LED led_44 (.in(relaydt_73_p3[0]));
  RAMDualPort #(.AddrBits(4), .isProgramMemory("true"), .Bits(16)) R2 (
    .A({relaydt_30_p2, relaydt_50_p3[0], relaydt_60_p3[0]}), .Din({{8{1'b0}}, BUS}), .str(LRAM), .C(CLOCK),
    .ld(1'b1), .D(R2_d));
  LED led_45 (.in(R2_d[6]));
  LED led_46 (.in(R2_d[7]));
  // RelayDT #(.poles(2)) relaydt_74: pin names not known; wires that end beside it: relay_44_p4, relay_44_p4, relaydt_74_p3[0], 1'b0, relaydt_21_p5, 1'b1, 1'b0
  LED led_47 (.in(R2_d[2]));
  LED led_48 (.in(R2_d[3]));
  LED led_49 (.in(R2_d[4]));
  LED led_50 (.in(R2_d[5]));
  Binary_to_BCD binary_to_bcd_1 (
    .In({relaydt_22_p2, relay_25_p5[0], relaydt_58_p3[0], relaydt_67_p3[0], relaydt_74_p3[0], relaydt_80_p3[0], relaydt_86_p3[0]}),
    ._100s(binary_to_bcd_1__100s), ._10s(binary_to_bcd_1__10s), ._1s(binary_to_bcd_1__1s));
  // Relay relay_45: pin names not known; wires that end beside it: relaydt_69_p2, relaydt_33_p11[1], 1'b0, relay_45_p4
  // Relay relay_46: pin names not known; wires that end beside it: relaydt_3_p8, relaydt_3_p5[1], 1'b0, relay_46_p4
  // Relay relay_47: pin names not known; wires that end beside it: relaydt_4_p8, relaydt_4_p5[1], 1'b0, relay_47_p4
  // Relay relay_48: pin names not known; wires that end beside it: relaydt_5_p8, relaydt_5_p5[1], 1'b0, relay_48_p4
  // Relay relay_49: pin names not known; wires that end beside it: relaydt_6_p8, relaydt_6_p5[1], 1'b0, relay_49_p4
  LED led_51 (.in(R2_d[0]));
  LED led_52 (.in(R2_d[1]));
  // Relay relay_50: pin names not known; wires that end beside it: relaydt_8_p8, relaydt_8_p5[1], 1'b0, relay_50_p4
  Seven_Seg_Hex seven_seg_hex_1 (.d(binary_to_bcd_1__100s), .dp(1'b0));
  // RelayDT #(.poles(2)) relaydt_75: pin names not known; wires that end beside it: relay_45_p4, relay_45_p4, uCIncrement[2], 1'b0, relaydt_68_p5, 1'b1, 1'b0
  LED led_53 (.in(uCIncrement[2]));
  // RelayDT #(.poles(2)) relaydt_76: pin names not known; wires that end beside it: relay_46_p4, relay_46_p4, relaydt_76_p3[0], 1'b0, relaydt_12_p6, 1'b1, 1'b0
  LED led_54 (.in(relaydt_76_p3[0]));
  // RelayDT #(.poles(2)) relaydt_77: pin names not known; wires that end beside it: relay_47_p4, relay_47_p4, REG_B[1], 1'b0, relaydt_14_p5, 1'b1, 1'b0
  LED led_55 (.in(REG_B[1]));
  // RelayDT #(.poles(2)) relaydt_78: pin names not known; wires that end beside it: relay_48_p4, relay_48_p4, REG_C[1], 1'b0, relaydt_16_p5, 1'b1, 1'b0
  LED led_56 (.in(REG_C[1]));
  // RelayDT #(.poles(2)) relaydt_79: pin names not known; wires that end beside it: relay_49_p4, relay_49_p4, relaydt_79_p3[0], 1'b0, relaydt_18_p5, 1'b1, 1'b0
  LED led_57 (.in(relaydt_79_p3[0]));
  // Relay #(.Bits(8)) relay_51: pin names not known; wires that end beside it: SRAM, R2_d[7:0], 1'b0, BUS
  // RelayDT #(.poles(2)) relaydt_80: pin names not known; wires that end beside it: relay_50_p4, relay_50_p4, relaydt_80_p3[0], 1'b0, relaydt_21_p5, 1'b1, 1'b0
  Seven_Seg_Hex seven_seg_hex_2 (.d(binary_to_bcd_1__10s), .dp(1'b0));
  // Relay relay_52: pin names not known; wires that end beside it: relaydt_69_p2, relaydt_33_p11[0], 1'b0, relay_52_p4
  // Relay relay_53: pin names not known; wires that end beside it: relaydt_3_p8, relaydt_3_p5[0], 1'b0, relay_53_p4
  // Relay relay_54: pin names not known; wires that end beside it: relaydt_4_p8, relaydt_4_p5[0], 1'b0, relay_54_p4
  // Relay relay_55: pin names not known; wires that end beside it: relaydt_5_p8, relaydt_5_p5[0], 1'b0, relay_55_p4
  // Relay relay_56: pin names not known; wires that end beside it: relaydt_6_p8, relaydt_6_p5[0], 1'b0, relay_56_p4
  // Relay relay_57: pin names not known; wires that end beside it: relaydt_8_p8, relaydt_8_p5[0], 1'b0, relay_57_p4
  Seven_Seg_Hex seven_seg_hex_3 (.d(binary_to_bcd_1__1s), .dp(1'b0));
  // RelayDT #(.poles(2)) relaydt_81: pin names not known; wires that end beside it: relay_52_p4, relay_52_p4, uCIncrement[1], 1'b0, relaydt_68_p5, 1'b1, 1'b0
  LED led_58 (.in(uCIncrement[1]));
  // RelayDT #(.poles(2)) relaydt_82: pin names not known; wires that end beside it: relay_53_p4, relay_53_p4, relaydt_82_p3[0], 1'b0, relaydt_12_p6, 1'b1, 1'b0
  LED led_59 (.in(relaydt_82_p3[0]));
  // RelayDT #(.poles(2)) relaydt_83: pin names not known; wires that end beside it: relay_54_p4, relay_54_p4, REG_B[0], 1'b0, relaydt_14_p5, 1'b1, 1'b0
  LED led_60 (.in(REG_B[0]));
  // RelayDT #(.poles(2)) relaydt_84: pin names not known; wires that end beside it: relay_55_p4, relay_55_p4, REG_C[0], 1'b0, relaydt_16_p5, 1'b1, 1'b0
  LED led_61 (.in(REG_C[0]));
  // RelayDT #(.poles(2)) relaydt_85: pin names not known; wires that end beside it: relay_56_p4, relay_56_p4, relaydt_85_p3[0], 1'b0, relaydt_18_p5, 1'b1, 1'b0
  LED led_62 (.in(relaydt_85_p3[0]));
  // RelayDT #(.poles(2)) relaydt_86: pin names not known; wires that end beside it: relay_57_p4, relay_57_p4, relaydt_86_p3[0], 1'b0, relaydt_21_p5, 1'b1, 1'b0
  // Relay relay_58: pin names not known; wires that end beside it: relaydt_69_p2, relaydt_62_p11[0], 1'b0, relay_58_p4
  // Relay #(.Bits(8)) relay_59: pin names not known; wires that end beside it: RSA, {relaydt_13_p2, relaydt_44_p3[0], relaydt_54_p3[0], relaydt_63_p3[0], relaydt_70_p3[0], relaydt_76_p3[0], relaydt_82_p3[0]}, 1'b0, BUS
  // Relay #(.Bits(8)) relay_60: pin names not known; wires that end beside it: RSB, {B_SIGN, REG_B}, 1'b0, BUS
  // Relay #(.Bits(8)) relay_61: pin names not known; wires that end beside it: in_17, REG_C, 1'b0, BUS
  // Relay #(.Bits(8)) relay_62: pin names not known; wires that end beside it: RSI, 1'b0, BUS
  // RelayDT #(.poles(2)) relaydt_87: pin names not known; wires that end beside it: relay_58_p4, relay_58_p4, uCIncrement[0], 1'b0, relaydt_68_p5, 1'b1, 1'b0
  LED led_63 (.in(uCIncrement[0]));
  LED led_64 (.in(relaydt_93_p3[1]));
  or or_9 (CARRY, relaydt_91_p1, relaydt_89_p1);
  LED led_65 (.in(relaydt_93_p9[1]));
  LED led_66 (.in(relaydt_93_p6[1]));
  // RelayDT relaydt_88: pin names not known; wires that end beside it: 1'b0, 1'b1, 1'b0
  // RelayDT relaydt_89: pin names not known; wires that end beside it: relaydt_89_p1, 1'b0, 1'b1, relaydt_89_p4, relaydt_89_p4, relaydt_89_p6
  // RelayDT relaydt_90: pin names not known; wires that end beside it: 1'b0, 1'b1, 1'b0
  // RelayDT relaydt_91: pin names not known; wires that end beside it: relaydt_91_p1, 1'b0, 1'b1, relaydt_91_p4, relaydt_91_p4, relaydt_91_p6
  // Relay relay_63: pin names not known; wires that end beside it: CLOCK, SCZL, relay_63_p3, relay_63_p4, 1'b0
  // RelayDT #(.poles(4)) relaydt_92: pin names not known; wires that end beside it: 1'b0, 1'b1, relaydt_92_p3, 1'b1, 1'b0, relaydt_92_p6, 1'b0, 1'b1, relaydt_92_p9, 1'b0, 1'b1, relaydt_92_p12, REG_C[7], 1'b0, 1'b0, 1'b1, relaydt_92_p17
  // RelayDT #(.poles(4)) relaydt_93: pin names not known; wires that end beside it: 1'b0, relaydt_92_p3, relaydt_93_p3[1], 1'b1, 1'b0, relaydt_93_p6[1], relaydt_92_p9, relaydt_92_p6, relaydt_93_p9[1], relaydt_92_p12, 1'b1, relaydt_93_p12[1], B_SIGN, 1'b0, 1'b0, relaydt_92_p17, relaydt_93_p3[0]
  LED led_67 (.in(relaydt_93_p12[1]));
  // RelayDT #(.poles(4)) relaydt_94: pin names not known; wires that end beside it: relaydt_94_p1, REG_C[7], relaydt_94_p1, relaydt_94_p4, relaydt_94_p5, 1'b0, relaydt_94_p7, relaydt_94_p8, relaydt_89_p6, relaydt_94_p10, relaydt_94_p10, relaydt_94_p7, relaydt_94_p8
  // RelayDT #(.poles(4)) relaydt_95: pin names not known; wires that end beside it: relaydt_95_p1, _1[7], relaydt_95_p1, relaydt_95_p4, relaydt_95_p5, 1'b0, relaydt_95_p7, relaydt_95_p8, relaydt_91_p6, relaydt_95_p10, relaydt_95_p10, relaydt_95_p7, relaydt_95_p8
  // RelayDT #(.poles(2)) relaydt_96: pin names not known; wires that end beside it: 1'b0, relay_63_p3, 1'b1, relaydt_96_p4, 1'b0, relaydt_96_p6, relaydt_96_p7, 1'b0, relaydt_96_p6, 1'b0
  // Relay relay_64: pin names not known; wires that end beside it: B_SIGN, relaydt_96_p4
  LED Sign (.in(SCZ[2]));
  // RelayDT #(.Bits(8)) relaydt_97: pin names not known; wires that end beside it: in_21, {8{1'b0}}, BUS, 1'b0, relaydt_97_p5
  LED led_68 (.in(HALT));
  LED led_69 (.in(relaydt_93_p3[0]));
  // RelayDT relaydt_98: pin names not known; wires that end beside it: 1'b1, relay_63_p4, relay_63_p4, 1'b0
  // RelayDT #(.poles(2)) relaydt_99: pin names not known; wires that end beside it: relaydt_96_p4, SCZ[2], relaydt_96_p7, 1'b1, 1'b0
  or or_10 (or_10_out, J, in_21);
  // RelayDT relaydt_100: pin names not known; wires that end beside it: 1'b0, 1'b1, 1'b0
  // RelayDT relaydt_101: pin names not known; wires that end beside it: 1'b0, 1'b1, relaydt_101_p3, relaydt_101_p3, relaydt_101_p5
  LED led_70 (.in(RML));
  LED led_71 (.in(LRAM));
  LED led_72 (.in(relaydt_93_p9[0]));
  LED led_73 (.in(relaydt_93_p6[0]));
  // RelayDT #(.poles(4)) relaydt_102: pin names not known; wires that end beside it: relaydt_102_p1, relaydt_102_p2, relaydt_89_p6, relaydt_94_p10, relaydt_94_p8, relaydt_102_p1, relaydt_102_p1, relaydt_102_p2, 1'b0, relaydt_94_p4, relaydt_102_p11[1], 1'b1, relaydt_94_p5, B_SIGN, 1'b0
  LED led_74 (.in(relaydt_102_p11[1]));
  // RelayDT #(.poles(4)) relaydt_103: pin names not known; wires that end beside it: relaydt_103_p1, relaydt_103_p2, relaydt_91_p6, relaydt_95_p10, relaydt_95_p8, relaydt_103_p1, relaydt_103_p1, relaydt_103_p2, 1'b0, relaydt_95_p4, relaydt_103_p11[1], 1'b1, relaydt_95_p5, B_SIGN, 1'b0
  LED led_75 (.in(relaydt_103_p11[1]));
  // Relay relay_65: pin names not known; wires that end beside it: CARRY, relay_65_p2
  or or_11 (or_11_out, CE, in_21, or_10_out);
  // RelayDT #(.poles(4)) relaydt_104: pin names not known; wires that end beside it: relaydt_104_p1, _1_2[3], relaydt_104_p1, relaydt_104_p4, relaydt_104_p5, 1'b0, relaydt_104_p7, relaydt_104_p8, relaydt_101_p5, relaydt_104_p10, relaydt_104_p10, relaydt_104_p7, relaydt_104_p8
  LED led_76 (.in(SRAM));
  // RelayDT #(.poles(4)) relaydt_105: pin names not known; wires that end beside it: 1'b1, 1'b0, relaydt_105_p3, 1'b0, 1'b1, relaydt_105_p6, 1'b0, 1'b1, relaydt_105_p9, REG_C[6], 1'b0, 1'b0, 1'b1, relaydt_105_p14
  // RelayDT #(.poles(4)) relaydt_106: pin names not known; wires that end beside it: 1'b1, 1'b0, relaydt_93_p6[0], relaydt_105_p6, relaydt_105_p3, relaydt_93_p9[0], relaydt_105_p9, 1'b1, relaydt_93_p12[0], REG_B[6], 1'b0, 1'b0, relaydt_105_p14, relaydt_106_p14[0]
  LED led_77 (.in(relaydt_93_p12[0]));
  // RelayDT relaydt_107: pin names not known; wires that end beside it: relaydt_94_p4, 1'b1, 1'b0
  // RelayDT relaydt_108: pin names not known; wires that end beside it: relaydt_94_p5, 1'b0, 1'b1, relaydt_108_p4, relaydt_108_p4, relaydt_108_p6
  // RelayDT relaydt_109: pin names not known; wires that end beside it: relaydt_95_p4, 1'b1, 1'b0
  // RelayDT relaydt_110: pin names not known; wires that end beside it: relaydt_95_p5, 1'b0, 1'b1, relaydt_110_p4, relaydt_110_p4, relaydt_110_p6
  // RelayDT #(.poles(2)) relaydt_111: pin names not known; wires that end beside it: relay_65_p2, relay_65_p2, SCZ[1], 1'b0, relaydt_96_p7, 1'b1, 1'b0
  LED u_Carry (.in(SCZ[1]));
  // RelayDT #(.Bits(4)) relaydt_112: pin names not known; wires that end beside it: or_10_out, relaydt_97_p5[3:0], CIncrement, 1'b0, relaydt_112_p5
  LED led_78 (.in(RSI));
  LED led_79 (.in(relaydt_106_p14[0]));
  // RelayDT #(.poles(4)) relaydt_113: pin names not known; wires that end beside it: relaydt_113_p1, REG_C[6], relaydt_113_p1, relaydt_113_p4, relaydt_113_p5, 1'b0, relaydt_113_p7, relaydt_113_p8, relaydt_108_p6, relaydt_113_p10, relaydt_113_p10, relaydt_113_p7, relaydt_113_p8
  // RelayDT #(.poles(4)) relaydt_114: pin names not known; wires that end beside it: relaydt_114_p1, _1[6], relaydt_114_p1, relaydt_114_p4, relaydt_114_p5, 1'b0, relaydt_114_p7, relaydt_114_p8, relaydt_110_p6, relaydt_114_p10, relaydt_114_p10, relaydt_114_p7, relaydt_114_p8
  // RelayDT relaydt_115: pin names not known; wires that end beside it: relaydt_104_p4, 1'b1, 1'b0
  // RelayDT relaydt_116: pin names not known; wires that end beside it: relaydt_104_p5, 1'b0, 1'b1, relaydt_116_p4, relaydt_116_p4, relaydt_116_p6
  // RelayDT #(.poles(4)) relaydt_117: pin names not known; wires that end beside it: relaydt_117_p1, relaydt_117_p2, relaydt_101_p5, relaydt_104_p10, relaydt_104_p8, relaydt_117_p1, relaydt_117_p1, relaydt_117_p2, 1'b0, relaydt_104_p4, relaydt_117_p11[1], 1'b1, relaydt_104_p5, REG_COUNT[3], 1'b0
  LED led_80 (.in(relaydt_117_p11[1]));
  EEPROMDualPort #(.AddrBits(10), .isProgramMemory("true"), .Bits(16)) R1 (
    .A({SCZ, INST, REG_uCOUNT}), .Din({16{1'b0}}), .str(1'b0), .C(CLOCK), .ld(1'b1),
    .D({HALT, RML, LRAM, SRAM, RSI, RLI, RS_F, ALU_F, RL_F, ROL, CE, J, SCZL}));
  LED led_81 (.in(RLI));
  LED led_82 (.in(RS_F[1]));
  LED led_83 (.in(relaydt_120_p6[0]));
  LED led_84 (.in(relaydt_120_p3[0]));
  // Relay relay_66: pin names not known; wires that end beside it: relay_63_p4, ZERO, 1'b0, relay_66_p4
  LED u_Zero (.in(SCZ[0]));
  // Relay relay_67: pin names not known; wires that end beside it: CLOCK, or_11_out, relay_67_p3
  // RelayDT #(.poles(4)) relaydt_118: pin names not known; wires that end beside it: relaydt_118_p1, _1_2[2], relaydt_118_p1, relaydt_118_p4, relaydt_118_p5, 1'b0, relaydt_118_p7, relaydt_118_p8, relaydt_116_p6, relaydt_118_p10, relaydt_118_p10, relaydt_118_p7, relaydt_118_p8
  LED led_85 (.in(RS_F[0]));
  // RelayDT #(.poles(4)) relaydt_119: pin names not known; wires that end beside it: 1'b1, 1'b0, relaydt_119_p3, 1'b0, 1'b1, relaydt_119_p6, 1'b0, 1'b1, relaydt_119_p9, REG_C[5], 1'b0, 1'b0, 1'b1, relaydt_119_p14
  // RelayDT #(.poles(4)) relaydt_120: pin names not known; wires that end beside it: 1'b1, 1'b0, relaydt_120_p3[0], relaydt_119_p6, relaydt_119_p3, relaydt_120_p6[0], relaydt_119_p9, 1'b1, relaydt_120_p9[0], REG_B[5], 1'b0, 1'b0, relaydt_119_p14, relaydt_120_p14[0]
  LED led_86 (.in(relaydt_120_p9[0]));
  // RelayDT relaydt_121: pin names not known; wires that end beside it: relaydt_113_p4, 1'b1, 1'b0
  // RelayDT relaydt_122: pin names not known; wires that end beside it: relaydt_113_p5, 1'b0, 1'b1, relaydt_122_p4, relaydt_122_p4, relaydt_122_p6
  // RelayDT #(.poles(4)) relaydt_123: pin names not known; wires that end beside it: relaydt_123_p1, relaydt_123_p2, relaydt_108_p6, relaydt_113_p10, relaydt_113_p8, relaydt_123_p1, relaydt_123_p1, relaydt_123_p2, 1'b0, relaydt_113_p4, relaydt_102_p11[0], 1'b1, relaydt_113_p5, REG_B[6], 1'b0
  LED led_87 (.in(relaydt_102_p11[0]));
  // RelayDT relaydt_124: pin names not known; wires that end beside it: relaydt_114_p4, 1'b1, 1'b0
  // RelayDT relaydt_125: pin names not known; wires that end beside it: relaydt_114_p5, 1'b0, 1'b1, relaydt_125_p4, relaydt_125_p4, relaydt_125_p6
  // RelayDT #(.poles(4)) relaydt_126: pin names not known; wires that end beside it: relaydt_126_p1, relaydt_126_p2, relaydt_110_p6, relaydt_114_p10, relaydt_114_p8, relaydt_126_p1, relaydt_126_p1, relaydt_126_p2, 1'b0, relaydt_114_p4, relaydt_103_p11[0], 1'b1, relaydt_114_p5, REG_B[6], 1'b0
  LED led_88 (.in(relaydt_103_p11[0]));
  // RelayDT #(.poles(2)) relaydt_127: pin names not known; wires that end beside it: relay_66_p4, relay_66_p4, SCZ[0], 1'b0, relaydt_96_p7, 1'b1, 1'b0
  // RelayDT #(.poles(2)) relaydt_128: pin names not known; wires that end beside it: 1'b0, relay_67_p3, 1'b1, relaydt_128_p4, 1'b0, relaydt_128_p6, relaydt_128_p7, 1'b0, relaydt_128_p6, 1'b0
  // Relay relay_68: pin names not known; wires that end beside it: relaydt_112_p5[3], relay_68_p2
  LED led_89 (.in(ALU_F[1]));
  LED led_90 (.in(relaydt_120_p14[0]));
  // RelayDT #(.poles(4)) relaydt_129: pin names not known; wires that end beside it: relaydt_129_p1, REG_C[5], relaydt_129_p1, relaydt_129_p4, relaydt_129_p5, 1'b0, relaydt_129_p7, relaydt_129_p8, relaydt_122_p6, relaydt_129_p10, relaydt_129_p10, relaydt_129_p7, relaydt_129_p8
  // RelayDT #(.poles(4)) relaydt_130: pin names not known; wires that end beside it: relaydt_130_p1, _1[5], relaydt_130_p1, relaydt_130_p4, relaydt_130_p5, 1'b0, relaydt_130_p7, relaydt_130_p8, relaydt_125_p6, relaydt_130_p10, relaydt_130_p10, relaydt_130_p7, relaydt_130_p8
  // RelayDT relaydt_131: pin names not known; wires that end beside it: 1'b1, relay_68_p2, relaydt_128_p4, 1'b0
  // RelayDT #(.poles(2)) relaydt_132: pin names not known; wires that end beside it: relay_68_p2, REG_COUNT[3], relaydt_128_p7, 1'b1, 1'b0
  LED led_91 (.in(REG_COUNT[3]));
  // RelayDT #(.poles(4)) relaydt_133: pin names not known; wires that end beside it: relaydt_133_p1, relaydt_133_p2, relaydt_116_p6, relaydt_118_p10, relaydt_118_p8, relaydt_133_p1, relaydt_133_p1, relaydt_133_p2, 1'b0, relaydt_118_p4, relaydt_117_p11[0], 1'b1, relaydt_118_p5, REG_COUNT[2], 1'b0
  LED led_92 (.in(RL_F[1]));
  LED led_93 (.in(ALU_F[0]));
  LED led_94 (.in(relaydt_138_p6[0]));
  LED led_95 (.in(relaydt_138_p3[0]));
  // RelayDT relaydt_134: pin names not known; wires that end beside it: relaydt_134_p1[0], 1'b1, 1'b0
  // RelayDT relaydt_135: pin names not known; wires that end beside it: relaydt_118_p4, 1'b1, 1'b0
  // RelayDT relaydt_136: pin names not known; wires that end beside it: relaydt_118_p5, 1'b0, 1'b1, relaydt_136_p4, relaydt_136_p4, relaydt_136_p6
  LED led_96 (.in(relaydt_117_p11[0]));
  LED led_97 (.in(RL_F[0]));
  // RelayDT #(.poles(4)) relaydt_137: pin names not known; wires that end beside it: 1'b1, 1'b0, relaydt_137_p3, 1'b0, 1'b1, relaydt_137_p6, 1'b0, 1'b1, relaydt_137_p9, REG_C[4], 1'b0, 1'b0, 1'b1, relaydt_137_p14
  // RelayDT #(.poles(4)) relaydt_138: pin names not known; wires that end beside it: 1'b1, 1'b0, relaydt_138_p3[0], relaydt_137_p6, relaydt_137_p3, relaydt_138_p6[0], relaydt_137_p9, 1'b1, relaydt_138_p9[0], REG_B[4], 1'b0, 1'b0, relaydt_137_p14, relaydt_138_p14[0]
  LED led_98 (.in(relaydt_138_p9[0]));
  // RelayDT #(.poles(4)) relaydt_139: pin names not known; wires that end beside it: relaydt_139_p1, relaydt_139_p2, relaydt_122_p6, relaydt_129_p10, relaydt_129_p8, relaydt_139_p1, relaydt_139_p1, relaydt_139_p2, 1'b0, relaydt_129_p4, relaydt_139_p11[0], 1'b1, relaydt_129_p5, REG_B[5], 1'b0
  // RelayDT #(.poles(4)) relaydt_140: pin names not known; wires that end beside it: relaydt_140_p1, relaydt_140_p2, relaydt_125_p6, relaydt_130_p10, relaydt_130_p8, relaydt_140_p1, relaydt_140_p1, relaydt_140_p2, 1'b0, relaydt_130_p4, relaydt_140_p11[0], 1'b1, relaydt_130_p5, REG_B[5], 1'b0
  // RelayDT relaydt_141: pin names not known; wires that end beside it: B_SIGN, 1'b0, 1'b1, B_SIGN, 1'b0, relaydt_141_p6, 1'b0
  LED led_99 (.in(relaydt_148_p1[1]));
  // Relay relay_69: pin names not known; wires that end beside it: relaydt_128_p4, relaydt_112_p5[2], 1'b0, relay_69_p4
  // RelayDT #(.poles(4)) relaydt_142: pin names not known; wires that end beside it: relaydt_142_p1, _1_2[1], relaydt_142_p1, relaydt_142_p4, relaydt_142_p5, 1'b0, relaydt_142_p7, relaydt_142_p8, relaydt_136_p6, relaydt_142_p10, relaydt_142_p10, relaydt_142_p7, relaydt_142_p8
  LED led_100 (.in(ROL));
  LED led_101 (.in(relaydt_138_p14[0]));
  // RelayDT relaydt_143: pin names not known; wires that end beside it: relaydt_129_p4, 1'b1, 1'b0
  // RelayDT relaydt_144: pin names not known; wires that end beside it: relaydt_129_p5, 1'b0, 1'b1, relaydt_144_p4, relaydt_144_p4, relaydt_144_p6
  LED led_102 (.in(relaydt_139_p11[0]));
  // RelayDT relaydt_145: pin names not known; wires that end beside it: relaydt_130_p4, 1'b1, 1'b0
  // RelayDT relaydt_146: pin names not known; wires that end beside it: relaydt_130_p5, 1'b0, 1'b1, relaydt_146_p4, relaydt_146_p4, relaydt_146_p6
  LED led_103 (.in(relaydt_140_p11[0]));
  // RelayDT relaydt_147: pin names not known; wires that end beside it: REG_B[6], 1'b0, relaydt_141_p6, REG_B[6], 1'b0, relaydt_147_p6, 1'b0
  // RelayDT relaydt_148: pin names not known; wires that end beside it: relaydt_148_p1[1], 1'b1, 1'b0
  LED led_104 (.in(relaydt_148_p1[0]));
  // RelayDT #(.poles(2)) relaydt_149: pin names not known; wires that end beside it: relay_69_p4, relay_69_p4, REG_COUNT[2], 1'b0, relaydt_128_p7, 1'b1, 1'b0
  LED led_105 (.in(REG_COUNT[2]));
  LED led_106 (.in(CE));
  LED led_107 (.in(J));
  LED led_108 (.in(relaydt_156_p6[0]));
  LED led_109 (.in(relaydt_156_p3[0]));
  // RelayDT #(.poles(4)) relaydt_150: pin names not known; wires that end beside it: relaydt_150_p1, REG_C[4], relaydt_150_p1, relaydt_150_p4, relaydt_150_p5, 1'b0, relaydt_150_p7, relaydt_150_p8, relaydt_144_p6, relaydt_150_p10, relaydt_150_p10, relaydt_150_p7, relaydt_150_p8
  // RelayDT #(.poles(4)) relaydt_151: pin names not known; wires that end beside it: relaydt_151_p1, _1[4], relaydt_151_p1, relaydt_151_p4, relaydt_151_p5, 1'b0, relaydt_151_p7, relaydt_151_p8, relaydt_146_p6, relaydt_151_p10, relaydt_151_p10, relaydt_151_p7, relaydt_151_p8
  // RelayDT relaydt_152: pin names not known; wires that end beside it: REG_B[5], 1'b0, relaydt_147_p6, REG_B[5], 1'b0, relaydt_152_p6, 1'b0
  // RelayDT relaydt_153: pin names not known; wires that end beside it: relaydt_148_p1[0], 1'b1, 1'b0
  LED led_110 (.in(relaydt_157_p1[0]));
  // Relay relay_70: pin names not known; wires that end beside it: relaydt_128_p4, relaydt_112_p5[1], 1'b0, relay_70_p4
  // RelayDT #(.poles(4)) relaydt_154: pin names not known; wires that end beside it: relaydt_154_p1, relaydt_154_p2, relaydt_136_p6, relaydt_142_p10, relaydt_142_p8, relaydt_154_p1, relaydt_154_p1, relaydt_154_p2, 1'b0, relaydt_142_p4, relaydt_154_p11[0], 1'b1, relaydt_142_p5, REG_COUNT[1], 1'b0
  LED led_111 (.in(SCZL));
  // RelayDT #(.poles(4)) relaydt_155: pin names not known; wires that end beside it: 1'b1, 1'b0, relaydt_155_p3, 1'b0, 1'b1, relaydt_155_p6, 1'b0, 1'b1, relaydt_155_p9, REG_C[3], 1'b0, 1'b0, 1'b1, relaydt_155_p14
  // RelayDT #(.poles(4)) relaydt_156: pin names not known; wires that end beside it: 1'b1, 1'b0, relaydt_156_p3[0], relaydt_155_p6, relaydt_155_p3, relaydt_156_p6[0], relaydt_155_p9, 1'b1, relaydt_156_p9[0], REG_B[3], 1'b0, 1'b0, relaydt_155_p14, relaydt_156_p14[0]
  LED led_112 (.in(relaydt_156_p9[0]));
  // RelayDT relaydt_157: pin names not known; wires that end beside it: relaydt_157_p1[0], 1'b1, 1'b0
  LED led_113 (.in(relaydt_164_p1[0]));
  // RelayDT #(.poles(2)) relaydt_158: pin names not known; wires that end beside it: relay_70_p4, relay_70_p4, REG_COUNT[1], 1'b0, relaydt_128_p7, 1'b1, 1'b0
  LED led_114 (.in(REG_COUNT[1]));
  // RelayDT relaydt_159: pin names not known; wires that end beside it: relaydt_142_p4, 1'b1, 1'b0
  // RelayDT relaydt_160: pin names not known; wires that end beside it: relaydt_142_p5, 1'b0, 1'b1, relaydt_160_p4, relaydt_160_p4, relaydt_160_p6
  LED led_115 (.in(relaydt_154_p11[0]));
  LED led_116 (.in(relaydt_156_p14[0]));
  // RelayDT #(.poles(4)) relaydt_161: pin names not known; wires that end beside it: relaydt_161_p1, relaydt_161_p2, relaydt_144_p6, relaydt_150_p10, relaydt_150_p8, relaydt_161_p1, relaydt_161_p1, relaydt_161_p2, 1'b0, relaydt_150_p4, relaydt_161_p11[0], 1'b1, relaydt_150_p5, REG_B[4], 1'b0
  // RelayDT #(.poles(4)) relaydt_162: pin names not known; wires that end beside it: relaydt_162_p1, relaydt_162_p2, relaydt_146_p6, relaydt_151_p10, relaydt_151_p8, relaydt_162_p1, relaydt_162_p1, relaydt_162_p2, 1'b0, relaydt_151_p4, relaydt_162_p11[0], 1'b1, relaydt_151_p5, REG_B[4], 1'b0
  // RelayDT relaydt_163: pin names not known; wires that end beside it: REG_B[4], 1'b0, relaydt_152_p6, REG_B[4], 1'b0, relaydt_163_p6, 1'b0
  // RelayDT relaydt_164: pin names not known; wires that end beside it: relaydt_164_p1[0], 1'b1, 1'b0
  // RelayDT #(.poles(4)) relaydt_165: pin names not known; wires that end beside it: relaydt_165_p1, _1_2[0], relaydt_165_p1, 1'b0, relaydt_165_p5, relaydt_165_p6, relaydt_160_p6, relaydt_165_p8, relaydt_165_p8, relaydt_165_p5, relaydt_165_p6
  LED led_117 (.in(relaydt_172_p6[0]));
  LED led_118 (.in(relaydt_172_p3[0]));
  // RelayDT relaydt_166: pin names not known; wires that end beside it: relaydt_150_p4, 1'b1, 1'b0
  // RelayDT relaydt_167: pin names not known; wires that end beside it: relaydt_150_p5, 1'b0, 1'b1, relaydt_167_p4, relaydt_167_p4, relaydt_167_p6
  LED led_119 (.in(relaydt_161_p11[0]));
  // RelayDT relaydt_168: pin names not known; wires that end beside it: relaydt_151_p4, 1'b1, 1'b0
  // RelayDT relaydt_169: pin names not known; wires that end beside it: relaydt_151_p5, 1'b0, 1'b1, relaydt_169_p4, relaydt_169_p4, relaydt_169_p6
  LED led_120 (.in(relaydt_162_p11[0]));
  // RelayDT relaydt_170: pin names not known; wires that end beside it: REG_B[3], 1'b0, relaydt_163_p6, REG_B[3], 1'b0, relaydt_170_p6, 1'b0
  LED led_121 (.in(relaydt_176_p1[0]));
  // Relay relay_71: pin names not known; wires that end beside it: relaydt_128_p4, relaydt_112_p5[0], 1'b0, relay_71_p4
  // RelayDT #(.poles(4)) relaydt_171: pin names not known; wires that end beside it: 1'b1, 1'b0, relaydt_171_p3, 1'b0, 1'b1, relaydt_171_p6, 1'b0, 1'b1, relaydt_171_p9, REG_C[2], 1'b0, 1'b0, 1'b1, relaydt_171_p14
  // RelayDT #(.poles(4)) relaydt_172: pin names not known; wires that end beside it: 1'b1, 1'b0, relaydt_172_p3[0], relaydt_171_p6, relaydt_171_p3, relaydt_172_p6[0], relaydt_171_p9, 1'b1, relaydt_172_p9[0], REG_B[2], 1'b0, 1'b0, relaydt_171_p14, relaydt_172_p14[0]
  LED led_122 (.in(relaydt_172_p9[0]));
  // RelayDT #(.poles(4)) relaydt_173: pin names not known; wires that end beside it: relaydt_173_p1, REG_C[3], relaydt_173_p1, relaydt_173_p4, relaydt_173_p5, 1'b0, relaydt_173_p7, relaydt_173_p8, relaydt_167_p6, relaydt_173_p10, relaydt_173_p10, relaydt_173_p7, relaydt_173_p8
  // RelayDT #(.poles(4)) relaydt_174: pin names not known; wires that end beside it: relaydt_174_p1, _1[3], relaydt_174_p1, relaydt_174_p4, relaydt_174_p5, 1'b0, relaydt_174_p7, relaydt_174_p8, relaydt_169_p6, relaydt_174_p10, relaydt_174_p10, relaydt_174_p7, relaydt_174_p8
  // RelayDT relaydt_175: pin names not known; wires that end beside it: REG_B[2], 1'b0, relaydt_170_p6, REG_B[2], 1'b0, relaydt_175_p6, 1'b0
  // RelayDT relaydt_176: pin names not known; wires that end beside it: relaydt_176_p1[0], 1'b1, 1'b0
  LED led_123 (.in(relaydt_181_p1[0]));
  // RelayDT #(.poles(2)) relaydt_177: pin names not known; wires that end beside it: relay_71_p4, relay_71_p4, REG_COUNT[0], 1'b0, relaydt_128_p7, 1'b1, 1'b0, CO, 1'b0
  LED led_124 (.in(REG_COUNT[0]));
  // RelayDT #(.poles(4)) relaydt_178: pin names not known; wires that end beside it: relaydt_178_p1, relaydt_178_p2, relaydt_160_p6, relaydt_165_p8, relaydt_165_p6, relaydt_178_p1, relaydt_178_p1, relaydt_178_p2, 1'b0, 1'b1, relaydt_178_p11[0], 1'b1, 1'b0, REG_COUNT[0], relaydt_178_p15, 1'b0
  LED led_125 (.in(relaydt_178_p11[0]));
  // RelayDT #(.poles(4)) relaydt_179: pin names not known; wires that end beside it: RL_F[1], 1'b1, 1'b0, 1'b1, 1'b0, 1'b0, 1'b1, 1'b0, 1'b1, 1'b0, relaydt_179_p11, relaydt_179_p12, relaydt_179_p13, relaydt_179_p14, RL_F[0], relaydt_179_p11, 1'b0, 1'b0, relaydt_179_p12, relaydt_179_p13, 1'b0, 1'b0, relaydt_179_p14
  LED led_126 (.in(relaydt_172_p14[0]));
  // RelayDT relaydt_180: pin names not known; wires that end beside it: REG_B[1], 1'b0, relaydt_175_p6, REG_B[1], 1'b0, relaydt_180_p6, 1'b0
  // RelayDT relaydt_181: pin names not known; wires that end beside it: relaydt_181_p1[0], 1'b1, 1'b0
  LED led_127 (.in(relaydt_185_p1[0]));
  // RelayDT #(.poles(4)) relaydt_182: pin names not known; wires that end beside it: 1'b0, RLC, RLB, RLA, relaydt_182_p5
  LED led_128 (.in(RLC));
  LED led_129 (.in(RLB));
  LED led_130 (.in(RLA));
  LED led_131 (.in(relaydt_182_p5));
  LED led_132 (.in(relaydt_188_p6[0]));
  LED led_133 (.in(relaydt_188_p3[0]));
  // RelayDT #(.poles(4)) relaydt_183: pin names not known; wires that end beside it: relaydt_183_p1, relaydt_183_p2, relaydt_167_p6, relaydt_173_p10, relaydt_173_p8, relaydt_183_p1, relaydt_183_p1, relaydt_183_p2, 1'b0, relaydt_173_p4, relaydt_183_p11[0], 1'b1, relaydt_173_p5, REG_B[3], 1'b0
  LED led_134 (.in(relaydt_183_p11[0]));
  // RelayDT #(.poles(4)) relaydt_184: pin names not known; wires that end beside it: relaydt_184_p1, relaydt_184_p2, relaydt_169_p6, relaydt_174_p10, relaydt_174_p8, relaydt_184_p1, relaydt_184_p1, relaydt_184_p2, 1'b0, relaydt_174_p4, relaydt_184_p11[0], 1'b1, relaydt_174_p5, REG_B[3], 1'b0
  LED led_135 (.in(relaydt_184_p11[0]));
  // RelayDT relaydt_185: pin names not known; wires that end beside it: relaydt_185_p1[0], 1'b1, 1'b0
  LED led_136 (.in(relaydt_134_p1[0]));
  // Relay #(.Bits(8)) relay_72: pin names not known; wires that end beside it: {4'b0000, REG_COUNT}, 1'b0, BUS
  // RelayDT #(.poles(2)) relaydt_186: pin names not known; wires that end beside it: nCLOCK, 1'b1, relaydt_186_p3, relaydt_186_p4, relaydt_186_p3, 1'b0
  // Relay relay_73: pin names not known; wires that end beside it: relaydt_117_p11[1], relay_73_p2
  LED led_137 (.in(CIncrement[3]));
  // RelayDT #(.poles(4)) relaydt_187: pin names not known; wires that end beside it: 1'b1, 1'b0, relaydt_187_p3, 1'b0, 1'b1, relaydt_187_p6, 1'b0, 1'b1, relaydt_187_p9, REG_C[1], 1'b0, 1'b0, 1'b1, relaydt_187_p14
  // RelayDT #(.poles(4)) relaydt_188: pin names not known; wires that end beside it: 1'b1, 1'b0, relaydt_188_p3[0], relaydt_187_p6, relaydt_187_p3, relaydt_188_p6[0], relaydt_187_p9, 1'b1, relaydt_188_p9[0], REG_B[1], 1'b0, 1'b0, relaydt_187_p14, relaydt_188_p14[0]
  LED led_138 (.in(relaydt_188_p9[0]));
  // RelayDT relaydt_189: pin names not known; wires that end beside it: relaydt_173_p4, 1'b1, 1'b0
  // RelayDT relaydt_190: pin names not known; wires that end beside it: relaydt_173_p5, 1'b0, 1'b1, relaydt_190_p4, relaydt_190_p4, relaydt_190_p6
  // RelayDT relaydt_191: pin names not known; wires that end beside it: relaydt_174_p4, 1'b1, 1'b0
  // RelayDT relaydt_192: pin names not known; wires that end beside it: relaydt_174_p5, 1'b0, 1'b1, relaydt_192_p4, relaydt_192_p4, relaydt_192_p6
  // RelayDT relaydt_193: pin names not known; wires that end beside it: REG_B[0], 1'b0, relaydt_180_p6, REG_B[0], 1'b0, ZERO, 1'b0
  // RelayDT relaydt_194: pin names not known; wires that end beside it: 1'b1, relay_73_p2, relaydt_178_p15, 1'b0
  // RelayDT #(.poles(2)) relaydt_195: pin names not known; wires that end beside it: relay_73_p2, CIncrement[3], relaydt_186_p4, 1'b1, 1'b0
  LED led_139 (.in(relaydt_188_p14[0]));
  // RelayDT #(.poles(4)) relaydt_196: pin names not known; wires that end beside it: relaydt_196_p1, REG_C[2], relaydt_196_p1, relaydt_196_p4, relaydt_196_p5, 1'b0, relaydt_196_p7, relaydt_196_p8, relaydt_190_p6, relaydt_196_p10, relaydt_196_p10, relaydt_196_p7, relaydt_196_p8
  // RelayDT #(.poles(4)) relaydt_197: pin names not known; wires that end beside it: relaydt_197_p1, _1[2], relaydt_197_p1, relaydt_197_p4, relaydt_197_p5, 1'b0, relaydt_197_p7, relaydt_197_p8, relaydt_192_p6, relaydt_197_p10, relaydt_197_p10, relaydt_197_p7, relaydt_197_p8
  // Relay #(.Bits(8)) relay_74: pin names not known; wires that end beside it: SHLB_E, {relaydt_148_p1, relaydt_157_p1[0], relaydt_164_p1[0], relaydt_176_p1[0], relaydt_181_p1[0], relaydt_185_p1[0], relaydt_134_p1[0]}, 1'b0, BUS
  // Relay relay_75: pin names not known; wires that end beside it: relaydt_178_p15, relaydt_117_p11[0], 1'b0, relay_75_p4
  // RelayDT #(.poles(4)) relaydt_198: pin names not known; wires that end beside it: RS_F[1], 1'b1, 1'b0, 1'b1, 1'b0, 1'b0, 1'b1, 1'b0, 1'b1, 1'b0, relaydt_198_p11, relaydt_198_p12, relaydt_198_p13, relaydt_198_p14, RS_F[0], relaydt_198_p11, 1'b0, 1'b0, relaydt_198_p12, relaydt_198_p13, 1'b0, 1'b0, relaydt_198_p14
  LED led_140 (.in(relaydt_202_p6[0]));
  LED led_141 (.in(relaydt_202_p3[0]));
  // Relay #(.Bits(8)) relay_76: pin names not known; wires that end beside it: AND_E, {relaydt_93_p3, relaydt_106_p14[0], relaydt_120_p14[0], relaydt_138_p14[0], relaydt_156_p14[0], relaydt_172_p14[0], relaydt_188_p14[0]}, BUS
  // RelayDT #(.poles(2)) relaydt_199: pin names not known; wires that end beside it: relay_75_p4, relay_75_p4, CIncrement[2], 1'b0, relaydt_186_p4, 1'b1, 1'b0
  LED led_142 (.in(CIncrement[2]));
  // RelayDT #(.poles(4)) relaydt_200: pin names not known; wires that end beside it: 1'b0, CO, RSB, RSA, relaydt_200_p5
  // RelayDT #(.poles(4)) relaydt_201: pin names not known; wires that end beside it: 1'b1, 1'b0, relaydt_201_p3, 1'b0, 1'b1, relaydt_201_p6, 1'b0, 1'b1, relaydt_201_p9, REG_C[0], 1'b0
  // RelayDT #(.poles(4)) relaydt_202: pin names not known; wires that end beside it: 1'b1, 1'b0, relaydt_202_p3[0], relaydt_201_p6, relaydt_201_p3, relaydt_202_p6[0], relaydt_201_p9, 1'b0, 1'b1, relaydt_202_p10[0], REG_B[0], 1'b0, OR_E, 1'b0
  LED led_143 (.in(relaydt_202_p10[0]));
  // RelayDT relaydt_203: pin names not known; wires that end beside it: relaydt_196_p4, 1'b1, 1'b0
  // RelayDT relaydt_204: pin names not known; wires that end beside it: relaydt_196_p5, 1'b0, 1'b1, relaydt_204_p4, relaydt_204_p4, relaydt_204_p6
  // RelayDT #(.poles(4)) relaydt_205: pin names not known; wires that end beside it: relaydt_205_p1, relaydt_205_p2, relaydt_190_p6, relaydt_196_p10, relaydt_196_p8, relaydt_205_p1, relaydt_205_p1, relaydt_205_p2, 1'b0, relaydt_196_p4, relaydt_205_p11[0], 1'b1, relaydt_196_p5, REG_B[2], 1'b0
  LED led_144 (.in(relaydt_205_p11[0]));
  // RelayDT relaydt_206: pin names not known; wires that end beside it: relaydt_197_p4, 1'b1, 1'b0
  // RelayDT relaydt_207: pin names not known; wires that end beside it: relaydt_197_p5, 1'b0, 1'b1, relaydt_207_p4, relaydt_207_p4, relaydt_207_p6
  // RelayDT #(.poles(4)) relaydt_208: pin names not known; wires that end beside it: relaydt_208_p1, relaydt_208_p2, relaydt_192_p6, relaydt_197_p10, relaydt_197_p8, relaydt_208_p1, relaydt_208_p1, relaydt_208_p2, 1'b0, relaydt_197_p4, relaydt_208_p11[0], 1'b1, relaydt_197_p5, REG_B[2], 1'b0
  LED led_145 (.in(relaydt_208_p11[0]));
  LED led_146 (.in(CO));
  LED led_147 (.in(RSB));
  LED led_148 (.in(RSA));
  LED led_149 (.in(relaydt_200_p5));
  // Relay #(.Bits(8)) relay_77: pin names not known; wires that end beside it: {relaydt_93_p12, relaydt_120_p9[0], relaydt_138_p9[0], relaydt_156_p9[0], relaydt_172_p9[0], relaydt_188_p9[0], relaydt_202_p10[0]}, XOR_E, BUS, 1'b0
  // Relay #(.Bits(8)) relay_78: pin names not known; wires that end beside it: {relaydt_93_p9, relaydt_120_p6[0], relaydt_138_p6[0], relaydt_156_p6[0], relaydt_172_p6[0], relaydt_188_p6[0], relaydt_202_p6[0]}, NOTB_E, BUS, 1'b0
  // Relay #(.Bits(8)) relay_79: pin names not known; wires that end beside it: {relaydt_93_p6, relaydt_120_p3[0], relaydt_138_p3[0], relaydt_156_p3[0], relaydt_172_p3[0], relaydt_188_p3[0], relaydt_202_p3[0]}, BUS
  // RelayDT #(.poles(4)) relaydt_209: pin names not known; wires that end beside it: relaydt_209_p1, REG_C[1], relaydt_209_p1, relaydt_209_p4, relaydt_209_p5, 1'b0, relaydt_209_p7, relaydt_209_p8, relaydt_204_p6, relaydt_209_p10, relaydt_209_p10, relaydt_209_p7, relaydt_209_p8
  // RelayDT #(.poles(4)) relaydt_210: pin names not known; wires that end beside it: relaydt_210_p1, _1[1], relaydt_210_p1, relaydt_210_p4, relaydt_210_p5, 1'b0, relaydt_210_p7, relaydt_210_p8, relaydt_207_p6, relaydt_210_p10, relaydt_210_p10, relaydt_210_p7, relaydt_210_p8
  // RelayDT #(.poles(4)) relaydt_211: pin names not known; wires that end beside it: ALU_F[1], 1'b1, 1'b0, 1'b1, 1'b0, 1'b0, 1'b1, 1'b0, 1'b1, 1'b0, relaydt_211_p11, relaydt_211_p12, relaydt_211_p13, relaydt_211_p14, ALU_F[0], relaydt_211_p11, 1'b0, 1'b0, relaydt_211_p12, relaydt_211_p13, 1'b0, 1'b0, relaydt_211_p14
  // Relay relay_80: pin names not known; wires that end beside it: relaydt_178_p15, relaydt_154_p11[0], 1'b0, relay_80_p4
  LED led_150 (.in(CIncrement[1]));
  // RelayDT #(.poles(4)) relaydt_212: pin names not known; wires that end beside it: 1'b0, NOTB_E, INCB_E, SUM_E, relaydt_212_p5
  // RelayDT #(.poles(2)) relaydt_213: pin names not known; wires that end beside it: relay_80_p4, relay_80_p4, CIncrement[1], 1'b0, relaydt_186_p4, 1'b1, 1'b0
  // RelayDT #(.poles(4)) relaydt_214: pin names not known; wires that end beside it: relaydt_214_p1, relaydt_214_p2, relaydt_204_p6, relaydt_209_p10, relaydt_209_p8, relaydt_214_p1, relaydt_214_p1, relaydt_214_p2, 1'b0, relaydt_209_p4, relaydt_214_p11[0], 1'b1, relaydt_209_p5, REG_B[1], 1'b0
  // RelayDT #(.poles(4)) relaydt_215: pin names not known; wires that end beside it: relaydt_215_p1, relaydt_215_p2, relaydt_207_p6, relaydt_210_p10, relaydt_210_p8, relaydt_215_p1, relaydt_215_p1, relaydt_215_p2, 1'b0, relaydt_210_p4, relaydt_215_p11[0], 1'b1, relaydt_210_p5, REG_B[1], 1'b0
  LED led_151 (.in(NOTB_E));
  LED led_152 (.in(INCB_E));
  LED led_153 (.in(SUM_E));
  LED led_154 (.in(relaydt_212_p5));
  // Relay relay_81: pin names not known; wires that end beside it: relaydt_178_p15, relaydt_178_p11[0], 1'b0, relay_81_p4
  // RelayDT relaydt_216: pin names not known; wires that end beside it: relaydt_209_p4, 1'b1, 1'b0
  // RelayDT relaydt_217: pin names not known; wires that end beside it: relaydt_209_p5, 1'b0, 1'b1, relaydt_217_p4, relaydt_217_p4, relaydt_217_p6
  LED led_155 (.in(relaydt_214_p11[0]));
  // RelayDT relaydt_218: pin names not known; wires that end beside it: relaydt_210_p4, 1'b1, 1'b0
  // RelayDT relaydt_219: pin names not known; wires that end beside it: relaydt_210_p5, 1'b0, 1'b1, relaydt_219_p4, relaydt_219_p4, relaydt_219_p6
  LED led_156 (.in(relaydt_215_p11[0]));
  // RelayDT #(.poles(2)) relaydt_220: pin names not known; wires that end beside it: relay_81_p4, relay_81_p4, CIncrement[0], 1'b0, relaydt_186_p4, 1'b1, 1'b0
  LED led_157 (.in(CIncrement[0]));
  // RelayDT #(.poles(4)) relaydt_221: pin names not known; wires that end beside it: relaydt_221_p1, REG_C[0], relaydt_221_p1, 1'b0, relaydt_221_p5, relaydt_221_p6, relaydt_217_p6, relaydt_221_p8, relaydt_221_p8, relaydt_221_p5, relaydt_221_p6
  // RelayDT #(.poles(4)) relaydt_222: pin names not known; wires that end beside it: relaydt_222_p1, _1[0], relaydt_222_p1, 1'b0, relaydt_222_p5, relaydt_222_p6, relaydt_219_p6, relaydt_222_p8, relaydt_222_p8, relaydt_222_p5, relaydt_222_p6
  // RelayDT #(.poles(4)) relaydt_223: pin names not known; wires that end beside it: relaydt_223_p1, relaydt_223_p2, relaydt_217_p6, relaydt_221_p8, relaydt_221_p6, relaydt_223_p1, relaydt_223_p1, relaydt_223_p2, 1'b0, 1'b1, relaydt_223_p11[0], 1'b1, 1'b0, REG_B[0], SUM_E, 1'b0
  // RelayDT #(.poles(4)) relaydt_224: pin names not known; wires that end beside it: relaydt_224_p1, relaydt_224_p2, relaydt_219_p6, relaydt_222_p8, relaydt_222_p6, relaydt_224_p1, relaydt_224_p1, relaydt_224_p2, 1'b0, 1'b1, relaydt_224_p11[0], 1'b1, 1'b0, REG_B[0], INCB_E, 1'b0
  // RelayDT #(.poles(4)) relaydt_225: pin names not known; wires that end beside it: in_19[2], 1'b1, 1'b0, 1'b1, 1'b0, 1'b0, 1'b1, 1'b0, 1'b1, 1'b0, relaydt_225_p11, relaydt_225_p12, relaydt_225_p13, relaydt_225_p14, in_19[1], relaydt_225_p11, 1'b0, 1'b0, relaydt_225_p12, relaydt_225_p13, 1'b0, 1'b0, relaydt_225_p14
  // Relay #(.Bits(8)) relay_82: pin names not known; wires that end beside it: {relaydt_102_p11, relaydt_139_p11[0], relaydt_161_p11[0], relaydt_183_p11[0], relaydt_205_p11[0], relaydt_214_p11[0], relaydt_223_p11[0]}, BUS
  LED led_158 (.in(relaydt_223_p11[0]));
  // Relay #(.Bits(8)) relay_83: pin names not known; wires that end beside it: {relaydt_103_p11, relaydt_140_p11[0], relaydt_162_p11[0], relaydt_184_p11[0], relaydt_208_p11[0], relaydt_215_p11[0], relaydt_224_p11[0]}, BUS
  LED led_159 (.in(relaydt_224_p11[0]));
  // RelayDT #(.poles(4)) relaydt_226: pin names not known; wires that end beside it: 1'b0, in_19[0]
  // RelayDT #(.poles(8)) relaydt_227: pin names not known; wires that end beside it: relaydt_227_p1, 1'b0, 1'b0, relaydt_227_p1, relaydt_227_p5, 1'b0, 1'b0, relaydt_227_p5, relaydt_227_p9, 1'b0, 1'b0, relaydt_227_p9, relaydt_227_p13, 1'b0, 1'b0, relaydt_227_p13, 1'b0, SHLB_E, relaydt_227_p19, XOR_E, OR_E, AND_E, relaydt_227_p23, relaydt_227_p24, relaydt_227_p25
  LED led_160 (.in(SHLB_E));
  LED led_161 (.in(relaydt_227_p19));
  LED led_162 (.in(XOR_E));
  LED led_163 (.in(OR_E));
  LED led_164 (.in(AND_E));
  LED led_165 (.in(relaydt_227_p23));
  LED led_166 (.in(relaydt_227_p24));
  LED led_167 (.in(relaydt_227_p25));

  // Other names for the same wires on the sheet: REG_B[7] = B_SIGN; RESET = in_21; RSC = in_17

  // Notes on the sheet:
  //   clk: Hz: 4
  //   clk_2: Hz: 8
  //   clk_3: Hz: 16
  //   clk_4: Hz: 2
  //   MANUAL: default 1
  //   _1: default 1
  //   _1_2: default 1
  //   _1_3: default 1
  //   CLOCK
  //   A Register
  //   B Register
  //   C Register
  //   Inst Register
  //   Mem Address Register
  //   Output Register
  //   uCounter
  //   ALU-Logic
  //   AND
  //   ALU-Arithmetic
  //   SCZ Register
  //   Counter
  //   XOR
  //   NOT_B
  //   OR
  //   SUM
  //   contents of R1 (hex, n*v repeats v):
  //   4300,1404,6*0,4300,1404,4800,1020,4*0,4300,1404,4800,1030,51,120
  //   ,0,0,4300,1404,4800,1010,4*0,4300,1404,4800,2200,4*0,4300,1404
  //   ,820,5*0,4300,1404,802,5*0,4300,1404,6*0,4300,1404,6*0,4300,1404
  //   ,6*0,4300,1404,4800,2100,12*0,4300,1404,d1,120,4*0,4300,1404,91
  //   ,120,4*0,4300,1404,208,5*0,4300,1404,8000,5*0,4300,1404,6*0,4300
  //   ,1404,4800,1020,4*0,4300,1404,4800,1030,51,120,0,0,4300,1404,4800
  //   ,1010,4*0,4300,1404,4800,2200,4*0,4300,1404,820,5*0,4300,1404
  //   ,802,5*0,4300,1404,6*0,4300,1404,802,5*0,4300,1404,6*0,4300,1404
  //   ,4800,2100,12*0,4300,1404,d1,120,4*0,4300,1404,91,120,4*0,4300
  //   ,1404,208,5*0,4300,1404,8000,5*0,4300,1404,6*0,4300,1404,4800
  //   ,1020,4*0,4300,1404,4800,1030,51,120,0,0,4300,1404,4800,1010,4*0
  //   ,4300,1404,4800,2200,4*0,4300,1404,820,5*0,4300,1404,802,5*0,4300
  //   ,1404,802,5*0,4300,1404,6*0,4300,1404,6*0,4300,1404,4800,2100
  //   ,12*0,4300,1404,d1,120,4*0,4300,1404,91,120,4*0,4300,1404,208
  //   ,5*0,4300,1404,8000,5*0,4300,1404,6*0,4300,1404,4800,1020,4*0
  //   ,4300,1404,4800,1030,51,120,0,0,4300,1404,4800,1010,4*0,4300,1404
  //   ,4800,2200,4*0,4300,1404,820,5*0,4300,1404,802,5*0,4300,1404,802
  //   ,5*0,4300,1404,802,5*0,4300,1404,6*0,4300,1404,4800,2100,12*0
  //   ,4300,1404,d1,120,4*0,4300,1404,91,120,4*0,4300,1404,208,5*0,4300
  //   ,1404,8000,5*0,4300,1404,6*0,4300,1404,4800,1020,4*0,4300,1404
  //   ,4800,1030,51,120,0,0,4300,1404,4800,1010,4*0,4300,1404,4800,2200
  //   ,4*0,4300,1404,820,5*0,4300,1404,802,5*0,4300,1404,6*0,4300,1404
  //   ,6*0,4300,1404,802,5*0,4300,1404,4800,2100,12*0,4300,1404,d1,120
  //   ,4*0,4300,1404,91,120,4*0,4300,1404,208,5*0,4300,1404,8000,5*0
  //   ,4300,1404,6*0,4300,1404,4800,1020,4*0,4300,1404,4800,1030,51
  //   ,120,0,0,4300,1404,4800,1010,4*0,4300,1404,4800,2200,4*0,4300
  //   ,1404,820,5*0,4300,1404,802,5*0,4300,1404,6*0,4300,1404,802,5*0
  //   ,4300,1404,802,5*0,4300,1404,4800,2100,12*0,4300,1404,d1,120,4*0
  //   ,4300,1404,91,120,4*0,4300,1404,208,5*0,4300,1404,8000,5*0,4300
  //   ,1404,6*0,4300,1404,4800,1020,4*0,4300,1404,4800,1030,51,120,0,0
  //   ,4300,1404,4800,1010,4*0,4300,1404,4800,2200,4*0,4300,1404,820
  //   ,5*0,4300,1404,802,5*0,4300,1404,802,5*0,4300,1404,6*0,4300,1404
  //   ,802,5*0,4300,1404,4800,2100,12*0,4300,1404,d1,120,4*0,4300,1404
  //   ,91,120,4*0,4300,1404,208,5*0,4300,1404,8000,5*0,4300,1404,6*0
  //   ,4300,1404,4800,1020,4*0,4300,1404,4800,1030,51,120,0,0,4300,1404
  //   ,4800,1010,4*0,4300,1404,4800,2200,4*0,4300,1404,820,5*0,4300
  //   ,1404,802,5*0,4300,1404,802,5*0,4300,1404,802,5*0,4300,1404,802
  //   ,5*0,4300,1404,4800,2100,12*0,4300,1404,d1,120,4*0,4300,1404,91
  //   ,120,4*0,4300,1404,208,5*0,4300,1404,8000
  //   SHL
  //   3-8 Decoder - no Z
endmodule
