// Digital circuit controlled_output.dig as structural Verilog
module controlled_output (
  input  [5:0] SRC,
  input  [5:0] REG,
  input  [7:0] VAL,
  output [7:0] OUT
);

  wire comparator_1_eq;

  Comparator #(.Bits(6)) comparator_1 (.a(SRC), .b(REG), .eq(comparator_1_eq));  // open: gt, lt
  assign OUT = comparator_1_eq ? VAL : 8'bz;  // Driver driver_1
endmodule
