// Digital circuit risc_like_8bit_digital.dig as structural Verilog
module risc_like_8bit_digital (
  input  clk,
  input  HALT,
  input  in_3,
  input  clk_2,
  input  clk_3,
  input  in_6,
  input  clk_4,
  input  MANUAL,
  input  HALT_2,
  input  in_10,
  input  in_11,
  input  [7:0] in_25,
  input  [7:0] in_26,
  output [7:0] Decimal,
  output [7:0] Binary,
  output [7:0] Signed_Decimal,
  output [7:0] out_15,
  output [7:0] out_16,
  output [7:0] out_17,
  output [7:0] out_18,
  output [7:0] out_19,
  output [7:0] out_20,
  output [7:0] out_21,
  output [7:0] Decimal_2,
  output [7:0] Binary_2,
  output [7:0] Signed_Decimal_2
);

  wire and_2_out, and_3_out, and_4_out, and_6_out, and_7_out, and_8_out, and_9_out, and_10_out, CLOCK,
       comparator_1_eq, data_memory_write_enable, execute_port_a_sel, execute_port_b_sel, nCLOCK,
       OP_RTYPE_eq, OP_UTYPE_eq, or_2_out, or_3_out, or_4_out, or_6_out, or_7_out, or_8_out, or_9_out,
       or_10_out, reg_write_enable, relaydt_1_p7, relaydt_1_p8, relaydt_2_p2, relaydt_2_p3, rs_ff_1_nq,
       rs_ff_1_q, STEP_out;
  wire [1:0] imm_select;
  wire [2:0] alu_op_sel, branch_op_sel, load_store_type, reg_write_data_sel;
  wire [4:0] demultiplexer_3_out_0;
  wire [5:0] demultiplexer_1_out_0, multiplexer_4_out;
  wire [6:5] demultiplexer_3_out_5;
  wire [7:0] a, add_1_s, and_1_out, b, demultiplexer_2_out_0, I_JALR_Type_out, multiplexer_2_out,
       multiplexer_3_out, multiplexer_5_out, multiplexer_6_out, multiplexer_7_out, multiplexer_11_out,
       multiplexer_12_out, multiplexer_13_out, multiplexer_14_out, multiplexer_15_out, or_1_out, PC, pc_next,
       RS1, RS2, S_B_Type_out, SLL_out, SRL_out, sub_1_s, write_data, x00_q, xor_1_out;
  wire [7:6] demultiplexer_1_out_6, multiplexer_4_out_2;
  wire [7:7] demultiplexer_3_out_7;
  wire [15:0] INSTRUCTION, mul_1_mul;

  Add #(.Bits(8)) add_1 (.a(a), .b(b), .c_i(1'b0), .s(add_1_s));  // open: c_o
  Sub #(.Bits(8)) sub_1 (.a(a), .b(b), .c_i(1'b0), .s(sub_1_s));  // open: c_o
  Mul #(.Bits(8), .Signed("true")) mul_1 (.a(a), .b(b), .mul(mul_1_mul));
  BarrelShifter #(.Bits(8)) SLL (.in(a), .shift(b[3:0]), .out(SLL_out));
  BarrelShifter #(.Bits(8), .direction("right")) SRL (.in(a), .shift(b[3:0]), .out(SRL_out));
  assign and_1_out = a & b;  // And and_1, 8 bits wide
  assign or_1_out = a | b;  // Or or_1, 8 bits wide
  assign xor_1_out = a ^ b;  // XOr xor_1, 8 bits wide
  EEPROMDualPort #(.AddrBits(8), .isProgramMemory("true"), .Bits(16)) eepromdualport_1 (
    .A(PC), .Din({16{1'b0}}), .str(1'b0), .C(1'b0), .ld(1'b1), .D(INSTRUCTION));
  Demultiplexer #(.Selector_Bits(3)) demultiplexer_1 (
    .sel(INSTRUCTION[13:11]), .in(1'b1), .out_0(demultiplexer_1_out_0[0]), .out_1(demultiplexer_1_out_0[1]),
    .out_2(demultiplexer_1_out_0[2]), .out_3(demultiplexer_1_out_0[3]), .out_4(demultiplexer_1_out_0[4]),
    .out_5(demultiplexer_1_out_0[5]), .out_6(demultiplexer_1_out_6[6]), .out_7(demultiplexer_1_out_6[7]));
  // RelayDT #(.poles(2)) relaydt_1: pin names not known; wires that end beside it: in_6, clk_3, clk_2, clk, clk_4, 1'b0, relaydt_1_p7, relaydt_1_p8, in_3, relaydt_1_p7, relaydt_1_p8
  or or_2 (or_2_out, HALT, HALT_2);
  and and_2 (and_2_out, reg_write_enable, demultiplexer_3_out_7[7]);
  and and_3 (and_3_out, reg_write_enable, demultiplexer_3_out_0[3]);
  // RelayDT relaydt_2: pin names not known; wires that end beside it: 1'b0, relaydt_2_p2, relaydt_2_p3
  Seven_Seg_Hex seven_seg_hex_1 (.d(INSTRUCTION[11:8]), .dp(1'b0));
  Seven_Seg_Hex seven_seg_hex_2 (.d(INSTRUCTION[15:12]), .dp(1'b0));
  Multiplexer #(.Selector_Bits(3), .Bits(8)) multiplexer_1 (
    .sel(alu_op_sel), .in_0(add_1_s), .in_1(sub_1_s), .in_2(mul_1_mul[7:0]), .in_3(SLL_out), .in_4(SRL_out),
    .in_5(and_1_out), .in_6(or_1_out), .in_7(xor_1_out), .out(Binary));
  Demultiplexer #(.Selector_Bits(3)) demultiplexer_2 (
    .sel(INSTRUCTION[10:8]), .in(1'b1), .out_0(demultiplexer_2_out_0[0]), .out_1(demultiplexer_2_out_0[1]),
    .out_2(demultiplexer_2_out_0[2]), .out_3(demultiplexer_2_out_0[3]), .out_4(demultiplexer_2_out_0[4]),
    .out_5(demultiplexer_2_out_0[5]), .out_6(demultiplexer_2_out_0[6]), .out_7(demultiplexer_2_out_0[7]));
  Multiplexer #(.Bits(8)) multiplexer_2 (.sel(in_11), .in_0(write_data), .in_1({8{1'b0}}), .out(multiplexer_2_out));
  or or_3 (or_3_out, in_11, and_2_out);
  Multiplexer #(.Bits(8)) multiplexer_3 (.sel(in_11), .in_0(write_data), .in_1({8{1'b0}}), .out(multiplexer_3_out));
  or or_4 (or_4_out, in_11, and_3_out);
  Button STEP (.out(STEP_out));
  and and_4 (and_4_out, STEP_out, MANUAL, ~or_2_out);  // And
  RS_FF rs_ff_1 (.S(relaydt_2_p3), .C(relaydt_2_p2), .R(~relaydt_2_p3), .Q(rs_ff_1_q), .nQ(rs_ff_1_nq));
  Seven_Seg_Hex seven_seg_hex_3 (.d(INSTRUCTION[3:0]), .dp(1'b0));
  Seven_Seg_Hex seven_seg_hex_4 (.d(INSTRUCTION[7:4]), .dp(1'b0));
  Seven_Seg_Hex seven_seg_hex_5 (.d(Binary[7:4]), .dp(1'b0));
  Demultiplexer #(.Selector_Bits(3)) demultiplexer_3 (
    .sel(INSTRUCTION[7:5]), .in(1'b1), .out_0(demultiplexer_3_out_0[0]), .out_1(demultiplexer_3_out_0[1]),
    .out_2(demultiplexer_3_out_0[2]), .out_3(demultiplexer_3_out_0[3]), .out_4(demultiplexer_3_out_0[4]),
    .out_5(demultiplexer_3_out_5[5]), .out_6(demultiplexer_3_out_5[6]), .out_7(demultiplexer_3_out_7[7]));
  Register #(.Bits(8)) x07 (.D(multiplexer_2_out), .C(CLOCK), .en(or_3_out), .Q(out_18));
  Register #(.Bits(8)) x03 (.D(multiplexer_3_out), .C(CLOCK), .en(or_4_out), .Q(out_20));
  and and_5 (relaydt_2_p3, ~MANUAL, ~or_2_out, rs_ff_1_nq);  // And
  Seven_Seg_Hex seven_seg_hex_6 (.d(Binary[3:0]), .dp(1'b0));
  Multiplexer #(.Selector_Bits(2), .Bits(8)) multiplexer_4 (
    .sel(INSTRUCTION[1:0]), .in_0(demultiplexer_2_out_0),
    .in_1({demultiplexer_3_out_7[7], demultiplexer_3_out_5, demultiplexer_3_out_0}),
    .in_2(demultiplexer_2_out_0), .in_3(demultiplexer_2_out_0), .out({multiplexer_4_out_2, multiplexer_4_out}));
  or or_5 (CLOCK, and_4_out, rs_ff_1_q);
  LED led_1 (.in(INSTRUCTION[0]));
  LED led_2 (.in(INSTRUCTION[1]));
  LED led_3 (.in(INSTRUCTION[2]));
  LED led_4 (.in(INSTRUCTION[3]));
  LED led_5 (.in(INSTRUCTION[4]));
  LED led_6 (.in(INSTRUCTION[5]));
  LED led_7 (.in(INSTRUCTION[6]));
  LED led_8 (.in(INSTRUCTION[7]));
  LED led_9 (.in(INSTRUCTION[8]));
  LED led_10 (.in(INSTRUCTION[9]));
  LED led_11 (.in(INSTRUCTION[10]));
  LED led_12 (.in(INSTRUCTION[11]));
  LED led_13 (.in(INSTRUCTION[12]));
  LED led_14 (.in(INSTRUCTION[13]));
  LED led_15 (.in(INSTRUCTION[14]));
  LED led_16 (.in(INSTRUCTION[15]));
  assign RS1 = multiplexer_4_out_2[7] ? out_18 : 8'bz;  // Driver driver_1
  assign RS2 = demultiplexer_1_out_6[7] ? out_18 : 8'bz;  // Driver driver_2
  assign RS1 = multiplexer_4_out[3] ? out_20 : 8'bz;  // Driver driver_3
  assign RS2 = demultiplexer_1_out_0[3] ? out_20 : 8'bz;  // Driver driver_4
  not not_1 (nCLOCK, CLOCK);
  and and_6 (and_6_out, reg_write_enable, demultiplexer_3_out_5[6]);
  LED led_17 (.in(CLOCK));
  LED led_18 (.in(nCLOCK));
  Multiplexer #(.Bits(8)) multiplexer_5 (.sel(in_11), .in_0(write_data), .in_1({8{1'b0}}), .out(multiplexer_5_out));
  or or_6 (or_6_out, in_11, and_6_out);
  and and_7 (and_7_out, reg_write_enable, demultiplexer_3_out_0[2]);
  Multiplexer #(.Bits(8)) multiplexer_6 (.sel(in_11), .in_0(write_data), .in_1({8{1'b0}}), .out(multiplexer_6_out));
  or or_7 (or_7_out, in_11, and_7_out);
  Add #(.Bits(8)) add_2 (.a(PC), .b(8'h1), .c_i(1'b0), .s(pc_next));  // open: c_o
  Register #(.Bits(8)) x06 (.D(multiplexer_5_out), .C(CLOCK), .en(or_6_out), .Q(out_17));
  Register #(.Bits(8)) x02 (.D(multiplexer_6_out), .C(CLOCK), .en(or_7_out), .Q(out_19));
  Multiplexer #(.Bits(8)) multiplexer_7 (.sel(in_10), .in_0(pc_next), .in_1(Binary), .out(multiplexer_7_out));
  assign RS1 = multiplexer_4_out_2[6] ? out_17 : 8'bz;  // Driver driver_5
  assign RS2 = demultiplexer_1_out_6[6] ? out_17 : 8'bz;  // Driver driver_6
  assign RS1 = multiplexer_4_out[2] ? out_19 : 8'bz;  // Driver driver_7
  assign RS2 = demultiplexer_1_out_0[2] ? out_19 : 8'bz;  // Driver driver_8
  Multiplexer #(.Selector_Bits(3), .Bits(8)) multiplexer_8 (
    .sel(reg_write_data_sel), .in_0(in_26), .in_1(Binary), .in_2(in_25), .in_3(Binary_2), .in_4(pc_next),
    .in_5({8{1'b0}}), .in_6({8{1'b0}}), .in_7({8{1'b0}}), .out(write_data));
  Multiplexer #(.Bits(8)) multiplexer_9 (.sel(execute_port_a_sel), .in_0(PC), .in_1(RS1), .out(a));
  Multiplexer #(.Bits(8)) multiplexer_10 (.sel(execute_port_b_sel), .in_0(Binary_2), .in_1(RS2), .out(b));
  Multiplexer #(.Bits(8)) multiplexer_11 (
    .sel(in_11), .in_0(multiplexer_7_out), .in_1({8{1'b0}}), .out(multiplexer_11_out));
  and and_8 (and_8_out, reg_write_enable, demultiplexer_3_out_5[5]);
  and and_9 (and_9_out, reg_write_enable, demultiplexer_3_out_0[1]);
  Multiplexer #(.Bits(8)) multiplexer_12 (.sel(in_11), .in_0(write_data), .in_1({8{1'b0}}), .out(multiplexer_12_out));
  or or_8 (or_8_out, in_11, and_8_out);
  Multiplexer #(.Bits(8)) multiplexer_13 (.sel(in_11), .in_0(write_data), .in_1({8{1'b0}}), .out(multiplexer_13_out));
  or or_9 (or_9_out, in_11, and_9_out);
  Seven_Seg_Hex seven_seg_hex_7 (.d(PC[7:4]), .dp(1'b0));
  Register #(.Bits(8)) u_PC (.D(multiplexer_11_out), .C(nCLOCK), .en(1'b1), .Q(PC));
  Register #(.Bits(8)) x05 (.D(multiplexer_12_out), .C(CLOCK), .en(or_8_out), .Q(out_16));
  Register #(.Bits(8)) x01 (.D(multiplexer_13_out), .C(CLOCK), .en(or_9_out), .Q(out_21));
  Seven_Seg_Hex seven_seg_hex_8 (.d(PC[3:0]), .dp(1'b0));
  assign RS1 = multiplexer_4_out[5] ? out_16 : 8'bz;  // Driver driver_9
  assign RS2 = demultiplexer_1_out_0[5] ? out_16 : 8'bz;  // Driver driver_10
  assign RS1 = multiplexer_4_out[1] ? out_21 : 8'bz;  // Driver driver_11
  assign RS2 = demultiplexer_1_out_0[1] ? out_21 : 8'bz;  // Driver driver_12
  and and_10 (and_10_out, reg_write_enable, demultiplexer_3_out_0[4]);
  Multiplexer #(.Bits(8)) multiplexer_14 (.sel(in_11), .in_0(write_data), .in_1({8{1'b0}}), .out(multiplexer_14_out));
  or or_10 (or_10_out, in_11, and_10_out);
  Register #(.Bits(8)) x00 (.D({8{1'b0}}), .C(CLOCK), .en(1'b0), .Q(x00_q));
  Register #(.Bits(8)) x04 (.D(multiplexer_14_out), .C(CLOCK), .en(or_10_out), .Q(out_15));
  assign RS1 = multiplexer_4_out[0] ? x00_q : 8'bz;  // Driver driver_13
  assign RS2 = demultiplexer_1_out_0[0] ? x00_q : 8'bz;  // Driver driver_14
  assign RS1 = multiplexer_4_out[4] ? out_15 : 8'bz;  // Driver driver_15
  assign RS2 = demultiplexer_1_out_0[4] ? out_15 : 8'bz;  // Driver driver_16
  Comparator #(.Bits(2)) OP_RTYPE (.a(INSTRUCTION[1:0]), .b(2'b10), .eq(OP_RTYPE_eq));  // open: gt, lt
  Comparator #(.Bits(5)) comparator_1 (.a(INSTRUCTION[4:0]), .b(5'b01100), .eq(comparator_1_eq));  // open: gt, lt
  BitExtender #(.inputBits(5), .outputBits(8)) I_JALR_Type (.in(INSTRUCTION[15:11]), .out(I_JALR_Type_out));
  BitExtender #(.inputBits(5), .outputBits(8)) S_B_Type (
    .in({INSTRUCTION[15:14], INSTRUCTION[7:5]}), .out(S_B_Type_out));
  assign in_10 = OP_RTYPE_eq ? 1'b0 : 1'bz;  // Driver driver_17
  assign reg_write_enable = OP_RTYPE_eq ? 1'b1 : 1'bz;  // Driver driver_18
  assign imm_select = OP_RTYPE_eq ? 2'b00 : 2'bz;  // Driver driver_19
  assign execute_port_a_sel = OP_RTYPE_eq ? 1'b1 : 1'bz;  // Driver driver_20
  assign execute_port_b_sel = OP_RTYPE_eq ? 1'b1 : 1'bz;  // Driver driver_21
  assign reg_write_data_sel = OP_RTYPE_eq ? 3'b001 : 3'bz;  // Driver driver_22
  assign load_store_type = OP_RTYPE_eq ? 3'b000 : 3'bz;  // Driver driver_23
  assign data_memory_write_enable = OP_RTYPE_eq ? 1'b0 : 1'bz;  // Driver driver_24
  assign alu_op_sel = OP_RTYPE_eq ? INSTRUCTION[4:2] : 3'bz;  // Driver driver_25
  assign branch_op_sel = OP_RTYPE_eq ? 3'b000 : 3'bz;  // Driver driver_26
  Multiplexer #(.Bits(8)) multiplexer_15 (
    .sel(comparator_1_eq), .in_0(I_JALR_Type_out), .in_1({3'b000, INSTRUCTION[15:11]}),
    .out(multiplexer_15_out));
  Multiplexer #(.Selector_Bits(2), .Bits(8)) multiplexer_16 (
    .sel(imm_select), .in_0({8{1'b0}}), .in_1(multiplexer_15_out), .in_2(INSTRUCTION[15:8]),
    .in_3(S_B_Type_out), .out(Binary_2));
  Comparator #(.Bits(2)) OP_UTYPE (.a(INSTRUCTION[1:0]), .b(2'b01), .eq(OP_UTYPE_eq));  // open: gt, lt
  assign in_10 = OP_UTYPE_eq ? 1'b0 : 1'bz;  // Driver driver_27
  assign reg_write_enable = OP_UTYPE_eq ? 1'b1 : 1'bz;  // Driver driver_28
  assign imm_select = OP_UTYPE_eq ? 2'b10 : 2'bz;  // Driver driver_29
  assign execute_port_a_sel = OP_UTYPE_eq ? 1'b1 : 1'bz;  // Driver driver_30
  assign execute_port_b_sel = OP_UTYPE_eq ? 1'b0 : 1'bz;  // Driver driver_31
  assign reg_write_data_sel = OP_UTYPE_eq ? 3'b001 : 3'bz;  // Driver driver_32
  assign load_store_type = OP_UTYPE_eq ? 3'b000 : 3'bz;  // Driver driver_33
  assign data_memory_write_enable = OP_UTYPE_eq ? 1'b0 : 1'bz;  // Driver driver_34
  assign alu_op_sel = OP_UTYPE_eq ? INSTRUCTION[4:2] : 3'bz;  // Driver driver_35
  assign branch_op_sel = OP_UTYPE_eq ? 3'b000 : 3'bz;  // Driver driver_36
  Seven_Seg_Hex seven_seg_hex_9 (.d(Binary_2[3:0]), .dp(1'b0));
  Seven_Seg_Hex seven_seg_hex_10 (.d(Binary_2[7:4]), .dp(1'b0));

  assign Decimal = Binary;
  assign Decimal_2 = Binary_2;
  assign Signed_Decimal = Binary;
  assign Signed_Decimal_2 = Binary_2;

  // Other names for the same wires on the sheet: alu_output[7:0] = Binary; branch_enable[7:0] = in_25;
  //   dmem_data[7:0] = in_26; HALT_t = HALT_2; IMM[7:0] = Binary_2; pc_mux_sel = in_10; RESET = in_11

  // Notes on the sheet:
  //   clk: Hz: 8
  //   clk_2: Hz: 16
  //   clk_3: Hz: 64
  //   clk_4: Hz: 2
  //   MANUAL: default 1
  //   CLOCK
  //   Instruction Memory
  //   ALU
  //   Register File
  //   contents of eepromdualport_1 (hex, n*v repeats v):
  //   6a1,121,41,61,181,1162,842,1822,181,ec97,f3
  //   RS2
  //   Use RD as input
  //   for U Type
  //   RS1
  //   alu_opsel
  //   000 - ADD
  //   001 - SUB
  //   010 - MUL
  //   011 - SLL
  //   100 - SRL
  //   101 - AND
  //   110 - OR
  //   111 - XOR
  //   RD
  //   To be implemented
  //   Program Counter
  //   RD MUX
  //   PORT A & B MUX
  //   branch_opsel
  //   000 - UNKNOWN
  //   001 - BEQ
  //   011 - BNE
  //   101 - BLTU
  //   111 - BGEU
  //   reg_write_data_sel
  //   000 -  dmem_data
  //   001 - alu_output
  //   010 - branch_enable
  //   011 - immediate
  //   100 - pc_next
  //   111 - N_A
  //   load_store_type
  //   000 - LS_N_A
  //   001 - L_B
  //   011 - L_BU
  //   111 - S_B
  //   Core Control Unit
  //   Imm Sign Extend
  //   U/J1 Type
  //   imm_select
  //   00 - Unknown
  //   01 - I/JALR
  //   10 - U/J1
  //   11 - S/B
endmodule
