// Digital circuit risc_like_8bit_relay.dig as structural Verilog
module risc_like_8bit_relay (
  input  in_1,
  input  in_2,
  input  in_3,
  input  in_4,
  input  in_5,
  input  in_6,
  input  in_7,
  input  in_8,
  input  [5:0] LOAD,
  input  [5:0] SELECT,
  input  clk,
  input  [5:0] SEL_ADDR,
  output [15:0] out_13,
  output [15:0] out_14
);

  wire and_1_out, B_0, B_1, B_2, B_3, B_4, B_5, B_6, B_7, counter_1_ovf, diodebackward_53_out,
       diodebackward_54_out, diodebackward_55_out, diodebackward_56_out, LOAD_CLK, multiplexer_1_out,
       or_1_out, pullup_1_out, pullup_2_out, pullup_3_out, pullup_4_out, pullup_5_out, pullup_6_out,
       pullup_7_out, pullup_8_out, relaydt_1_p3, relaydt_2_p3, relaydt_3_p3, relaydt_4_p3, relaydt_5_p3,
       relaydt_6_p3, relaydt_7_p3, relaydt_8_p3, relaydt_9_p2, relaydt_10_p2, relaydt_11_p2, relaydt_12_p2,
       relaydt_13_p2, relaydt_14_p2, relaydt_15_p2, relaydt_16_p2, relaydt_17_p2, relaydt_18_p2,
       relaydt_19_p2, relaydt_20_p2, relaydt_21_p2, relaydt_22_p2, relaydt_23_p2, relaydt_24_p2,
       relaydt_25_p2, relaydt_26_p2, relaydt_27_p2, relaydt_28_p2, relaydt_29_p2, relaydt_30_p2,
       relaydt_31_p2, relaydt_32_p2, relaydt_33_p2, relaydt_34_p2, relaydt_35_p2, relaydt_36_p2,
       relaydt_37_p2, relaydt_38_p2, relaydt_39_p2, relaydt_40_p2, relaydt_41_p2, relaydt_42_p2,
       relaydt_43_p2, relaydt_44_p2, relaydt_45_p2, relaydt_46_p2, relaydt_47_p2, relaydt_48_p2,
       relaydt_49_p4, relaydt_49_p5, relaydt_50_p1, relaydt_50_p4, relaydt_50_p8, relaydt_51_p4,
       relaydt_51_p5, relaydt_52_p1, relaydt_52_p4, relaydt_52_p8, relaydt_53_p4, relaydt_53_p5,
       relaydt_54_p1, relaydt_54_p4, relaydt_54_p8, relaydt_55_p5, relaydt_56_p4, relaydt_56_p5,
       relaydt_57_p1, relaydt_57_p4, relaydt_57_p8, relaydt_58_p5, relaydt_60_p5, relaydt_62_p5,
       relaydt_65_p5, relaydt_67_p5, relaydt_69_p5, relaydt_71_p5, relaydt_73_p6, relaydt_73_p9,
       relaydt_74_p5, relaydt_75_p6, relaydt_75_p9, relaydt_76_p5, relaydt_77_p6, relaydt_77_p9,
       relaydt_78_p5, relaydt_79_p6, relaydt_79_p9, relaydt_80_p5, relaydt_81_p5, relaydt_82_p5,
       relaydt_83_p5, relaydt_85_p5, relaydt_87_p6, relaydt_87_p9, relaydt_89_p6, relaydt_89_p9,
       relaydt_91_p6, relaydt_91_p9, relaydt_92_p5, relaydt_93_p6, relaydt_93_p9, relaydt_94_p5,
       relaydt_95_p5, relaydt_96_p5, relaydt_97_p5, relaydt_99_p5, relaydt_101_p5, relaydt_103_p5,
       relaydt_105_p6, relaydt_105_p9, relaydt_106_p5, relaydt_107_p6, relaydt_107_p9, relaydt_108_p5,
       relaydt_109_p6, relaydt_109_p9, relaydt_110_p5, relaydt_111_p6, relaydt_111_p9, relaydt_112_p5,
       relaydt_113_p5, relaydt_114_p5, relaydt_115_p5, relaydt_117_p5, relaydt_119_p6, relaydt_119_p9,
       relaydt_121_p6, relaydt_121_p9, relaydt_123_p6, relaydt_123_p9, relaydt_124_p5, relaydt_125_p6,
       relaydt_125_p9, relaydt_126_p5, relaydt_127_p5, relaydt_128_p5, relaydt_129_p5, relaydt_131_p5,
       relaydt_133_p5, relaydt_135_p5, relaydt_137_p6, relaydt_137_p9, relaydt_138_p5, relaydt_139_p6,
       relaydt_139_p9, relaydt_140_p5, relaydt_141_p6, relaydt_141_p9, relaydt_142_p5, relaydt_143_p6,
       relaydt_143_p9, relaydt_144_p5, relaydt_145_p5, relaydt_146_p5, relaydt_147_p5, relaydt_149_p5,
       relaydt_151_p6, relaydt_151_p9, relaydt_153_p6, relaydt_153_p9, relaydt_155_p6, relaydt_155_p9,
       relaydt_156_p5, relaydt_157_p6, relaydt_157_p9, relaydt_158_p5, relaydt_159_p5, relaydt_160_p5,
       relaydt_161_p5, relaydt_163_p5, relaydt_165_p5, relaydt_167_p5, relaydt_169_p6, relaydt_169_p9,
       relaydt_170_p5, relaydt_171_p6, relaydt_171_p9, relaydt_172_p5, relaydt_173_p6, relaydt_173_p9,
       relaydt_174_p5, relaydt_175_p6, relaydt_175_p9, relaydt_176_p5, relaydt_177_p5, relaydt_178_p5,
       relaydt_179_p5, relaydt_181_p5, relaydt_185_p3, relaydt_186_p3, relaydt_187_p3, relaydt_188_p3,
       relaydt_189_p2, relaydt_190_p2, relaydt_191_p2, relaydt_192_p2, relaydt_193_p2, relaydt_194_p2,
       relaydt_195_p2, relaydt_196_p2, relaydt_197_p2, relaydt_198_p2, relaydt_199_p2, relaydt_200_p2,
       relaydt_201_p2, relaydt_202_p2, relaydt_203_p2, relaydt_204_p2, relaydt_205_p2, relaydt_206_p2,
       relaydt_207_p2, relaydt_208_p2, relaydt_209_p3, relaydt_209_p4, relaydt_210_p1, relaydt_210_p4,
       relaydt_210_p7, relaydt_211_p3, relaydt_211_p4, relaydt_212_p1, relaydt_212_p4, relaydt_212_p7,
       relaydt_213_p4, relaydt_214_p5, relaydt_215_p3, relaydt_216_p5, relaydt_217_p6, relaydt_218_p5,
       relaydt_219_p6, relaydt_219_p9, relaydt_220_p5, relaydt_221_p6, relaydt_221_p9, relaydt_222_p5,
       relaydt_223_p5, relaydt_224_p5, relaydt_225_p6, relaydt_225_p9, relaydt_226_p6, relaydt_226_p9,
       relaydt_227_p5, relaydt_228_p5, relaydt_229_p5, relaydt_230_p5, relaydt_231_p6, relaydt_231_p9,
       relaydt_232_p5, relaydt_233_p6, relaydt_233_p9, relaydt_234_p5, relaydt_235_p5, relaydt_236_p5,
       rs_ff_1_nq, START_LOAD_p1, START_LOAD_p2, t_ff_1_nq;
  wire [5:0] LOAD_ADDR, not_1_out, not_2_out, not_3_out, not_4_out, not_5_out, not_6_out;

  assign not_1_out = ~{6{1'b0}};  // Not not_1, 6 bits wide
  PullUp pullup_1 (.out(pullup_1_out));
  PullUp pullup_2 (.out(pullup_2_out));
  assign not_2_out = ~6'b000001;  // Not not_2, 6 bits wide
  PullUp pullup_3 (.out(pullup_3_out));
  PullUp pullup_4 (.out(pullup_4_out));
  assign not_3_out = ~6'b000010;  // Not not_3, 6 bits wide
  PullUp pullup_5 (.out(pullup_5_out));
  LED led_1 (.in(pullup_5_out));
  PullUp pullup_6 (.out(pullup_6_out));
  LED led_2 (.in(pullup_6_out));
  assign not_4_out = ~6'b000011;  // Not not_4, 6 bits wide
  PullUp pullup_7 (.out(pullup_7_out));
  LED led_3 (.in(pullup_7_out));
  PullUp pullup_8 (.out(pullup_8_out));
  LED led_4 (.in(pullup_8_out));
  // ButtonLED START_LOAD: pin names not known; wires that end beside it: START_LOAD_p1, START_LOAD_p2
  // RelayDT relaydt_1: pin names not known; wires that end beside it: LOAD_ADDR[5], 1'b0, relaydt_1_p3, LOAD_ADDR[4]
  DiodeBackward diodebackward_1 (.in(relaydt_1_p3), .out(pullup_1_out));
  LED led_5 (.in(pullup_1_out));
  // RelayDT relaydt_2: pin names not known; wires that end beside it: SEL_ADDR[5], 1'b0, relaydt_2_p3, SEL_ADDR[4]
  DiodeBackward diodebackward_2 (.in(relaydt_2_p3), .out(pullup_2_out));
  LED led_6 (.in(pullup_2_out));
  // RelayDT relaydt_3: pin names not known; wires that end beside it: LOAD_ADDR[5], 1'b0, relaydt_3_p3, LOAD_ADDR[4]
  DiodeBackward diodebackward_3 (.in(relaydt_3_p3), .out(pullup_3_out));
  LED led_7 (.in(pullup_3_out));
  // RelayDT relaydt_4: pin names not known; wires that end beside it: SEL_ADDR[5], 1'b0, relaydt_4_p3, SEL_ADDR[4]
  DiodeBackward diodebackward_4 (.in(relaydt_4_p3), .out(pullup_4_out));
  LED led_8 (.in(pullup_4_out));
  // RelayDT relaydt_5: pin names not known; wires that end beside it: LOAD_ADDR[5], 1'b0, relaydt_5_p3, LOAD_ADDR[4]
  DiodeBackward diodebackward_5 (.in(relaydt_5_p3), .out(pullup_5_out));
  // RelayDT relaydt_6: pin names not known; wires that end beside it: SEL_ADDR[5], 1'b0, relaydt_6_p3, SEL_ADDR[4]
  DiodeBackward diodebackward_6 (.in(relaydt_6_p3), .out(pullup_6_out));
  // RelayDT relaydt_7: pin names not known; wires that end beside it: LOAD_ADDR[5], 1'b0, relaydt_7_p3, LOAD_ADDR[4]
  DiodeBackward diodebackward_7 (.in(relaydt_7_p3), .out(pullup_7_out));
  // RelayDT relaydt_8: pin names not known; wires that end beside it: SEL_ADDR[5], 1'b0, relaydt_8_p3, SEL_ADDR[4]
  DiodeBackward diodebackward_8 (.in(relaydt_8_p3), .out(pullup_8_out));
  or or_1 (or_1_out, counter_1_ovf, START_LOAD_p1);
  // RelayDT relaydt_9: pin names not known; wires that end beside it: 1'b0, relaydt_9_p2, LOAD_ADDR[3]
  DiodeBackward diodebackward_9 (.in(relaydt_9_p2), .out(pullup_1_out));
  // RelayDT relaydt_10: pin names not known; wires that end beside it: 1'b0, relaydt_10_p2, SEL_ADDR[3]
  DiodeBackward diodebackward_10 (.in(relaydt_10_p2), .out(pullup_2_out));
  // RelayDT relaydt_11: pin names not known; wires that end beside it: 1'b0, relaydt_11_p2, LOAD_ADDR[3]
  DiodeBackward diodebackward_11 (.in(relaydt_11_p2), .out(pullup_3_out));
  // RelayDT relaydt_12: pin names not known; wires that end beside it: 1'b0, relaydt_12_p2, SEL_ADDR[3]
  DiodeBackward diodebackward_12 (.in(relaydt_12_p2), .out(pullup_4_out));
  // RelayDT relaydt_13: pin names not known; wires that end beside it: 1'b0, relaydt_13_p2, LOAD_ADDR[3]
  DiodeBackward diodebackward_13 (.in(relaydt_13_p2), .out(pullup_5_out));
  // RelayDT relaydt_14: pin names not known; wires that end beside it: 1'b0, relaydt_14_p2, SEL_ADDR[3]
  DiodeBackward diodebackward_14 (.in(relaydt_14_p2), .out(pullup_6_out));
  // RelayDT relaydt_15: pin names not known; wires that end beside it: 1'b0, relaydt_15_p2, LOAD_ADDR[3]
  DiodeBackward diodebackward_15 (.in(relaydt_15_p2), .out(pullup_7_out));
  // RelayDT relaydt_16: pin names not known; wires that end beside it: 1'b0, relaydt_16_p2, SEL_ADDR[3]
  DiodeBackward diodebackward_16 (.in(relaydt_16_p2), .out(pullup_8_out));
  T_FF t_ff_1 (.T(1'b1), .C(or_1_out), .Q(START_LOAD_p2), .nQ(t_ff_1_nq));
  // RelayDT relaydt_17: pin names not known; wires that end beside it: 1'b0, relaydt_17_p2, LOAD_ADDR[2]
  DiodeBackward diodebackward_17 (.in(relaydt_17_p2), .out(pullup_1_out));
  // RelayDT relaydt_18: pin names not known; wires that end beside it: 1'b0, relaydt_18_p2, SEL_ADDR[2]
  DiodeBackward diodebackward_18 (.in(relaydt_18_p2), .out(pullup_2_out));
  // RelayDT relaydt_19: pin names not known; wires that end beside it: 1'b0, relaydt_19_p2, LOAD_ADDR[2]
  DiodeBackward diodebackward_19 (.in(relaydt_19_p2), .out(pullup_3_out));
  // RelayDT relaydt_20: pin names not known; wires that end beside it: 1'b0, relaydt_20_p2, SEL_ADDR[2]
  DiodeBackward diodebackward_20 (.in(relaydt_20_p2), .out(pullup_4_out));
  // RelayDT relaydt_21: pin names not known; wires that end beside it: 1'b0, relaydt_21_p2, LOAD_ADDR[2]
  DiodeBackward diodebackward_21 (.in(relaydt_21_p2), .out(pullup_5_out));
  // RelayDT relaydt_22: pin names not known; wires that end beside it: 1'b0, relaydt_22_p2, SEL_ADDR[2]
  DiodeBackward diodebackward_22 (.in(relaydt_22_p2), .out(pullup_6_out));
  // RelayDT relaydt_23: pin names not known; wires that end beside it: 1'b0, relaydt_23_p2, LOAD_ADDR[2]
  DiodeBackward diodebackward_23 (.in(relaydt_23_p2), .out(pullup_7_out));
  // RelayDT relaydt_24: pin names not known; wires that end beside it: 1'b0, relaydt_24_p2, SEL_ADDR[2]
  DiodeBackward diodebackward_24 (.in(relaydt_24_p2), .out(pullup_8_out));
  // RelayDT relaydt_25: pin names not known; wires that end beside it: 1'b0, relaydt_25_p2, LOAD_ADDR[1]
  DiodeBackward diodebackward_25 (.in(relaydt_25_p2), .out(pullup_1_out));
  // RelayDT relaydt_26: pin names not known; wires that end beside it: 1'b0, relaydt_26_p2, SEL_ADDR[1]
  DiodeBackward diodebackward_26 (.in(relaydt_26_p2), .out(pullup_2_out));
  // RelayDT relaydt_27: pin names not known; wires that end beside it: 1'b0, relaydt_27_p2, LOAD_ADDR[1]
  DiodeBackward diodebackward_27 (.in(relaydt_27_p2), .out(pullup_3_out));
  // RelayDT relaydt_28: pin names not known; wires that end beside it: 1'b0, relaydt_28_p2, SEL_ADDR[1]
  DiodeBackward diodebackward_28 (.in(relaydt_28_p2), .out(pullup_4_out));
  // RelayDT relaydt_29: pin names not known; wires that end beside it: 1'b0, relaydt_29_p2, LOAD_ADDR[1]
  DiodeBackward diodebackward_29 (.in(relaydt_29_p2), .out(pullup_5_out));
  // RelayDT relaydt_30: pin names not known; wires that end beside it: 1'b0, relaydt_30_p2, SEL_ADDR[1]
  DiodeBackward diodebackward_30 (.in(relaydt_30_p2), .out(pullup_6_out));
  // RelayDT relaydt_31: pin names not known; wires that end beside it: 1'b0, relaydt_31_p2, LOAD_ADDR[1]
  DiodeBackward diodebackward_31 (.in(relaydt_31_p2), .out(pullup_7_out));
  // RelayDT relaydt_32: pin names not known; wires that end beside it: 1'b0, relaydt_32_p2, SEL_ADDR[1]
  DiodeBackward diodebackward_32 (.in(relaydt_32_p2), .out(pullup_8_out));
  and and_1 (and_1_out, ~t_ff_1_nq, rs_ff_1_nq);  // And
  // RelayDT relaydt_33: pin names not known; wires that end beside it: 1'b0, relaydt_33_p2, LOAD_ADDR[0]
  DiodeBackward diodebackward_33 (.in(relaydt_33_p2), .out(pullup_1_out));
  // RelayDT relaydt_34: pin names not known; wires that end beside it: 1'b0, relaydt_34_p2, SEL_ADDR[0]
  DiodeBackward diodebackward_34 (.in(relaydt_34_p2), .out(pullup_2_out));
  // RelayDT relaydt_35: pin names not known; wires that end beside it: 1'b0, relaydt_35_p2, LOAD_ADDR[0]
  DiodeBackward diodebackward_35 (.in(relaydt_35_p2), .out(pullup_3_out));
  // RelayDT relaydt_36: pin names not known; wires that end beside it: 1'b0, relaydt_36_p2, SEL_ADDR[0]
  DiodeBackward diodebackward_36 (.in(relaydt_36_p2), .out(pullup_4_out));
  // RelayDT relaydt_37: pin names not known; wires that end beside it: 1'b0, relaydt_37_p2, LOAD_ADDR[0]
  DiodeBackward diodebackward_37 (.in(relaydt_37_p2), .out(pullup_5_out));
  // RelayDT relaydt_38: pin names not known; wires that end beside it: 1'b0, relaydt_38_p2, SEL_ADDR[0]
  DiodeBackward diodebackward_38 (.in(relaydt_38_p2), .out(pullup_6_out));
  // RelayDT relaydt_39: pin names not known; wires that end beside it: 1'b0, relaydt_39_p2, LOAD_ADDR[0]
  DiodeBackward diodebackward_39 (.in(relaydt_39_p2), .out(pullup_7_out));
  // RelayDT relaydt_40: pin names not known; wires that end beside it: 1'b0, relaydt_40_p2, SEL_ADDR[0]
  DiodeBackward diodebackward_40 (.in(relaydt_40_p2), .out(pullup_8_out));
  RS_FF rs_ff_1 (.S(and_1_out), .C(clk), .R(~and_1_out), .Q(LOAD_CLK), .nQ(rs_ff_1_nq));
  // RelayDT relaydt_41: pin names not known; wires that end beside it: 1'b0, relaydt_41_p2
  DiodeBackward diodebackward_41 (.in(relaydt_41_p2), .out(pullup_1_out));
  // RelayDT relaydt_42: pin names not known; wires that end beside it: 1'b0, relaydt_42_p2
  DiodeBackward diodebackward_42 (.in(relaydt_42_p2), .out(pullup_2_out));
  // RelayDT relaydt_43: pin names not known; wires that end beside it: 1'b0, relaydt_43_p2
  DiodeBackward diodebackward_43 (.in(relaydt_43_p2), .out(pullup_3_out));
  // RelayDT relaydt_44: pin names not known; wires that end beside it: 1'b0, relaydt_44_p2
  DiodeBackward diodebackward_44 (.in(relaydt_44_p2), .out(pullup_4_out));
  // RelayDT relaydt_45: pin names not known; wires that end beside it: 1'b0, relaydt_45_p2
  DiodeBackward diodebackward_45 (.in(relaydt_45_p2), .out(pullup_5_out));
  DiodeBackward diodebackward_46 (.in(LOAD_CLK), .out(pullup_5_out));
  // RelayDT relaydt_46: pin names not known; wires that end beside it: 1'b0, relaydt_46_p2
  DiodeBackward diodebackward_47 (.in(relaydt_46_p2), .out(pullup_6_out));
  // RelayDT relaydt_47: pin names not known; wires that end beside it: 1'b0, relaydt_47_p2
  DiodeBackward diodebackward_48 (.in(relaydt_47_p2), .out(pullup_7_out));
  DiodeBackward diodebackward_49 (.in(LOAD_CLK), .out(pullup_7_out));
  // RelayDT relaydt_48: pin names not known; wires that end beside it: 1'b0, relaydt_48_p2
  DiodeBackward diodebackward_50 (.in(relaydt_48_p2), .out(pullup_8_out));
  DiodeBackward diodebackward_51 (.in(LOAD_CLK), .out(pullup_1_out));
  DiodeBackward diodebackward_52 (.in(LOAD_CLK), .out(pullup_3_out));
  Multiplexer multiplexer_1 (.sel(t_ff_1_nq), .in_0(rs_ff_1_nq), .in_1(START_LOAD_p1), .out(multiplexer_1_out));
  LED led_9 (.in(LOAD_CLK));
  // RelayDT #(.poles(2)) relaydt_49: pin names not known; wires that end beside it: pullup_1_out, 1'b1, 1'b1, relaydt_49_p4, relaydt_49_p5
  // RelayDT #(.poles(2)) relaydt_50: pin names not known; wires that end beside it: relaydt_50_p1, 1'b0, out_14[15], relaydt_50_p4, 1'b0, relaydt_50_p4, out_14[14], relaydt_50_p8, 1'b0
  // RelayDT #(.poles(2)) relaydt_51: pin names not known; wires that end beside it: pullup_3_out, 1'b1, 1'b1, relaydt_51_p4, relaydt_51_p5
  // RelayDT #(.poles(2)) relaydt_52: pin names not known; wires that end beside it: relaydt_52_p1, 1'b0, out_14[15], relaydt_52_p4, 1'b0, relaydt_52_p4, out_14[14], relaydt_52_p8, 1'b0
  // RelayDT #(.poles(2)) relaydt_53: pin names not known; wires that end beside it: pullup_5_out, 1'b1, 1'b1, relaydt_53_p4, relaydt_53_p5
  // RelayDT #(.poles(2)) relaydt_54: pin names not known; wires that end beside it: relaydt_54_p1, 1'b0, out_14[15], relaydt_54_p4, 1'b0, relaydt_54_p4, out_14[14], relaydt_54_p8, 1'b0
  // RelayDT #(.poles(2)) relaydt_55: pin names not known; wires that end beside it: relaydt_54_p4, 1'b1, relaydt_53_p5, 1'b0, relaydt_55_p5
  // RelayDT #(.poles(2)) relaydt_56: pin names not known; wires that end beside it: pullup_7_out, 1'b1, 1'b1, relaydt_56_p4, relaydt_56_p5
  // RelayDT #(.poles(2)) relaydt_57: pin names not known; wires that end beside it: relaydt_57_p1, 1'b0, out_14[15], relaydt_57_p4, 1'b0, relaydt_57_p4, out_14[14], relaydt_57_p8, 1'b0
  // RelayDT #(.poles(2)) relaydt_58: pin names not known; wires that end beside it: relaydt_57_p4, 1'b1, relaydt_56_p5, 1'b0, relaydt_58_p5
  Counter #(.Bits(6)) counter_1 (
    .en(1'b1), .C(multiplexer_1_out), .clr(t_ff_1_nq), .out(LOAD_ADDR), .ovf(counter_1_ovf));
  // RelayDT #(.poles(2)) relaydt_59: pin names not known; wires that end beside it: relaydt_49_p4, 1'b1, 1'b0, relaydt_50_p1
  // RelayDT #(.poles(2)) relaydt_60: pin names not known; wires that end beside it: relaydt_50_p4, 1'b1, relaydt_49_p5, 1'b0, relaydt_60_p5
  LED led_10 (.in(relaydt_60_p5));
  // RelayDT #(.poles(2)) relaydt_61: pin names not known; wires that end beside it: 1'b1, relaydt_52_p1
  // RelayDT #(.poles(2)) relaydt_62: pin names not known; wires that end beside it: relaydt_52_p4, 1'b1, relaydt_51_p5, 1'b0, relaydt_62_p5
  LED led_11 (.in(relaydt_62_p5));
  // RelayDT #(.poles(2)) relaydt_63: pin names not known; wires that end beside it: relaydt_53_p4, 1'b1, relaydt_54_p1
  LED led_12 (.in(relaydt_55_p5));
  // RelayDT #(.poles(2)) relaydt_64: pin names not known; wires that end beside it: 1'b1, relaydt_57_p1
  LED led_13 (.in(relaydt_58_p5));
  // RelayDT #(.poles(2)) relaydt_65: pin names not known; wires that end beside it: relaydt_50_p8, 1'b1, relaydt_49_p5, 1'b0, relaydt_65_p5
  LED led_14 (.in(relaydt_65_p5));
  // RelayDT #(.poles(2)) relaydt_66: pin names not known; wires that end beside it: relaydt_51_p4, relaydt_60_p5, out_13[15], 1'b0, relaydt_65_p5, out_13[14], pullup_2_out, 1'b0
  // RelayDT #(.poles(2)) relaydt_67: pin names not known; wires that end beside it: relaydt_52_p8, 1'b1, relaydt_51_p5, 1'b0, relaydt_67_p5
  LED led_15 (.in(relaydt_67_p5));
  // RelayDT #(.poles(2)) relaydt_68: pin names not known; wires that end beside it: relaydt_62_p5, out_13[15], 1'b0, relaydt_67_p5, out_13[14], pullup_4_out, 1'b0
  // RelayDT #(.poles(2)) relaydt_69: pin names not known; wires that end beside it: relaydt_54_p8, 1'b1, relaydt_53_p5, 1'b0, relaydt_69_p5
  LED led_16 (.in(relaydt_69_p5));
  // RelayDT #(.poles(2)) relaydt_70: pin names not known; wires that end beside it: relaydt_56_p4, relaydt_55_p5, out_13[15], 1'b0, relaydt_69_p5, out_13[14], pullup_6_out, 1'b0
  // RelayDT #(.poles(2)) relaydt_71: pin names not known; wires that end beside it: relaydt_57_p8, 1'b1, relaydt_56_p5, 1'b0, relaydt_71_p5
  LED led_17 (.in(relaydt_71_p5));
  // RelayDT #(.poles(2)) relaydt_72: pin names not known; wires that end beside it: relaydt_58_p5, out_13[15], relaydt_71_p5, out_13[14], pullup_8_out, 1'b0
  EEPROMDualPort #(.AddrBits(6), .isProgramMemory("true"), .Bits(16)) eepromdualport_1 (
    .A(LOAD_ADDR), .Din({16{1'b0}}), .str(1'b0), .C(LOAD_CLK), .ld(1'b1), .D(out_14));
  // RelayDT #(.poles(2)) relaydt_73: pin names not known; wires that end beside it: relaydt_50_p8, relaydt_50_p1, 1'b0, 1'b0, out_14[13], relaydt_73_p6, relaydt_73_p6, out_14[12], relaydt_73_p9, 1'b0
  // RelayDT #(.poles(2)) relaydt_74: pin names not known; wires that end beside it: relaydt_73_p6, 1'b1, relaydt_49_p5, 1'b0, relaydt_74_p5
  // RelayDT #(.poles(2)) relaydt_75: pin names not known; wires that end beside it: relaydt_52_p8, relaydt_52_p1, 1'b0, 1'b0, out_14[13], relaydt_75_p6, relaydt_75_p6, out_14[12], relaydt_75_p9, 1'b0
  // RelayDT #(.poles(2)) relaydt_76: pin names not known; wires that end beside it: relaydt_75_p6, 1'b1, relaydt_51_p5, 1'b0, relaydt_76_p5
  // RelayDT #(.poles(2)) relaydt_77: pin names not known; wires that end beside it: relaydt_54_p8, relaydt_54_p1, 1'b0, 1'b0, out_14[13], relaydt_77_p6, relaydt_77_p6, out_14[12], relaydt_77_p9, 1'b0
  // RelayDT #(.poles(2)) relaydt_78: pin names not known; wires that end beside it: relaydt_77_p6, 1'b1, relaydt_53_p5, 1'b0, relaydt_78_p5
  LED led_18 (.in(relaydt_78_p5));
  // RelayDT #(.poles(2)) relaydt_79: pin names not known; wires that end beside it: relaydt_57_p8, relaydt_57_p1, 1'b0, 1'b0, out_14[13], relaydt_79_p6, relaydt_79_p6, out_14[12], relaydt_79_p9, 1'b0
  // RelayDT #(.poles(2)) relaydt_80: pin names not known; wires that end beside it: relaydt_79_p6, 1'b1, relaydt_56_p5, 1'b0, relaydt_80_p5
  LED led_19 (.in(relaydt_80_p5));
  Seven_Seg_Hex seven_seg_hex_1 (.d({2'b00, LOAD_ADDR[5:4]}), .dp(1'b0));
  Seven_Seg_Hex seven_seg_hex_2 (.d(LOAD_ADDR[3:0]), .dp(1'b0));
  // RelayDT #(.poles(2)) relaydt_81: pin names not known; wires that end beside it: relaydt_73_p9, 1'b1, relaydt_49_p5, 1'b0, relaydt_81_p5
  LED led_20 (.in(relaydt_74_p5));
  // RelayDT #(.poles(2)) relaydt_82: pin names not known; wires that end beside it: relaydt_75_p9, 1'b1, relaydt_51_p5, 1'b0, relaydt_82_p5
  LED led_21 (.in(relaydt_76_p5));
  // RelayDT #(.poles(2)) relaydt_83: pin names not known; wires that end beside it: relaydt_77_p9, 1'b1, relaydt_53_p5, 1'b0, relaydt_83_p5
  // RelayDT #(.poles(2)) relaydt_84: pin names not known; wires that end beside it: relaydt_78_p5, out_13[13], relaydt_83_p5, out_13[12], pullup_6_out, 1'b0
  // RelayDT #(.poles(2)) relaydt_85: pin names not known; wires that end beside it: relaydt_79_p9, 1'b1, relaydt_56_p5, 1'b0, relaydt_85_p5
  // RelayDT #(.poles(2)) relaydt_86: pin names not known; wires that end beside it: relaydt_80_p5, out_13[13], relaydt_85_p5, out_13[12], pullup_8_out, 1'b0
  // RelayDT #(.poles(2)) relaydt_87: pin names not known; wires that end beside it: relaydt_73_p9, relaydt_50_p1, 1'b0, 1'b0, out_14[11], relaydt_87_p6, relaydt_87_p6, out_14[10], relaydt_87_p9, 1'b0
  LED led_22 (.in(relaydt_81_p5));
  // RelayDT #(.poles(2)) relaydt_88: pin names not known; wires that end beside it: relaydt_74_p5, out_13[13], relaydt_81_p5, out_13[12], pullup_2_out, 1'b0
  // RelayDT #(.poles(2)) relaydt_89: pin names not known; wires that end beside it: relaydt_75_p9, relaydt_52_p1, 1'b0, 1'b0, out_14[11], relaydt_89_p6, relaydt_89_p6, out_14[10], relaydt_89_p9, 1'b0
  LED led_23 (.in(relaydt_82_p5));
  // RelayDT #(.poles(2)) relaydt_90: pin names not known; wires that end beside it: relaydt_76_p5, out_13[13], relaydt_82_p5, out_13[12], pullup_4_out, 1'b0
  // RelayDT #(.poles(2)) relaydt_91: pin names not known; wires that end beside it: relaydt_77_p9, relaydt_54_p1, 1'b0, 1'b0, out_14[11], relaydt_91_p6, relaydt_91_p6, out_14[10], relaydt_91_p9, 1'b0
  // RelayDT #(.poles(2)) relaydt_92: pin names not known; wires that end beside it: relaydt_91_p6, 1'b1, relaydt_53_p5, 1'b0, relaydt_92_p5
  LED led_24 (.in(relaydt_83_p5));
  // RelayDT #(.poles(2)) relaydt_93: pin names not known; wires that end beside it: relaydt_79_p9, relaydt_57_p1, 1'b0, 1'b0, out_14[11], relaydt_93_p6, relaydt_93_p6, out_14[10], relaydt_93_p9, 1'b0
  // RelayDT #(.poles(2)) relaydt_94: pin names not known; wires that end beside it: relaydt_93_p6, 1'b1, relaydt_56_p5, 1'b0, relaydt_94_p5
  LED led_25 (.in(relaydt_85_p5));
  // RelayDT #(.poles(2)) relaydt_95: pin names not known; wires that end beside it: relaydt_87_p6, 1'b1, relaydt_49_p5, 1'b0, relaydt_95_p5
  LED led_26 (.in(relaydt_95_p5));
  // RelayDT #(.poles(2)) relaydt_96: pin names not known; wires that end beside it: relaydt_89_p6, 1'b1, relaydt_51_p5, 1'b0, relaydt_96_p5
  LED led_27 (.in(relaydt_96_p5));
  LED led_28 (.in(relaydt_92_p5));
  LED led_29 (.in(relaydt_94_p5));
  // RelayDT #(.poles(2)) relaydt_97: pin names not known; wires that end beside it: relaydt_87_p9, 1'b1, relaydt_49_p5, 1'b0, relaydt_97_p5
  LED led_30 (.in(relaydt_97_p5));
  // RelayDT #(.poles(2)) relaydt_98: pin names not known; wires that end beside it: relaydt_95_p5, out_13[11], relaydt_97_p5, out_13[10], pullup_2_out, 1'b0
  // RelayDT #(.poles(2)) relaydt_99: pin names not known; wires that end beside it: relaydt_89_p9, 1'b1, relaydt_51_p5, 1'b0, relaydt_99_p5
  LED led_31 (.in(relaydt_99_p5));
  // RelayDT #(.poles(2)) relaydt_100: pin names not known; wires that end beside it: relaydt_96_p5, out_13[11], relaydt_99_p5, out_13[10], pullup_4_out, 1'b0
  // RelayDT #(.poles(2)) relaydt_101: pin names not known; wires that end beside it: relaydt_91_p9, 1'b1, relaydt_53_p5, 1'b0, relaydt_101_p5
  LED led_32 (.in(relaydt_101_p5));
  // RelayDT #(.poles(2)) relaydt_102: pin names not known; wires that end beside it: relaydt_92_p5, out_13[11], relaydt_101_p5, out_13[10], pullup_6_out, 1'b0
  // RelayDT #(.poles(2)) relaydt_103: pin names not known; wires that end beside it: relaydt_93_p9, 1'b1, relaydt_56_p5, 1'b0, relaydt_103_p5
  LED led_33 (.in(relaydt_103_p5));
  // RelayDT #(.poles(2)) relaydt_104: pin names not known; wires that end beside it: relaydt_94_p5, out_13[11], relaydt_103_p5, out_13[10], pullup_8_out, 1'b0
  // RelayDT #(.poles(2)) relaydt_105: pin names not known; wires that end beside it: relaydt_87_p9, relaydt_50_p1, 1'b0, 1'b0, out_14[9], relaydt_105_p6, relaydt_105_p6, out_14[8], relaydt_105_p9, 1'b0
  // RelayDT #(.poles(2)) relaydt_106: pin names not known; wires that end beside it: relaydt_105_p6, 1'b1, relaydt_49_p5, 1'b0, relaydt_106_p5
  // RelayDT #(.poles(2)) relaydt_107: pin names not known; wires that end beside it: relaydt_89_p9, relaydt_52_p1, 1'b0, 1'b0, out_14[9], relaydt_107_p6, relaydt_107_p6, out_14[8], relaydt_107_p9, 1'b0
  // RelayDT #(.poles(2)) relaydt_108: pin names not known; wires that end beside it: relaydt_107_p6, 1'b1, relaydt_51_p5, 1'b0, relaydt_108_p5
  // RelayDT #(.poles(2)) relaydt_109: pin names not known; wires that end beside it: relaydt_91_p9, relaydt_54_p1, 1'b0, 1'b0, out_14[9], relaydt_109_p6, relaydt_109_p6, out_14[8], relaydt_109_p9, 1'b0
  // RelayDT #(.poles(2)) relaydt_110: pin names not known; wires that end beside it: relaydt_109_p6, 1'b1, relaydt_53_p5, 1'b0, relaydt_110_p5
  LED led_34 (.in(relaydt_110_p5));
  // RelayDT #(.poles(2)) relaydt_111: pin names not known; wires that end beside it: relaydt_93_p9, relaydt_57_p1, 1'b0, 1'b0, out_14[9], relaydt_111_p6, relaydt_111_p6, out_14[8], relaydt_111_p9, 1'b0
  // RelayDT #(.poles(2)) relaydt_112: pin names not known; wires that end beside it: relaydt_111_p6, 1'b1, relaydt_56_p5, 1'b0, relaydt_112_p5
  LED led_35 (.in(relaydt_112_p5));
  // RelayDT #(.poles(2)) relaydt_113: pin names not known; wires that end beside it: relaydt_105_p9, 1'b1, relaydt_49_p5, 1'b0, relaydt_113_p5
  LED led_36 (.in(relaydt_106_p5));
  // RelayDT #(.poles(2)) relaydt_114: pin names not known; wires that end beside it: relaydt_107_p9, 1'b1, relaydt_51_p5, 1'b0, relaydt_114_p5
  LED led_37 (.in(relaydt_108_p5));
  // RelayDT #(.poles(2)) relaydt_115: pin names not known; wires that end beside it: relaydt_109_p9, 1'b1, relaydt_53_p5, 1'b0, relaydt_115_p5
  // RelayDT #(.poles(2)) relaydt_116: pin names not known; wires that end beside it: relaydt_110_p5, out_13[9], relaydt_115_p5, out_13[8], pullup_6_out, 1'b0
  // RelayDT #(.poles(2)) relaydt_117: pin names not known; wires that end beside it: relaydt_111_p9, 1'b1, relaydt_56_p5, 1'b0, relaydt_117_p5
  // RelayDT #(.poles(2)) relaydt_118: pin names not known; wires that end beside it: relaydt_112_p5, out_13[9], relaydt_117_p5, out_13[8], pullup_8_out, 1'b0
  // RelayDT #(.poles(2)) relaydt_119: pin names not known; wires that end beside it: relaydt_105_p9, relaydt_50_p1, 1'b0, 1'b0, out_14[7], relaydt_119_p6, relaydt_119_p6, out_14[6], relaydt_119_p9, 1'b0
  LED led_38 (.in(relaydt_113_p5));
  // RelayDT #(.poles(2)) relaydt_120: pin names not known; wires that end beside it: relaydt_106_p5, out_13[9], relaydt_113_p5, out_13[8], pullup_2_out, 1'b0
  // RelayDT #(.poles(2)) relaydt_121: pin names not known; wires that end beside it: relaydt_107_p9, relaydt_52_p1, 1'b0, 1'b0, out_14[7], relaydt_121_p6, relaydt_121_p6, out_14[6], relaydt_121_p9, 1'b0
  LED led_39 (.in(relaydt_114_p5));
  // RelayDT #(.poles(2)) relaydt_122: pin names not known; wires that end beside it: relaydt_108_p5, out_13[9], relaydt_114_p5, out_13[8], pullup_4_out, 1'b0
  // RelayDT #(.poles(2)) relaydt_123: pin names not known; wires that end beside it: relaydt_109_p9, relaydt_54_p1, 1'b0, 1'b0, out_14[7], relaydt_123_p6, relaydt_123_p6, out_14[6], relaydt_123_p9, 1'b0
  // RelayDT #(.poles(2)) relaydt_124: pin names not known; wires that end beside it: relaydt_123_p6, 1'b1, relaydt_53_p5, 1'b0, relaydt_124_p5
  LED led_40 (.in(relaydt_115_p5));
  // RelayDT #(.poles(2)) relaydt_125: pin names not known; wires that end beside it: relaydt_111_p9, relaydt_57_p1, 1'b0, 1'b0, out_14[7], relaydt_125_p6, relaydt_125_p6, out_14[6], relaydt_125_p9, 1'b0
  // RelayDT #(.poles(2)) relaydt_126: pin names not known; wires that end beside it: relaydt_125_p6, 1'b1, relaydt_56_p5, 1'b0, relaydt_126_p5
  LED led_41 (.in(relaydt_117_p5));
  // RelayDT #(.poles(2)) relaydt_127: pin names not known; wires that end beside it: relaydt_119_p6, 1'b1, relaydt_49_p5, 1'b0, relaydt_127_p5
  LED led_42 (.in(relaydt_127_p5));
  // RelayDT #(.poles(2)) relaydt_128: pin names not known; wires that end beside it: relaydt_121_p6, 1'b1, relaydt_51_p5, 1'b0, relaydt_128_p5
  LED led_43 (.in(relaydt_128_p5));
  LED led_44 (.in(relaydt_124_p5));
  LED led_45 (.in(relaydt_126_p5));
  // RelayDT #(.poles(2)) relaydt_129: pin names not known; wires that end beside it: relaydt_119_p9, 1'b1, relaydt_49_p5, 1'b0, relaydt_129_p5
  LED led_46 (.in(relaydt_129_p5));
  // RelayDT #(.poles(2)) relaydt_130: pin names not known; wires that end beside it: relaydt_127_p5, out_13[7], relaydt_129_p5, out_13[6], pullup_2_out, 1'b0
  // RelayDT #(.poles(2)) relaydt_131: pin names not known; wires that end beside it: relaydt_121_p9, 1'b1, relaydt_51_p5, 1'b0, relaydt_131_p5
  LED led_47 (.in(relaydt_131_p5));
  // RelayDT #(.poles(2)) relaydt_132: pin names not known; wires that end beside it: relaydt_128_p5, out_13[7], relaydt_131_p5, out_13[6], pullup_4_out, 1'b0
  // RelayDT #(.poles(2)) relaydt_133: pin names not known; wires that end beside it: relaydt_123_p9, 1'b1, relaydt_53_p5, 1'b0, relaydt_133_p5
  LED led_48 (.in(relaydt_133_p5));
  // RelayDT #(.poles(2)) relaydt_134: pin names not known; wires that end beside it: relaydt_124_p5, out_13[7], relaydt_133_p5, out_13[6], pullup_6_out, 1'b0
  // RelayDT #(.poles(2)) relaydt_135: pin names not known; wires that end beside it: relaydt_125_p9, 1'b1, relaydt_56_p5, 1'b0, relaydt_135_p5
  LED led_49 (.in(relaydt_135_p5));
  // RelayDT #(.poles(2)) relaydt_136: pin names not known; wires that end beside it: relaydt_126_p5, out_13[7], relaydt_135_p5, out_13[6], pullup_8_out, 1'b0
  // RelayDT #(.poles(2)) relaydt_137: pin names not known; wires that end beside it: relaydt_119_p9, relaydt_50_p1, 1'b0, 1'b0, out_14[5], relaydt_137_p6, relaydt_137_p6, out_14[4], relaydt_137_p9, 1'b0
  // RelayDT #(.poles(2)) relaydt_138: pin names not known; wires that end beside it: relaydt_137_p6, 1'b1, relaydt_49_p5, 1'b0, relaydt_138_p5
  // RelayDT #(.poles(2)) relaydt_139: pin names not known; wires that end beside it: relaydt_121_p9, relaydt_52_p1, 1'b0, 1'b0, out_14[5], relaydt_139_p6, relaydt_139_p6, out_14[4], relaydt_139_p9, 1'b0
  // RelayDT #(.poles(2)) relaydt_140: pin names not known; wires that end beside it: relaydt_139_p6, 1'b1, relaydt_51_p5, 1'b0, relaydt_140_p5
  // RelayDT #(.poles(2)) relaydt_141: pin names not known; wires that end beside it: relaydt_123_p9, relaydt_54_p1, 1'b0, 1'b0, out_14[5], relaydt_141_p6, relaydt_141_p6, out_14[4], relaydt_141_p9, 1'b0
  // RelayDT #(.poles(2)) relaydt_142: pin names not known; wires that end beside it: relaydt_141_p6, 1'b1, relaydt_53_p5, 1'b0, relaydt_142_p5
  LED led_50 (.in(relaydt_142_p5));
  // RelayDT #(.poles(2)) relaydt_143: pin names not known; wires that end beside it: relaydt_125_p9, relaydt_57_p1, 1'b0, 1'b0, out_14[5], relaydt_143_p6, relaydt_143_p6, out_14[4], relaydt_143_p9, 1'b0
  // RelayDT #(.poles(2)) relaydt_144: pin names not known; wires that end beside it: relaydt_143_p6, 1'b1, relaydt_56_p5, 1'b0, relaydt_144_p5
  LED led_51 (.in(relaydt_144_p5));
  // RelayDT #(.poles(2)) relaydt_145: pin names not known; wires that end beside it: relaydt_137_p9, 1'b1, relaydt_49_p5, 1'b0, relaydt_145_p5
  LED led_52 (.in(relaydt_138_p5));
  // RelayDT #(.poles(2)) relaydt_146: pin names not known; wires that end beside it: relaydt_139_p9, 1'b1, relaydt_51_p5, 1'b0, relaydt_146_p5
  LED led_53 (.in(relaydt_140_p5));
  // RelayDT #(.poles(2)) relaydt_147: pin names not known; wires that end beside it: relaydt_141_p9, 1'b1, relaydt_53_p5, 1'b0, relaydt_147_p5
  // RelayDT #(.poles(2)) relaydt_148: pin names not known; wires that end beside it: relaydt_142_p5, out_13[5], relaydt_147_p5, out_13[4], pullup_6_out, 1'b0
  // RelayDT #(.poles(2)) relaydt_149: pin names not known; wires that end beside it: relaydt_143_p9, 1'b1, relaydt_56_p5, 1'b0, relaydt_149_p5
  // RelayDT #(.poles(2)) relaydt_150: pin names not known; wires that end beside it: relaydt_144_p5, out_13[5], relaydt_149_p5, out_13[4], pullup_8_out, 1'b0
  // RelayDT #(.poles(2)) relaydt_151: pin names not known; wires that end beside it: relaydt_137_p9, relaydt_50_p1, 1'b0, 1'b0, out_14[3], relaydt_151_p6, relaydt_151_p6, out_14[2], relaydt_151_p9, 1'b0
  LED led_54 (.in(relaydt_145_p5));
  // RelayDT #(.poles(2)) relaydt_152: pin names not known; wires that end beside it: relaydt_138_p5, out_13[5], relaydt_145_p5, out_13[4], pullup_2_out, 1'b0
  // RelayDT #(.poles(2)) relaydt_153: pin names not known; wires that end beside it: relaydt_139_p9, relaydt_52_p1, 1'b0, 1'b0, out_14[3], relaydt_153_p6, relaydt_153_p6, out_14[2], relaydt_153_p9, 1'b0
  LED led_55 (.in(relaydt_146_p5));
  // RelayDT #(.poles(2)) relaydt_154: pin names not known; wires that end beside it: relaydt_140_p5, out_13[5], relaydt_146_p5, out_13[4], pullup_4_out, 1'b0
  // RelayDT #(.poles(2)) relaydt_155: pin names not known; wires that end beside it: relaydt_141_p9, relaydt_54_p1, 1'b0, 1'b0, out_14[3], relaydt_155_p6, relaydt_155_p6, out_14[2], relaydt_155_p9, 1'b0
  // RelayDT #(.poles(2)) relaydt_156: pin names not known; wires that end beside it: relaydt_155_p6, 1'b1, relaydt_53_p5, 1'b0, relaydt_156_p5
  LED led_56 (.in(relaydt_147_p5));
  // RelayDT #(.poles(2)) relaydt_157: pin names not known; wires that end beside it: relaydt_143_p9, relaydt_57_p1, 1'b0, 1'b0, out_14[3], relaydt_157_p6, relaydt_157_p6, out_14[2], relaydt_157_p9, 1'b0
  // RelayDT #(.poles(2)) relaydt_158: pin names not known; wires that end beside it: relaydt_157_p6, 1'b1, relaydt_56_p5, 1'b0, relaydt_158_p5
  LED led_57 (.in(relaydt_149_p5));
  // RelayDT #(.poles(2)) relaydt_159: pin names not known; wires that end beside it: relaydt_151_p6, 1'b1, relaydt_49_p5, 1'b0, relaydt_159_p5
  LED led_58 (.in(relaydt_159_p5));
  // RelayDT #(.poles(2)) relaydt_160: pin names not known; wires that end beside it: relaydt_153_p6, 1'b1, relaydt_51_p5, 1'b0, relaydt_160_p5
  LED led_59 (.in(relaydt_160_p5));
  LED led_60 (.in(relaydt_156_p5));
  LED led_61 (.in(relaydt_158_p5));
  // RelayDT #(.poles(2)) relaydt_161: pin names not known; wires that end beside it: relaydt_151_p9, 1'b1, relaydt_49_p5, 1'b0, relaydt_161_p5
  LED led_62 (.in(relaydt_161_p5));
  // RelayDT #(.poles(2)) relaydt_162: pin names not known; wires that end beside it: relaydt_159_p5, out_13[3], relaydt_161_p5, out_13[2], pullup_2_out, 1'b0
  // RelayDT #(.poles(2)) relaydt_163: pin names not known; wires that end beside it: relaydt_153_p9, 1'b1, relaydt_51_p5, 1'b0, relaydt_163_p5
  LED led_63 (.in(relaydt_163_p5));
  // RelayDT #(.poles(2)) relaydt_164: pin names not known; wires that end beside it: relaydt_160_p5, out_13[3], relaydt_163_p5, out_13[2], pullup_4_out, 1'b0
  // RelayDT #(.poles(2)) relaydt_165: pin names not known; wires that end beside it: relaydt_155_p9, 1'b1, relaydt_53_p5, 1'b0, relaydt_165_p5
  LED led_64 (.in(relaydt_165_p5));
  // RelayDT #(.poles(2)) relaydt_166: pin names not known; wires that end beside it: relaydt_156_p5, out_13[3], relaydt_165_p5, out_13[2], pullup_6_out, 1'b0
  // RelayDT #(.poles(2)) relaydt_167: pin names not known; wires that end beside it: relaydt_157_p9, 1'b1, relaydt_56_p5, 1'b0, relaydt_167_p5
  LED led_65 (.in(relaydt_167_p5));
  // RelayDT #(.poles(2)) relaydt_168: pin names not known; wires that end beside it: relaydt_158_p5, out_13[3], relaydt_167_p5, out_13[2], pullup_8_out, 1'b0
  // RelayDT #(.poles(2)) relaydt_169: pin names not known; wires that end beside it: relaydt_151_p9, relaydt_50_p1, 1'b0, 1'b0, out_14[1], relaydt_169_p6, relaydt_169_p6, out_14[0], relaydt_169_p9, 1'b0, relaydt_169_p9
  // RelayDT #(.poles(2)) relaydt_170: pin names not known; wires that end beside it: relaydt_169_p6, 1'b1, relaydt_49_p5, 1'b0, relaydt_170_p5
  // RelayDT #(.poles(2)) relaydt_171: pin names not known; wires that end beside it: relaydt_153_p9, relaydt_52_p1, 1'b0, 1'b0, out_14[1], relaydt_171_p6, relaydt_171_p6, out_14[0], relaydt_171_p9, 1'b0, relaydt_171_p9
  // RelayDT #(.poles(2)) relaydt_172: pin names not known; wires that end beside it: relaydt_171_p6, 1'b1, relaydt_51_p5, 1'b0, relaydt_172_p5
  // RelayDT #(.poles(2)) relaydt_173: pin names not known; wires that end beside it: relaydt_155_p9, relaydt_54_p1, 1'b0, 1'b0, out_14[1], relaydt_173_p6, relaydt_173_p6, out_14[0], relaydt_173_p9, 1'b0, relaydt_173_p9
  // RelayDT #(.poles(2)) relaydt_174: pin names not known; wires that end beside it: relaydt_173_p6, 1'b1, relaydt_53_p5, 1'b0, relaydt_174_p5
  LED led_66 (.in(relaydt_174_p5));
  // RelayDT #(.poles(2)) relaydt_175: pin names not known; wires that end beside it: relaydt_157_p9, relaydt_57_p1, 1'b0, 1'b0, out_14[1], relaydt_175_p6, relaydt_175_p6, out_14[0], relaydt_175_p9, 1'b0, relaydt_175_p9
  // RelayDT #(.poles(2)) relaydt_176: pin names not known; wires that end beside it: relaydt_175_p6, 1'b1, relaydt_56_p5, 1'b0, relaydt_176_p5
  LED led_67 (.in(relaydt_176_p5));
  // RelayDT #(.poles(2)) relaydt_177: pin names not known; wires that end beside it: relaydt_169_p9, 1'b1, relaydt_49_p5, 1'b0, relaydt_177_p5
  LED led_68 (.in(relaydt_170_p5));
  // RelayDT #(.poles(2)) relaydt_178: pin names not known; wires that end beside it: relaydt_171_p9, 1'b1, relaydt_51_p5, 1'b0, relaydt_178_p5
  LED led_69 (.in(relaydt_172_p5));
  // RelayDT #(.poles(2)) relaydt_179: pin names not known; wires that end beside it: relaydt_173_p9, 1'b1, relaydt_53_p5, 1'b0, relaydt_179_p5
  // RelayDT #(.poles(2)) relaydt_180: pin names not known; wires that end beside it: relaydt_174_p5, out_13[1], relaydt_179_p5, out_13[0], 1'b0, pullup_6_out, 1'b0
  // RelayDT #(.poles(2)) relaydt_181: pin names not known; wires that end beside it: relaydt_175_p9, 1'b1, relaydt_56_p5, 1'b0, relaydt_181_p5
  // RelayDT #(.poles(2)) relaydt_182: pin names not known; wires that end beside it: relaydt_176_p5, out_13[1], relaydt_181_p5, out_13[0], 1'b0, pullup_8_out, 1'b0
  LED led_70 (.in(relaydt_177_p5));
  // RelayDT #(.poles(2)) relaydt_183: pin names not known; wires that end beside it: relaydt_170_p5, out_13[1], relaydt_177_p5, out_13[0], 1'b0, pullup_2_out, 1'b0
  LED led_71 (.in(relaydt_178_p5));
  // RelayDT #(.poles(2)) relaydt_184: pin names not known; wires that end beside it: relaydt_172_p5, out_13[1], relaydt_178_p5, out_13[0], 1'b0, pullup_4_out, 1'b0
  LED led_72 (.in(relaydt_179_p5));
  LED led_73 (.in(relaydt_181_p5));
  assign not_5_out = ~6'b000010;  // Not not_5, 6 bits wide
  assign not_6_out = ~6'b000011;  // Not not_6, 6 bits wide
  // RelayDT relaydt_185: pin names not known; wires that end beside it: SELECT[5], 1'b0, relaydt_185_p3, SELECT[4]
  DiodeBackward diodebackward_53 (.in(relaydt_185_p3), .out(diodebackward_53_out));
  PullUp pullup_9 (.out(diodebackward_53_out));
  LED led_74 (.in(diodebackward_53_out));
  // RelayDT relaydt_186: pin names not known; wires that end beside it: LOAD[5], 1'b0, relaydt_186_p3, LOAD[4]
  DiodeBackward diodebackward_54 (.in(relaydt_186_p3), .out(diodebackward_54_out));
  PullUp pullup_10 (.out(diodebackward_54_out));
  LED led_75 (.in(diodebackward_54_out));
  // RelayDT relaydt_187: pin names not known; wires that end beside it: SELECT[5], 1'b0, relaydt_187_p3, SELECT[4]
  DiodeBackward diodebackward_55 (.in(relaydt_187_p3), .out(diodebackward_55_out));
  PullUp pullup_11 (.out(diodebackward_55_out));
  LED led_76 (.in(diodebackward_55_out));
  // RelayDT relaydt_188: pin names not known; wires that end beside it: LOAD[5], 1'b0, relaydt_188_p3, LOAD[4]
  DiodeBackward diodebackward_56 (.in(relaydt_188_p3), .out(diodebackward_56_out));
  PullUp pullup_12 (.out(diodebackward_56_out));
  LED led_77 (.in(diodebackward_56_out));
  // RelayDT relaydt_189: pin names not known; wires that end beside it: 1'b0, relaydt_189_p2, SELECT[3]
  DiodeBackward diodebackward_57 (.in(relaydt_189_p2), .out(diodebackward_53_out));
  // RelayDT relaydt_190: pin names not known; wires that end beside it: 1'b0, relaydt_190_p2, LOAD[3]
  DiodeBackward diodebackward_58 (.in(relaydt_190_p2), .out(diodebackward_54_out));
  // RelayDT relaydt_191: pin names not known; wires that end beside it: 1'b0, relaydt_191_p2, SELECT[3]
  DiodeBackward diodebackward_59 (.in(relaydt_191_p2), .out(diodebackward_55_out));
  // RelayDT relaydt_192: pin names not known; wires that end beside it: 1'b0, relaydt_192_p2, LOAD[3]
  DiodeBackward diodebackward_60 (.in(relaydt_192_p2), .out(diodebackward_56_out));
  // RelayDT relaydt_193: pin names not known; wires that end beside it: 1'b0, relaydt_193_p2, SELECT[2]
  DiodeBackward diodebackward_61 (.in(relaydt_193_p2), .out(diodebackward_53_out));
  // RelayDT relaydt_194: pin names not known; wires that end beside it: 1'b0, relaydt_194_p2, LOAD[2]
  DiodeBackward diodebackward_62 (.in(relaydt_194_p2), .out(diodebackward_54_out));
  // RelayDT relaydt_195: pin names not known; wires that end beside it: 1'b0, relaydt_195_p2, SELECT[2]
  DiodeBackward diodebackward_63 (.in(relaydt_195_p2), .out(diodebackward_55_out));
  // RelayDT relaydt_196: pin names not known; wires that end beside it: 1'b0, relaydt_196_p2, LOAD[2]
  DiodeBackward diodebackward_64 (.in(relaydt_196_p2), .out(diodebackward_56_out));
  // RelayDT relaydt_197: pin names not known; wires that end beside it: 1'b0, relaydt_197_p2, SELECT[1]
  DiodeBackward diodebackward_65 (.in(relaydt_197_p2), .out(diodebackward_53_out));
  // RelayDT relaydt_198: pin names not known; wires that end beside it: 1'b0, relaydt_198_p2, LOAD[1]
  DiodeBackward diodebackward_66 (.in(relaydt_198_p2), .out(diodebackward_54_out));
  // RelayDT relaydt_199: pin names not known; wires that end beside it: 1'b0, relaydt_199_p2, SELECT[1]
  DiodeBackward diodebackward_67 (.in(relaydt_199_p2), .out(diodebackward_55_out));
  // RelayDT relaydt_200: pin names not known; wires that end beside it: 1'b0, relaydt_200_p2, LOAD[1]
  DiodeBackward diodebackward_68 (.in(relaydt_200_p2), .out(diodebackward_56_out));
  // RelayDT relaydt_201: pin names not known; wires that end beside it: 1'b0, relaydt_201_p2, SELECT[0]
  DiodeBackward diodebackward_69 (.in(relaydt_201_p2), .out(diodebackward_53_out));
  // RelayDT relaydt_202: pin names not known; wires that end beside it: 1'b0, relaydt_202_p2, LOAD[0]
  DiodeBackward diodebackward_70 (.in(relaydt_202_p2), .out(diodebackward_54_out));
  // RelayDT relaydt_203: pin names not known; wires that end beside it: 1'b0, relaydt_203_p2, SELECT[0]
  DiodeBackward diodebackward_71 (.in(relaydt_203_p2), .out(diodebackward_55_out));
  // RelayDT relaydt_204: pin names not known; wires that end beside it: 1'b0, relaydt_204_p2, LOAD[0]
  DiodeBackward diodebackward_72 (.in(relaydt_204_p2), .out(diodebackward_56_out));
  // RelayDT relaydt_205: pin names not known; wires that end beside it: 1'b0, relaydt_205_p2, diodebackward_54_out, 1'b0
  DiodeBackward diodebackward_73 (.in(relaydt_205_p2), .out(diodebackward_53_out));
  // RelayDT relaydt_206: pin names not known; wires that end beside it: 1'b0, relaydt_206_p2
  DiodeBackward diodebackward_74 (.in(relaydt_206_p2), .out(diodebackward_54_out));
  // RelayDT relaydt_207: pin names not known; wires that end beside it: 1'b0, relaydt_207_p2, diodebackward_56_out, 1'b0
  DiodeBackward diodebackward_75 (.in(relaydt_207_p2), .out(diodebackward_55_out));
  // RelayDT relaydt_208: pin names not known; wires that end beside it: 1'b0, relaydt_208_p2
  DiodeBackward diodebackward_76 (.in(relaydt_208_p2), .out(diodebackward_56_out));
  // RelayDT #(.poles(2)) relaydt_209: pin names not known; wires that end beside it: 1'b1, 1'b1, relaydt_209_p3, relaydt_209_p4
  // RelayDT #(.poles(2)) relaydt_210: pin names not known; wires that end beside it: relaydt_210_p1, 1'b0, B_7, relaydt_210_p4, relaydt_210_p4, B_6, relaydt_210_p7, 1'b0
  // RelayDT #(.poles(2)) relaydt_211: pin names not known; wires that end beside it: 1'b1, 1'b1, relaydt_211_p3, relaydt_211_p4
  // RelayDT #(.poles(2)) relaydt_212: pin names not known; wires that end beside it: relaydt_212_p1, 1'b0, B_7, relaydt_212_p4, relaydt_212_p4, B_6, relaydt_212_p7, 1'b0
  DiodeForward diodeforward_1 (.in(in_8), .out(B_7));
  DiodeForward diodeforward_2 (.in(in_7), .out(B_6));
  LED led_78 (.in(B_7));
  LED led_79 (.in(B_6));
  PullDown pulldown_1 (.out(B_7));
  PullDown pulldown_2 (.out(B_6));
  // RelayDT #(.poles(2)) relaydt_213: pin names not known; wires that end beside it: relaydt_209_p3, 1'b1, 1'b0, relaydt_213_p4
  // RelayDT #(.poles(2)) relaydt_214: pin names not known; wires that end beside it: relaydt_210_p4, 1'b1, relaydt_209_p4, 1'b0, relaydt_214_p5
  LED led_80 (.in(relaydt_214_p5));
  // RelayDT #(.poles(2)) relaydt_215: pin names not known; wires that end beside it: relaydt_211_p3, 1'b1, relaydt_215_p3
  // RelayDT #(.poles(2)) relaydt_216: pin names not known; wires that end beside it: relaydt_212_p4, 1'b1, relaydt_211_p4, 1'b0, relaydt_216_p5
  LED led_81 (.in(relaydt_216_p5));
  DiodeForward diodeforward_3 (.in(in_6), .out(B_5));
  DiodeForward diodeforward_4 (.in(in_5), .out(B_4));
  LED led_82 (.in(B_5));
  LED led_83 (.in(B_4));
  PullDown pulldown_3 (.out(B_5));
  PullDown pulldown_4 (.out(B_4));
  // RelayDT #(.poles(2)) relaydt_217: pin names not known; wires that end beside it: relaydt_210_p7, 1'b1, 1'b0, relaydt_209_p4, 1'b0, relaydt_217_p6
  // RelayDT #(.poles(2)) relaydt_218: pin names not known; wires that end beside it: relaydt_212_p7, 1'b1, relaydt_211_p4, 1'b0, relaydt_218_p5
  DiodeForward diodeforward_5 (.in(in_4), .out(B_3));
  DiodeForward diodeforward_6 (.in(in_3), .out(B_2));
  LED led_84 (.in(B_3));
  LED led_85 (.in(B_2));
  PullDown pulldown_5 (.out(B_3));
  PullDown pulldown_6 (.out(B_2));
  DiodeForward diodeforward_7 (.in(diodebackward_53_out), .out(relaydt_210_p1));
  DiodeForward diodeforward_8 (.in(relaydt_213_p4), .out(relaydt_210_p1));
  PullDown pulldown_7 (.out(relaydt_210_p1));
  // RelayDT #(.poles(2)) relaydt_219: pin names not known; wires that end beside it: relaydt_210_p7, relaydt_210_p1, 1'b0, 1'b0, B_5, relaydt_219_p6, relaydt_219_p6, B_4, relaydt_219_p9, 1'b0
  // RelayDT #(.poles(2)) relaydt_220: pin names not known; wires that end beside it: relaydt_219_p6, 1'b1, relaydt_209_p4, 1'b0, relaydt_220_p5
  LED led_86 (.in(relaydt_217_p6));
  DiodeForward diodeforward_9 (.in(diodebackward_55_out), .out(relaydt_212_p1));
  DiodeForward diodeforward_10 (.in(relaydt_215_p3), .out(relaydt_212_p1));
  PullDown pulldown_8 (.out(relaydt_212_p1));
  // RelayDT #(.poles(2)) relaydt_221: pin names not known; wires that end beside it: relaydt_212_p7, relaydt_212_p1, 1'b0, 1'b0, B_5, relaydt_221_p6, relaydt_221_p6, B_4, relaydt_221_p9, 1'b0
  // RelayDT #(.poles(2)) relaydt_222: pin names not known; wires that end beside it: relaydt_221_p6, 1'b1, relaydt_211_p4, 1'b0, relaydt_222_p5
  LED led_87 (.in(relaydt_218_p5));
  DiodeForward diodeforward_11 (.in(in_2), .out(B_1));
  DiodeForward diodeforward_12 (.in(in_1), .out(B_0));
  LED led_88 (.in(B_1));
  LED led_89 (.in(B_0));
  PullDown pulldown_9 (.out(B_1));
  PullDown pulldown_10 (.out(B_0));
  // RelayDT #(.poles(2)) relaydt_223: pin names not known; wires that end beside it: relaydt_219_p9, 1'b1, relaydt_209_p4, 1'b0, relaydt_223_p5
  LED led_90 (.in(relaydt_220_p5));
  // RelayDT #(.poles(2)) relaydt_224: pin names not known; wires that end beside it: relaydt_221_p9, 1'b1, relaydt_211_p4, 1'b0, relaydt_224_p5
  LED led_91 (.in(relaydt_222_p5));
  // RelayDT #(.poles(2)) relaydt_225: pin names not known; wires that end beside it: relaydt_219_p9, relaydt_210_p1, 1'b0, 1'b0, B_3, relaydt_225_p6, relaydt_225_p6, B_2, relaydt_225_p9, 1'b0
  LED led_92 (.in(relaydt_223_p5));
  // RelayDT #(.poles(2)) relaydt_226: pin names not known; wires that end beside it: relaydt_221_p9, relaydt_212_p1, 1'b0, 1'b0, B_3, relaydt_226_p6, relaydt_226_p6, B_2, relaydt_226_p9, 1'b0
  LED led_93 (.in(relaydt_224_p5));
  // RelayDT #(.poles(2)) relaydt_227: pin names not known; wires that end beside it: relaydt_225_p6, 1'b1, relaydt_209_p4, 1'b0, relaydt_227_p5
  LED led_94 (.in(relaydt_227_p5));
  // RelayDT #(.poles(2)) relaydt_228: pin names not known; wires that end beside it: relaydt_226_p6, 1'b1, relaydt_211_p4, 1'b0, relaydt_228_p5
  LED led_95 (.in(relaydt_228_p5));
  // RelayDT #(.poles(2)) relaydt_229: pin names not known; wires that end beside it: relaydt_225_p9, 1'b1, relaydt_209_p4, 1'b0, relaydt_229_p5
  // RelayDT #(.poles(2)) relaydt_230: pin names not known; wires that end beside it: relaydt_226_p9, 1'b1, relaydt_211_p4, 1'b0, relaydt_230_p5
  // RelayDT #(.poles(2)) relaydt_231: pin names not known; wires that end beside it: relaydt_225_p9, relaydt_210_p1, 1'b0, 1'b0, B_1, relaydt_231_p6, relaydt_231_p6, B_0, relaydt_231_p9, 1'b0, relaydt_231_p9, 1'b0
  // RelayDT #(.poles(2)) relaydt_232: pin names not known; wires that end beside it: relaydt_231_p6, 1'b1, relaydt_209_p4, 1'b0, relaydt_232_p5
  LED led_96 (.in(relaydt_229_p5));
  // RelayDT #(.poles(2)) relaydt_233: pin names not known; wires that end beside it: relaydt_226_p9, relaydt_212_p1, 1'b0, 1'b0, B_1, relaydt_233_p6, relaydt_233_p6, B_0, relaydt_233_p9, 1'b0, relaydt_233_p9, 1'b0
  // RelayDT #(.poles(2)) relaydt_234: pin names not known; wires that end beside it: relaydt_233_p6, 1'b1, relaydt_211_p4, 1'b0, relaydt_234_p5
  LED led_97 (.in(relaydt_230_p5));
  // RelayDT #(.poles(2)) relaydt_235: pin names not known; wires that end beside it: relaydt_231_p9, 1'b1, relaydt_209_p4, 1'b0, relaydt_235_p5
  LED led_98 (.in(relaydt_232_p5));
  // RelayDT #(.poles(2)) relaydt_236: pin names not known; wires that end beside it: relaydt_233_p9, 1'b1, relaydt_211_p4, 1'b0, relaydt_236_p5
  LED led_99 (.in(relaydt_234_p5));
  LED led_100 (.in(relaydt_235_p5));
  LED led_101 (.in(relaydt_236_p5));

  // Other names for the same wires on the sheet: PROG[15:0] = out_13; L_0 = LOAD[0]; L_1 = LOAD[1]; L_2 = LOAD[2];
  //   L_3 = LOAD[3]; L_4 = LOAD[4]; L_5 = LOAD[5]; LOAD_PROG[15:0] = out_14; S_0 = SELECT[0]; S_1 = SELECT[1];
  //   S_2 = SELECT[2]; S_3 = SELECT[3]; S_4 = SELECT[4]; S_5 = SELECT[5]

  // Notes on the sheet:
  //   PROGRAM STORAGE
  //   contents of eepromdualport_1 (hex, n*v repeats v):
  //   6043,4804,110,4031,cf,403,43e0,464,40e0,4071,5*0,c000
  //   TODO: 60 more rows
  //   TODO: Program decoder
  //   PC
  //   REGA
  //   BUS
  //   TODO: Program counter
endmodule
