// Digital circuit rv32i_digital_part_1.dig as structural Verilog
module rv32i_digital_part_1 (
  input  clk,
  input  HALT,
  input  _2x,
  input  clk_2,
  input  clk_3,
  input  _4x,
  input  clk_4,
  input  MANUAL,
  input  HALT_2,
  input  in_10,
  input  [31:0] PC
);

  wire and_1_out, and_2_out, CLOCK, nCLOCK, or_1_out, relaydt_1_p7, relaydt_1_p8, relaydt_2_p2, rs_ff_1_nq,
       rs_ff_1_q, STEP_out;
  wire [31:0] INSTRUCTION;

  ROM #(.AddrBits(24), .isProgramMemory("true"), .Bits(32)) Instruction_ROM (.A(PC[25:2]), .sel(1'b1), .D(INSTRUCTION));
  // RelayDT #(.poles(2)) relaydt_1: pin names not known; wires that end beside it: _4x, clk_3, clk_2, clk, clk_4, 1'b0, relaydt_1_p7, relaydt_1_p8, _2x, relaydt_1_p7, relaydt_1_p8
  or or_1 (or_1_out, HALT, HALT_2);
  Seven_Seg_Hex seven_seg_hex_1 (.d(INSTRUCTION[31:28]), .dp(1'b0));
  // RelayDT relaydt_2: pin names not known; wires that end beside it: 1'b0, relaydt_2_p2
  Seven_Seg_Hex seven_seg_hex_2 (.d(INSTRUCTION[27:24]), .dp(1'b0));
  Seven_Seg_Hex seven_seg_hex_3 (.d(INSTRUCTION[23:20]), .dp(1'b0));
  Button STEP (.out(STEP_out));
  and and_1 (and_1_out, STEP_out, MANUAL, ~or_1_out);  // And
  RS_FF rs_ff_1 (.S(and_2_out), .C(relaydt_2_p2), .R(~and_2_out), .Q(rs_ff_1_q), .nQ(rs_ff_1_nq));
  Seven_Seg_Hex seven_seg_hex_4 (.d(INSTRUCTION[19:16]), .dp(1'b0));
  Seven_Seg_Hex seven_seg_hex_5 (.d(INSTRUCTION[15:12]), .dp(1'b0));
  and and_2 (and_2_out, ~MANUAL, ~or_1_out, rs_ff_1_nq);  // And
  Seven_Seg_Hex seven_seg_hex_6 (.d(INSTRUCTION[11:8]), .dp(1'b0));
  Seven_Seg_Hex seven_seg_hex_7 (.d(INSTRUCTION[7:4]), .dp(1'b0));
  or or_2 (CLOCK, and_1_out, rs_ff_1_q);
  Seven_Seg_Hex seven_seg_hex_8 (.d(INSTRUCTION[3:0]), .dp(1'b0));
  not not_1 (nCLOCK, CLOCK);
  LED led_1 (.in(CLOCK));
  LED led_2 (.in(nCLOCK));

  // Other names for the same wires on the sheet: HALT_t = HALT_2; RESET = in_10

  // Notes on the sheet:
  //   clk: Hz: 8
  //   clk_2: Hz: 16
  //   clk_3: Hz: 64
  //   clk_4: Hz: 2
  //   MANUAL: default 1
  //   CLOCK
  //   Instruction Memory
  //   Instruction_ROM loads rom_part_1.hex
  //   RISC-V Instructions are 4 bytes long
  //   The PC will be incremented in that size step
  //   so we pull out that step size to pull
  //   from our Instruction array
  //   To Be Implemented
endmodule
