// Digital circuit rv32i_digital_part_3.dig as structural Verilog
module rv32i_digital_part_3 (
  input  clk,
  input  HALT,
  input  _2x,
  input  clk_2,
  input  clk_3,
  input  _4x,
  input  clk_4,
  input  MANUAL,
  input  HALT_2,
  input  in_10,
  input  [31:0] in_11,
  input  [31:0] in_12,
  output [31:0] Decimal,
  output [31:0] Binary,
  output [31:0] Signed_Decimal
);

  wire and_2_out, and_3_out, CLOCK, data_memory_write_enable, execute_port_a_sel, execute_port_b_sel, nCLOCK,
       OP_RTYPE_eq, or_2_out, pc_mux_sel, reg_write_enable, relaydt_1_p7, relaydt_1_p8, relaydt_2_p2,
       rs_ff_1_nq, rs_ff_1_q, STEP_out;
  wire [0:0] SLT_lt, SLTU_lt;
  wire [2:0] branch_op_sel, imm_select, reg_write_data_sel;
  wire [3:0] alu_op_sel, load_store_type;
  wire [31:0] add_1_s, and_1_out, INSTRUCTION, multiplexer_2_out, multiplexer_3_out, or_1_out, PC, pc_next,
       SLL_out, SRA_out, SRL_out, sub_1_s, xor_1_out;

  Add #(.Bits(32)) add_1 (.a(in_11), .b(in_12), .c_i(1'b0), .s(add_1_s));  // open: c_o
  BarrelShifter #(.Bits(32)) SLL (.in(in_11), .shift(in_12[5:0]), .out(SLL_out));
  Comparator #(.Signed("true"), .Bits(32)) SLT (.a(in_11), .b(in_12), .lt(SLT_lt[0]));  // open: gt, eq
  Comparator #(.Bits(32)) SLTU (.a(in_11), .b(in_12), .lt(SLTU_lt[0]));  // open: gt, eq
  assign xor_1_out = in_11 ^ in_12;  // XOr xor_1, 32 bits wide
  BarrelShifter #(.Bits(32), .direction("right")) SRL (.in(in_11), .shift(in_12[5:0]), .out(SRL_out));
  assign or_1_out = in_11 | in_12;  // Or or_1, 32 bits wide
  assign and_1_out = in_11 & in_12;  // And and_1, 32 bits wide
  Sub #(.Bits(32)) sub_1 (.a(in_11), .b(in_12), .c_i(1'b0), .s(sub_1_s));  // open: c_o
  BarrelShifter #(.Bits(32), .barrelShifterMode("arithmetic"), .direction("right")) SRA (
    .in(in_11), .shift(in_12[5:0]), .out(SRA_out));
  ROM #(.AddrBits(24), .isProgramMemory("true"), .Bits(32)) Instruction_ROM (.A(PC[25:2]), .sel(1'b1), .D(INSTRUCTION));
  // RelayDT #(.poles(2)) relaydt_1: pin names not known; wires that end beside it: _4x, clk_3, clk_2, clk, clk_4, 1'b0, relaydt_1_p7, relaydt_1_p8, _2x, relaydt_1_p7, relaydt_1_p8
  or or_2 (or_2_out, HALT, HALT_2);
  Seven_Seg_Hex seven_seg_hex_1 (.d(INSTRUCTION[31:28]), .dp(1'b0));
  // RelayDT relaydt_2: pin names not known; wires that end beside it: 1'b0, relaydt_2_p2
  Seven_Seg_Hex seven_seg_hex_2 (.d(INSTRUCTION[23:20]), .dp(1'b0));
  Seven_Seg_Hex seven_seg_hex_3 (.d(INSTRUCTION[27:24]), .dp(1'b0));
  Multiplexer #(.Selector_Bits(4), .Bits(32)) multiplexer_1 (
    .sel(alu_op_sel), .in_0(add_1_s), .in_1(SLL_out), .in_2({{31{1'b0}}, SLT_lt[0]}),
    .in_3({{31{1'b0}}, SLTU_lt[0]}), .in_4(xor_1_out), .in_5(SRL_out), .in_6(or_1_out), .in_7(and_1_out),
    .in_8(sub_1_s), .in_9({32{1'b0}}), .in_10({32{1'b0}}), .in_11({32{1'b0}}), .in_12({32{1'b0}}),
    .in_13(SRA_out), .in_14({32{1'b0}}), .in_15({32{1'b0}}), .out(Binary));
  Seven_Seg_Hex seven_seg_hex_4 (.d(Binary[31:28]), .dp(1'b0));
  Button STEP (.out(STEP_out));
  and and_2 (and_2_out, STEP_out, MANUAL, ~or_2_out);  // And
  RS_FF rs_ff_1 (.S(and_3_out), .C(relaydt_2_p2), .R(~and_3_out), .Q(rs_ff_1_q), .nQ(rs_ff_1_nq));
  Seven_Seg_Hex seven_seg_hex_5 (.d(INSTRUCTION[15:12]), .dp(1'b0));
  Seven_Seg_Hex seven_seg_hex_6 (.d(INSTRUCTION[19:16]), .dp(1'b0));
  Seven_Seg_Hex seven_seg_hex_7 (.d(Binary[23:20]), .dp(1'b0));
  Seven_Seg_Hex seven_seg_hex_8 (.d(Binary[27:24]), .dp(1'b0));
  and and_3 (and_3_out, ~MANUAL, ~or_2_out, rs_ff_1_nq);  // And
  Seven_Seg_Hex seven_seg_hex_9 (.d(INSTRUCTION[7:4]), .dp(1'b0));
  Seven_Seg_Hex seven_seg_hex_10 (.d(INSTRUCTION[11:8]), .dp(1'b0));
  Seven_Seg_Hex seven_seg_hex_11 (.d(Binary[15:12]), .dp(1'b0));
  Seven_Seg_Hex seven_seg_hex_12 (.d(Binary[19:16]), .dp(1'b0));
  or or_3 (CLOCK, and_2_out, rs_ff_1_q);
  Seven_Seg_Hex seven_seg_hex_13 (.d(INSTRUCTION[3:0]), .dp(1'b0));
  Seven_Seg_Hex seven_seg_hex_14 (.d(Binary[7:4]), .dp(1'b0));
  Seven_Seg_Hex seven_seg_hex_15 (.d(Binary[11:8]), .dp(1'b0));
  not not_1 (nCLOCK, CLOCK);
  Seven_Seg_Hex seven_seg_hex_16 (.d(Binary[3:0]), .dp(1'b0));
  LED led_1 (.in(CLOCK));
  LED led_2 (.in(nCLOCK));
  Add #(.Bits(32)) add_2 (.a(PC), .b(32'h4), .c_i(1'b0), .s(pc_next));  // open: c_o
  Multiplexer #(.Bits(32)) multiplexer_2 (.sel(pc_mux_sel), .in_0(pc_next), .in_1(Binary), .out(multiplexer_2_out));
  Multiplexer #(.Bits(32)) multiplexer_3 (
    .sel(in_10), .in_0(multiplexer_2_out), .in_1({32{1'b0}}), .out(multiplexer_3_out));
  Seven_Seg_Hex seven_seg_hex_17 (.d(PC[31:28]), .dp(1'b0));
  Register #(.Bits(32)) u_PC (.D(multiplexer_3_out), .C(nCLOCK), .en(1'b1), .Q(PC));
  Seven_Seg_Hex seven_seg_hex_18 (.d(PC[27:24]), .dp(1'b0));
  Seven_Seg_Hex seven_seg_hex_19 (.d(PC[23:20]), .dp(1'b0));
  Seven_Seg_Hex seven_seg_hex_20 (.d(PC[19:16]), .dp(1'b0));
  Seven_Seg_Hex seven_seg_hex_21 (.d(PC[15:12]), .dp(1'b0));
  Seven_Seg_Hex seven_seg_hex_22 (.d(PC[11:8]), .dp(1'b0));
  Seven_Seg_Hex seven_seg_hex_23 (.d(PC[7:4]), .dp(1'b0));
  Seven_Seg_Hex seven_seg_hex_24 (.d(PC[3:0]), .dp(1'b0));
  Comparator #(.Bits(7)) OP_RTYPE (.a(INSTRUCTION[6:0]), .b(7'b0110011), .eq(OP_RTYPE_eq));  // open: gt, lt
  assign pc_mux_sel = OP_RTYPE_eq ? 1'b0 : 1'bz;  // Driver driver_1
  assign reg_write_enable = OP_RTYPE_eq ? 1'b1 : 1'bz;  // Driver driver_2
  assign imm_select = OP_RTYPE_eq ? 3'b111 : 3'bz;  // Driver driver_3
  assign execute_port_a_sel = OP_RTYPE_eq ? 1'b1 : 1'bz;  // Driver driver_4
  assign execute_port_b_sel = OP_RTYPE_eq ? 1'b1 : 1'bz;  // Driver driver_5
  assign reg_write_data_sel = OP_RTYPE_eq ? 3'b001 : 3'bz;  // Driver driver_6
  assign load_store_type = OP_RTYPE_eq ? 4'b1111 : 4'bz;  // Driver driver_7
  assign data_memory_write_enable = OP_RTYPE_eq ? 1'b0 : 1'bz;  // Driver driver_8
  assign alu_op_sel = OP_RTYPE_eq ? {INSTRUCTION[30], INSTRUCTION[14:12]} : 4'bz;  // Driver driver_9
  assign branch_op_sel = OP_RTYPE_eq ? 3'b010 : 3'bz;  // Driver driver_10

  assign Decimal = Binary;
  assign Signed_Decimal = Binary;

  // Other names for the same wires on the sheet: a[31:0] = in_11; alu_output[31:0] = Binary; b[31:0] = in_12;
  //   HALT_t = HALT_2; RESET = in_10

  // Notes on the sheet:
  //   clk: Hz: 8
  //   clk_2: Hz: 16
  //   clk_3: Hz: 64
  //   clk_4: Hz: 2
  //   MANUAL: default 1
  //   CLOCK
  //   Instruction Memory
  //   ALU
  //   Instruction_ROM loads rom_part_3.hex
  //   RISC-V Instructions are 4 bytes long
  //   The PC will be incremented in that size step
  //   so we pull out that step size to pull
  //   from our Instruction array
  //   alu_opsel
  //   from funct7[30]funct3[14:12]
  //   0000 - ADD
  //   0001 - SLL
  //   0010 - SLT
  //   0011 - SLTU
  //   0100 - XOR
  //   0101 - SRL
  //   0110 - OR
  //   0111 - AND
  //   1000 - SUB
  //   1101 - SRA
  //   1111 - UNKNOWN
  //   To Be Implemented
  //   Program Counter
  //   imm_select
  //   from oppcode [6][4][3]
  //   000 - S Type
  //   001 - 
  //   010 - U Type
  //   011 - 
  //   100 - B Type
  //   101 - J Type
  //   110 - I Type
  //   111 - Unknown Type
  //   load_store_type
  //   0000 - L_B
  //   0001 - L_H
  //   0010 - L_W
  //   0100 - L_BU
  //   0101 - L_HU
  //   1000 - S_B
  //   1001 - S_H
  //   1010 - S_W
  //   1111- LS_N_A
  //   branch_opsel
  //   from funct3[14:12]
  //   000 - BEQ
  //   001 - BNE
  //   010 - UNKNOWN
  //   100 - BLT
  //   101 - BGE
  //   110 - BLTU
  //   111 - BGEU
  //   reg_write_data_sel
  //   000 -  dmem_data
  //   001 - alu_output
  //   010 - branch_enable
  //   011 - immediate
  //   100 - pc_next
  //   111 - N_A
  //   Core Control Unit
endmodule
