// Digital circuit rv32i_digital_part_8.dig as structural Verilog
module rv32i_digital_part_8 (
  input  clk,
  input  HALT,
  input  _2x,
  input  clk_2,
  input  clk_3,
  input  _4x,
  input  clk_4,
  input  MANUAL,
  input  in_9,
  output [31:0] Decimal,
  output [31:0] Binary,
  output [31:0] Signed_Decimal,
  output [31:0] Decimal_2,
  output [31:0] Binary_2,
  output [31:0] Signed_Decimal_2,
  output [31:0] out_16,
  output [31:0] out_17,
  output [31:0] out_18,
  output [31:0] out_19,
  output [31:0] out_20,
  output [31:0] out_21,
  output [31:0] out_22,
  output [31:0] out_23,
  output [31:0] out_24,
  output [31:0] out_25,
  output [31:0] out_26,
  output [31:0] out_27,
  output [31:0] out_28,
  output [31:0] out_29,
  output [31:0] out_30,
  output [31:0] out_31,
  output [31:0] out_32,
  output [31:0] out_33,
  output [31:0] out_34,
  output [31:0] out_35,
  output [31:0] out_36,
  output [31:0] out_37,
  output [31:0] out_38,
  output [31:0] out_39,
  output [31:0] out_40,
  output [31:0] out_41,
  output [31:0] out_42,
  output [31:0] out_43,
  output [31:0] out_44,
  output [31:0] out_45,
  output [31:0] out_46
);

  wire and_2_out, and_3_out, and_4_out, and_5_out, and_6_out, and_7_out, and_8_out, and_9_out, and_10_out,
       and_11_out, and_12_out, and_13_out, and_14_out, and_15_out, and_16_out, and_17_out, and_18_out,
       and_19_out, and_20_out, and_21_out, and_22_out, and_23_out, and_24_out, and_25_out, and_26_out,
       and_27_out, and_28_out, and_29_out, and_30_out, and_31_out, and_32_out, and_33_out, and_34_out, CLOCK,
       comparator_1_eq, comparator_1_lt, comparator_2_lt, data_memory_write_enable, execute_port_a_sel,
       execute_port_b_sel, HALT_t, nCLOCK, not_2_out, not_3_out, not_4_out, not_5_out, OP_BTYPE_eq,
       OP_I_ALU_TYPE_eq, OP_I_JALR_TYPE_eq, OP_I_LOAD_TYPE_eq, OP_JTYPE_eq, OP_RTYPE_eq, OP_S_TYPE_eq,
       OP_U_AUIPC_TYPE_eq, OP_U_LUI_TYPE_eq, or_2_out, or_3_out, or_4_out, or_5_out, or_6_out, or_8_out,
       or_9_out, or_10_out, or_11_out, or_12_out, or_13_out, or_14_out, or_15_out, or_16_out, or_17_out,
       or_18_out, or_19_out, or_20_out, or_21_out, or_22_out, or_23_out, or_24_out, or_25_out, or_26_out,
       or_27_out, or_28_out, or_29_out, or_30_out, or_31_out, or_32_out, or_33_out, or_34_out, pc_mux_sel,
       reg_write_enable, relaydt_1_p7, relaydt_1_p8, relaydt_2_p2, rs_ff_1_nq, rs_ff_1_q, STEP_out;
  wire [0:0] branch_enable, SLT_lt, SLTU_lt;
  wire [2:0] branch_op_sel, imm_select, reg_write_data_sel;
  wire [3:0] _32_bit_binary_to_bcd_1__1e2s, _32_bit_binary_to_bcd_1__1e3s, _32_bit_binary_to_bcd_1__1e4s,
       _32_bit_binary_to_bcd_1__1e5s, _32_bit_binary_to_bcd_1__1e6s, _32_bit_binary_to_bcd_1__1e7s,
       _32_bit_binary_to_bcd_1__1e9s, _32_bit_binary_to_bcd_1__1e10s, _32_bit_binary_to_bcd_1__1s,
       _32_bit_binary_to_bcd_1__10s, alu_op_sel, load_store_type;
  wire [7:0] ADDR1_0, ADDR1_1, ADDR1_2, ADDR1_3, ADDR2_0, ADDR2_1, ADDR2_2, ADDR2_3, ramdualport_1_d,
       WriteAddr_0, WriteAddr_1, WriteAddr_2, WriteAddr_3;
  wire [15:8] ramdualport_1_d_2;
  wire [31:0] a, add_1_s, and_1_out, b, B_Type_out, bitextender_1_out, bitextender_2_out, dmem_data,
       driver_105_out, I_Type_out, INSTRUCTION, J_Type_out, multiplexer_1_out, multiplexer_2_out,
       multiplexer_3_out, multiplexer_4_out, multiplexer_6_out, multiplexer_7_out, multiplexer_8_out,
       multiplexer_9_out, multiplexer_10_out, multiplexer_12_out, multiplexer_13_out, multiplexer_14_out,
       multiplexer_15_out, multiplexer_16_out, multiplexer_18_out, multiplexer_19_out, multiplexer_20_out,
       multiplexer_21_out, multiplexer_22_out, multiplexer_23_out, multiplexer_26_out, multiplexer_27_out,
       multiplexer_28_out, multiplexer_29_out, multiplexer_30_out, multiplexer_31_out, multiplexer_32_out,
       multiplexer_33_out, multiplexer_34_out, multiplexer_36_out, multiplexer_37_out, multiplexer_38_out,
       multiplexer_39_out, multiplexer_40_out, multiplexer_41_out, multiplexer_42_out, notconnected_1_out,
       notconnected_2_out, or_1_out, PC, pc_next, RS1, RS2, S_Type_out, SLL_out, SRA_out, SRL_out, sub_1_s,
       write_data, x00_q, xor_1_out;
  wire [31:16] ramdualport_1_d_3;

  Add #(.Bits(32)) add_1 (.a(a), .b(b), .c_i(1'b0), .s(add_1_s));  // open: c_o
  BarrelShifter #(.Bits(32)) SLL (.in(a), .shift(b[5:0]), .out(SLL_out));
  Comparator #(.Signed("true"), .Bits(32)) SLT (.a(a), .b(b), .lt(SLT_lt[0]));  // open: gt, eq
  Comparator #(.Bits(32)) SLTU (.a(a), .b(b), .lt(SLTU_lt[0]));  // open: gt, eq
  assign xor_1_out = a ^ b;  // XOr xor_1, 32 bits wide
  BarrelShifter #(.Bits(32), .direction("right")) SRL (.in(a), .shift(b[5:0]), .out(SRL_out));
  assign or_1_out = a | b;  // Or or_1, 32 bits wide
  assign and_1_out = a & b;  // And and_1, 32 bits wide
  Sub #(.Bits(32)) sub_1 (.a(a), .b(b), .c_i(1'b0), .s(sub_1_s));  // open: c_o
  BarrelShifter #(.Bits(32), .barrelShifterMode("arithmetic"), .direction("right")) SRA (
    .in(a), .shift(b[5:0]), .out(SRA_out));
  and and_2 (and_2_out, reg_write_enable, WriteAddr_0[7]);
  and and_3 (and_3_out, reg_write_enable, WriteAddr_1[7]);
  ROM #(.AddrBits(24), .isProgramMemory("true"), .Bits(32)) Instruction_ROM (.A(PC[25:2]), .sel(1'b1), .D(INSTRUCTION));
  Multiplexer #(.Bits(32)) multiplexer_1 (.sel(in_9), .in_0(write_data), .in_1({32{1'b0}}), .out(multiplexer_1_out));
  or or_2 (or_2_out, in_9, and_2_out);
  Multiplexer #(.Bits(32)) multiplexer_2 (.sel(in_9), .in_0(write_data), .in_1({32{1'b0}}), .out(multiplexer_2_out));
  or or_3 (or_3_out, in_9, and_3_out);
  and and_4 (and_4_out, reg_write_enable, WriteAddr_2[7]);
  and and_5 (and_5_out, reg_write_enable, WriteAddr_3[7]);
  // RelayDT #(.poles(2)) relaydt_1: pin names not known; wires that end beside it: _4x, clk_3, clk_2, clk, clk_4, 1'b0, relaydt_1_p7, relaydt_1_p8, _2x, relaydt_1_p7, relaydt_1_p8
  or or_4 (or_4_out, HALT, HALT_t);
  Seven_Seg_Hex seven_seg_hex_1 (.d(INSTRUCTION[31:28]), .dp(1'b0));
  Multiplexer #(.Bits(32)) multiplexer_3 (.sel(in_9), .in_0(write_data), .in_1({32{1'b0}}), .out(multiplexer_3_out));
  or or_5 (or_5_out, in_9, and_4_out);
  Multiplexer #(.Bits(32)) multiplexer_4 (.sel(in_9), .in_0(write_data), .in_1({32{1'b0}}), .out(multiplexer_4_out));
  or or_6 (or_6_out, in_9, and_5_out);
  // RelayDT relaydt_2: pin names not known; wires that end beside it: 1'b0, relaydt_2_p2
  Seven_Seg_Hex seven_seg_hex_2 (.d(INSTRUCTION[23:20]), .dp(1'b0));
  Seven_Seg_Hex seven_seg_hex_3 (.d(INSTRUCTION[27:24]), .dp(1'b0));
  Multiplexer #(.Selector_Bits(4), .Bits(32)) multiplexer_5 (
    .sel(alu_op_sel), .in_0(add_1_s), .in_1(SLL_out), .in_2({{31{1'b0}}, SLT_lt[0]}),
    .in_3({{31{1'b0}}, SLTU_lt[0]}), .in_4(xor_1_out), .in_5(SRL_out), .in_6(or_1_out), .in_7(and_1_out),
    .in_8(sub_1_s), .in_9({32{1'b0}}), .in_10({32{1'b0}}), .in_11({32{1'b0}}), .in_12({32{1'b0}}),
    .in_13(SRA_out), .in_14({32{1'b0}}), .in_15({32{1'b0}}), .out(Binary));
  Seven_Seg_Hex seven_seg_hex_4 (.d(Binary[31:28]), .dp(1'b0));
  Register #(.Bits(32)) x07 (.D(multiplexer_1_out), .C(CLOCK), .en(or_2_out), .Q(out_21));
  Register #(.Bits(32)) x15 (.D(multiplexer_2_out), .C(CLOCK), .en(or_3_out), .Q(out_30));
  Register #(.Bits(32)) x23 (.D(multiplexer_3_out), .C(CLOCK), .en(or_5_out), .Q(out_31));
  Register #(.Bits(32)) x31 (.D(multiplexer_4_out), .C(CLOCK), .en(or_6_out), .Q(out_46));
  Button STEP (.out(STEP_out));
  and and_6 (and_6_out, STEP_out, MANUAL, ~or_4_out);  // And
  RS_FF rs_ff_1 (.S(and_7_out), .C(relaydt_2_p2), .R(~and_7_out), .Q(rs_ff_1_q), .nQ(rs_ff_1_nq));
  Seven_Seg_Hex seven_seg_hex_5 (.d(INSTRUCTION[15:12]), .dp(1'b0));
  Seven_Seg_Hex seven_seg_hex_6 (.d(INSTRUCTION[19:16]), .dp(1'b0));
  Seven_Seg_Hex seven_seg_hex_7 (.d(Binary[23:20]), .dp(1'b0));
  Seven_Seg_Hex seven_seg_hex_8 (.d(Binary[27:24]), .dp(1'b0));
  assign RS1 = ADDR1_0[7] ? out_21 : 32'bz;  // Driver driver_1
  assign RS2 = ADDR2_0[7] ? out_21 : 32'bz;  // Driver driver_2
  assign RS1 = ADDR1_1[7] ? out_30 : 32'bz;  // Driver driver_3
  assign RS2 = ADDR2_1[7] ? out_30 : 32'bz;  // Driver driver_4
  assign RS1 = ADDR1_2[7] ? out_31 : 32'bz;  // Driver driver_5
  assign RS2 = ADDR2_2[7] ? out_31 : 32'bz;  // Driver driver_6
  and and_7 (and_7_out, ~MANUAL, ~or_4_out, rs_ff_1_nq);  // And
  Seven_Seg_Hex seven_seg_hex_9 (.d(INSTRUCTION[7:4]), .dp(1'b0));
  Seven_Seg_Hex seven_seg_hex_10 (.d(INSTRUCTION[11:8]), .dp(1'b0));
  Seven_Seg_Hex seven_seg_hex_11 (.d(Binary[15:12]), .dp(1'b0));
  Seven_Seg_Hex seven_seg_hex_12 (.d(Binary[19:16]), .dp(1'b0));
  assign RS1 = ADDR1_3[7] ? out_46 : 32'bz;  // Driver driver_7
  assign RS2 = ADDR2_3[7] ? out_46 : 32'bz;  // Driver driver_8
  or or_7 (CLOCK, and_6_out, rs_ff_1_q);
  Seven_Seg_Hex seven_seg_hex_13 (.d(INSTRUCTION[3:0]), .dp(1'b0));
  Seven_Seg_Hex seven_seg_hex_14 (.d(Binary[7:4]), .dp(1'b0));
  Seven_Seg_Hex seven_seg_hex_15 (.d(Binary[11:8]), .dp(1'b0));
  and and_8 (and_8_out, reg_write_enable, WriteAddr_0[6]);
  and and_9 (and_9_out, reg_write_enable, WriteAddr_1[6]);
  and and_10 (and_10_out, reg_write_enable, WriteAddr_2[6]);
  and and_11 (and_11_out, reg_write_enable, WriteAddr_3[6]);
  not not_1 (nCLOCK, CLOCK);
  Seven_Seg_Hex seven_seg_hex_16 (.d(Binary[3:0]), .dp(1'b0));
  Multiplexer #(.Bits(32)) multiplexer_6 (.sel(in_9), .in_0(write_data), .in_1({32{1'b0}}), .out(multiplexer_6_out));
  or or_8 (or_8_out, in_9, and_8_out);
  Multiplexer #(.Bits(32)) multiplexer_7 (.sel(in_9), .in_0(write_data), .in_1({32{1'b0}}), .out(multiplexer_7_out));
  or or_9 (or_9_out, in_9, and_9_out);
  Multiplexer #(.Bits(32)) multiplexer_8 (.sel(in_9), .in_0(write_data), .in_1({32{1'b0}}), .out(multiplexer_8_out));
  or or_10 (or_10_out, in_9, and_10_out);
  Multiplexer #(.Bits(32)) multiplexer_9 (.sel(in_9), .in_0(write_data), .in_1({32{1'b0}}), .out(multiplexer_9_out));
  or or_11 (or_11_out, in_9, and_11_out);
  LED led_1 (.in(CLOCK));
  LED led_2 (.in(nCLOCK));
  Register #(.Bits(32)) x06 (.D(multiplexer_6_out), .C(CLOCK), .en(or_8_out), .Q(out_20));
  Register #(.Bits(32)) x14 (.D(multiplexer_7_out), .C(CLOCK), .en(or_9_out), .Q(out_29));
  Register #(.Bits(32)) x22 (.D(multiplexer_8_out), .C(CLOCK), .en(or_10_out), .Q(out_32));
  Register #(.Bits(32)) x30 (.D(multiplexer_9_out), .C(CLOCK), .en(or_11_out), .Q(out_45));
  Add #(.Bits(32)) add_2 (.a(PC), .b(32'h4), .c_i(1'b0), .s(pc_next));  // open: c_o
  assign RS1 = ADDR1_0[6] ? out_20 : 32'bz;  // Driver driver_9
  assign RS2 = ADDR2_0[6] ? out_20 : 32'bz;  // Driver driver_10
  assign RS1 = ADDR1_1[6] ? out_29 : 32'bz;  // Driver driver_11
  assign RS2 = ADDR2_1[6] ? out_29 : 32'bz;  // Driver driver_12
  assign RS1 = ADDR1_2[6] ? out_32 : 32'bz;  // Driver driver_13
  assign RS2 = ADDR2_2[6] ? out_32 : 32'bz;  // Driver driver_14
  assign RS1 = ADDR1_3[6] ? out_45 : 32'bz;  // Driver driver_15
  assign RS2 = ADDR2_3[6] ? out_45 : 32'bz;  // Driver driver_16
  Multiplexer #(.Bits(32)) multiplexer_10 (.sel(pc_mux_sel), .in_0(pc_next), .in_1(Binary), .out(multiplexer_10_out));
  and and_12 (and_12_out, reg_write_enable, WriteAddr_0[5]);
  and and_13 (and_13_out, reg_write_enable, WriteAddr_1[5]);
  Multiplexer #(.Selector_Bits(3), .Bits(32)) multiplexer_11 (
    .sel(reg_write_data_sel), .in_0(dmem_data), .in_1(Binary), .in_2({{31{1'b0}}, branch_enable[0]}),
    .in_3(Binary_2), .in_4(pc_next), .in_5({32{1'b0}}), .in_6({32{1'b0}}), .in_7({32{1'b0}}), .out(write_data));
  Multiplexer #(.Bits(32)) multiplexer_12 (.sel(in_9), .in_0(write_data), .in_1({32{1'b0}}), .out(multiplexer_12_out));
  or or_12 (or_12_out, in_9, and_12_out);
  Multiplexer #(.Bits(32)) multiplexer_13 (.sel(in_9), .in_0(write_data), .in_1({32{1'b0}}), .out(multiplexer_13_out));
  or or_13 (or_13_out, in_9, and_13_out);
  and and_14 (and_14_out, reg_write_enable, WriteAddr_2[5]);
  and and_15 (and_15_out, reg_write_enable, WriteAddr_3[5]);
  Multiplexer #(.Bits(32)) multiplexer_14 (
    .sel(in_9), .in_0(multiplexer_10_out), .in_1({32{1'b0}}), .out(multiplexer_14_out));
  BitExtender #(.inputBits(12), .outputBits(32)) S_Type (
    .in({INSTRUCTION[31:25], INSTRUCTION[11:7]}), .out(S_Type_out));
  Multiplexer #(.Bits(32)) multiplexer_15 (.sel(in_9), .in_0(write_data), .in_1({32{1'b0}}), .out(multiplexer_15_out));
  or or_14 (or_14_out, in_9, and_14_out);
  Multiplexer #(.Bits(32)) multiplexer_16 (.sel(in_9), .in_0(write_data), .in_1({32{1'b0}}), .out(multiplexer_16_out));
  or or_15 (or_15_out, in_9, and_15_out);
  BitExtender #(.inputBits(13), .outputBits(32)) B_Type (
    .in({INSTRUCTION[31], INSTRUCTION[7], INSTRUCTION[30:25], INSTRUCTION[11:8], 1'b0}), .out(B_Type_out));
  BitExtender #(.inputBits(21), .outputBits(32)) J_Type (
    .in({INSTRUCTION[31], INSTRUCTION[19:12], INSTRUCTION[20], INSTRUCTION[30:21], 1'b0}), .out(J_Type_out));
  BitExtender #(.inputBits(12), .outputBits(32)) I_Type (.in(INSTRUCTION[31:20]), .out(I_Type_out));
  Register #(.Bits(32)) x05 (.D(multiplexer_12_out), .C(CLOCK), .en(or_12_out), .Q(out_19));
  Register #(.Bits(32)) x13 (.D(multiplexer_13_out), .C(CLOCK), .en(or_13_out), .Q(out_28));
  Register #(.Bits(32)) x21 (.D(multiplexer_15_out), .C(CLOCK), .en(or_14_out), .Q(out_33));
  Register #(.Bits(32)) x29 (.D(multiplexer_16_out), .C(CLOCK), .en(or_15_out), .Q(out_44));
  Seven_Seg_Hex seven_seg_hex_17 (.d(PC[31:28]), .dp(1'b0));
  Register #(.Bits(32)) u_PC (.D(multiplexer_14_out), .C(nCLOCK), .en(1'b1), .Q(PC));
  assign RS1 = ADDR1_0[5] ? out_19 : 32'bz;  // Driver driver_17
  assign RS2 = ADDR2_0[5] ? out_19 : 32'bz;  // Driver driver_18
  assign RS1 = ADDR1_1[5] ? out_28 : 32'bz;  // Driver driver_19
  assign RS2 = ADDR2_1[5] ? out_28 : 32'bz;  // Driver driver_20
  assign RS1 = ADDR1_2[5] ? out_33 : 32'bz;  // Driver driver_21
  assign RS2 = ADDR2_2[5] ? out_33 : 32'bz;  // Driver driver_22
  Seven_Seg_Hex seven_seg_hex_18 (.d(PC[27:24]), .dp(1'b0));
  Seven_Seg_Hex seven_seg_hex_19 (.d(PC[23:20]), .dp(1'b0));
  Multiplexer #(.Selector_Bits(3), .Bits(32)) multiplexer_17 (
    .sel(imm_select), .in_0(S_Type_out), .in_1({32{1'b0}}), .in_2({INSTRUCTION[31:12], {12{1'b0}}}),
    .in_3({32{1'b0}}), .in_4(B_Type_out), .in_5(J_Type_out), .in_6(I_Type_out), .in_7({32{1'b0}}),
    .out(Binary_2));
  Seven_Seg_Hex seven_seg_hex_20 (.d(Binary_2[27:24]), .dp(1'b0));
  Seven_Seg_Hex seven_seg_hex_21 (.d(Binary_2[31:28]), .dp(1'b0));
  Demultiplexer #(.Selector_Bits(5)) demultiplexer_1 (
    .sel(INSTRUCTION[19:15]), .in(1'b1), .out_0(ADDR1_0[0]), .out_1(ADDR1_0[1]), .out_2(ADDR1_0[2]),
    .out_3(ADDR1_0[3]), .out_4(ADDR1_0[4]), .out_5(ADDR1_0[5]), .out_6(ADDR1_0[6]), .out_7(ADDR1_0[7]),
    .out_8(ADDR1_1[0]), .out_9(ADDR1_1[1]), .out_10(ADDR1_1[2]), .out_11(ADDR1_1[3]), .out_12(ADDR1_1[4]),
    .out_13(ADDR1_1[5]), .out_14(ADDR1_1[6]), .out_15(ADDR1_1[7]), .out_16(ADDR1_2[0]), .out_17(ADDR1_2[1]),
    .out_18(ADDR1_2[2]), .out_19(ADDR1_2[3]), .out_20(ADDR1_2[4]), .out_21(ADDR1_2[5]), .out_22(ADDR1_2[6]),
    .out_23(ADDR1_2[7]), .out_24(ADDR1_3[0]), .out_25(ADDR1_3[1]), .out_26(ADDR1_3[2]), .out_27(ADDR1_3[3]),
    .out_28(ADDR1_3[4]), .out_29(ADDR1_3[5]), .out_30(ADDR1_3[6]), .out_31(ADDR1_3[7]));
  assign RS1 = ADDR1_3[5] ? out_44 : 32'bz;  // Driver driver_23
  assign RS2 = ADDR2_3[5] ? out_44 : 32'bz;  // Driver driver_24
  Seven_Seg_Hex seven_seg_hex_22 (.d(PC[19:16]), .dp(1'b0));
  Seven_Seg_Hex seven_seg_hex_23 (.d(PC[15:12]), .dp(1'b0));
  Seven_Seg_Hex seven_seg_hex_24 (.d(Binary_2[19:16]), .dp(1'b0));
  Seven_Seg_Hex seven_seg_hex_25 (.d(Binary_2[23:20]), .dp(1'b0));
  and and_16 (and_16_out, reg_write_enable, WriteAddr_0[4]);
  and and_17 (and_17_out, reg_write_enable, WriteAddr_1[4]);
  and and_18 (and_18_out, reg_write_enable, WriteAddr_2[4]);
  and and_19 (and_19_out, reg_write_enable, WriteAddr_3[4]);
  Seven_Seg_Hex seven_seg_hex_26 (.d(PC[11:8]), .dp(1'b0));
  Seven_Seg_Hex seven_seg_hex_27 (.d(PC[7:4]), .dp(1'b0));
  Seven_Seg_Hex seven_seg_hex_28 (.d(Binary_2[11:8]), .dp(1'b0));
  Seven_Seg_Hex seven_seg_hex_29 (.d(Binary_2[15:12]), .dp(1'b0));
  Multiplexer #(.Bits(32)) multiplexer_18 (.sel(in_9), .in_0(write_data), .in_1({32{1'b0}}), .out(multiplexer_18_out));
  or or_16 (or_16_out, in_9, and_16_out);
  Multiplexer #(.Bits(32)) multiplexer_19 (.sel(in_9), .in_0(write_data), .in_1({32{1'b0}}), .out(multiplexer_19_out));
  or or_17 (or_17_out, in_9, and_17_out);
  Multiplexer #(.Bits(32)) multiplexer_20 (.sel(in_9), .in_0(write_data), .in_1({32{1'b0}}), .out(multiplexer_20_out));
  or or_18 (or_18_out, in_9, and_18_out);
  Multiplexer #(.Bits(32)) multiplexer_21 (.sel(in_9), .in_0(write_data), .in_1({32{1'b0}}), .out(multiplexer_21_out));
  or or_19 (or_19_out, in_9, and_19_out);
  Seven_Seg_Hex seven_seg_hex_30 (.d(PC[3:0]), .dp(1'b0));
  Seven_Seg_Hex seven_seg_hex_31 (.d(Binary_2[3:0]), .dp(1'b0));
  Seven_Seg_Hex seven_seg_hex_32 (.d(Binary_2[7:4]), .dp(1'b0));
  Register #(.Bits(32)) x04 (.D(multiplexer_18_out), .C(CLOCK), .en(or_16_out), .Q(out_18));
  Register #(.Bits(32)) x12 (.D(multiplexer_19_out), .C(CLOCK), .en(or_17_out), .Q(out_27));
  Register #(.Bits(32)) x20 (.D(multiplexer_20_out), .C(CLOCK), .en(or_18_out), .Q(out_34));
  Register #(.Bits(32)) x28 (.D(multiplexer_21_out), .C(CLOCK), .en(or_19_out), .Q(out_43));
  assign RS1 = ADDR1_0[4] ? out_18 : 32'bz;  // Driver driver_25
  assign RS2 = ADDR2_0[4] ? out_18 : 32'bz;  // Driver driver_26
  assign RS1 = ADDR1_1[4] ? out_27 : 32'bz;  // Driver driver_27
  assign RS2 = ADDR2_1[4] ? out_27 : 32'bz;  // Driver driver_28
  assign RS1 = ADDR1_2[4] ? out_34 : 32'bz;  // Driver driver_29
  assign RS2 = ADDR2_2[4] ? out_34 : 32'bz;  // Driver driver_30
  assign RS1 = ADDR1_3[4] ? out_43 : 32'bz;  // Driver driver_31
  assign RS2 = ADDR2_3[4] ? out_43 : 32'bz;  // Driver driver_32
  Seven_Seg_Hex seven_seg_hex_33 (.d(_32_bit_binary_to_bcd_1__1e10s), .dp(1'b0));
  and and_20 (and_20_out, reg_write_enable, WriteAddr_0[3]);
  and and_21 (and_21_out, reg_write_enable, WriteAddr_1[3]);
  Seven_Seg_Hex seven_seg_hex_34 (.d(_32_bit_binary_to_bcd_1__1e9s), .dp(1'b0));
  Multiplexer #(.Bits(32)) multiplexer_22 (.sel(in_9), .in_0(write_data), .in_1({32{1'b0}}), .out(multiplexer_22_out));
  or or_20 (or_20_out, in_9, and_20_out);
  Multiplexer #(.Bits(32)) multiplexer_23 (.sel(in_9), .in_0(write_data), .in_1({32{1'b0}}), .out(multiplexer_23_out));
  or or_21 (or_21_out, in_9, and_21_out);
  and and_22 (and_22_out, reg_write_enable, WriteAddr_2[3]);
  and and_23 (and_23_out, reg_write_enable, WriteAddr_3[3]);
  Multiplexer #(.Bits(32)) multiplexer_24 (.sel(execute_port_a_sel), .in_0(PC), .in_1(RS1), .out(a));
  Multiplexer #(.Bits(32)) multiplexer_25 (.sel(execute_port_b_sel), .in_0(Binary_2), .in_1(RS2), .out(b));
  Seven_Seg_Hex seven_seg_hex_35 (.d(_32_bit_binary_to_bcd_1__1e7s), .dp(1'b0));
  Multiplexer #(.Bits(32)) multiplexer_26 (.sel(in_9), .in_0(write_data), .in_1({32{1'b0}}), .out(multiplexer_26_out));
  or or_22 (or_22_out, in_9, and_22_out);
  Multiplexer #(.Bits(32)) multiplexer_27 (.sel(in_9), .in_0(write_data), .in_1({32{1'b0}}), .out(multiplexer_27_out));
  or or_23 (or_23_out, in_9, and_23_out);
  Comparator #(.Bits(7)) OP_RTYPE (.a(INSTRUCTION[6:0]), .b(7'b0110011), .eq(OP_RTYPE_eq));  // open: gt, lt
  LED led_3 (.in(INSTRUCTION[6]));
  Seven_Seg_Hex seven_seg_hex_36 (.d(_32_bit_binary_to_bcd_1__1e5s), .dp(1'b0));
  Seven_Seg_Hex seven_seg_hex_37 (.d(_32_bit_binary_to_bcd_1__1e6s), .dp(1'b0));
  _32_bit_Binary_to_BCD _32_bit_binary_to_bcd_1 (
    .In(out_26), ._1e10s(_32_bit_binary_to_bcd_1__1e10s), ._1e9s(_32_bit_binary_to_bcd_1__1e9s),
    ._1e7s(_32_bit_binary_to_bcd_1__1e7s), ._1e6s(_32_bit_binary_to_bcd_1__1e6s),
    ._1e5s(_32_bit_binary_to_bcd_1__1e5s), ._1e4s(_32_bit_binary_to_bcd_1__1e4s),
    ._1e3s(_32_bit_binary_to_bcd_1__1e3s), ._1e2s(_32_bit_binary_to_bcd_1__1e2s),
    ._10s(_32_bit_binary_to_bcd_1__10s), ._1s(_32_bit_binary_to_bcd_1__1s));  // open: _1e8s
  Demultiplexer #(.Selector_Bits(5)) demultiplexer_2 (
    .sel(INSTRUCTION[24:20]), .in(1'b1), .out_0(ADDR2_0[0]), .out_1(ADDR2_0[1]), .out_2(ADDR2_0[2]),
    .out_3(ADDR2_0[3]), .out_4(ADDR2_0[4]), .out_5(ADDR2_0[5]), .out_6(ADDR2_0[6]), .out_7(ADDR2_0[7]),
    .out_8(ADDR2_1[0]), .out_9(ADDR2_1[1]), .out_10(ADDR2_1[2]), .out_11(ADDR2_1[3]), .out_12(ADDR2_1[4]),
    .out_13(ADDR2_1[5]), .out_14(ADDR2_1[6]), .out_15(ADDR2_1[7]), .out_16(ADDR2_2[0]), .out_17(ADDR2_2[1]),
    .out_18(ADDR2_2[2]), .out_19(ADDR2_2[3]), .out_20(ADDR2_2[4]), .out_21(ADDR2_2[5]), .out_22(ADDR2_2[6]),
    .out_23(ADDR2_2[7]), .out_24(ADDR2_3[0]), .out_25(ADDR2_3[1]), .out_26(ADDR2_3[2]), .out_27(ADDR2_3[3]),
    .out_28(ADDR2_3[4]), .out_29(ADDR2_3[5]), .out_30(ADDR2_3[6]), .out_31(ADDR2_3[7]));
  Register #(.Bits(32)) x03 (.D(multiplexer_22_out), .C(CLOCK), .en(or_20_out), .Q(out_17));
  Register #(.Bits(32)) x11 (.D(multiplexer_23_out), .C(CLOCK), .en(or_21_out), .Q(out_26));
  Register #(.Bits(32)) x19 (.D(multiplexer_26_out), .C(CLOCK), .en(or_22_out), .Q(out_35));
  Register #(.Bits(32)) x27 (.D(multiplexer_27_out), .C(CLOCK), .en(or_23_out), .Q(out_42));
  LED led_4 (.in(INSTRUCTION[5]));
  LED led_5 (.in(INSTRUCTION[4]));
  Seven_Seg_Hex seven_seg_hex_38 (.d(_32_bit_binary_to_bcd_1__1e4s), .dp(1'b0));
  assign RS1 = ADDR1_0[3] ? out_17 : 32'bz;  // Driver driver_33
  assign RS2 = ADDR2_0[3] ? out_17 : 32'bz;  // Driver driver_34
  assign RS1 = ADDR1_1[3] ? out_26 : 32'bz;  // Driver driver_35
  assign RS2 = ADDR2_1[3] ? out_26 : 32'bz;  // Driver driver_36
  assign RS1 = ADDR1_2[3] ? out_35 : 32'bz;  // Driver driver_37
  assign RS2 = ADDR2_2[3] ? out_35 : 32'bz;  // Driver driver_38
  assign pc_mux_sel = OP_RTYPE_eq ? 1'b0 : 1'bz;  // Driver driver_39
  assign reg_write_enable = OP_RTYPE_eq ? 1'b1 : 1'bz;  // Driver driver_40
  assign imm_select = OP_RTYPE_eq ? 3'b111 : 3'bz;  // Driver driver_41
  assign execute_port_a_sel = OP_RTYPE_eq ? 1'b1 : 1'bz;  // Driver driver_42
  assign execute_port_b_sel = OP_RTYPE_eq ? 1'b1 : 1'bz;  // Driver driver_43
  assign reg_write_data_sel = OP_RTYPE_eq ? 3'b001 : 3'bz;  // Driver driver_44
  assign load_store_type = OP_RTYPE_eq ? 4'b1111 : 4'bz;  // Driver driver_45
  assign data_memory_write_enable = OP_RTYPE_eq ? 1'b0 : 1'bz;  // Driver driver_46
  assign alu_op_sel = OP_RTYPE_eq ? {INSTRUCTION[30], INSTRUCTION[14:12]} : 4'bz;  // Driver driver_47
  assign branch_op_sel = OP_RTYPE_eq ? 3'b010 : 3'bz;  // Driver driver_48
  LED led_6 (.in(INSTRUCTION[3]));
  LED led_7 (.in(INSTRUCTION[2]));
  Seven_Seg_Hex seven_seg_hex_39 (.d(_32_bit_binary_to_bcd_1__1e3s), .dp(1'b0));
  assign RS1 = ADDR1_3[3] ? out_42 : 32'bz;  // Driver driver_49
  assign RS2 = ADDR2_3[3] ? out_42 : 32'bz;  // Driver driver_50
  LED led_8 (.in(INSTRUCTION[1]));
  LED led_9 (.in(INSTRUCTION[0]));
  Seven_Seg_Hex seven_seg_hex_40 (.d(_32_bit_binary_to_bcd_1__1e2s), .dp(1'b0));
  Seven_Seg_Hex seven_seg_hex_41 (.d(_32_bit_binary_to_bcd_1__10s), .dp(1'b0));
  and and_24 (and_24_out, reg_write_enable, WriteAddr_0[2]);
  and and_25 (and_25_out, reg_write_enable, WriteAddr_1[2]);
  and and_26 (and_26_out, reg_write_enable, WriteAddr_2[2]);
  and and_27 (and_27_out, reg_write_enable, WriteAddr_3[2]);
  Seven_Seg_Hex seven_seg_hex_42 (.d(_32_bit_binary_to_bcd_1__1s), .dp(1'b0));
  Multiplexer #(.Bits(32)) multiplexer_28 (.sel(in_9), .in_0(write_data), .in_1({32{1'b0}}), .out(multiplexer_28_out));
  or or_24 (or_24_out, in_9, and_24_out);
  Multiplexer #(.Bits(32)) multiplexer_29 (.sel(in_9), .in_0(write_data), .in_1({32{1'b0}}), .out(multiplexer_29_out));
  or or_25 (or_25_out, in_9, and_25_out);
  Multiplexer #(.Bits(32)) multiplexer_30 (.sel(in_9), .in_0(write_data), .in_1({32{1'b0}}), .out(multiplexer_30_out));
  or or_26 (or_26_out, in_9, and_26_out);
  Multiplexer #(.Bits(32)) multiplexer_31 (.sel(in_9), .in_0(write_data), .in_1({32{1'b0}}), .out(multiplexer_31_out));
  or or_27 (or_27_out, in_9, and_27_out);
  Comparator #(.Bits(7)) OP_U_LUI_TYPE (.a(INSTRUCTION[6:0]), .b(7'b0110111), .eq(OP_U_LUI_TYPE_eq));  // open: gt, lt
  LED led_10 (.in(pc_mux_sel));
  LED led_11 (.in(reg_write_enable));
  Register #(.Bits(32)) x02 (.D(multiplexer_28_out), .C(CLOCK), .en(or_24_out), .Q(out_16));
  Register #(.Bits(32)) x10 (.D(multiplexer_29_out), .C(CLOCK), .en(or_25_out), .Q(out_25));
  Register #(.Bits(32)) x18 (.D(multiplexer_30_out), .C(CLOCK), .en(or_26_out), .Q(out_36));
  assign pc_mux_sel = OP_U_LUI_TYPE_eq ? 1'b0 : 1'bz;  // Driver driver_51
  assign reg_write_enable = OP_U_LUI_TYPE_eq ? 1'b1 : 1'bz;  // Driver driver_52
  assign imm_select = OP_U_LUI_TYPE_eq ? 3'b010 : 3'bz;  // Driver driver_53
  assign execute_port_a_sel = OP_U_LUI_TYPE_eq ? 1'b0 : 1'bz;  // Driver driver_54
  assign execute_port_b_sel = OP_U_LUI_TYPE_eq ? 1'b0 : 1'bz;  // Driver driver_55
  assign reg_write_data_sel = OP_U_LUI_TYPE_eq ? 3'b011 : 3'bz;  // Driver driver_56
  assign load_store_type = OP_U_LUI_TYPE_eq ? 4'b1111 : 4'bz;  // Driver driver_57
  assign data_memory_write_enable = OP_U_LUI_TYPE_eq ? 1'b0 : 1'bz;  // Driver driver_58
  assign alu_op_sel = OP_U_LUI_TYPE_eq ? 4'b1111 : 4'bz;  // Driver driver_59
  assign branch_op_sel = OP_U_LUI_TYPE_eq ? 3'b010 : 3'bz;  // Driver driver_60
  LED led_12 (.in(imm_select[2]));
  LED led_13 (.in(imm_select[1]));
  Multiplexer #(.Bits(32)) multiplexer_32 (
    .sel(execute_port_b_sel), .in_0(RS2), .in_1(Binary_2), .out(multiplexer_32_out));
  Register #(.Bits(32)) x26 (.D(multiplexer_31_out), .C(CLOCK), .en(or_27_out), .Q(out_41));
  LED led_14 (.in(imm_select[0]));
  LED led_15 (.in(execute_port_a_sel));
  Comparator #(.Signed("true"), .Bits(32)) comparator_1 (
    .a(RS1), .b(multiplexer_32_out), .eq(comparator_1_eq), .lt(comparator_1_lt));  // open: gt
  Comparator #(.Bits(32)) comparator_2 (.a(RS1), .b(multiplexer_32_out), .lt(comparator_2_lt));  // open: gt, eq
  assign RS1 = ADDR1_0[2] ? out_16 : 32'bz;  // Driver driver_61
  assign RS2 = ADDR2_0[2] ? out_16 : 32'bz;  // Driver driver_62
  assign RS1 = ADDR1_1[2] ? out_25 : 32'bz;  // Driver driver_63
  assign RS2 = ADDR2_1[2] ? out_25 : 32'bz;  // Driver driver_64
  assign RS1 = ADDR1_2[2] ? out_36 : 32'bz;  // Driver driver_65
  assign RS2 = ADDR2_2[2] ? out_36 : 32'bz;  // Driver driver_66
  assign RS1 = ADDR1_3[2] ? out_41 : 32'bz;  // Driver driver_67
  assign RS2 = ADDR2_3[2] ? out_41 : 32'bz;  // Driver driver_68
  LED led_16 (.in(execute_port_b_sel));
  LED led_17 (.in(reg_write_data_sel[2]));
  not not_2 (not_2_out, comparator_1_eq);
  not not_3 (not_3_out, comparator_1_lt);
  not not_4 (not_4_out, comparator_2_lt);
  Demultiplexer #(.Selector_Bits(5)) demultiplexer_3 (
    .sel(INSTRUCTION[11:7]), .in(1'b1), .out_0(WriteAddr_0[0]), .out_1(WriteAddr_0[1]),
    .out_2(WriteAddr_0[2]), .out_3(WriteAddr_0[3]), .out_4(WriteAddr_0[4]), .out_5(WriteAddr_0[5]),
    .out_6(WriteAddr_0[6]), .out_7(WriteAddr_0[7]), .out_8(WriteAddr_1[0]), .out_9(WriteAddr_1[1]),
    .out_10(WriteAddr_1[2]), .out_11(WriteAddr_1[3]), .out_12(WriteAddr_1[4]), .out_13(WriteAddr_1[5]),
    .out_14(WriteAddr_1[6]), .out_15(WriteAddr_1[7]), .out_16(WriteAddr_2[0]), .out_17(WriteAddr_2[1]),
    .out_18(WriteAddr_2[2]), .out_19(WriteAddr_2[3]), .out_20(WriteAddr_2[4]), .out_21(WriteAddr_2[5]),
    .out_22(WriteAddr_2[6]), .out_23(WriteAddr_2[7]), .out_24(WriteAddr_3[0]), .out_25(WriteAddr_3[1]),
    .out_26(WriteAddr_3[2]), .out_27(WriteAddr_3[3]), .out_28(WriteAddr_3[4]), .out_29(WriteAddr_3[5]),
    .out_30(WriteAddr_3[6]), .out_31(WriteAddr_3[7]));
  and and_28 (and_28_out, reg_write_enable, WriteAddr_0[1]);
  and and_29 (and_29_out, reg_write_enable, WriteAddr_1[1]);
  LED led_18 (.in(reg_write_data_sel[1]));
  LED led_19 (.in(reg_write_data_sel[0]));
  Seven_Seg_Hex seven_seg_hex_43 (.d(4'b0000), .dp(1'b0));
  Seven_Seg_Hex seven_seg_hex_44 (.d(4'b0000), .dp(1'b0));
  Multiplexer #(.Bits(32)) multiplexer_33 (.sel(in_9), .in_0(write_data), .in_1({32{1'b0}}), .out(multiplexer_33_out));
  or or_28 (or_28_out, in_9, and_28_out);
  Multiplexer #(.Bits(32)) multiplexer_34 (.sel(in_9), .in_0(write_data), .in_1({32{1'b0}}), .out(multiplexer_34_out));
  or or_29 (or_29_out, in_9, and_29_out);
  and and_30 (and_30_out, reg_write_enable, WriteAddr_2[1]);
  and and_31 (and_31_out, reg_write_enable, WriteAddr_3[1]);
  Comparator #(.Bits(7)) OP_I_ALU_TYPE (.a(INSTRUCTION[6:0]), .b(7'b0010011), .eq(OP_I_ALU_TYPE_eq));  // open: gt, lt
  LED led_20 (.in(load_store_type[3]));
  LED led_21 (.in(load_store_type[2]));
  Multiplexer #(.Selector_Bits(3)) multiplexer_35 (
    .sel(branch_op_sel), .in_0(comparator_1_eq), .in_1(not_2_out), .in_2(1'b0), .in_3(1'b0),
    .in_4(comparator_1_lt), .in_5(not_3_out), .in_6(comparator_2_lt), .in_7(not_4_out), .out(branch_enable[0]));
  Seven_Seg_Hex seven_seg_hex_45 (.d(4'b0000), .dp(1'b0));
  Seven_Seg_Hex seven_seg_hex_46 (.d(4'b0000), .dp(1'b0));
  Seven_Seg_Hex seven_seg_hex_47 (.d(RS1[27:24]), .dp(1'b0));
  Seven_Seg_Hex seven_seg_hex_48 (.d(RS1[31:28]), .dp(1'b0));
  Multiplexer #(.Bits(32)) multiplexer_36 (.sel(in_9), .in_0(write_data), .in_1({32{1'b0}}), .out(multiplexer_36_out));
  or or_30 (or_30_out, in_9, and_30_out);
  Multiplexer #(.Bits(32)) multiplexer_37 (.sel(in_9), .in_0(write_data), .in_1({32{1'b0}}), .out(multiplexer_37_out));
  or or_31 (or_31_out, in_9, and_31_out);
  assign pc_mux_sel = OP_I_ALU_TYPE_eq ? 1'b0 : 1'bz;  // Driver driver_69
  assign reg_write_enable = OP_I_ALU_TYPE_eq ? 1'b1 : 1'bz;  // Driver driver_70
  assign imm_select = OP_I_ALU_TYPE_eq ? 3'b110 : 3'bz;  // Driver driver_71
  assign execute_port_a_sel = OP_I_ALU_TYPE_eq ? 1'b1 : 1'bz;  // Driver driver_72
  assign execute_port_b_sel = OP_I_ALU_TYPE_eq ? 1'b0 : 1'bz;  // Driver driver_73
  assign reg_write_data_sel = OP_I_ALU_TYPE_eq ? 3'b001 : 3'bz;  // Driver driver_74
  assign load_store_type = OP_I_ALU_TYPE_eq ? 4'b1111 : 4'bz;  // Driver driver_75
  assign data_memory_write_enable = OP_I_ALU_TYPE_eq ? 1'b0 : 1'bz;  // Driver driver_76
  assign alu_op_sel = OP_I_ALU_TYPE_eq ? {1'b0, INSTRUCTION[14:12]} : 4'bz;  // Driver driver_77
  assign branch_op_sel = OP_I_ALU_TYPE_eq ? 3'b010 : 3'bz;  // Driver driver_78
  LED led_22 (.in(load_store_type[1]));
  LED led_23 (.in(load_store_type[0]));
  Seven_Seg_Hex seven_seg_hex_49 (.d(4'b0000), .dp(1'b0));
  Seven_Seg_Hex seven_seg_hex_50 (.d(4'b0000), .dp(1'b0));
  Seven_Seg_Hex seven_seg_hex_51 (.d(RS1[19:16]), .dp(1'b0));
  Seven_Seg_Hex seven_seg_hex_52 (.d(RS1[23:20]), .dp(1'b0));
  Register #(.Bits(32)) x01 (.D(multiplexer_33_out), .C(CLOCK), .en(or_28_out), .Q(out_22));
  Register #(.Bits(32)) x09 (.D(multiplexer_34_out), .C(CLOCK), .en(or_29_out), .Q(out_24));
  Register #(.Bits(32)) x17 (.D(multiplexer_36_out), .C(CLOCK), .en(or_30_out), .Q(out_37));
  Register #(.Bits(32)) x25 (.D(multiplexer_37_out), .C(CLOCK), .en(or_31_out), .Q(out_40));
  LED led_24 (.in(data_memory_write_enable));
  LED led_25 (.in(alu_op_sel[3]));
  Seven_Seg_Hex seven_seg_hex_53 (.d({3'b000, branch_enable[0]}), .dp(1'b0));
  Seven_Seg_Hex seven_seg_hex_54 (.d(4'b0000), .dp(1'b0));
  Seven_Seg_Hex seven_seg_hex_55 (.d(RS1[11:8]), .dp(1'b0));
  Seven_Seg_Hex seven_seg_hex_56 (.d(RS1[15:12]), .dp(1'b0));
  assign RS1 = ADDR1_0[1] ? out_22 : 32'bz;  // Driver driver_79
  assign RS2 = ADDR2_0[1] ? out_22 : 32'bz;  // Driver driver_80
  assign RS1 = ADDR1_1[1] ? out_24 : 32'bz;  // Driver driver_81
  assign RS2 = ADDR2_1[1] ? out_24 : 32'bz;  // Driver driver_82
  assign RS1 = ADDR1_2[1] ? out_37 : 32'bz;  // Driver driver_83
  assign RS2 = ADDR2_2[1] ? out_37 : 32'bz;  // Driver driver_84
  LED led_26 (.in(alu_op_sel[2]));
  LED led_27 (.in(alu_op_sel[1]));
  Seven_Seg_Hex seven_seg_hex_57 (.d(RS1[3:0]), .dp(1'b0));
  Seven_Seg_Hex seven_seg_hex_58 (.d(RS1[7:4]), .dp(1'b0));
  assign RS1 = ADDR1_3[1] ? out_40 : 32'bz;  // Driver driver_85
  assign RS2 = ADDR2_3[1] ? out_40 : 32'bz;  // Driver driver_86
  LED led_28 (.in(alu_op_sel[0]));
  LED led_29 (.in(branch_op_sel[2]));
  Seven_Seg_Hex seven_seg_hex_59 (.d(RS2[31:28]), .dp(1'b0));
  and and_32 (and_32_out, reg_write_enable, WriteAddr_1[0]);
  and and_33 (and_33_out, reg_write_enable, WriteAddr_2[0]);
  and and_34 (and_34_out, reg_write_enable, WriteAddr_3[0]);
  Comparator #(.Bits(7)) OP_BTYPE (.a(INSTRUCTION[6:0]), .b(7'b1100011), .eq(OP_BTYPE_eq));  // open: gt, lt
  LED led_30 (.in(branch_op_sel[1]));
  LED led_31 (.in(branch_op_sel[0]));
  Seven_Seg_Hex seven_seg_hex_60 (.d(RS2[23:20]), .dp(1'b0));
  Seven_Seg_Hex seven_seg_hex_61 (.d(RS2[27:24]), .dp(1'b0));
  Multiplexer #(.Bits(32)) multiplexer_38 (.sel(in_9), .in_0(write_data), .in_1({32{1'b0}}), .out(multiplexer_38_out));
  or or_32 (or_32_out, in_9, and_32_out);
  Multiplexer #(.Bits(32)) multiplexer_39 (.sel(in_9), .in_0(write_data), .in_1({32{1'b0}}), .out(multiplexer_39_out));
  or or_33 (or_33_out, in_9, and_33_out);
  Multiplexer #(.Bits(32)) multiplexer_40 (.sel(in_9), .in_0(write_data), .in_1({32{1'b0}}), .out(multiplexer_40_out));
  or or_34 (or_34_out, in_9, and_34_out);
  assign pc_mux_sel = OP_BTYPE_eq ? branch_enable[0] : 1'bz;  // Driver driver_87
  assign reg_write_enable = OP_BTYPE_eq ? 1'b0 : 1'bz;  // Driver driver_88
  assign imm_select = OP_BTYPE_eq ? 3'b100 : 3'bz;  // Driver driver_89
  assign execute_port_a_sel = OP_BTYPE_eq ? 1'b0 : 1'bz;  // Driver driver_90
  assign execute_port_b_sel = OP_BTYPE_eq ? 1'b0 : 1'bz;  // Driver driver_91
  assign reg_write_data_sel = OP_BTYPE_eq ? 3'b111 : 3'bz;  // Driver driver_92
  assign load_store_type = OP_BTYPE_eq ? 4'b1111 : 4'bz;  // Driver driver_93
  assign data_memory_write_enable = OP_BTYPE_eq ? 1'b0 : 1'bz;  // Driver driver_94
  assign alu_op_sel = OP_BTYPE_eq ? 4'b0000 : 4'bz;  // Driver driver_95
  assign branch_op_sel = OP_BTYPE_eq ? INSTRUCTION[14:12] : 3'bz;  // Driver driver_96
  BitExtender #(.outputBits(32)) bitextender_1 (.in(ramdualport_1_d), .out(bitextender_1_out));
  BitExtender #(.inputBits(16), .outputBits(32)) bitextender_2 (
    .in({ramdualport_1_d_2, ramdualport_1_d}), .out(bitextender_2_out));
  Seven_Seg_Hex seven_seg_hex_62 (.d(RS2[15:12]), .dp(1'b0));
  Seven_Seg_Hex seven_seg_hex_63 (.d(RS2[19:16]), .dp(1'b0));
  Register #(.Bits(32)) x00 (.D({32{1'b0}}), .C(CLOCK), .en(1'b0), .Q(x00_q));
  Register #(.Bits(32)) x08 (.D(multiplexer_38_out), .C(CLOCK), .en(or_32_out), .Q(out_23));
  Register #(.Bits(32)) x16 (.D(multiplexer_39_out), .C(CLOCK), .en(or_33_out), .Q(out_38));
  Seven_Seg_Hex seven_seg_hex_64 (.d(RS2[7:4]), .dp(1'b0));
  Seven_Seg_Hex seven_seg_hex_65 (.d(RS2[11:8]), .dp(1'b0));
  Register #(.Bits(32)) x24 (.D(multiplexer_40_out), .C(CLOCK), .en(or_34_out), .Q(out_39));
  Multiplexer #(.Selector_Bits(3), .Bits(32)) multiplexer_41 (
    .sel(load_store_type[2:0]), .in_0({{24{1'b0}}, RS2[7:0]}), .in_1({{16{1'b0}}, RS2[15:0]}), .in_2(RS2),
    .in_3(notconnected_1_out), .in_4(notconnected_1_out), .in_5(notconnected_1_out),
    .in_6(notconnected_1_out), .in_7(notconnected_1_out), .out(multiplexer_41_out));
  // NotConnected on notconnected_1_out
  Multiplexer #(.Selector_Bits(3), .Bits(32)) multiplexer_42 (
    .sel(load_store_type[2:0]), .in_0(bitextender_1_out), .in_1(bitextender_2_out),
    .in_2({ramdualport_1_d_3, ramdualport_1_d_2, ramdualport_1_d}), .in_3(notconnected_2_out),
    .in_4({{24{1'b0}}, ramdualport_1_d}), .in_5({{16{1'b0}}, ramdualport_1_d_2, ramdualport_1_d}),
    .in_6(notconnected_2_out), .in_7(notconnected_2_out), .out(multiplexer_42_out));
  // NotConnected on notconnected_2_out
  Seven_Seg_Hex seven_seg_hex_66 (.d(RS2[3:0]), .dp(1'b0));
  assign RS1 = ADDR1_0[0] ? x00_q : 32'bz;  // Driver driver_97
  assign RS2 = ADDR2_0[0] ? x00_q : 32'bz;  // Driver driver_98
  assign RS1 = ADDR1_1[0] ? out_23 : 32'bz;  // Driver driver_99
  assign RS2 = ADDR2_1[0] ? out_23 : 32'bz;  // Driver driver_100
  assign RS1 = ADDR1_2[0] ? out_38 : 32'bz;  // Driver driver_101
  assign RS2 = ADDR2_2[0] ? out_38 : 32'bz;  // Driver driver_102
  assign RS1 = ADDR1_3[0] ? out_39 : 32'bz;  // Driver driver_103
  assign RS2 = ADDR2_3[0] ? out_39 : 32'bz;  // Driver driver_104
  Comparator #(.Bits(7)) OP_JTYPE (.a(INSTRUCTION[6:0]), .b(7'b1101111), .eq(OP_JTYPE_eq));  // open: gt, lt
  assign driver_105_out = load_store_type[3] ? multiplexer_41_out : 32'bz;  // Driver driver_105
  not not_5 (not_5_out, load_store_type[3]);
  assign dmem_data = not_5_out ? multiplexer_42_out : 32'bz;  // Driver driver_106
  assign pc_mux_sel = OP_JTYPE_eq ? 1'b1 : 1'bz;  // Driver driver_107
  assign reg_write_enable = OP_JTYPE_eq ? 1'b1 : 1'bz;  // Driver driver_108
  assign imm_select = OP_JTYPE_eq ? 3'b101 : 3'bz;  // Driver driver_109
  assign execute_port_a_sel = OP_JTYPE_eq ? 1'b0 : 1'bz;  // Driver driver_110
  assign execute_port_b_sel = OP_JTYPE_eq ? 1'b0 : 1'bz;  // Driver driver_111
  assign reg_write_data_sel = OP_JTYPE_eq ? 3'b100 : 3'bz;  // Driver driver_112
  assign load_store_type = OP_JTYPE_eq ? 4'b1111 : 4'bz;  // Driver driver_113
  assign data_memory_write_enable = OP_JTYPE_eq ? 1'b0 : 1'bz;  // Driver driver_114
  assign alu_op_sel = OP_JTYPE_eq ? 4'b0000 : 4'bz;  // Driver driver_115
  assign branch_op_sel = OP_JTYPE_eq ? 3'b010 : 3'bz;  // Driver driver_116
  RAMDualPort #(.AddrBits(24), .Bits(32)) ramdualport_1 (
    .A(Binary[25:2]), .Din(driver_105_out), .str(data_memory_write_enable), .C(CLOCK), .ld(not_5_out),
    .D({ramdualport_1_d_3, ramdualport_1_d_2, ramdualport_1_d}));
  Comparator #(.Bits(7)) OP_I_JALR_TYPE (.a(INSTRUCTION[6:0]), .b(7'b1100111), .eq(OP_I_JALR_TYPE_eq));  // open: gt, lt
  assign pc_mux_sel = OP_I_JALR_TYPE_eq ? 1'b1 : 1'bz;  // Driver driver_117
  assign reg_write_enable = OP_I_JALR_TYPE_eq ? 1'b1 : 1'bz;  // Driver driver_118
  assign imm_select = OP_I_JALR_TYPE_eq ? 3'b110 : 3'bz;  // Driver driver_119
  assign execute_port_a_sel = OP_I_JALR_TYPE_eq ? 1'b1 : 1'bz;  // Driver driver_120
  assign execute_port_b_sel = OP_I_JALR_TYPE_eq ? 1'b0 : 1'bz;  // Driver driver_121
  assign reg_write_data_sel = OP_I_JALR_TYPE_eq ? 3'b100 : 3'bz;  // Driver driver_122
  assign load_store_type = OP_I_JALR_TYPE_eq ? 4'b1111 : 4'bz;  // Driver driver_123
  assign data_memory_write_enable = OP_I_JALR_TYPE_eq ? 1'b0 : 1'bz;  // Driver driver_124
  assign alu_op_sel = OP_I_JALR_TYPE_eq ? 4'b0000 : 4'bz;  // Driver driver_125
  assign branch_op_sel = OP_I_JALR_TYPE_eq ? 3'b010 : 3'bz;  // Driver driver_126
  Comparator #(.Bits(7)) OP_S_TYPE (.a(INSTRUCTION[6:0]), .b(7'b0100011), .eq(OP_S_TYPE_eq));  // open: gt, lt
  assign pc_mux_sel = OP_S_TYPE_eq ? 1'b0 : 1'bz;  // Driver driver_127
  assign reg_write_enable = OP_S_TYPE_eq ? 1'b0 : 1'bz;  // Driver driver_128
  assign imm_select = OP_S_TYPE_eq ? 3'b000 : 3'bz;  // Driver driver_129
  assign execute_port_a_sel = OP_S_TYPE_eq ? 1'b1 : 1'bz;  // Driver driver_130
  assign execute_port_b_sel = OP_S_TYPE_eq ? 1'b0 : 1'bz;  // Driver driver_131
  assign reg_write_data_sel = OP_S_TYPE_eq ? 3'b111 : 3'bz;  // Driver driver_132
  assign load_store_type = OP_S_TYPE_eq ? {1'b1, INSTRUCTION[14:12]} : 4'bz;  // Driver driver_133
  assign data_memory_write_enable = OP_S_TYPE_eq ? 1'b1 : 1'bz;  // Driver driver_134
  assign alu_op_sel = OP_S_TYPE_eq ? 4'b0000 : 4'bz;  // Driver driver_135
  assign branch_op_sel = OP_S_TYPE_eq ? 3'b010 : 3'bz;  // Driver driver_136
  Comparator #(.Bits(7)) OP_I_LOAD_TYPE (.a(INSTRUCTION[6:0]), .b(7'b0000011), .eq(OP_I_LOAD_TYPE_eq));  // open: gt, lt
  assign pc_mux_sel = OP_I_LOAD_TYPE_eq ? 1'b0 : 1'bz;  // Driver driver_137
  assign reg_write_enable = OP_I_LOAD_TYPE_eq ? 1'b1 : 1'bz;  // Driver driver_138
  assign imm_select = OP_I_LOAD_TYPE_eq ? 3'b110 : 3'bz;  // Driver driver_139
  assign execute_port_a_sel = OP_I_LOAD_TYPE_eq ? 1'b1 : 1'bz;  // Driver driver_140
  assign execute_port_b_sel = OP_I_LOAD_TYPE_eq ? 1'b0 : 1'bz;  // Driver driver_141
  assign reg_write_data_sel = OP_I_LOAD_TYPE_eq ? 3'b000 : 3'bz;  // Driver driver_142
  assign load_store_type = OP_I_LOAD_TYPE_eq ? {1'b0, INSTRUCTION[14:12]} : 4'bz;  // Driver driver_143
  assign data_memory_write_enable = OP_I_LOAD_TYPE_eq ? 1'b0 : 1'bz;  // Driver driver_144
  assign alu_op_sel = OP_I_LOAD_TYPE_eq ? 4'b0000 : 4'bz;  // Driver driver_145
  assign branch_op_sel = OP_I_LOAD_TYPE_eq ? 3'b010 : 3'bz;  // Driver driver_146
  Comparator #(.Bits(7)) OP_U_AUIPC_TYPE (
    .a(INSTRUCTION[6:0]), .b(7'b0010111), .eq(OP_U_AUIPC_TYPE_eq));  // open: gt, lt
  assign pc_mux_sel = OP_U_AUIPC_TYPE_eq ? 1'b0 : 1'bz;  // Driver driver_147
  assign reg_write_enable = OP_U_AUIPC_TYPE_eq ? 1'b1 : 1'bz;  // Driver driver_148
  assign imm_select = OP_U_AUIPC_TYPE_eq ? 3'b010 : 3'bz;  // Driver driver_149
  assign execute_port_a_sel = OP_U_AUIPC_TYPE_eq ? 1'b0 : 1'bz;  // Driver driver_150
  assign execute_port_b_sel = OP_U_AUIPC_TYPE_eq ? 1'b0 : 1'bz;  // Driver driver_151
  assign reg_write_data_sel = OP_U_AUIPC_TYPE_eq ? 3'b001 : 3'bz;  // Driver driver_152
  assign load_store_type = OP_U_AUIPC_TYPE_eq ? 4'b1111 : 4'bz;  // Driver driver_153
  assign data_memory_write_enable = OP_U_AUIPC_TYPE_eq ? 1'b0 : 1'bz;  // Driver driver_154
  assign alu_op_sel = OP_U_AUIPC_TYPE_eq ? 4'b0000 : 4'bz;  // Driver driver_155
  assign branch_op_sel = OP_U_AUIPC_TYPE_eq ? 3'b010 : 3'bz;  // Driver driver_156
  Comparator #(.Bits(7)) OP_HALT (.a(INSTRUCTION[6:0]), .b({7{1'b0}}), .eq(HALT_t));  // open: gt, lt

  assign Decimal = Binary;
  assign Decimal_2 = Binary_2;
  assign Signed_Decimal = Binary;
  assign Signed_Decimal_2 = Binary_2;

  // Other names for the same wires on the sheet: alu_output[31:0] = Binary; IMM[31:0] = Binary_2; RESET = in_9;
  //   RETURN_VALUE[31:0] = out_26

  // Notes on the sheet:
  //   clk: Hz: 8
  //   clk_2: Hz: 16
  //   clk_3: Hz: 64
  //   clk_4: Hz: 2
  //   MANUAL: default 1
  //   CLOCK
  //   Instruction Memory
  //   ALU
  //   Register File
  //   Instruction_ROM loads rom_part_8.hex
  //   RISC-V Instructions are 4 bytes long
  //   The PC will be incremented in that size step
  //   so we pull out that step size to pull
  //   from our Instruction array
  //   alu_opsel
  //   from funct7[30]funct3[14:12]
  //   0000 - ADD
  //   0001 - SLL
  //   0010 - SLT
  //   0011 - SLTU
  //   0100 - XOR
  //   0101 - SRL
  //   0110 - OR
  //   0111 - AND
  //   1000 - SUB
  //   1101 - SRA
  //   1111 - UNKNOWN
  //   Program Counter
  //   RD MUX
  //   Imm Sign Extend
  //   ADDR1
  //   U Type
  //   reg_write_data_sel
  //   000 -  dmem_data
  //   001 - alu_output
  //   010 - branch_enable
  //   011 - immediate
  //   100 - pc_next
  //   111 - N_A
  //   imm_select
  //   from oppcode [6][4][3]
  //   000 - S Type
  //   001 - 
  //   010 - U Type
  //   011 - 
  //   100 - B Type
  //   101 - J Type
  //   110 - I Type
  //   111 - Unknown Type
  //   ADDR2
  //   Core Control Unit
  //   PORT A & B MUX
  //   Function Return Value
  //   Comparitor Unit
  //   branch_opsel
  //   from funct3[14:12]
  //   000 - BEQ
  //   001 - BNE
  //   010 - UNKNOWN
  //   011 - UNKNOWN
  //   100 - BLT
  //   101 - BGE
  //   110 - BLTU
  //   111 - BGEU
  //   WriteAddr
  //   Data Memory/LSU
  //   RISC-V Memory Addresses are 
  //   4 bytes long. The address offsets 
  //   will be incremented in that size 
  //   stepso we pull out that step 
  //   size to pullfrom our data memory
  //   array
  //   STORE
  //   LOAD
  //   load_store_type
  //   0000 - L_B
  //   0001 - L_H
  //   0010 - L_W
  //   0100 - L_BU
  //   0101 - L_HU
  //   1000 - S_B
  //   1001 - S_H
  //   1010 - S_W
  //   1111- LS_N_A
endmodule
