// Digital circuit rv32i_digital.dig as structural Verilog
module rv32i_digital (
  input  clk,
  input  HALT,
  input  in_3,
  input  clk_2,
  input  clk_3,
  input  in_6,
  input  clk_4,
  input  MANUAL,
  input  HALT_2,
  input  [31:0] WriteData,
  input  in_11,
  input  [4:0] in_12,
  input  [4:0] in_13,
  input  [4:0] in_14,
  input  [31:0] in_15,
  input  [2:0] in_16,
  input  [31:0] in_17,
  input  [31:0] in_18,
  input  [31:0] in_19
);

  wire and_1_out, and_2_out, and_3_out, and_4_out, and_5_out, and_6_out, and_7_out, and_8_out, and_9_out,
       and_10_out, and_11_out, and_12_out, and_13_out, and_14_out, and_15_out, and_16_out, and_17_out,
       and_18_out, and_19_out, and_20_out, and_21_out, and_22_out, and_23_out, and_24_out, and_25_out,
       and_26_out, and_27_out, and_28_out, and_29_out, and_30_out, and_31_out, and_32_out, and_33_out, CLOCK,
       comparator_1_eq, comparator_2_eq, comparator_3_eq, comparator_4_eq, comparator_5_eq, comparator_6_eq,
       comparator_7_eq, comparator_7_lt, comparator_8_lt, comparator_9_eq, comparator_10_eq,
       comparator_11_eq, comparator_12_eq, data_memory_write_enable, nCLOCK, not_2_out, not_3_out, not_4_out,
       or_1_out, or_2_out, or_3_out, or_4_out, or_5_out, or_6_out, or_7_out, or_8_out, or_9_out, or_10_out,
       or_11_out, or_12_out, or_14_out, or_15_out, or_16_out, or_17_out, or_18_out, or_19_out, or_20_out,
       or_21_out, or_22_out, or_23_out, or_24_out, or_25_out, or_26_out, or_27_out, or_28_out, or_29_out,
       or_30_out, or_31_out, or_32_out, or_33_out, relaydt_1_p7, relaydt_1_p8, relaydt_2_p2, rs_ff_1_nq,
       rs_ff_1_q, STEP_out;
  wire [0:0] branch_enable;
  wire [2:0] branch_op_sel, notconnected_1_out, notconnected_3_out, notconnected_4_out, notconnected_6_out;
  wire [3:0] alu_op_sel, load_store_type, multiplexer_36_out, multiplexer_38_out, notconnected_2_out,
       notconnected_5_out, notconnected_7_out, notconnected_8_out, notconnected_9_out, notconnected_10_out;
  wire [7:0] ADDR1_0, ADDR1_1, ADDR1_2, ADDR1_3, ADDR2_0, ADDR2_1, ADDR2_2, ADDR2_3, WriteAddr_0,
       WriteAddr_1, WriteAddr_2, WriteAddr_3;
  wire [31:0] a, add_1_s, alu_output, and_34_out, b, B_Type_out, I_Type_out, IMM, J_Type_out,
       multiplexer_1_out, multiplexer_2_out, multiplexer_3_out, multiplexer_4_out, multiplexer_5_out,
       multiplexer_6_out, multiplexer_7_out, multiplexer_8_out, multiplexer_9_out, multiplexer_10_out,
       multiplexer_11_out, multiplexer_12_out, multiplexer_13_out, multiplexer_14_out, multiplexer_15_out,
       multiplexer_16_out, multiplexer_17_out, multiplexer_18_out, multiplexer_19_out, multiplexer_20_out,
       multiplexer_21_out, multiplexer_22_out, multiplexer_23_out, multiplexer_24_out, multiplexer_26_out,
       multiplexer_27_out, multiplexer_28_out, multiplexer_32_out, multiplexer_33_out, multiplexer_34_out,
       multiplexer_35_out, or_34_out, RS1, RS2, S_Type_out, SLL_out, SRA_out, SRL_out, sub_1_s, x00_q, x01_q,
       x02_q, x03_q, x04_q, x05_q, x06_q, x07_q, x08_q, x09_q, x10_q, x11_q, x12_q, x13_q, x14_q, x15_q,
       x16_q, x17_q, x18_q, x19_q, x20_q, x21_q, x22_q, x23_q, x24_q, x25_q, x26_q, x27_q, x28_q, x29_q,
       x30_q, x31_q, xor_1_out;

  and and_1 (and_1_out, data_memory_write_enable, WriteAddr_0[7]);
  and and_2 (and_2_out, data_memory_write_enable, WriteAddr_1[7]);
  and and_3 (and_3_out, data_memory_write_enable, WriteAddr_2[7]);
  Multiplexer #(.Bits(32)) multiplexer_1 (.sel(in_11), .in_0(WriteData), .in_1({32{1'b0}}), .out(multiplexer_1_out));
  or or_1 (or_1_out, in_11, and_1_out);
  Multiplexer #(.Bits(32)) multiplexer_2 (.sel(in_11), .in_0(WriteData), .in_1({32{1'b0}}), .out(multiplexer_2_out));
  or or_2 (or_2_out, in_11, and_2_out);
  Multiplexer #(.Bits(32)) multiplexer_3 (.sel(in_11), .in_0(WriteData), .in_1({32{1'b0}}), .out(multiplexer_3_out));
  or or_3 (or_3_out, in_11, and_3_out);
  and and_4 (and_4_out, data_memory_write_enable, WriteAddr_3[7]);
  Register #(.Bits(32)) x07 (.D(multiplexer_1_out), .C(CLOCK), .en(or_1_out), .Q(x07_q));
  Register #(.Bits(32)) x15 (.D(multiplexer_2_out), .C(CLOCK), .en(or_2_out), .Q(x15_q));
  Multiplexer #(.Bits(32)) multiplexer_4 (.sel(in_11), .in_0(WriteData), .in_1({32{1'b0}}), .out(multiplexer_4_out));
  or or_4 (or_4_out, in_11, and_4_out);
  Register #(.Bits(32)) x23 (.D(multiplexer_3_out), .C(CLOCK), .en(or_3_out), .Q(x23_q));
  Register #(.Bits(32)) x31 (.D(multiplexer_4_out), .C(CLOCK), .en(or_4_out), .Q(x31_q));
  assign RS1 = ADDR1_0[7] ? x07_q : 32'bz;  // Driver driver_1
  assign RS2 = ADDR2_0[7] ? x07_q : 32'bz;  // Driver driver_2
  assign RS1 = ADDR1_1[7] ? x15_q : 32'bz;  // Driver driver_3
  assign RS2 = ADDR2_1[7] ? x15_q : 32'bz;  // Driver driver_4
  assign RS1 = ADDR1_2[7] ? x23_q : 32'bz;  // Driver driver_5
  assign RS2 = ADDR2_2[7] ? x23_q : 32'bz;  // Driver driver_6
  assign RS1 = ADDR1_3[7] ? x31_q : 32'bz;  // Driver driver_7
  assign RS2 = ADDR2_3[7] ? x31_q : 32'bz;  // Driver driver_8
  and and_5 (and_5_out, data_memory_write_enable, WriteAddr_0[6]);
  and and_6 (and_6_out, data_memory_write_enable, WriteAddr_1[6]);
  and and_7 (and_7_out, data_memory_write_enable, WriteAddr_2[6]);
  and and_8 (and_8_out, data_memory_write_enable, WriteAddr_3[6]);
  Multiplexer #(.Bits(32)) multiplexer_5 (.sel(in_11), .in_0(WriteData), .in_1({32{1'b0}}), .out(multiplexer_5_out));
  or or_5 (or_5_out, in_11, and_5_out);
  Multiplexer #(.Bits(32)) multiplexer_6 (.sel(in_11), .in_0(WriteData), .in_1({32{1'b0}}), .out(multiplexer_6_out));
  or or_6 (or_6_out, in_11, and_6_out);
  Multiplexer #(.Bits(32)) multiplexer_7 (.sel(in_11), .in_0(WriteData), .in_1({32{1'b0}}), .out(multiplexer_7_out));
  or or_7 (or_7_out, in_11, and_7_out);
  Multiplexer #(.Bits(32)) multiplexer_8 (.sel(in_11), .in_0(WriteData), .in_1({32{1'b0}}), .out(multiplexer_8_out));
  or or_8 (or_8_out, in_11, and_8_out);
  Register #(.Bits(32)) x06 (.D(multiplexer_5_out), .C(CLOCK), .en(or_5_out), .Q(x06_q));
  Register #(.Bits(32)) x14 (.D(multiplexer_6_out), .C(CLOCK), .en(or_6_out), .Q(x14_q));
  Register #(.Bits(32)) x22 (.D(multiplexer_7_out), .C(CLOCK), .en(or_7_out), .Q(x22_q));
  Register #(.Bits(32)) x30 (.D(multiplexer_8_out), .C(CLOCK), .en(or_8_out), .Q(x30_q));
  // RelayDT #(.poles(2)) relaydt_1: pin names not known; wires that end beside it: in_6, clk_3, clk_2, clk, clk_4, 1'b0, relaydt_1_p7, relaydt_1_p8, in_3, relaydt_1_p7, relaydt_1_p8
  or or_9 (or_9_out, HALT, HALT_2);
  assign RS1 = ADDR1_0[6] ? x06_q : 32'bz;  // Driver driver_9
  assign RS2 = ADDR2_0[6] ? x06_q : 32'bz;  // Driver driver_10
  assign RS1 = ADDR1_1[6] ? x14_q : 32'bz;  // Driver driver_11
  assign RS2 = ADDR2_1[6] ? x14_q : 32'bz;  // Driver driver_12
  // RelayDT relaydt_2: pin names not known; wires that end beside it: 1'b0, relaydt_2_p2
  assign RS1 = ADDR1_2[6] ? x22_q : 32'bz;  // Driver driver_13
  assign RS2 = ADDR2_2[6] ? x22_q : 32'bz;  // Driver driver_14
  assign RS1 = ADDR1_3[6] ? x30_q : 32'bz;  // Driver driver_15
  assign RS2 = ADDR2_3[6] ? x30_q : 32'bz;  // Driver driver_16
  Button STEP (.out(STEP_out));
  and and_9 (and_9_out, data_memory_write_enable, WriteAddr_0[5]);
  and and_10 (and_10_out, data_memory_write_enable, WriteAddr_1[5]);
  and and_11 (and_11_out, data_memory_write_enable, WriteAddr_2[5]);
  and and_12 (and_12_out, STEP_out, MANUAL, ~or_9_out);  // And
  RS_FF rs_ff_1 (.S(and_13_out), .C(relaydt_2_p2), .R(~and_13_out), .Q(rs_ff_1_q), .nQ(rs_ff_1_nq));
  and and_13 (and_13_out, ~MANUAL, ~or_9_out, rs_ff_1_nq);  // And
  Multiplexer #(.Bits(32)) multiplexer_9 (.sel(in_11), .in_0(WriteData), .in_1({32{1'b0}}), .out(multiplexer_9_out));
  or or_10 (or_10_out, in_11, and_9_out);
  Multiplexer #(.Bits(32)) multiplexer_10 (.sel(in_11), .in_0(WriteData), .in_1({32{1'b0}}), .out(multiplexer_10_out));
  or or_11 (or_11_out, in_11, and_10_out);
  Multiplexer #(.Bits(32)) multiplexer_11 (.sel(in_11), .in_0(WriteData), .in_1({32{1'b0}}), .out(multiplexer_11_out));
  or or_12 (or_12_out, in_11, and_11_out);
  and and_14 (and_14_out, data_memory_write_enable, WriteAddr_3[5]);
  or or_13 (CLOCK, and_12_out, rs_ff_1_q);
  Register #(.Bits(32)) x05 (.D(multiplexer_9_out), .C(CLOCK), .en(or_10_out), .Q(x05_q));
  Register #(.Bits(32)) x13 (.D(multiplexer_10_out), .C(CLOCK), .en(or_11_out), .Q(x13_q));
  Multiplexer #(.Bits(32)) multiplexer_12 (.sel(in_11), .in_0(WriteData), .in_1({32{1'b0}}), .out(multiplexer_12_out));
  or or_14 (or_14_out, in_11, and_14_out);
  not not_1 (nCLOCK, CLOCK);
  Register #(.Bits(32)) x21 (.D(multiplexer_11_out), .C(CLOCK), .en(or_12_out), .Q(x21_q));
  Register #(.Bits(32)) x29 (.D(multiplexer_12_out), .C(CLOCK), .en(or_14_out), .Q(x29_q));
  LED led_1 (.in(CLOCK));
  LED led_2 (.in(nCLOCK));
  assign RS1 = ADDR1_0[5] ? x05_q : 32'bz;  // Driver driver_17
  assign RS2 = ADDR2_0[5] ? x05_q : 32'bz;  // Driver driver_18
  assign RS1 = ADDR1_1[5] ? x13_q : 32'bz;  // Driver driver_19
  assign RS2 = ADDR2_1[5] ? x13_q : 32'bz;  // Driver driver_20
  assign RS1 = ADDR1_2[5] ? x21_q : 32'bz;  // Driver driver_21
  assign RS2 = ADDR2_2[5] ? x21_q : 32'bz;  // Driver driver_22
  assign RS1 = ADDR1_3[5] ? x29_q : 32'bz;  // Driver driver_23
  assign RS2 = ADDR2_3[5] ? x29_q : 32'bz;  // Driver driver_24
  Demultiplexer #(.Selector_Bits(5)) demultiplexer_1 (
    .sel(in_12), .in(1'b1), .out_0(ADDR1_0[0]), .out_1(ADDR1_0[1]), .out_2(ADDR1_0[2]), .out_3(ADDR1_0[3]),
    .out_4(ADDR1_0[4]), .out_5(ADDR1_0[5]), .out_6(ADDR1_0[6]), .out_7(ADDR1_0[7]), .out_8(ADDR1_1[0]),
    .out_9(ADDR1_1[1]), .out_10(ADDR1_1[2]), .out_11(ADDR1_1[3]), .out_12(ADDR1_1[4]), .out_13(ADDR1_1[5]),
    .out_14(ADDR1_1[6]), .out_15(ADDR1_1[7]), .out_16(ADDR1_2[0]), .out_17(ADDR1_2[1]), .out_18(ADDR1_2[2]),
    .out_19(ADDR1_2[3]), .out_20(ADDR1_2[4]), .out_21(ADDR1_2[5]), .out_22(ADDR1_2[6]), .out_23(ADDR1_2[7]),
    .out_24(ADDR1_3[0]), .out_25(ADDR1_3[1]), .out_26(ADDR1_3[2]), .out_27(ADDR1_3[3]), .out_28(ADDR1_3[4]),
    .out_29(ADDR1_3[5]), .out_30(ADDR1_3[6]), .out_31(ADDR1_3[7]));
  and and_15 (and_15_out, data_memory_write_enable, WriteAddr_0[4]);
  and and_16 (and_16_out, data_memory_write_enable, WriteAddr_1[4]);
  and and_17 (and_17_out, data_memory_write_enable, WriteAddr_2[4]);
  and and_18 (and_18_out, data_memory_write_enable, WriteAddr_3[4]);
  Multiplexer #(.Bits(32)) multiplexer_13 (.sel(in_11), .in_0(WriteData), .in_1({32{1'b0}}), .out(multiplexer_13_out));
  or or_15 (or_15_out, in_11, and_15_out);
  Multiplexer #(.Bits(32)) multiplexer_14 (.sel(in_11), .in_0(WriteData), .in_1({32{1'b0}}), .out(multiplexer_14_out));
  or or_16 (or_16_out, in_11, and_16_out);
  Multiplexer #(.Bits(32)) multiplexer_15 (.sel(in_11), .in_0(WriteData), .in_1({32{1'b0}}), .out(multiplexer_15_out));
  or or_17 (or_17_out, in_11, and_17_out);
  Multiplexer #(.Bits(32)) multiplexer_16 (.sel(in_11), .in_0(WriteData), .in_1({32{1'b0}}), .out(multiplexer_16_out));
  or or_18 (or_18_out, in_11, and_18_out);
  Register #(.Bits(32)) x04 (.D(multiplexer_13_out), .C(CLOCK), .en(or_15_out), .Q(x04_q));
  Register #(.Bits(32)) x12 (.D(multiplexer_14_out), .C(CLOCK), .en(or_16_out), .Q(x12_q));
  Register #(.Bits(32)) x20 (.D(multiplexer_15_out), .C(CLOCK), .en(or_17_out), .Q(x20_q));
  Register #(.Bits(32)) x28 (.D(multiplexer_16_out), .C(CLOCK), .en(or_18_out), .Q(x28_q));
  assign RS1 = ADDR1_0[4] ? x04_q : 32'bz;  // Driver driver_25
  assign RS2 = ADDR2_0[4] ? x04_q : 32'bz;  // Driver driver_26
  assign RS1 = ADDR1_1[4] ? x12_q : 32'bz;  // Driver driver_27
  assign RS2 = ADDR2_1[4] ? x12_q : 32'bz;  // Driver driver_28
  assign RS1 = ADDR1_2[4] ? x20_q : 32'bz;  // Driver driver_29
  assign RS2 = ADDR2_2[4] ? x20_q : 32'bz;  // Driver driver_30
  assign RS1 = ADDR1_3[4] ? x28_q : 32'bz;  // Driver driver_31
  assign RS2 = ADDR2_3[4] ? x28_q : 32'bz;  // Driver driver_32
  and and_19 (and_19_out, data_memory_write_enable, WriteAddr_0[3]);
  and and_20 (and_20_out, data_memory_write_enable, WriteAddr_1[3]);
  and and_21 (and_21_out, data_memory_write_enable, WriteAddr_2[3]);
  Multiplexer #(.Bits(32)) multiplexer_17 (.sel(in_11), .in_0(WriteData), .in_1({32{1'b0}}), .out(multiplexer_17_out));
  or or_19 (or_19_out, in_11, and_19_out);
  Multiplexer #(.Bits(32)) multiplexer_18 (.sel(in_11), .in_0(WriteData), .in_1({32{1'b0}}), .out(multiplexer_18_out));
  or or_20 (or_20_out, in_11, and_20_out);
  Multiplexer #(.Bits(32)) multiplexer_19 (.sel(in_11), .in_0(WriteData), .in_1({32{1'b0}}), .out(multiplexer_19_out));
  or or_21 (or_21_out, in_11, and_21_out);
  and and_22 (and_22_out, data_memory_write_enable, WriteAddr_3[3]);
  Demultiplexer #(.Selector_Bits(5)) demultiplexer_2 (
    .sel(in_13), .in(1'b1), .out_0(ADDR2_0[0]), .out_1(ADDR2_0[1]), .out_2(ADDR2_0[2]), .out_3(ADDR2_0[3]),
    .out_4(ADDR2_0[4]), .out_5(ADDR2_0[5]), .out_6(ADDR2_0[6]), .out_7(ADDR2_0[7]), .out_8(ADDR2_1[0]),
    .out_9(ADDR2_1[1]), .out_10(ADDR2_1[2]), .out_11(ADDR2_1[3]), .out_12(ADDR2_1[4]), .out_13(ADDR2_1[5]),
    .out_14(ADDR2_1[6]), .out_15(ADDR2_1[7]), .out_16(ADDR2_2[0]), .out_17(ADDR2_2[1]), .out_18(ADDR2_2[2]),
    .out_19(ADDR2_2[3]), .out_20(ADDR2_2[4]), .out_21(ADDR2_2[5]), .out_22(ADDR2_2[6]), .out_23(ADDR2_2[7]),
    .out_24(ADDR2_3[0]), .out_25(ADDR2_3[1]), .out_26(ADDR2_3[2]), .out_27(ADDR2_3[3]), .out_28(ADDR2_3[4]),
    .out_29(ADDR2_3[5]), .out_30(ADDR2_3[6]), .out_31(ADDR2_3[7]));
  Register #(.Bits(32)) x03 (.D(multiplexer_17_out), .C(CLOCK), .en(or_19_out), .Q(x03_q));
  Register #(.Bits(32)) x11 (.D(multiplexer_18_out), .C(CLOCK), .en(or_20_out), .Q(x11_q));
  Multiplexer #(.Bits(32)) multiplexer_20 (.sel(in_11), .in_0(WriteData), .in_1({32{1'b0}}), .out(multiplexer_20_out));
  or or_22 (or_22_out, in_11, and_22_out);
  Register #(.Bits(32)) x19 (.D(multiplexer_19_out), .C(CLOCK), .en(or_21_out), .Q(x19_q));
  Register #(.Bits(32)) x27 (.D(multiplexer_20_out), .C(CLOCK), .en(or_22_out), .Q(x27_q));
  BitExtender #(.inputBits(12), .outputBits(32)) S_Type (.in({in_15[31:25], in_15[11:7]}), .out(S_Type_out));
  assign RS1 = ADDR1_0[3] ? x03_q : 32'bz;  // Driver driver_33
  assign RS2 = ADDR2_0[3] ? x03_q : 32'bz;  // Driver driver_34
  assign RS1 = ADDR1_1[3] ? x11_q : 32'bz;  // Driver driver_35
  assign RS2 = ADDR2_1[3] ? x11_q : 32'bz;  // Driver driver_36
  assign RS1 = ADDR1_2[3] ? x19_q : 32'bz;  // Driver driver_37
  assign RS2 = ADDR2_2[3] ? x19_q : 32'bz;  // Driver driver_38
  assign RS1 = ADDR1_3[3] ? x27_q : 32'bz;  // Driver driver_39
  assign RS2 = ADDR2_3[3] ? x27_q : 32'bz;  // Driver driver_40
  BitExtender #(.inputBits(13), .outputBits(32)) B_Type (
    .in({in_15[31], in_15[7], in_15[30:25], in_15[11:8], 1'b0}), .out(B_Type_out));
  BitExtender #(.inputBits(21), .outputBits(32)) J_Type (
    .in({in_15[31], in_15[19:12], in_15[20], in_15[30:21], 1'b0}), .out(J_Type_out));
  BitExtender #(.inputBits(12), .outputBits(32)) I_Type (.in(in_15[31:20]), .out(I_Type_out));
  and and_23 (and_23_out, data_memory_write_enable, WriteAddr_0[2]);
  and and_24 (and_24_out, data_memory_write_enable, WriteAddr_1[2]);
  and and_25 (and_25_out, data_memory_write_enable, WriteAddr_2[2]);
  and and_26 (and_26_out, data_memory_write_enable, WriteAddr_3[2]);
  Multiplexer #(.Bits(32)) multiplexer_21 (.sel(in_11), .in_0(WriteData), .in_1({32{1'b0}}), .out(multiplexer_21_out));
  or or_23 (or_23_out, in_11, and_23_out);
  Multiplexer #(.Bits(32)) multiplexer_22 (.sel(in_11), .in_0(WriteData), .in_1({32{1'b0}}), .out(multiplexer_22_out));
  or or_24 (or_24_out, in_11, and_24_out);
  Multiplexer #(.Bits(32)) multiplexer_23 (.sel(in_11), .in_0(WriteData), .in_1({32{1'b0}}), .out(multiplexer_23_out));
  or or_25 (or_25_out, in_11, and_25_out);
  Multiplexer #(.Bits(32)) multiplexer_24 (.sel(in_11), .in_0(WriteData), .in_1({32{1'b0}}), .out(multiplexer_24_out));
  or or_26 (or_26_out, in_11, and_26_out);
  Multiplexer #(.Selector_Bits(3), .Bits(32)) multiplexer_25 (
    .sel(in_16), .in_0(S_Type_out), .in_1({32{1'b0}}), .in_2({in_15[31:12], {12{1'b0}}}), .in_3({32{1'b0}}),
    .in_4(B_Type_out), .in_5(J_Type_out), .in_6(I_Type_out), .in_7({32{1'b0}}), .out(IMM));
  Register #(.Bits(32)) x02 (.D(multiplexer_21_out), .C(CLOCK), .en(or_23_out), .Q(x02_q));
  Register #(.Bits(32)) x10 (.D(multiplexer_22_out), .C(CLOCK), .en(or_24_out), .Q(x10_q));
  Register #(.Bits(32)) x18 (.D(multiplexer_23_out), .C(CLOCK), .en(or_25_out), .Q(x18_q));
  Register #(.Bits(32)) x26 (.D(multiplexer_24_out), .C(CLOCK), .en(or_26_out), .Q(x26_q));
  assign RS1 = ADDR1_0[2] ? x02_q : 32'bz;  // Driver driver_41
  assign RS2 = ADDR2_0[2] ? x02_q : 32'bz;  // Driver driver_42
  assign RS1 = ADDR1_1[2] ? x10_q : 32'bz;  // Driver driver_43
  assign RS2 = ADDR2_1[2] ? x10_q : 32'bz;  // Driver driver_44
  assign RS1 = ADDR1_2[2] ? x18_q : 32'bz;  // Driver driver_45
  assign RS2 = ADDR2_2[2] ? x18_q : 32'bz;  // Driver driver_46
  assign RS1 = ADDR1_3[2] ? x26_q : 32'bz;  // Driver driver_47
  assign RS2 = ADDR2_3[2] ? x26_q : 32'bz;  // Driver driver_48
  Demultiplexer #(.Selector_Bits(5)) demultiplexer_3 (
    .sel(in_14), .in(1'b1), .out_0(WriteAddr_0[0]), .out_1(WriteAddr_0[1]), .out_2(WriteAddr_0[2]),
    .out_3(WriteAddr_0[3]), .out_4(WriteAddr_0[4]), .out_5(WriteAddr_0[5]), .out_6(WriteAddr_0[6]),
    .out_7(WriteAddr_0[7]), .out_8(WriteAddr_1[0]), .out_9(WriteAddr_1[1]), .out_10(WriteAddr_1[2]),
    .out_11(WriteAddr_1[3]), .out_12(WriteAddr_1[4]), .out_13(WriteAddr_1[5]), .out_14(WriteAddr_1[6]),
    .out_15(WriteAddr_1[7]), .out_16(WriteAddr_2[0]), .out_17(WriteAddr_2[1]), .out_18(WriteAddr_2[2]),
    .out_19(WriteAddr_2[3]), .out_20(WriteAddr_2[4]), .out_21(WriteAddr_2[5]), .out_22(WriteAddr_2[6]),
    .out_23(WriteAddr_2[7]), .out_24(WriteAddr_3[0]), .out_25(WriteAddr_3[1]), .out_26(WriteAddr_3[2]),
    .out_27(WriteAddr_3[3]), .out_28(WriteAddr_3[4]), .out_29(WriteAddr_3[5]), .out_30(WriteAddr_3[6]),
    .out_31(WriteAddr_3[7]));
  and and_27 (and_27_out, data_memory_write_enable, WriteAddr_0[1]);
  and and_28 (and_28_out, data_memory_write_enable, WriteAddr_1[1]);
  and and_29 (and_29_out, data_memory_write_enable, WriteAddr_2[1]);
  Multiplexer #(.Bits(32)) multiplexer_26 (.sel(in_11), .in_0(WriteData), .in_1({32{1'b0}}), .out(multiplexer_26_out));
  or or_27 (or_27_out, in_11, and_27_out);
  Multiplexer #(.Bits(32)) multiplexer_27 (.sel(in_11), .in_0(WriteData), .in_1({32{1'b0}}), .out(multiplexer_27_out));
  or or_28 (or_28_out, in_11, and_28_out);
  Multiplexer #(.Bits(32)) multiplexer_28 (.sel(in_11), .in_0(WriteData), .in_1({32{1'b0}}), .out(multiplexer_28_out));
  or or_29 (or_29_out, in_11, and_29_out);
  and and_30 (and_30_out, data_memory_write_enable, WriteAddr_3[1]);
  Multiplexer #(.Bits(32)) multiplexer_29 (.sel(data_memory_write_enable), .in_0(in_17), .in_1(RS1), .out(a));
  Multiplexer #(.Bits(32)) multiplexer_30 (.sel(data_memory_write_enable), .in_0(IMM), .in_1(RS2), .out(b));
  Multiplexer #(.Selector_Bits(3), .Bits(32)) multiplexer_31 (
    .sel(branch_op_sel), .in_0(in_19), .in_1(alu_output), .in_2({{31{1'b0}}, branch_enable[0]}), .in_3(IMM),
    .in_4(in_18), .in_5({32{1'b0}}), .in_6({32{1'b0}}), .in_7({32{1'b0}}), .out(WriteData));
  Register #(.Bits(32)) x01 (.D(multiplexer_26_out), .C(CLOCK), .en(or_27_out), .Q(x01_q));
  Register #(.Bits(32)) x09 (.D(multiplexer_27_out), .C(CLOCK), .en(or_28_out), .Q(x09_q));
  Multiplexer #(.Bits(32)) multiplexer_32 (.sel(in_11), .in_0(WriteData), .in_1({32{1'b0}}), .out(multiplexer_32_out));
  or or_30 (or_30_out, in_11, and_30_out);
  Register #(.Bits(32)) x17 (.D(multiplexer_28_out), .C(CLOCK), .en(or_29_out), .Q(x17_q));
  Register #(.Bits(32)) x25 (.D(multiplexer_32_out), .C(CLOCK), .en(or_30_out), .Q(x25_q));
  assign RS1 = ADDR1_0[1] ? x01_q : 32'bz;  // Driver driver_49
  assign RS2 = ADDR2_0[1] ? x01_q : 32'bz;  // Driver driver_50
  assign RS1 = ADDR1_1[1] ? x09_q : 32'bz;  // Driver driver_51
  assign RS2 = ADDR2_1[1] ? x09_q : 32'bz;  // Driver driver_52
  assign RS1 = ADDR1_2[1] ? x17_q : 32'bz;  // Driver driver_53
  assign RS2 = ADDR2_2[1] ? x17_q : 32'bz;  // Driver driver_54
  assign RS1 = ADDR1_3[1] ? x25_q : 32'bz;  // Driver driver_55
  assign RS2 = ADDR2_3[1] ? x25_q : 32'bz;  // Driver driver_56
  and and_31 (and_31_out, data_memory_write_enable, WriteAddr_1[0]);
  and and_32 (and_32_out, data_memory_write_enable, WriteAddr_2[0]);
  and and_33 (and_33_out, data_memory_write_enable, WriteAddr_3[0]);
  Multiplexer #(.Bits(32)) multiplexer_33 (.sel(in_11), .in_0(WriteData), .in_1({32{1'b0}}), .out(multiplexer_33_out));
  or or_31 (or_31_out, in_11, and_31_out);
  Multiplexer #(.Bits(32)) multiplexer_34 (.sel(in_11), .in_0(WriteData), .in_1({32{1'b0}}), .out(multiplexer_34_out));
  or or_32 (or_32_out, in_11, and_32_out);
  Multiplexer #(.Bits(32)) multiplexer_35 (.sel(in_11), .in_0(WriteData), .in_1({32{1'b0}}), .out(multiplexer_35_out));
  or or_33 (or_33_out, in_11, and_33_out);
  Register #(.Bits(32)) x00 (.D({32{1'b0}}), .C(CLOCK), .en(1'b0), .Q(x00_q));
  Register #(.Bits(32)) x08 (.D(multiplexer_33_out), .C(CLOCK), .en(or_31_out), .Q(x08_q));
  Register #(.Bits(32)) x16 (.D(multiplexer_34_out), .C(CLOCK), .en(or_32_out), .Q(x16_q));
  Register #(.Bits(32)) x24 (.D(multiplexer_35_out), .C(CLOCK), .en(or_33_out), .Q(x24_q));
  assign RS1 = ADDR1_0[0] ? x00_q : 32'bz;  // Driver driver_57
  assign RS2 = ADDR2_0[0] ? x00_q : 32'bz;  // Driver driver_58
  assign RS1 = ADDR1_1[0] ? x08_q : 32'bz;  // Driver driver_59
  assign RS2 = ADDR2_1[0] ? x08_q : 32'bz;  // Driver driver_60
  assign RS1 = ADDR1_2[0] ? x16_q : 32'bz;  // Driver driver_61
  assign RS2 = ADDR2_2[0] ? x16_q : 32'bz;  // Driver driver_62
  assign RS1 = ADDR1_3[0] ? x24_q : 32'bz;  // Driver driver_63
  assign RS2 = ADDR2_3[0] ? x24_q : 32'bz;  // Driver driver_64
  Seven_Seg_Hex seven_seg_hex_1 (.d(RS1[31:28]), .dp(1'b0));
  Seven_Seg_Hex seven_seg_hex_2 (.d(RS2[31:28]), .dp(1'b0));
  Seven_Seg_Hex seven_seg_hex_3 (.d(RS1[27:24]), .dp(1'b0));
  Seven_Seg_Hex seven_seg_hex_4 (.d(RS2[27:24]), .dp(1'b0));
  Comparator #(.Bits(7)) comparator_1 (.a(7'b0110011), .b(in_15[6:0]), .eq(comparator_1_eq));  // open: gt, lt
  Comparator #(.Bits(7)) comparator_2 (.a(7'b1100011), .b(in_15[6:0]), .eq(comparator_2_eq));  // open: gt, lt
  Seven_Seg_Hex seven_seg_hex_5 (.d(RS1[23:20]), .dp(1'b0));
  Seven_Seg_Hex seven_seg_hex_6 (.d(RS2[23:20]), .dp(1'b0));
  assign alu_op_sel = comparator_1_eq ? {in_15[30], in_15[14:12]} : 4'bz;  // Driver driver_65
  assign branch_op_sel = comparator_2_eq ? in_15[14:12] : 3'bz;  // Driver driver_66
  Seven_Seg_Hex seven_seg_hex_7 (.d(RS1[19:16]), .dp(1'b0));
  Seven_Seg_Hex seven_seg_hex_8 (.d(RS2[19:16]), .dp(1'b0));
  assign data_memory_write_enable = comparator_1_eq ? 1'b1 : 1'bz;  // Driver driver_67
  assign data_memory_write_enable = comparator_1_eq ? 1'b0 : 1'bz;  // Driver driver_68
  assign branch_op_sel = comparator_1_eq ? 3'b001 : 3'bz;  // Driver driver_69
  assign load_store_type = comparator_1_eq ? 4'b1100 : 4'bz;  // Driver driver_70
  assign data_memory_write_enable = comparator_2_eq ? 1'b0 : 1'bz;  // Driver driver_71
  assign data_memory_write_enable = comparator_2_eq ? branch_enable[0] : 1'bz;  // Driver driver_72
  // NotConnected on notconnected_1_out
  Seven_Seg_Hex seven_seg_hex_9 (.d(RS1[15:12]), .dp(1'b0));
  Seven_Seg_Hex seven_seg_hex_10 (.d(RS2[15:12]), .dp(1'b0));
  assign branch_op_sel = comparator_2_eq ? notconnected_1_out : 3'bz;  // Driver driver_73
  assign load_store_type = comparator_2_eq ? 4'b1100 : 4'bz;  // Driver driver_74
  Seven_Seg_Hex seven_seg_hex_11 (.d(RS1[11:8]), .dp(1'b0));
  Seven_Seg_Hex seven_seg_hex_12 (.d(RS2[11:8]), .dp(1'b0));
  Seven_Seg_Hex seven_seg_hex_13 (.d(RS1[7:4]), .dp(1'b0));
  Seven_Seg_Hex seven_seg_hex_14 (.d(RS2[7:4]), .dp(1'b0));
  Seven_Seg_Hex seven_seg_hex_15 (.d(RS1[3:0]), .dp(1'b0));
  Seven_Seg_Hex seven_seg_hex_16 (.d(RS2[3:0]), .dp(1'b0));
  Comparator #(.Bits(7)) comparator_3 (.a(7'b0100011), .b(in_15[6:0]), .eq(comparator_3_eq));  // open: gt, lt
  // NotConnected on notconnected_2_out
  Comparator #(.Bits(7)) comparator_4 (.a(7'b1100111), .b(in_15[6:0]), .eq(comparator_4_eq));  // open: gt, lt
  Multiplexer #(.Selector_Bits(3), .Bits(4)) multiplexer_36 (
    .sel(in_15[14:12]), .in_0(4'b1010), .in_1(4'b1001), .in_2(4'b1000), .in_3(notconnected_2_out),
    .in_4(notconnected_2_out), .in_5(notconnected_2_out), .in_6(notconnected_2_out),
    .in_7(notconnected_2_out), .out(multiplexer_36_out));
  Seven_Seg_Hex seven_seg_hex_17 (.d(alu_output[31:28]), .dp(1'b0));
  assign data_memory_write_enable = comparator_3_eq ? 1'b0 : 1'bz;  // Driver driver_75
  assign data_memory_write_enable = comparator_3_eq ? 1'b1 : 1'bz;  // Driver driver_76
  assign alu_op_sel = comparator_3_eq ? 4'b0000 : 4'bz;  // Driver driver_77
  // NotConnected on notconnected_3_out
  assign data_memory_write_enable = comparator_4_eq ? 1'b0 : 1'bz;  // Driver driver_78
  assign data_memory_write_enable = comparator_4_eq ? 1'b1 : 1'bz;  // Driver driver_79
  Seven_Seg_Hex seven_seg_hex_18 (.d(alu_output[27:24]), .dp(1'b0));
  assign branch_op_sel = comparator_3_eq ? notconnected_3_out : 3'bz;  // Driver driver_80
  assign load_store_type = comparator_3_eq ? multiplexer_36_out : 4'bz;  // Driver driver_81
  assign branch_op_sel = comparator_4_eq ? 3'b100 : 3'bz;  // Driver driver_82
  assign load_store_type = comparator_4_eq ? 4'b1100 : 4'bz;  // Driver driver_83
  assign alu_op_sel = comparator_4_eq ? 4'b0000 : 4'bz;  // Driver driver_84
  Add #(.Bits(32)) add_1 (.a(a), .b(b), .c_i(1'b0), .s(add_1_s));  // open: c_o
  Sub #(.Bits(32)) sub_1 (.a(a), .b(b), .c_i(1'b0), .s(sub_1_s));  // open: c_o
  BarrelShifter #(.Bits(32)) SLL (.in(a), .shift(b[5:0]), .out(SLL_out));
  assign xor_1_out = a ^ b;  // XOr xor_1, 32 bits wide
  BarrelShifter #(.Bits(32), .direction("right")) SRL (.in(a), .shift(b[5:0]), .out(SRL_out));
  BarrelShifter #(.Bits(32), .barrelShifterMode("arithmetic"), .direction("right")) SRA (
    .in(a), .shift(b[5:0]), .out(SRA_out));
  assign or_34_out = a | b;  // Or or_34, 32 bits wide
  assign and_34_out = a & b;  // And and_34, 32 bits wide
  Seven_Seg_Hex seven_seg_hex_19 (.d(alu_output[23:20]), .dp(1'b0));
  Seven_Seg_Hex seven_seg_hex_20 (.d(alu_output[19:16]), .dp(1'b0));
  Seven_Seg_Hex seven_seg_hex_21 (.d(alu_output[15:12]), .dp(1'b0));
  Multiplexer #(.Selector_Bits(4), .Bits(32)) multiplexer_37 (
    .sel(alu_op_sel), .in_0(add_1_s), .in_1(SLL_out), .in_2({32{1'b0}}), .in_3({32{1'b0}}), .in_4(xor_1_out),
    .in_5(SRL_out), .in_6(or_34_out), .in_7(and_34_out), .in_8(sub_1_s), .in_9({32{1'b0}}),
    .in_10({32{1'b0}}), .in_11({32{1'b0}}), .in_12({32{1'b0}}), .in_13(SRA_out), .in_14({32{1'b0}}),
    .in_15({32{1'b0}}), .out(alu_output));
  Seven_Seg_Hex seven_seg_hex_22 (.d(alu_output[11:8]), .dp(1'b0));
  Comparator #(.Bits(7)) comparator_5 (.a(7'b0100011), .b(in_15[6:0]), .eq(comparator_5_eq));  // open: gt, lt
  Comparator #(.Bits(7)) comparator_6 (.a(7'b0001111), .b(in_15[6:0]), .eq(comparator_6_eq));  // open: gt, lt
  Seven_Seg_Hex seven_seg_hex_23 (.d(alu_output[7:4]), .dp(1'b0));
  Multiplexer #(.Selector_Bits(3), .Bits(4)) multiplexer_38 (
    .sel(in_15[14:12]), .in_0(4'b0011), .in_1(4'b0001), .in_2(4'b0000), .in_3(4'b0000), .in_4(4'b0100),
    .in_5(4'b0010), .in_6(4'b0000), .in_7(4'b0000), .out(multiplexer_38_out));
  Seven_Seg_Hex seven_seg_hex_24 (.d(alu_output[3:0]), .dp(1'b0));
  assign data_memory_write_enable = comparator_5_eq ? 1'b0 : 1'bz;  // Driver driver_85
  assign data_memory_write_enable = comparator_5_eq ? 1'b1 : 1'bz;  // Driver driver_86
  assign alu_op_sel = comparator_5_eq ? 4'b0000 : 4'bz;  // Driver driver_87
  assign data_memory_write_enable = comparator_6_eq ? 1'b0 : 1'bz;  // Driver driver_88
  assign data_memory_write_enable = comparator_6_eq ? 1'b1 : 1'bz;  // Driver driver_89
  assign branch_op_sel = comparator_6_eq ? notconnected_4_out : 3'bz;  // Driver driver_90
  // NotConnected on notconnected_4_out
  assign load_store_type = comparator_6_eq ? notconnected_5_out : 4'bz;  // Driver driver_91
  // NotConnected on notconnected_5_out
  assign branch_op_sel = comparator_5_eq ? 3'b000 : 3'bz;  // Driver driver_92
  assign load_store_type = comparator_5_eq ? multiplexer_38_out : 4'bz;  // Driver driver_93
  Seven_Seg_Hex seven_seg_hex_25 (.d(4'b0000), .dp(1'b0));
  Comparator #(.Bits(32)) comparator_7 (.a(a), .b(b), .eq(comparator_7_eq), .lt(comparator_7_lt));  // open: gt
  Comparator #(.Signed("true"), .Bits(32)) comparator_8 (.a(a), .b(b), .lt(comparator_8_lt));  // open: gt, eq
  Seven_Seg_Hex seven_seg_hex_26 (.d(4'b0000), .dp(1'b0));
  Comparator #(.Bits(7)) comparator_9 (.a(7'b1110011), .b(in_15[6:0]), .eq(comparator_9_eq));  // open: gt, lt
  not not_2 (not_2_out, comparator_7_eq);
  not not_3 (not_3_out, comparator_7_lt);
  not not_4 (not_4_out, comparator_8_lt);
  Seven_Seg_Hex seven_seg_hex_27 (.d(4'b0000), .dp(1'b0));
  Multiplexer #(.Selector_Bits(3)) multiplexer_39 (
    .sel(branch_op_sel), .in_0(comparator_7_eq), .in_1(not_2_out), .in_2(1'b0), .in_3(1'b0),
    .in_4(comparator_8_lt), .in_5(not_4_out), .in_6(comparator_7_lt), .in_7(not_3_out), .out(branch_enable[0]));
  Seven_Seg_Hex seven_seg_hex_28 (.d(4'b0000), .dp(1'b0));
  assign data_memory_write_enable = comparator_9_eq ? 1'b0 : 1'bz;  // Driver driver_94
  assign data_memory_write_enable = comparator_9_eq ? 1'b1 : 1'bz;  // Driver driver_95
  assign branch_op_sel = comparator_9_eq ? notconnected_6_out : 3'bz;  // Driver driver_96
  // NotConnected on notconnected_6_out
  assign load_store_type = comparator_9_eq ? notconnected_7_out : 4'bz;  // Driver driver_97
  // NotConnected on notconnected_7_out
  Seven_Seg_Hex seven_seg_hex_29 (.d(4'b0000), .dp(1'b0));
  Seven_Seg_Hex seven_seg_hex_30 (.d(4'b0000), .dp(1'b0));
  Seven_Seg_Hex seven_seg_hex_31 (.d(4'b0000), .dp(1'b0));
  Seven_Seg_Hex seven_seg_hex_32 (.d({3'b000, branch_enable[0]}), .dp(1'b0));
  Comparator #(.Bits(7)) comparator_10 (.a(7'b0110111), .b(in_15[6:0]), .eq(comparator_10_eq));  // open: gt, lt
  assign data_memory_write_enable = comparator_10_eq ? 1'b0 : 1'bz;  // Driver driver_98
  assign data_memory_write_enable = comparator_10_eq ? 1'b1 : 1'bz;  // Driver driver_99
  // NotConnected on notconnected_8_out
  assign branch_op_sel = comparator_10_eq ? 3'b011 : 3'bz;  // Driver driver_100
  assign load_store_type = comparator_10_eq ? notconnected_8_out : 4'bz;  // Driver driver_101
  Comparator #(.Bits(7)) comparator_11 (.a(7'b0010111), .b(in_15[6:0]), .eq(comparator_11_eq));  // open: gt, lt
  // NotConnected on notconnected_9_out
  assign data_memory_write_enable = comparator_11_eq ? 1'b0 : 1'bz;  // Driver driver_102
  assign data_memory_write_enable = comparator_11_eq ? 1'b1 : 1'bz;  // Driver driver_103
  assign branch_op_sel = comparator_11_eq ? 3'b001 : 3'bz;  // Driver driver_104
  assign load_store_type = comparator_11_eq ? notconnected_9_out : 4'bz;  // Driver driver_105
  assign alu_op_sel = comparator_11_eq ? 4'b0000 : 4'bz;  // Driver driver_106
  Comparator #(.Bits(7)) comparator_12 (.a(7'b1101111), .b(in_15[6:0]), .eq(comparator_12_eq));  // open: gt, lt
  assign data_memory_write_enable = comparator_12_eq ? 1'b0 : 1'bz;  // Driver driver_107
  assign data_memory_write_enable = comparator_12_eq ? 1'b1 : 1'bz;  // Driver driver_108
  assign branch_op_sel = comparator_12_eq ? 3'b100 : 3'bz;  // Driver driver_109
  assign load_store_type = comparator_12_eq ? notconnected_10_out : 4'bz;  // Driver driver_110
  // NotConnected on notconnected_10_out
  assign alu_op_sel = comparator_12_eq ? 4'b0000 : 4'bz;  // Driver driver_111

  // Other names for the same wires on the sheet: dmem_data[31:0] = in_19; HALT_t = HALT_2; imm_set[2:0] = in_16;
  //   INSTRUCTION[31:0] = in_15; PC[31:0] = in_17; pc_next[31:0] = in_18; reg_write_data_sel[2:0] = branch_op_sel;
  //   execute_port_a_sel = data_memory_write_enable; execute_port_b_sel = data_memory_write_enable;
  //   pc_mux_sel = data_memory_write_enable; reg_write_enable = data_memory_write_enable; RESET = in_11;
  //   write_data[31:0] = WriteData

  // Notes on the sheet:
  //   clk: Hz: 8
  //   clk_2: Hz: 16
  //   clk_3: Hz: 64
  //   clk_4: Hz: 2
  //   MANUAL: default 1
  //   Register File
  //   CLOCK
  //   ADDR1
  //   ADDR2
  //   Imm Sign Extend
  //   WriteAddr
  //   oppcode [6][4][3]
  //   000 - S Type
  //   001 - 
  //   010 - U Type
  //   011 - 
  //   100 - B Type
  //   101 - J Type
  //   110 - I Type
  //   111 -
  //   MUX A & B & RD
  //   RD MUX
  //   000 -  dmem_data
  //   001 - alu_output
  //   010 - branch_enable
  //   011 - immediate
  //   100 - pc_next
  //   OP_R_TYPE
  //   OP_B_TYPE
  //   TODO:
  //   I_ALU_TYPE
  //   OP_S_TYPE
  //   OP_I_JALR_TYPE
  //   ALU
  //   OP_I_LOAD_TYPE
  //   OP_I_FENCE_TYPE
  //   funct7[30]funct3[14:12]
  //   0000 - ADD
  //   0001 - SLL
  //   0100 - XOR
  //   0101 - SRL
  //   0110 - OR
  //   0111 - AND
  //   1000 - SUB
  //   1101 - SRA
  //   1111 - UNKNOWN
  //   CU
  //   funct3[14:12]
  //   000 - BEQ
  //   001 - BNE
  //   010 - UNKNOWN
  //   100 - BLT
  //   101 - BGE
  //   110 - BLTU
  //   111 - BGEU
  //   OP_I_ECALL_TYPE
  //   OP_U_LUI_TYPE
  //   load_store_type
  //   0000 -  L_W
  //   0001 - L_H
  //   0010 - L_HU
  //   0011 - L_B
  //   0100 - L_BU
  //   1000 - S_W
  //   1001 - S_H
  //   1010 - S_B
  //   1100 - LS_N_A
  //   OP_U_AUIPC_TYPE
  //   OP_J_TYPE
endmodule
