// Digital circuit rv32i_relay.dig as structural Verilog
module rv32i_relay (
  input  clk,
  input  in_2,
  input  clk_2,
  input  clk_3,
  input  in_5,
  input  clk_4,
  input  MANUAL,
  input  SELECT,
  input  [31:0] in_9,
  input  in_10,
  input  [31:0] in_11,
  input  [31:0] in_12,
  input  in_13,
  input  in_14,
  input  [4:0] in_15,
  input  [4:0] in_16,
  input  [6:0] in_17,
  input  [6:0] in_19,
  input  [2:0] in_21,
  input  [2:0] in_22,
  output [6:0] out_18,
  output [6:0] out_20
);

  wire and_1_out, and_2_out, CLOCK, nCLOCK, or_2_out, relay_2_p3, relay_2_p4, relay_3_p3, relay_4_p3,
       relay_5_p3, relay_6_p3, relay_7_p3, relay_8_p3, relay_9_p3, relay_10_p3, relay_11_p5, relay_12_p3,
       relay_13_p3, relay_14_p3, relay_15_p5, relay_16_p3, relay_17_p3, relay_18_p3, relay_19_p5,
       relay_20_p3, relay_21_p3, relay_22_p3, relay_23_p5, relay_24_p3, relay_25_p3, relay_26_p3,
       relay_27_p5, relay_28_p3, relay_29_p3, relay_30_p3, relay_31_p5, relay_32_p3, relay_33_p3,
       relay_34_p3, relaydt_1_p7, relaydt_1_p8, relaydt_2_p2, relaydt_3_p3, relaydt_3_p4, relaydt_3_p6,
       relaydt_3_p9, relaydt_3_p10, relaydt_3_p12, relaydt_3_p15, relaydt_5_p6, relaydt_5_p7, relaydt_10_p1,
       relaydt_10_p3, relaydt_10_p6, relaydt_10_p7, relaydt_10_p9, relaydt_10_p14, relaydt_10_p15,
       relaydt_10_p16, relaydt_10_p19, relaydt_10_p24, relaydt_10_p25, relaydt_16_p1, relaydt_16_p3,
       relaydt_16_p10, relaydt_16_p11, relaydt_16_p12, relaydt_16_p13, relaydt_16_p17, relaydt_17_p4,
       relaydt_17_p5, relaydt_17_p6, relaydt_17_p7, relaydt_17_p11, relaydt_17_p18, relaydt_17_p19,
       relaydt_17_p20, relaydt_17_p21, relaydt_17_p25, relaydt_17_p32, relaydt_17_p33, relaydt_17_p34,
       relaydt_17_p35, relaydt_17_p39, relaydt_17_p46, relaydt_17_p47, relaydt_17_p48, relaydt_17_p51,
       relaydt_17_p56, relaydt_17_p57, relaydt_17_p58, relaydt_18_p4, relaydt_18_p10, relaydt_18_p14,
       relaydt_18_p20, relaydt_35_p1, relaydt_35_p3, relaydt_35_p9, relaydt_35_p15, relaydt_35_p21,
       relaydt_35_p28, relaydt_35_p29, relaydt_35_p31, relaydt_35_p34, relaydt_35_p35, relaydt_35_p37,
       relaydt_35_p40, relaydt_44_p1, relaydt_44_p3, relaydt_44_p6, relaydt_44_p7, relaydt_44_p9,
       relaydt_44_p14, relaydt_44_p15, relaydt_44_p16, relaydt_44_p19, relaydt_44_p24, relaydt_44_p25,
       relaydt_45_p1, relaydt_45_p3, relaydt_45_p10, relaydt_45_p11, relaydt_45_p12, relaydt_45_p13,
       relaydt_45_p17, relaydt_46_p4, relaydt_46_p5, relaydt_46_p6, relaydt_46_p7, relaydt_46_p11,
       relaydt_46_p18, relaydt_46_p19, relaydt_46_p20, relaydt_46_p21, relaydt_46_p25, relaydt_46_p32,
       relaydt_46_p33, relaydt_46_p34, relaydt_46_p35, relaydt_46_p39, relaydt_46_p46, relaydt_46_p47,
       relaydt_46_p48, relaydt_46_p51, relaydt_46_p56, relaydt_46_p57, relaydt_46_p58, relaydt_46_p61,
       relaydt_46_p66, relaydt_47_p4, relaydt_47_p10, relaydt_47_p14, relaydt_47_p20, relaydt_49_p3,
       relaydt_49_p5, relaydt_50_p1, relaydt_50_p4, relaydt_50_p5, relaydt_50_p7, relaydt_50_p8,
       relaydt_50_p10, relaydt_52_p4, relaydt_52_p6, relaydt_53_p1, relaydt_53_p2, relaydt_54_p3,
       relaydt_54_p6, relaydt_54_p9, relaydt_54_p12, relaydt_54_p17, relaydt_56_p1, relaydt_56_p4,
       relaydt_56_p5, relaydt_56_p7, relaydt_56_p8, relaydt_56_p10, relaydt_57_p17, relaydt_57_p18,
       relaydt_57_p19, relaydt_57_p20, relaydt_57_p21, relaydt_57_p22, relaydt_58_p1, relaydt_58_p2,
       relaydt_59_p3, relaydt_59_p6, relaydt_59_p9, relaydt_59_p14, relaydt_61_p2, relaydt_61_p3,
       relaydt_61_p4, relaydt_61_p5, relaydt_61_p6, relaydt_63_p4, relaydt_63_p6, relaydt_64_p2,
       relaydt_64_p3, relaydt_64_p4, relaydt_64_p5, relaydt_64_p6, relaydt_65_p1, relaydt_65_p4,
       relaydt_65_p5, relaydt_65_p7, relaydt_65_p8, relaydt_65_p10, relaydt_66_p3, relaydt_66_p6,
       relaydt_66_p9, relaydt_66_p14, relaydt_68_p3, relaydt_68_p8, relaydt_68_p9, relaydt_68_p26,
       relaydt_68_p28, relaydt_68_p30, relaydt_68_p32, relaydt_68_p34, relaydt_68_p36, relaydt_68_p38,
       relaydt_69_p1, relaydt_69_p2, relaydt_70_p2, relaydt_70_p4, relaydt_70_p6, relaydt_70_p8,
       relaydt_70_p10, relaydt_70_p12, relaydt_70_p14, relaydt_72_p4, relaydt_72_p6, relaydt_73_p2,
       relaydt_73_p4, relaydt_73_p6, relaydt_73_p8, relaydt_73_p10, relaydt_73_p12, relaydt_73_p14,
       relaydt_74_p1, relaydt_74_p4, relaydt_74_p5, relaydt_74_p7, relaydt_74_p8, relaydt_74_p10,
       relaydt_75_p3, relaydt_75_p6, relaydt_75_p9, relaydt_75_p14, relaydt_77_p2, relaydt_77_p4,
       relaydt_77_p6, relaydt_77_p8, relaydt_77_p10, relaydt_77_p12, relaydt_77_p14, relaydt_78_p2,
       relaydt_78_p4, relaydt_78_p6, relaydt_78_p8, relaydt_78_p10, relaydt_78_p12, relaydt_78_p14,
       relaydt_79_p1, relaydt_79_p2, relaydt_80_p2, relaydt_80_p4, relaydt_80_p6, relaydt_80_p8,
       relaydt_80_p10, relaydt_80_p12, relaydt_80_p14, relaydt_82_p4, relaydt_82_p6, relaydt_83_p3,
       relaydt_83_p6, relaydt_83_p9, relaydt_83_p14, relaydt_86_p1, relaydt_86_p4, relaydt_86_p5,
       relaydt_86_p7, relaydt_86_p8, relaydt_86_p10, relaydt_88_p4, relaydt_88_p6, relaydt_89_p1,
       relaydt_89_p2, relaydt_90_p3, relaydt_90_p6, relaydt_90_p9, relaydt_90_p14, relaydt_92_p1,
       relaydt_92_p4, relaydt_92_p5, relaydt_92_p7, relaydt_92_p8, relaydt_92_p10, relaydt_93_p1,
       relaydt_93_p2, relaydt_94_p3, relaydt_94_p6, relaydt_94_p9, relaydt_94_p14, relaydt_95_p13,
       relaydt_97_p4, relaydt_97_p6, relaydt_98_p1, relaydt_98_p4, relaydt_98_p5, relaydt_98_p7,
       relaydt_98_p8, relaydt_98_p10, relaydt_99_p3, relaydt_99_p6, relaydt_99_p9, relaydt_100_p5,
       relaydt_100_p8, relaydt_101_p1, relaydt_101_p2, relaydt_103_p4, relaydt_103_p6, relaydt_104_p1,
       relaydt_104_p5, relaydt_104_p6, relaydt_104_p8, relaydt_105_p1, relaydt_105_p2, relaydt_105_p11,
       rs_ff_1_nq, rs_ff_1_q, STEP_out, WriteData;
  wire [0:0] relaydt_19_p3, relaydt_20_p2, relaydt_21_p2, relaydt_22_p3, relaydt_23_p3, relaydt_24_p2,
       relaydt_25_p2, relaydt_26_p3, relaydt_27_p3, relaydt_28_p2, relaydt_29_p2, relaydt_30_p3,
       relaydt_31_p3, relaydt_32_p2, relaydt_33_p2, relaydt_34_p3, relaydt_36_p3, relaydt_37_p2,
       relaydt_38_p2, relaydt_39_p3, relaydt_40_p3, relaydt_41_p2, relaydt_42_p2, relaydt_43_p3,
       relaydt_60_p13, relaydt_67_p5, relaydt_67_p8, relaydt_67_p13, relaydt_69_p11, relaydt_76_p5,
       relaydt_76_p8, relaydt_76_p13, relaydt_79_p11, relaydt_84_p5, relaydt_84_p8, relaydt_84_p13,
       relaydt_89_p11, relaydt_91_p5, relaydt_91_p8, relaydt_91_p13, relaydt_93_p11, relaydt_95_p5,
       relaydt_95_p8, relaydt_101_p11;
  wire [1:0] relaydt_6_p2, relaydt_7_p2, relaydt_8_p2, relaydt_9_p3, relaydt_53_p11, relaydt_55_p3,
       relaydt_55_p8, relaydt_55_p11;
  wire [1:1] ADDR2_0;
  wire [7:0] ADDR1_0;
  wire [31:0] relaydt_4_p5, RS1, RS2;

  Seven_Seg_Hex seven_seg_hex_1 (.d(RS1[31:28]), .dp(1'b0));
  Seven_Seg_Hex seven_seg_hex_2 (.d(RS2[31:28]), .dp(1'b0));
  Seven_Seg_Hex seven_seg_hex_3 (.d(RS1[27:24]), .dp(1'b0));
  Seven_Seg_Hex seven_seg_hex_4 (.d(RS2[27:24]), .dp(1'b0));
  Seven_Seg_Hex seven_seg_hex_5 (.d(RS1[23:20]), .dp(1'b0));
  Seven_Seg_Hex seven_seg_hex_6 (.d(RS2[23:20]), .dp(1'b0));
  // RelayDT #(.poles(2)) relaydt_1: pin names not known; wires that end beside it: in_5, clk_3, clk_2, clk, clk_4, 1'b0, relaydt_1_p7, relaydt_1_p8, in_2, relaydt_1_p7, relaydt_1_p8
  Seven_Seg_Hex seven_seg_hex_7 (.d(RS1[19:16]), .dp(1'b0));
  Seven_Seg_Hex seven_seg_hex_8 (.d(RS2[19:16]), .dp(1'b0));
  // RelayDT relaydt_2: pin names not known; wires that end beside it: 1'b0, relaydt_2_p2
  Seven_Seg_Hex seven_seg_hex_9 (.d(RS1[15:12]), .dp(1'b0));
  Seven_Seg_Hex seven_seg_hex_10 (.d(RS2[15:12]), .dp(1'b0));
  Button STEP (.out(STEP_out));
  and and_1 (and_1_out, STEP_out, MANUAL, ~in_13);  // And
  RS_FF rs_ff_1 (.S(and_2_out), .C(relaydt_2_p2), .R(~and_2_out), .Q(rs_ff_1_q), .nQ(rs_ff_1_nq));
  // Relay #(.Bits(32)) relay_1: pin names not known; wires that end beside it: SELECT, in_9, 1'b0, WriteData
  Seven_Seg_Hex seven_seg_hex_11 (.d(RS1[11:8]), .dp(1'b0));
  Seven_Seg_Hex seven_seg_hex_12 (.d(RS2[11:8]), .dp(1'b0));
  or or_1 (CLOCK, and_1_out, rs_ff_1_q);
  and and_2 (and_2_out, ~MANUAL, ~in_13, rs_ff_1_nq);  // And
  Seven_Seg_Hex seven_seg_hex_13 (.d(RS1[7:4]), .dp(1'b0));
  Seven_Seg_Hex seven_seg_hex_14 (.d(RS2[7:4]), .dp(1'b0));
  not not_1 (nCLOCK, CLOCK);
  Seven_Seg_Hex seven_seg_hex_15 (.d(RS1[3:0]), .dp(1'b0));
  Seven_Seg_Hex seven_seg_hex_16 (.d(RS2[3:0]), .dp(1'b0));
  LED led_1 (.in(CLOCK));
  LED led_2 (.in(nCLOCK));
  // RelayDT #(.poles(32)) relaydt_3: pin names not known; wires that end beside it: 1'b0, in_15[0], relaydt_3_p3, relaydt_3_p4, 1'b0, relaydt_3_p6, 1'b0, relaydt_3_p4, relaydt_3_p9, relaydt_3_p10, 1'b0, relaydt_3_p12, 1'b0, relaydt_3_p10, relaydt_3_p15
  or or_2 (or_2_out, in_10, in_14);
  // RelayDT #(.Bits(32)) relaydt_4: pin names not known; wires that end beside it: in_14, {32{1'b0}}, WriteData, 1'b0, relaydt_4_p5
  // Relay relay_2: pin names not known; wires that end beside it: CLOCK, or_2_out, relay_2_p3, relay_2_p4, 1'b0
  // Relay relay_3: pin names not known; wires that end beside it: relaydt_4_p5[31], relay_2_p4, relay_3_p3, 1'b0
  // Relay relay_4: pin names not known; wires that end beside it: relaydt_4_p5[23], relay_2_p4, relay_4_p3, 1'b0
  // Relay relay_5: pin names not known; wires that end beside it: relaydt_4_p5[15], 1'b0, relay_5_p3
  // Relay relay_6: pin names not known; wires that end beside it: relay_2_p4, relaydt_4_p5[7], relay_6_p3
  LED led_3 (.in(relaydt_9_p3[1]));
  // RelayDT #(.poles(2)) relaydt_5: pin names not known; wires that end beside it: 1'b0, relay_2_p3, 1'b1, relay_3_p3, 1'b0, relaydt_5_p6, relaydt_5_p7, 1'b0, relaydt_5_p6, 1'b0
  // RelayDT #(.poles(2)) relaydt_6: pin names not known; wires that end beside it: relay_3_p3, relaydt_6_p2[1], relay_4_p3, relaydt_5_p7, 1'b1, 1'b0, 1'b0
  LED led_4 (.in(relaydt_6_p2[1]));
  // RelayDT #(.poles(2)) relaydt_7: pin names not known; wires that end beside it: relay_4_p3, relaydt_7_p2[1], relay_5_p3, relaydt_5_p7, 1'b1, 1'b0, 1'b0
  LED led_5 (.in(relaydt_7_p2[1]));
  // RelayDT #(.poles(2)) relaydt_8: pin names not known; wires that end beside it: relay_5_p3, relaydt_8_p2[1], 1'b0, relaydt_5_p7, 1'b1, 1'b0
  LED led_6 (.in(relaydt_8_p2[1]));
  // RelayDT #(.poles(2)) relaydt_9: pin names not known; wires that end beside it: relay_6_p3, relay_6_p3, relaydt_9_p3[1], relaydt_5_p7, 1'b1, 1'b0
  // RelayDT #(.poles(16)) relaydt_10: pin names not known; wires that end beside it: relaydt_10_p1, 1'b0, relaydt_10_p3, 1'b0, relaydt_10_p1, relaydt_10_p6, relaydt_10_p7, 1'b0, relaydt_10_p9, 1'b0, 1'b0, in_15[1], relaydt_10_p7, relaydt_10_p14, relaydt_10_p15, relaydt_10_p16, 1'b0, 1'b0, relaydt_10_p19, 1'b0, 1'b0, relaydt_10_p15, relaydt_10_p16, relaydt_10_p24, relaydt_10_p25, 1'b0
  // RelayDT relaydt_11: pin names not known; wires that end beside it: 1'b1, relay_2_p4, relay_2_p4, 1'b0
  // Relay relay_7: pin names not known; wires that end beside it: relaydt_4_p5[30], relay_2_p4, relay_7_p3, 1'b0
  // Relay relay_8: pin names not known; wires that end beside it: relaydt_4_p5[22], relay_2_p4, relay_8_p3, 1'b0
  // Relay relay_9: pin names not known; wires that end beside it: relaydt_4_p5[14], 1'b0, relay_9_p3
  // Relay relay_10: pin names not known; wires that end beside it: relay_2_p4, relaydt_4_p5[6], relay_10_p3
  // RelayDT #(.poles(2)) relaydt_12: pin names not known; wires that end beside it: relay_7_p3, relay_7_p3, relaydt_6_p2[0], relay_8_p3, 1'b0, relaydt_5_p7, 1'b1, 1'b0, 1'b0
  LED led_7 (.in(relaydt_6_p2[0]));
  // RelayDT #(.poles(2)) relaydt_13: pin names not known; wires that end beside it: relay_8_p3, relaydt_7_p2[0], relay_9_p3, relaydt_5_p7, 1'b1, 1'b0, 1'b0
  LED led_8 (.in(relaydt_7_p2[0]));
  // RelayDT #(.poles(2)) relaydt_14: pin names not known; wires that end beside it: relay_9_p3, relaydt_8_p2[0], 1'b0, relaydt_5_p7, 1'b1, 1'b0
  LED led_9 (.in(relaydt_8_p2[0]));
  // RelayDT #(.poles(2)) relaydt_15: pin names not known; wires that end beside it: relay_10_p3, relay_10_p3, relaydt_9_p3[0], relaydt_5_p7, 1'b1, 1'b0
  LED led_10 (.in(relaydt_9_p3[0]));
  // RelayDT #(.poles(8)) relaydt_16: pin names not known; wires that end beside it: relaydt_16_p1, 1'b0, relaydt_16_p3, 1'b0, 1'b0, 1'b0, in_15[2], relaydt_10_p25, relaydt_16_p1, relaydt_16_p10, relaydt_16_p11, relaydt_16_p12, relaydt_16_p13, 1'b0, 1'b0, 1'b0, relaydt_16_p17, 1'b0, 1'b0, relaydt_16_p11, relaydt_16_p12
  // RelayDT #(.poles(4)) relaydt_17: pin names not known; wires that end beside it: 1'b0, 1'b0, relaydt_16_p13, relaydt_17_p4, relaydt_17_p5, relaydt_17_p6, relaydt_17_p7, 1'b0, 1'b0, 1'b0, relaydt_17_p11, 1'b0, 1'b0, 1'b0, relaydt_17_p5, relaydt_17_p6, relaydt_17_p7, relaydt_17_p18, relaydt_17_p19, relaydt_17_p20, relaydt_17_p21, 1'b0, 1'b0, 1'b0, relaydt_17_p25, 1'b0, 1'b0, 1'b0, relaydt_17_p19, relaydt_17_p20, relaydt_17_p21, relaydt_17_p32, relaydt_17_p33, relaydt_17_p34, relaydt_17_p35, 1'b0, 1'b0, 1'b0, relaydt_17_p39, 1'b0, 1'b0, 1'b0, relaydt_17_p33, relaydt_17_p34, relaydt_17_p35, relaydt_17_p46, relaydt_17_p47, relaydt_17_p48, 1'b0, 1'b0, relaydt_17_p51, 1'b0, 1'b0, relaydt_17_p47, relaydt_17_p48, relaydt_17_p56, relaydt_17_p57, relaydt_17_p58, 1'b0, 1'b0, 1'b0, 1'b0, relaydt_17_p57, relaydt_17_p58
  // RelayDT #(.poles(4)) relaydt_18: pin names not known; wires that end beside it: in_15[3], 1'b0, in_15[4], relaydt_18_p4, relaydt_18_p4, 1'b1, 1'b0, 1'b0, 1'b0, relaydt_18_p10, 1'b1, relaydt_18_p10, 1'b0, relaydt_18_p14, relaydt_18_p14, 1'b0, 1'b0, 1'b1, 1'b0, relaydt_18_p20, 1'b0, relaydt_18_p20, 1'b1
  // Relay relay_11: pin names not known; wires that end beside it: relay_2_p4, relaydt_4_p5[29], relay_2_p4, 1'b0, relay_11_p5, 1'b0
  // Relay relay_12: pin names not known; wires that end beside it: relaydt_4_p5[21], relay_2_p4, relay_12_p3, 1'b0
  // Relay relay_13: pin names not known; wires that end beside it: relaydt_4_p5[13], 1'b0, relay_13_p3
  // Relay relay_14: pin names not known; wires that end beside it: relay_2_p4, relaydt_4_p5[5], relay_14_p3
  LED led_11 (.in(relaydt_22_p3[0]));
  // RelayDT #(.poles(2)) relaydt_19: pin names not known; wires that end beside it: relay_11_p5, relay_11_p5, relaydt_19_p3[0], relay_12_p3, 1'b0, relaydt_5_p7, 1'b1, 1'b0, 1'b0
  LED led_12 (.in(relaydt_19_p3[0]));
  // RelayDT #(.poles(2)) relaydt_20: pin names not known; wires that end beside it: relay_12_p3, relaydt_20_p2[0], relay_13_p3, relaydt_5_p7, 1'b1, 1'b0, 1'b0
  LED led_13 (.in(relaydt_20_p2[0]));
  // RelayDT #(.poles(2)) relaydt_21: pin names not known; wires that end beside it: relay_13_p3, relaydt_21_p2[0], 1'b0, relaydt_5_p7, 1'b1, 1'b0
  LED led_14 (.in(relaydt_21_p2[0]));
  // RelayDT #(.poles(2)) relaydt_22: pin names not known; wires that end beside it: relay_14_p3, relay_14_p3, relaydt_22_p3[0], relaydt_5_p7, 1'b1, 1'b0
  // Relay relay_15: pin names not known; wires that end beside it: relay_2_p4, relaydt_4_p5[28], relay_2_p4, 1'b0, relay_15_p5, 1'b0
  // Relay relay_16: pin names not known; wires that end beside it: relaydt_4_p5[20], relay_2_p4, relay_16_p3, 1'b0
  // Relay relay_17: pin names not known; wires that end beside it: relaydt_4_p5[12], 1'b0, relay_17_p3
  // Relay relay_18: pin names not known; wires that end beside it: relay_2_p4, relaydt_4_p5[4], relay_18_p3
  // RelayDT #(.poles(2)) relaydt_23: pin names not known; wires that end beside it: relay_15_p5, relay_15_p5, relaydt_23_p3[0], relay_16_p3, 1'b0, relaydt_5_p7, 1'b1, 1'b0, 1'b0
  LED led_15 (.in(relaydt_23_p3[0]));
  // RelayDT #(.poles(2)) relaydt_24: pin names not known; wires that end beside it: relay_16_p3, relaydt_24_p2[0], relay_17_p3, relaydt_5_p7, 1'b1, 1'b0, 1'b0
  LED led_16 (.in(relaydt_24_p2[0]));
  // RelayDT #(.poles(2)) relaydt_25: pin names not known; wires that end beside it: relay_17_p3, relaydt_25_p2[0], 1'b0, relaydt_5_p7, 1'b1, 1'b0
  LED led_17 (.in(relaydt_25_p2[0]));
  // RelayDT #(.poles(2)) relaydt_26: pin names not known; wires that end beside it: relay_18_p3, relay_18_p3, relaydt_26_p3[0], relaydt_5_p7, 1'b1, 1'b0
  LED led_18 (.in(relaydt_26_p3[0]));
  // Relay relay_19: pin names not known; wires that end beside it: relay_2_p4, relaydt_4_p5[27], relay_2_p4, 1'b0, relay_19_p5, 1'b0
  // Relay relay_20: pin names not known; wires that end beside it: relaydt_4_p5[19], relay_2_p4, relay_20_p3, 1'b0
  // Relay relay_21: pin names not known; wires that end beside it: relaydt_4_p5[11], 1'b0, relay_21_p3
  // Relay relay_22: pin names not known; wires that end beside it: relay_2_p4, relaydt_4_p5[3], relay_22_p3
  LED led_19 (.in(relaydt_30_p3[0]));
  // RelayDT #(.poles(2)) relaydt_27: pin names not known; wires that end beside it: relay_19_p5, relay_19_p5, relaydt_27_p3[0], relay_20_p3, 1'b0, relaydt_5_p7, 1'b1, 1'b0, 1'b0
  LED led_20 (.in(relaydt_27_p3[0]));
  // RelayDT #(.poles(2)) relaydt_28: pin names not known; wires that end beside it: relay_20_p3, relaydt_28_p2[0], relay_21_p3, relaydt_5_p7, 1'b1, 1'b0, 1'b0
  LED led_21 (.in(relaydt_28_p2[0]));
  // RelayDT #(.poles(2)) relaydt_29: pin names not known; wires that end beside it: relay_21_p3, relaydt_29_p2[0], 1'b0, relaydt_5_p7, 1'b1, 1'b0
  LED led_22 (.in(relaydt_29_p2[0]));
  // RelayDT #(.poles(2)) relaydt_30: pin names not known; wires that end beside it: relay_22_p3, relay_22_p3, relaydt_30_p3[0], relaydt_5_p7, 1'b1, 1'b0
  // Relay relay_23: pin names not known; wires that end beside it: relay_2_p4, relaydt_4_p5[26], relay_2_p4, 1'b0, relay_23_p5, 1'b0
  // Relay relay_24: pin names not known; wires that end beside it: relaydt_4_p5[18], relay_2_p4, relay_24_p3, 1'b0
  // Relay relay_25: pin names not known; wires that end beside it: relaydt_4_p5[10], 1'b0, relay_25_p3
  // Relay relay_26: pin names not known; wires that end beside it: relay_2_p4, relaydt_4_p5[2], relay_26_p3
  // RelayDT #(.poles(2)) relaydt_31: pin names not known; wires that end beside it: relay_23_p5, relay_23_p5, relaydt_31_p3[0], relay_24_p3, 1'b0, relaydt_5_p7, 1'b1, 1'b0, 1'b0
  LED led_23 (.in(relaydt_31_p3[0]));
  // RelayDT #(.poles(2)) relaydt_32: pin names not known; wires that end beside it: relay_24_p3, relaydt_32_p2[0], relay_25_p3, relaydt_5_p7, 1'b1, 1'b0, 1'b0
  LED led_24 (.in(relaydt_32_p2[0]));
  // RelayDT #(.poles(2)) relaydt_33: pin names not known; wires that end beside it: relay_25_p3, relaydt_33_p2[0], 1'b0, relaydt_5_p7, 1'b1, 1'b0
  LED led_25 (.in(relaydt_33_p2[0]));
  // RelayDT #(.poles(2)) relaydt_34: pin names not known; wires that end beside it: relay_26_p3, relay_26_p3, relaydt_34_p3[0], relaydt_5_p7, 1'b1, 1'b0
  LED led_26 (.in(relaydt_34_p3[0]));
  // Relay relay_27: pin names not known; wires that end beside it: relay_2_p4, relaydt_4_p5[25], relay_2_p4, 1'b0, relay_27_p5, 1'b0
  // Relay relay_28: pin names not known; wires that end beside it: relaydt_4_p5[17], relay_2_p4, relay_28_p3, 1'b0
  // Relay relay_29: pin names not known; wires that end beside it: relaydt_4_p5[9], 1'b0, relay_29_p3
  // Relay relay_30: pin names not known; wires that end beside it: relay_2_p4, relaydt_4_p5[1], relay_30_p3
  LED led_27 (.in(relaydt_39_p3[0]));
  // RelayDT #(.poles(32)) relaydt_35: pin names not known; wires that end beside it: relaydt_35_p1, ADDR1_0[7], relaydt_35_p3, 1'b0, ADDR1_0[6], 1'b0, relaydt_35_p3, ADDR1_0[5], relaydt_35_p9, 1'b0, ADDR1_0[4], 1'b0, relaydt_35_p9, ADDR1_0[3], relaydt_35_p15, 1'b0, ADDR1_0[2], 1'b0, relaydt_35_p15, ADDR1_0[1], relaydt_35_p21, 1'b0, ADDR1_0[0], 1'b0, relaydt_35_p21, 1'b0, in_16[0], relaydt_35_p28, relaydt_35_p29, 1'b0, relaydt_35_p31, 1'b0, relaydt_35_p29, relaydt_35_p34, relaydt_35_p35, 1'b0, relaydt_35_p37, 1'b0, relaydt_35_p35, relaydt_35_p40
  // RelayDT #(.poles(2)) relaydt_36: pin names not known; wires that end beside it: relay_27_p5, relay_27_p5, relaydt_36_p3[0], relay_28_p3, 1'b0, relaydt_5_p7, 1'b1, 1'b0, 1'b0
  LED led_28 (.in(relaydt_36_p3[0]));
  // RelayDT #(.poles(2)) relaydt_37: pin names not known; wires that end beside it: relay_28_p3, relaydt_37_p2[0], relay_29_p3, relaydt_5_p7, 1'b1, 1'b0, 1'b0
  LED led_29 (.in(relaydt_37_p2[0]));
  // RelayDT #(.poles(2)) relaydt_38: pin names not known; wires that end beside it: relay_29_p3, relaydt_38_p2[0], 1'b0, relaydt_5_p7, 1'b1, 1'b0
  LED led_30 (.in(relaydt_38_p2[0]));
  // RelayDT #(.poles(2)) relaydt_39: pin names not known; wires that end beside it: relay_30_p3, relay_30_p3, relaydt_39_p3[0], relaydt_5_p7, 1'b1, 1'b0
  // Relay relay_31: pin names not known; wires that end beside it: relay_2_p4, relaydt_4_p5[24], relay_2_p4, 1'b0, relay_31_p5, 1'b0
  // Relay relay_32: pin names not known; wires that end beside it: relaydt_4_p5[16], relay_2_p4, relay_32_p3, 1'b0
  // Relay relay_33: pin names not known; wires that end beside it: relaydt_4_p5[8], 1'b0, relay_33_p3
  // Relay relay_34: pin names not known; wires that end beside it: relay_2_p4, relaydt_4_p5[0], relay_34_p3
  // RelayDT #(.poles(2)) relaydt_40: pin names not known; wires that end beside it: relay_31_p5, relay_31_p5, relaydt_40_p3[0], relay_32_p3, 1'b0, relaydt_5_p7, 1'b1, 1'b0, 1'b0
  LED led_31 (.in(relaydt_40_p3[0]));
  // RelayDT #(.poles(2)) relaydt_41: pin names not known; wires that end beside it: relay_32_p3, relaydt_41_p2[0], relay_33_p3, relaydt_5_p7, 1'b1, 1'b0, 1'b0
  LED led_32 (.in(relaydt_41_p2[0]));
  // RelayDT #(.poles(2)) relaydt_42: pin names not known; wires that end beside it: relay_33_p3, relaydt_42_p2[0], 1'b0, relaydt_5_p7, 1'b1, 1'b0
  LED led_33 (.in(relaydt_42_p2[0]));
  // RelayDT #(.poles(2)) relaydt_43: pin names not known; wires that end beside it: relay_34_p3, relay_34_p3, relaydt_43_p3[0], relaydt_5_p7, 1'b1, 1'b0
  LED led_34 (.in(relaydt_43_p3[0]));
  // RelayDT #(.poles(16)) relaydt_44: pin names not known; wires that end beside it: relaydt_44_p1, 1'b0, relaydt_44_p3, 1'b0, relaydt_44_p1, relaydt_44_p6, relaydt_44_p7, 1'b0, relaydt_44_p9, 1'b0, 1'b0, in_16[1], relaydt_44_p7, relaydt_44_p14, relaydt_44_p15, relaydt_44_p16, 1'b0, 1'b0, relaydt_44_p19, 1'b0, 1'b0, relaydt_44_p15, relaydt_44_p16, relaydt_44_p24, relaydt_44_p25, 1'b0
  // Relay #(.Bits(32)) relay_35: pin names not known; wires that end beside it: ADDR1_0[1], {relaydt_6_p2, relaydt_19_p3[0], relaydt_23_p3[0], relaydt_27_p3[0], relaydt_31_p3[0], relaydt_36_p3[0], relaydt_40_p3[0], relaydt_7_p2, relaydt_20_p2[0], relaydt_24_p2[0], relaydt_28_p2[0], relaydt_32_p2[0], relaydt_37_p2[0], relaydt_41_p2[0], relaydt_8_p2, relaydt_21_p2[0], relaydt_25_p2[0], relaydt_29_p2[0], relaydt_33_p2[0], relaydt_38_p2[0], relaydt_42_p2[0], relaydt_9_p3, relaydt_22_p3[0], relaydt_26_p3[0], relaydt_30_p3[0], relaydt_34_p3[0], relaydt_39_p3[0], relaydt_43_p3[0]}, 1'b0, RS1
  // Relay #(.Bits(32)) relay_36: pin names not known; wires that end beside it: {relaydt_6_p2, relaydt_19_p3[0], relaydt_23_p3[0], relaydt_27_p3[0], relaydt_31_p3[0], relaydt_36_p3[0], relaydt_40_p3[0], relaydt_7_p2, relaydt_20_p2[0], relaydt_24_p2[0], relaydt_28_p2[0], relaydt_32_p2[0], relaydt_37_p2[0], relaydt_41_p2[0], relaydt_8_p2, relaydt_21_p2[0], relaydt_25_p2[0], relaydt_29_p2[0], relaydt_33_p2[0], relaydt_38_p2[0], relaydt_42_p2[0], relaydt_9_p3, relaydt_22_p3[0], relaydt_26_p3[0], relaydt_30_p3[0], relaydt_34_p3[0], relaydt_39_p3[0], relaydt_43_p3[0]}, ADDR2_0[1], RS2, 1'b0
  // RelayDT #(.poles(8)) relaydt_45: pin names not known; wires that end beside it: relaydt_45_p1, 1'b0, relaydt_45_p3, 1'b0, 1'b0, 1'b0, in_16[2], relaydt_44_p25, relaydt_45_p1, relaydt_45_p10, relaydt_45_p11, relaydt_45_p12, relaydt_45_p13, 1'b0, 1'b0, 1'b0, relaydt_45_p17, 1'b0, 1'b0, relaydt_45_p11, relaydt_45_p12
  // RelayDT #(.poles(4)) relaydt_46: pin names not known; wires that end beside it: 1'b0, 1'b0, relaydt_45_p13, relaydt_46_p4, relaydt_46_p5, relaydt_46_p6, relaydt_46_p7, 1'b0, 1'b0, 1'b0, relaydt_46_p11, 1'b0, 1'b0, 1'b0, relaydt_46_p5, relaydt_46_p6, relaydt_46_p7, relaydt_46_p18, relaydt_46_p19, relaydt_46_p20, relaydt_46_p21, 1'b0, 1'b0, 1'b0, relaydt_46_p25, 1'b0, 1'b0, 1'b0, relaydt_46_p19, relaydt_46_p20, relaydt_46_p21, relaydt_46_p32, relaydt_46_p33, relaydt_46_p34, relaydt_46_p35, 1'b0, 1'b0, 1'b0, relaydt_46_p39, 1'b0, 1'b0, 1'b0, relaydt_46_p33, relaydt_46_p34, relaydt_46_p35, relaydt_46_p46, relaydt_46_p47, relaydt_46_p48, 1'b0, 1'b0, relaydt_46_p51, 1'b0, 1'b0, relaydt_46_p47, relaydt_46_p48, relaydt_46_p56, relaydt_46_p57, relaydt_46_p58, 1'b0, 1'b0, relaydt_46_p61, 1'b0, 1'b0, relaydt_46_p57, relaydt_46_p58, relaydt_46_p66
  // RelayDT #(.poles(4)) relaydt_47: pin names not known; wires that end beside it: in_16[3], 1'b0, in_16[4], relaydt_47_p4, relaydt_47_p4, 1'b1, 1'b0, 1'b0, 1'b0, relaydt_47_p10, 1'b1, relaydt_47_p10, 1'b0, relaydt_47_p14, relaydt_47_p14, 1'b0, 1'b0, 1'b1, 1'b0, relaydt_47_p20, 1'b0, relaydt_47_p20, 1'b1
  // RelayDT relaydt_48: pin names not known; wires that end beside it: 1'b0, 1'b1, 1'b0
  // RelayDT relaydt_49: pin names not known; wires that end beside it: 1'b0, 1'b1, relaydt_49_p3, relaydt_49_p3, relaydt_49_p5
  // RelayDT #(.poles(4)) relaydt_50: pin names not known; wires that end beside it: relaydt_50_p1, in_11[31], relaydt_50_p1, relaydt_50_p4, relaydt_50_p5, 1'b0, relaydt_50_p7, relaydt_50_p8, relaydt_49_p5, relaydt_50_p10, relaydt_50_p10, relaydt_50_p7, relaydt_50_p8
  LED led_35 (.in(relaydt_55_p3[1]));
  LED led_36 (.in(relaydt_55_p11[1]));
  LED led_37 (.in(relaydt_55_p8[1]));
  // RelayDT relaydt_51: pin names not known; wires that end beside it: relaydt_50_p4, 1'b1, 1'b0
  // RelayDT relaydt_52: pin names not known; wires that end beside it: relaydt_50_p5, 1'b0, 1'b1, relaydt_52_p4, relaydt_52_p4, relaydt_52_p6
  // RelayDT #(.poles(4)) relaydt_53: pin names not known; wires that end beside it: relaydt_53_p1, relaydt_53_p2, relaydt_49_p5, relaydt_50_p10, relaydt_50_p8, relaydt_53_p1, relaydt_53_p1, relaydt_53_p2, 1'b0, relaydt_50_p4, relaydt_53_p11[1], 1'b1, relaydt_50_p5, in_12[31], 1'b0
  LED led_38 (.in(relaydt_53_p11[1]));
  // RelayDT #(.poles(4)) relaydt_54: pin names not known; wires that end beside it: 1'b0, 1'b1, relaydt_54_p3, 1'b1, 1'b0, relaydt_54_p6, 1'b0, 1'b1, relaydt_54_p9, 1'b0, 1'b1, relaydt_54_p12, in_11[31], 1'b0, 1'b0, 1'b1, relaydt_54_p17
  // RelayDT #(.poles(4)) relaydt_55: pin names not known; wires that end beside it: 1'b0, relaydt_54_p3, relaydt_55_p3[1], 1'b1, 1'b0, relaydt_54_p9, relaydt_54_p6, relaydt_55_p8[1], relaydt_54_p12, 1'b1, relaydt_55_p11[1], in_12[31], 1'b0, 1'b0, relaydt_54_p17, relaydt_55_p3[0]
  // RelayDT #(.poles(4)) relaydt_56: pin names not known; wires that end beside it: relaydt_56_p1, in_11[30], relaydt_56_p1, relaydt_56_p4, relaydt_56_p5, 1'b0, relaydt_56_p7, relaydt_56_p8, relaydt_52_p6, relaydt_56_p10, relaydt_56_p10, relaydt_56_p7, relaydt_56_p8
  LED led_39 (.in(relaydt_55_p3[0]));
  LED led_40 (.in(relaydt_55_p11[0]));
  LED led_41 (.in(relaydt_55_p8[0]));
  // RelayDT #(.poles(7)) relaydt_57: pin names not known; wires that end beside it: in_22[0], 1'b1, 1'b0, 1'b1, 1'b1, 1'b1, 1'b0, 1'b0, 1'b0, 1'b1, 1'b0, 1'b0, 1'b0, 1'b1, 1'b0, 1'b0, relaydt_57_p17, relaydt_57_p18, relaydt_57_p19, relaydt_57_p20, relaydt_57_p21, relaydt_57_p22, in_22[1], relaydt_57_p17, 1'b0, relaydt_57_p18, 1'b0, 1'b1, relaydt_57_p19, 1'b0, 1'b0, relaydt_57_p20, 1'b0, 1'b1, relaydt_57_p21
  // RelayDT #(.poles(4)) relaydt_58: pin names not known; wires that end beside it: relaydt_58_p1, relaydt_58_p2, relaydt_52_p6, relaydt_56_p10, relaydt_56_p8, relaydt_58_p1, relaydt_58_p1, relaydt_58_p2, 1'b0, relaydt_56_p4, relaydt_53_p11[0], 1'b1, relaydt_56_p5, in_12[30], 1'b0
  // RelayDT #(.poles(4)) relaydt_59: pin names not known; wires that end beside it: 1'b1, 1'b0, relaydt_59_p3, 1'b0, 1'b1, relaydt_59_p6, 1'b0, 1'b1, relaydt_59_p9, in_11[30], 1'b0, 1'b0, 1'b1, relaydt_59_p14
  // RelayDT #(.poles(4)) relaydt_60: pin names not known; wires that end beside it: 1'b1, 1'b0, relaydt_59_p6, relaydt_59_p3, relaydt_55_p8[0], relaydt_59_p9, 1'b1, relaydt_55_p11[0], in_12[30], 1'b0, 1'b0, relaydt_59_p14, relaydt_60_p13[0]
  // RelayDT #(.poles(7)) relaydt_61: pin names not known; wires that end beside it: 1'b0, relaydt_61_p2, relaydt_61_p3, relaydt_61_p4, relaydt_61_p5, relaydt_61_p6, in_22[2], relaydt_61_p2, 1'b0, relaydt_61_p3, 1'b0, relaydt_61_p4, 1'b0, 1'b1, 1'b0, 1'b1, relaydt_61_p5
  // RelayDT relaydt_62: pin names not known; wires that end beside it: relaydt_56_p4, 1'b1, 1'b0
  // RelayDT relaydt_63: pin names not known; wires that end beside it: relaydt_56_p5, 1'b0, 1'b1, relaydt_63_p4, relaydt_63_p4, relaydt_63_p6
  LED led_42 (.in(relaydt_53_p11[0]));
  LED led_43 (.in(relaydt_60_p13[0]));
  // RelayDT #(.poles(7)) relaydt_64: pin names not known; wires that end beside it: 1'b0, relaydt_64_p2, relaydt_64_p3, relaydt_64_p4, relaydt_64_p5, relaydt_64_p6
  // RelayDT #(.poles(4)) relaydt_65: pin names not known; wires that end beside it: relaydt_65_p1, in_11[29], relaydt_65_p1, relaydt_65_p4, relaydt_65_p5, 1'b0, relaydt_65_p7, relaydt_65_p8, relaydt_63_p6, relaydt_65_p10, relaydt_65_p10, relaydt_65_p7, relaydt_65_p8
  LED led_44 (.in(relaydt_67_p8[0]));
  LED led_45 (.in(relaydt_67_p5[0]));
  // RelayDT #(.poles(4)) relaydt_66: pin names not known; wires that end beside it: 1'b1, 1'b0, relaydt_66_p3, 1'b0, 1'b1, relaydt_66_p6, 1'b0, 1'b1, relaydt_66_p9, in_11[29], 1'b0, 1'b0, 1'b1, relaydt_66_p14
  // RelayDT #(.poles(4)) relaydt_67: pin names not known; wires that end beside it: 1'b1, 1'b0, relaydt_66_p6, relaydt_66_p3, relaydt_67_p5[0], relaydt_66_p9, 1'b1, relaydt_67_p8[0], in_12[29], 1'b0, 1'b0, relaydt_66_p14, relaydt_67_p13[0]
  // RelayDT #(.poles(7)) relaydt_68: pin names not known; wires that end beside it: 1'b1, relaydt_57_p22, relaydt_68_p3, 1'b1, relaydt_61_p6, 1'b1, relaydt_68_p3, relaydt_68_p8, relaydt_68_p9, relaydt_68_p9, in_17[5], in_17[6], in_17[4], in_17[5], in_17[3], in_17[4], in_17[2], in_17[3], in_17[1], in_17[2], in_17[0], in_17[1], 1'b0, in_17[0], 1'b0, relaydt_68_p26, relaydt_68_p8, relaydt_68_p28, relaydt_68_p26, relaydt_68_p30, relaydt_68_p28, relaydt_68_p32, relaydt_68_p30, relaydt_68_p34, relaydt_68_p32, relaydt_68_p36, relaydt_68_p34, relaydt_68_p38, relaydt_68_p36, 1'b0, relaydt_68_p38
  // RelayDT #(.poles(4)) relaydt_69: pin names not known; wires that end beside it: relaydt_69_p1, relaydt_69_p2, relaydt_63_p6, relaydt_65_p10, relaydt_65_p8, relaydt_69_p1, relaydt_69_p1, relaydt_69_p2, 1'b0, relaydt_65_p4, relaydt_69_p11[0], 1'b1, relaydt_65_p5, in_12[29], 1'b0
  LED led_46 (.in(relaydt_67_p13[0]));
  // RelayDT #(.poles(7)) relaydt_70: pin names not known; wires that end beside it: 1'b0, relaydt_70_p2, relaydt_64_p6, relaydt_70_p4, relaydt_70_p2, relaydt_70_p6, relaydt_70_p4, relaydt_70_p8, relaydt_70_p6, relaydt_70_p10, relaydt_70_p8, relaydt_70_p12, relaydt_70_p10, relaydt_70_p14, relaydt_70_p12, 1'b0, relaydt_70_p14
  // RelayDT relaydt_71: pin names not known; wires that end beside it: relaydt_65_p4, 1'b1, 1'b0
  // RelayDT relaydt_72: pin names not known; wires that end beside it: relaydt_65_p5, 1'b0, 1'b1, relaydt_72_p4, relaydt_72_p4, relaydt_72_p6
  LED led_47 (.in(relaydt_69_p11[0]));
  LED led_48 (.in(relaydt_76_p8[0]));
  LED led_49 (.in(relaydt_76_p5[0]));
  // RelayDT #(.poles(7)) relaydt_73: pin names not known; wires that end beside it: 1'b0, relaydt_73_p2, relaydt_64_p5, relaydt_73_p4, relaydt_73_p2, relaydt_73_p6, relaydt_73_p4, relaydt_73_p8, relaydt_73_p6, relaydt_73_p10, relaydt_73_p8, relaydt_73_p12, relaydt_73_p10, relaydt_73_p14, relaydt_73_p12, 1'b0, relaydt_73_p14
  // RelayDT #(.poles(4)) relaydt_74: pin names not known; wires that end beside it: relaydt_74_p1, in_11[28], relaydt_74_p1, relaydt_74_p4, relaydt_74_p5, 1'b0, relaydt_74_p7, relaydt_74_p8, relaydt_72_p6, relaydt_74_p10, relaydt_74_p10, relaydt_74_p7, relaydt_74_p8
  // RelayDT #(.poles(4)) relaydt_75: pin names not known; wires that end beside it: 1'b1, 1'b0, relaydt_75_p3, 1'b0, 1'b1, relaydt_75_p6, 1'b0, 1'b1, relaydt_75_p9, in_11[28], 1'b0, 1'b0, 1'b1, relaydt_75_p14
  // RelayDT #(.poles(4)) relaydt_76: pin names not known; wires that end beside it: 1'b1, 1'b0, relaydt_75_p6, relaydt_75_p3, relaydt_76_p5[0], relaydt_75_p9, 1'b1, relaydt_76_p8[0], in_12[28], 1'b0, 1'b0, relaydt_75_p14, relaydt_76_p13[0]
  // RelayDT #(.poles(7)) relaydt_77: pin names not known; wires that end beside it: 1'b0, relaydt_77_p2, relaydt_64_p4, relaydt_77_p4, relaydt_77_p2, relaydt_77_p6, relaydt_77_p4, relaydt_77_p8, relaydt_77_p6, relaydt_77_p10, relaydt_77_p8, relaydt_77_p12, relaydt_77_p10, relaydt_77_p14, relaydt_77_p12, 1'b0, relaydt_77_p14
  LED led_50 (.in(relaydt_76_p13[0]));
  // RelayDT #(.poles(7)) relaydt_78: pin names not known; wires that end beside it: 1'b0, relaydt_78_p2, relaydt_64_p3, relaydt_78_p4, relaydt_78_p2, relaydt_78_p6, relaydt_78_p4, relaydt_78_p8, relaydt_78_p6, relaydt_78_p10, relaydt_78_p8, relaydt_78_p12, relaydt_78_p10, relaydt_78_p14, relaydt_78_p12, 1'b0, relaydt_78_p14
  // RelayDT #(.poles(4)) relaydt_79: pin names not known; wires that end beside it: relaydt_79_p1, relaydt_79_p2, relaydt_72_p6, relaydt_74_p10, relaydt_74_p8, relaydt_79_p1, relaydt_79_p1, relaydt_79_p2, 1'b0, relaydt_74_p4, relaydt_79_p11[0], 1'b1, relaydt_74_p5, in_12[28], 1'b0
  LED led_51 (.in(relaydt_79_p11[0]));
  LED led_52 (.in(relaydt_84_p8[0]));
  LED led_53 (.in(relaydt_84_p5[0]));
  // RelayDT #(.poles(7)) relaydt_80: pin names not known; wires that end beside it: 1'b0, relaydt_80_p2, relaydt_64_p2, relaydt_80_p4, relaydt_80_p2, relaydt_80_p6, relaydt_80_p4, relaydt_80_p8, relaydt_80_p6, relaydt_80_p10, relaydt_80_p8, relaydt_80_p12, relaydt_80_p10, relaydt_80_p14, relaydt_80_p12, 1'b0, relaydt_80_p14
  // RelayDT relaydt_81: pin names not known; wires that end beside it: relaydt_74_p4, 1'b1, 1'b0
  // RelayDT relaydt_82: pin names not known; wires that end beside it: relaydt_74_p5, 1'b0, 1'b1, relaydt_82_p4, relaydt_82_p4, relaydt_82_p6
  // RelayDT #(.poles(4)) relaydt_83: pin names not known; wires that end beside it: 1'b1, 1'b0, relaydt_83_p3, 1'b0, 1'b1, relaydt_83_p6, 1'b0, 1'b1, relaydt_83_p9, in_11[27], 1'b0, 1'b0, 1'b1, relaydt_83_p14
  // RelayDT #(.poles(4)) relaydt_84: pin names not known; wires that end beside it: 1'b1, 1'b0, relaydt_83_p6, relaydt_83_p3, relaydt_84_p5[0], relaydt_83_p9, 1'b1, relaydt_84_p8[0], in_12[27], 1'b0, 1'b0, relaydt_83_p14, relaydt_84_p13[0]
  // RelayDT #(.poles(7)) relaydt_85: pin names not known; wires that end beside it: 1'b0
  // RelayDT #(.poles(4)) relaydt_86: pin names not known; wires that end beside it: relaydt_86_p1, in_11[27], relaydt_86_p1, relaydt_86_p4, relaydt_86_p5, 1'b0, relaydt_86_p7, relaydt_86_p8, relaydt_82_p6, relaydt_86_p10, relaydt_86_p10, relaydt_86_p7, relaydt_86_p8
  LED led_54 (.in(relaydt_84_p13[0]));
  BarrelShifter #(.Bits(7)) barrelshifter_1 (.in(in_19), .shift(in_21), .out(out_20));
  LED led_55 (.in(relaydt_91_p8[0]));
  LED led_56 (.in(relaydt_91_p5[0]));
  // RelayDT relaydt_87: pin names not known; wires that end beside it: relaydt_86_p4, 1'b1, 1'b0
  // RelayDT relaydt_88: pin names not known; wires that end beside it: relaydt_86_p5, 1'b0, 1'b1, relaydt_88_p4, relaydt_88_p4, relaydt_88_p6
  // RelayDT #(.poles(4)) relaydt_89: pin names not known; wires that end beside it: relaydt_89_p1, relaydt_89_p2, relaydt_82_p6, relaydt_86_p10, relaydt_86_p8, relaydt_89_p1, relaydt_89_p1, relaydt_89_p2, 1'b0, relaydt_86_p4, relaydt_89_p11[0], 1'b1, relaydt_86_p5, in_12[27], 1'b0
  LED led_57 (.in(relaydt_89_p11[0]));
  // RelayDT #(.poles(4)) relaydt_90: pin names not known; wires that end beside it: 1'b1, 1'b0, relaydt_90_p3, 1'b0, 1'b1, relaydt_90_p6, 1'b0, 1'b1, relaydt_90_p9, in_11[26], 1'b0, 1'b0, 1'b1, relaydt_90_p14
  // RelayDT #(.poles(4)) relaydt_91: pin names not known; wires that end beside it: 1'b1, 1'b0, relaydt_90_p6, relaydt_90_p3, relaydt_91_p5[0], relaydt_90_p9, 1'b1, relaydt_91_p8[0], in_12[26], 1'b0, 1'b0, relaydt_90_p14, relaydt_91_p13[0]
  // RelayDT #(.poles(4)) relaydt_92: pin names not known; wires that end beside it: relaydt_92_p1, in_11[26], relaydt_92_p1, relaydt_92_p4, relaydt_92_p5, 1'b0, relaydt_92_p7, relaydt_92_p8, relaydt_88_p6, relaydt_92_p10, relaydt_92_p10, relaydt_92_p7, relaydt_92_p8
  LED led_58 (.in(relaydt_91_p13[0]));
  LED led_59 (.in(relaydt_95_p8[0]));
  LED led_60 (.in(relaydt_95_p5[0]));
  // RelayDT #(.poles(4)) relaydt_93: pin names not known; wires that end beside it: relaydt_93_p1, relaydt_93_p2, relaydt_88_p6, relaydt_92_p10, relaydt_92_p8, relaydt_93_p1, relaydt_93_p1, relaydt_93_p2, 1'b0, relaydt_92_p4, relaydt_93_p11[0], 1'b1, relaydt_92_p5, in_12[26], 1'b0
  // RelayDT #(.poles(4)) relaydt_94: pin names not known; wires that end beside it: 1'b1, 1'b0, relaydt_94_p3, 1'b0, 1'b1, relaydt_94_p6, 1'b0, 1'b1, relaydt_94_p9, in_11[25], 1'b0, 1'b0, 1'b1, relaydt_94_p14
  // RelayDT #(.poles(4)) relaydt_95: pin names not known; wires that end beside it: 1'b1, 1'b0, relaydt_94_p6, relaydt_94_p3, relaydt_95_p5[0], relaydt_94_p9, 1'b1, relaydt_95_p8[0], in_12[25], 1'b0, 1'b0, relaydt_94_p14, relaydt_95_p13
  // RelayDT relaydt_96: pin names not known; wires that end beside it: relaydt_92_p4, 1'b1, 1'b0
  // RelayDT relaydt_97: pin names not known; wires that end beside it: relaydt_92_p5, 1'b0, 1'b1, relaydt_97_p4, relaydt_97_p4, relaydt_97_p6
  LED led_61 (.in(relaydt_93_p11[0]));
  LED led_62 (.in(relaydt_95_p13));
  // RelayDT #(.poles(4)) relaydt_98: pin names not known; wires that end beside it: relaydt_98_p1, in_11[25], relaydt_98_p1, relaydt_98_p4, relaydt_98_p5, 1'b0, relaydt_98_p7, relaydt_98_p8, relaydt_97_p6, relaydt_98_p10, relaydt_98_p10, relaydt_98_p7, relaydt_98_p8
  LED led_63 (.in(relaydt_100_p8));
  LED led_64 (.in(relaydt_100_p5));
  // RelayDT #(.poles(4)) relaydt_99: pin names not known; wires that end beside it: 1'b1, 1'b0, relaydt_99_p3, 1'b0, 1'b1, relaydt_99_p6, 1'b0, 1'b1, relaydt_99_p9, in_11[24], 1'b0
  // RelayDT #(.poles(4)) relaydt_100: pin names not known; wires that end beside it: 1'b1, 1'b0, relaydt_99_p6, relaydt_99_p3, relaydt_100_p5, relaydt_99_p9, 1'b1, relaydt_100_p8, in_12[24], 1'b0
  // RelayDT #(.poles(4)) relaydt_101: pin names not known; wires that end beside it: relaydt_101_p1, relaydt_101_p2, relaydt_97_p6, relaydt_98_p10, relaydt_98_p8, relaydt_101_p1, relaydt_101_p1, relaydt_101_p2, 1'b0, relaydt_98_p4, relaydt_101_p11[0], 1'b1, relaydt_98_p5, in_12[25], 1'b0
  // RelayDT relaydt_102: pin names not known; wires that end beside it: relaydt_98_p4, 1'b1, 1'b0
  // RelayDT relaydt_103: pin names not known; wires that end beside it: relaydt_98_p5, 1'b0, 1'b1, relaydt_103_p4, relaydt_103_p4, relaydt_103_p6
  LED led_65 (.in(relaydt_101_p11[0]));
  // RelayDT #(.poles(4)) relaydt_104: pin names not known; wires that end beside it: relaydt_104_p1, in_11[24], relaydt_104_p1, 1'b0, relaydt_104_p5, relaydt_104_p6, relaydt_103_p6, relaydt_104_p8, relaydt_104_p8, relaydt_104_p5, relaydt_104_p6
  // RelayDT #(.poles(4)) relaydt_105: pin names not known; wires that end beside it: relaydt_105_p1, relaydt_105_p2, relaydt_103_p6, relaydt_104_p8, relaydt_104_p6, relaydt_105_p1, relaydt_105_p1, relaydt_105_p2, 1'b0, 1'b1, relaydt_105_p11, 1'b1, 1'b0, in_12[24]
  LED led_66 (.in(relaydt_105_p11));

  // Other names for the same wires on the sheet: a[31:0] = in_11; b[31:0] = in_12; HALT = in_13; RESET = in_14;
  //   WriteAddr_0 = in_10

  // Notes on the sheet:
  //   clk: Hz: 4
  //   clk_2: Hz: 8
  //   clk_3: Hz: 16
  //   clk_4: Hz: 2
  //   MANUAL: default 1
  //   CLOCK
  //   x01 Register
  //   ADDR1
  //   ADDR2
  //   ALU-Logic
  //   AND
  //   XOR
  //   OR
  //   SUM
  //   SLL
endmodule
