// Digital circuit sap_6502_digital.dig as structural Verilog
module sap_6502_digital (
  input  clk,
  input  HALT,
  input  in_3,
  input  clk_2,
  input  clk_3,
  input  in_6,
  input  clk_4,
  input  MANUAL,
  input  [7:0] in_9,
  input  Manual_Load_BUS,
  input  in_11,
  input  in_12,
  input  in_13,
  input  in_14,
  input  in_15,
  input  in_16,
  input  in_17,
  input  in_18,
  input  in_19,
  input  in_20,
  input  in_21,
  input  in_22,
  input  in_23,
  input  in_24,
  input  in_25,
  input  in_26
);

  wire add_1_c_o, AI, and_1_out, and_2_out, AO, BI, CE, CLOCK, CO, decoder_1_out_0, decoder_1_out_1,
       decoder_1_out_2, decoder_1_out_3, decoder_1_out_4, decoder_1_out_5, decoder_1_out_6, decoder_1_out_7,
       decoder_1_out_8, decoder_1_out_9, decoder_1_out_10, decoder_1_out_11, decoder_1_out_12,
       decoder_1_out_13, decoder_1_out_14, decoder_1_out_15, decoder_2_out_0, decoder_2_out_1,
       decoder_2_out_2, decoder_2_out_3, decoder_2_out_4, decoder_2_out_5, decoder_2_out_6, decoder_2_out_7,
       decoder_2_out_8, decoder_2_out_9, decoder_2_out_10, decoder_2_out_11, decoder_2_out_12,
       decoder_2_out_13, decoder_2_out_14, decoder_2_out_15, EO, FI, HALT_t, II, IO, J, MI, nCLOCK,
       nSeqReset, OI, or_1_out, or_3_out, or_4_out, or_5_out, or_6_out, or_7_out, or_8_out, or_9_out,
       or_10_out, or_11_out, or_12_out, or_13_out, or_14_out, relaydt_1_p7, relaydt_1_p8, relaydt_2_p2, RI,
       RO, rs_ff_1_nq, rs_ff_1_q, STEP_out, SU, sub_1_c_o;
  wire [1:0] FLAGS, multiplexer_4_out;
  wire [2:0] counterpreset_1_out;
  wire [3:0] binary_to_bcd_1__1s, binary_to_bcd_1__10s, binary_to_bcd_1__100s, counterpreset_2_out,
       Mem_Address_Register_q, multiplexer_1_out;
  wire [7:0] A_Reg, A_Register_q, Accumulator_q, add_1_s, B_Reg, BUS, Constant_q, EBH_Register_q,
       EBL_Register_q, Inst_Reg, multiplexer_2_out, multiplexer_3_out, multiplexer_5_out, multiplexer_6_out,
       multiplexer_7_out, multiplexer_8_out, multiplexer_9_out, multiplexer_10_out, multiplexer_11_out,
       multiplexer_12_out, multiplexer_13_out, Stack_Pointer_q, sub_1_s, X_Register_q, Y_Register_q;
  wire [12:8] counterpreset_3_out;
  wire [15:0] R2_d;
  wire [39:0] d_ff_1_q, R1_d;

  LED u_MI (.in(MI));
  LED HT (.in(HALT_t));
  CounterPreset #(.maxValue(4), .Bits(3)) counterpreset_1 (
    .en(1'b1), .C(nCLOCK), .dir(1'b0), .in(3'b000), .ld(1'b0), .clr(in_11), .out(counterpreset_1_out));  // open: ovf
  LED u_RO (.in(RO));
  LED u_RI (.in(RI));
  // RelayDT #(.poles(2)) relaydt_1: pin names not known; wires that end beside it: in_6, clk_3, clk_2, clk, clk_4, 1'b0, relaydt_1_p7, relaydt_1_p8, in_3, relaydt_1_p7, relaydt_1_p8
  or or_1 (or_1_out, HALT, HALT_t);
  LED led_1 (.in(counterpreset_1_out[0]));
  LED led_2 (.in(counterpreset_1_out[2]));
  LED led_3 (.in(counterpreset_1_out[1]));
  LED u_IO (.in(IO));
  LED u_II (.in(II));
  // RelayDT relaydt_2: pin names not known; wires that end beside it: 1'b0, relaydt_2_p2
  EEPROMDualPort #(.AddrBits(9), .isProgramMemory("true"), .Bits(16)) R4 (
    .A({FLAGS, 4'b0000, counterpreset_1_out}), .Din({16{1'b0}}), .str(1'b0), .C(CLOCK), .ld(1'b1),
    .D({HALT_t, MI, RI, RO, IO, II, AI, AO, EO, SU, BI, OI, CE, CO, J, FI}));
  LED u_AI (.in(AI));
  LED u_AO (.in(AO));
  Button STEP (.out(STEP_out));
  and and_1 (and_1_out, STEP_out, MANUAL, ~or_1_out);  // And
  RS_FF rs_ff_1 (.S(and_2_out), .C(relaydt_2_p2), .R(~and_2_out), .Q(rs_ff_1_q), .nQ(rs_ff_1_nq));
  LED u_SU (.in(SU));
  LED E0 (.in(EO));
  and and_2 (and_2_out, ~MANUAL, ~or_1_out, rs_ff_1_nq);  // And
  LED u_OI (.in(OI));
  LED u_BI (.in(BI));
  or or_2 (CLOCK, and_1_out, rs_ff_1_q);
  LED u_CE (.in(CE));
  LED u_CO (.in(CO));
  not not_1 (nCLOCK, CLOCK);
  LED u_J (.in(J));
  LED u_FI (.in(FI));
  LED led_4 (.in(CLOCK));
  LED led_5 (.in(nCLOCK));
  LED led_6 (.in(BUS[7]));
  LED led_7 (.in(BUS[5]));
  LED led_8 (.in(BUS[6]));
  LED led_9 (.in(BUS[3]));
  LED led_10 (.in(BUS[4]));
  CounterPreset #(.Bits(4)) counterpreset_2 (
    .en(CE), .C(CLOCK), .dir(1'b0), .in(BUS[3:0]), .ld(J), .clr(in_11), .out(counterpreset_2_out));  // open: ovf
  assign BUS = Manual_Load_BUS ? in_9 : 8'bz;  // Driver driver_1
  LED led_11 (.in(BUS[1]));
  LED led_12 (.in(BUS[2]));
  LED led_13 (.in(counterpreset_2_out[2]));
  LED led_14 (.in(counterpreset_2_out[1]));
  LED led_15 (.in(counterpreset_2_out[3]));
  LED led_16 (.in(BUS[0]));
  LED led_17 (.in(counterpreset_2_out[0]));
  assign BUS = CO ? {4'b0000, counterpreset_2_out} : 8'bz;  // Driver driver_2
  Register #(.Bits(8)) A_Register (.D(BUS), .C(CLOCK), .en(OI), .Q(A_Register_q));
  Binary_to_BCD binary_to_bcd_1 (
    .In(A_Register_q), ._100s(binary_to_bcd_1__100s), ._10s(binary_to_bcd_1__10s), ._1s(binary_to_bcd_1__1s));
  Seven_Seg_Hex seven_seg_hex_1 (.d(binary_to_bcd_1__100s), .dp(1'b0));
  Multiplexer #(.Bits(4)) multiplexer_1 (.sel(in_11), .in_0(BUS[3:0]), .in_1(4'b0000), .out(multiplexer_1_out));
  or or_3 (or_3_out, in_11, MI);
  Seven_Seg_Hex seven_seg_hex_2 (.d(binary_to_bcd_1__10s), .dp(1'b0));
  Seven_Seg_Hex seven_seg_hex_3 (.d(binary_to_bcd_1__1s), .dp(1'b0));
  Register #(.Bits(4)) Mem_Address_Register (
    .D(multiplexer_1_out), .C(CLOCK), .en(or_3_out), .Q(Mem_Address_Register_q));
  LED led_18 (.in(R2_d[7]));
  RAMDualPort #(.AddrBits(4), .isProgramMemory("true"), .Bits(16)) R2 (
    .A(Mem_Address_Register_q), .Din({{8{1'b0}}, BUS}), .str(RI), .C(CLOCK), .ld(1'b1), .D(R2_d));
  LED led_19 (.in(R2_d[3]));
  LED led_20 (.in(R2_d[4]));
  LED led_21 (.in(R2_d[5]));
  LED led_22 (.in(R2_d[6]));
  LED led_23 (.in(R2_d[0]));
  LED led_24 (.in(R2_d[1]));
  LED led_25 (.in(R2_d[2]));
  assign BUS = RO ? R2_d[7:0] : 8'bz;  // Driver driver_3
  Multiplexer #(.Bits(8)) multiplexer_2 (.sel(in_11), .in_0(BUS), .in_1({8{1'b0}}), .out(multiplexer_2_out));
  or or_4 (or_4_out, in_11, in_18);
  Add #(.Bits(8)) add_1 (.a(A_Reg), .b(B_Reg), .c_i(1'b0), .s(add_1_s), .c_o(add_1_c_o));
  Sub #(.Bits(8)) sub_1 (.a(A_Reg), .b(B_Reg), .c_i(1'b0), .s(sub_1_s), .c_o(sub_1_c_o));
  Register #(.Bits(8)) Constant (.D(multiplexer_2_out), .C(CLOCK), .en(or_4_out), .Q(Constant_q));
  LED led_26 (.in(Constant_q[7]));
  LED led_27 (.in(Constant_q[6]));
  LED led_28 (.in(Constant_q[5]));
  LED led_29 (.in(Constant_q[4]));
  LED led_30 (.in(Constant_q[3]));
  LED led_31 (.in(Constant_q[2]));
  LED led_32 (.in(Constant_q[1]));
  Multiplexer #(.Bits(8)) multiplexer_3 (.sel(SU), .in_0(add_1_s), .in_1(sub_1_s), .out(multiplexer_3_out));
  Multiplexer multiplexer_4 (.sel(SU), .in_0(add_1_c_o), .in_1(sub_1_c_o), .out(multiplexer_4_out[0]));
  assign BUS = in_19 ? Constant_q : 8'bz;  // Driver driver_4
  LED led_33 (.in(Constant_q[0]));
  assign BUS = EO ? multiplexer_3_out : 8'bz;  // Driver driver_5
  Comparator #(.Bits(8)) comparator_1 (
    .a(multiplexer_3_out), .b({8{1'b0}}), .eq(multiplexer_4_out[1]));  // open: gt, lt
  Register #(.Bits(2)) Flag_Register (.D(multiplexer_4_out), .C(CLOCK), .en(FI), .Q(FLAGS));
  LED led_34 (.in(FLAGS[0]));
  LED led_35 (.in(FLAGS[1]));
  Multiplexer #(.Bits(8)) multiplexer_5 (.sel(in_11), .in_0(BUS), .in_1({8{1'b0}}), .out(multiplexer_5_out));
  or or_5 (or_5_out, in_11, in_24);
  Multiplexer #(.Bits(8)) multiplexer_6 (.sel(in_11), .in_0(BUS), .in_1({8{1'b0}}), .out(multiplexer_6_out));
  or or_6 (or_6_out, in_11, in_22);
  Multiplexer #(.Bits(8)) multiplexer_7 (.sel(in_11), .in_0(BUS), .in_1({8{1'b0}}), .out(multiplexer_7_out));
  or or_7 (or_7_out, in_11, in_20);
  Multiplexer #(.Bits(8)) multiplexer_8 (.sel(in_11), .in_0(BUS), .in_1({8{1'b0}}), .out(multiplexer_8_out));
  or or_8 (or_8_out, in_11, in_13);
  Multiplexer #(.Bits(8)) multiplexer_9 (.sel(in_11), .in_0(BUS), .in_1({8{1'b0}}), .out(multiplexer_9_out));
  or or_9 (or_9_out, in_11, in_12);
  Multiplexer #(.Bits(8)) multiplexer_10 (.sel(in_11), .in_0(BUS), .in_1({8{1'b0}}), .out(multiplexer_10_out));
  or or_10 (or_10_out, in_11, in_16);
  Multiplexer #(.Bits(8)) multiplexer_11 (.sel(in_11), .in_0(BUS), .in_1({8{1'b0}}), .out(multiplexer_11_out));
  or or_11 (or_11_out, in_11, AI);
  Multiplexer #(.Bits(8)) multiplexer_12 (.sel(in_11), .in_0(BUS), .in_1({8{1'b0}}), .out(multiplexer_12_out));
  or or_12 (or_12_out, in_11, BI);
  Multiplexer #(.Bits(8)) multiplexer_13 (.sel(in_11), .in_0(BUS), .in_1({8{1'b0}}), .out(multiplexer_13_out));
  or or_13 (or_13_out, in_11, II);
  LED led_36 (.in(EBH_Register_q[7]));
  LED led_37 (.in(EBH_Register_q[6]));
  LED led_38 (.in(EBL_Register_q[7]));
  LED led_39 (.in(EBL_Register_q[6]));
  LED led_40 (.in(Stack_Pointer_q[7]));
  LED led_41 (.in(Stack_Pointer_q[6]));
  LED led_42 (.in(Y_Register_q[7]));
  LED led_43 (.in(Y_Register_q[6]));
  LED led_44 (.in(X_Register_q[7]));
  LED led_45 (.in(X_Register_q[6]));
  LED led_46 (.in(Accumulator_q[7]));
  LED led_47 (.in(Accumulator_q[6]));
  LED led_48 (.in(A_Reg[7]));
  LED led_49 (.in(A_Reg[6]));
  LED led_50 (.in(B_Reg[7]));
  LED led_51 (.in(B_Reg[6]));
  LED led_52 (.in(Inst_Reg[7]));
  LED led_53 (.in(Inst_Reg[6]));
  Register #(.Bits(8)) EBH_Register (.D(multiplexer_5_out), .C(CLOCK), .en(or_5_out), .Q(EBH_Register_q));
  LED led_54 (.in(EBH_Register_q[5]));
  LED led_55 (.in(EBH_Register_q[4]));
  LED led_56 (.in(EBH_Register_q[3]));
  LED led_57 (.in(EBH_Register_q[2]));
  Register #(.Bits(8)) EBL_Register (.D(multiplexer_6_out), .C(CLOCK), .en(or_6_out), .Q(EBL_Register_q));
  LED led_58 (.in(EBL_Register_q[5]));
  LED led_59 (.in(EBL_Register_q[4]));
  LED led_60 (.in(EBL_Register_q[3]));
  LED led_61 (.in(EBL_Register_q[2]));
  Register #(.Bits(8)) Stack_Pointer (.D(multiplexer_7_out), .C(CLOCK), .en(or_7_out), .Q(Stack_Pointer_q));
  LED led_62 (.in(Stack_Pointer_q[5]));
  LED led_63 (.in(Stack_Pointer_q[4]));
  LED led_64 (.in(Stack_Pointer_q[3]));
  LED led_65 (.in(Stack_Pointer_q[2]));
  Register #(.Bits(8)) Y_Register (.D(multiplexer_8_out), .C(CLOCK), .en(or_8_out), .Q(Y_Register_q));
  LED led_66 (.in(Y_Register_q[5]));
  LED led_67 (.in(Y_Register_q[4]));
  LED led_68 (.in(Y_Register_q[3]));
  LED led_69 (.in(Y_Register_q[2]));
  Register #(.Bits(8)) X_Register (.D(multiplexer_9_out), .C(CLOCK), .en(or_9_out), .Q(X_Register_q));
  LED led_70 (.in(X_Register_q[5]));
  LED led_71 (.in(X_Register_q[4]));
  LED led_72 (.in(X_Register_q[3]));
  LED led_73 (.in(X_Register_q[2]));
  Register #(.Bits(8)) Accumulator (.D(multiplexer_10_out), .C(CLOCK), .en(or_10_out), .Q(Accumulator_q));
  LED led_74 (.in(Accumulator_q[5]));
  LED led_75 (.in(Accumulator_q[4]));
  LED led_76 (.in(Accumulator_q[3]));
  LED led_77 (.in(Accumulator_q[2]));
  Register #(.Bits(8)) A_Register_2 (.D(multiplexer_11_out), .C(CLOCK), .en(or_11_out), .Q(A_Reg));
  LED led_78 (.in(A_Reg[5]));
  LED led_79 (.in(A_Reg[4]));
  LED led_80 (.in(A_Reg[3]));
  LED led_81 (.in(A_Reg[2]));
  Register #(.Bits(8)) B_Register (.D(multiplexer_12_out), .C(CLOCK), .en(or_12_out), .Q(B_Reg));
  LED led_82 (.in(B_Reg[5]));
  LED led_83 (.in(B_Reg[4]));
  LED led_84 (.in(B_Reg[3]));
  LED led_85 (.in(B_Reg[2]));
  Register #(.Bits(8)) Inst_Register (.D(multiplexer_13_out), .C(CLOCK), .en(or_13_out), .Q(Inst_Reg));
  LED led_86 (.in(Inst_Reg[3]));
  LED led_87 (.in(Inst_Reg[2]));
  LED led_88 (.in(Inst_Reg[4]));
  LED led_89 (.in(Inst_Reg[5]));
  assign BUS = in_25 ? EBH_Register_q : 8'bz;  // Driver driver_6
  LED led_90 (.in(EBH_Register_q[1]));
  LED led_91 (.in(EBH_Register_q[0]));
  assign BUS = in_23 ? EBL_Register_q : 8'bz;  // Driver driver_7
  LED led_92 (.in(EBL_Register_q[1]));
  LED led_93 (.in(EBL_Register_q[0]));
  assign BUS = in_21 ? Stack_Pointer_q : 8'bz;  // Driver driver_8
  LED led_94 (.in(Stack_Pointer_q[1]));
  LED led_95 (.in(Stack_Pointer_q[0]));
  assign BUS = in_15 ? Y_Register_q : 8'bz;  // Driver driver_9
  LED led_96 (.in(Y_Register_q[1]));
  LED led_97 (.in(Y_Register_q[0]));
  assign BUS = in_14 ? X_Register_q : 8'bz;  // Driver driver_10
  LED led_98 (.in(X_Register_q[1]));
  LED led_99 (.in(X_Register_q[0]));
  assign BUS = in_17 ? Accumulator_q : 8'bz;  // Driver driver_11
  LED led_100 (.in(Accumulator_q[1]));
  LED led_101 (.in(Accumulator_q[0]));
  LED led_102 (.in(A_Reg[1]));
  LED led_103 (.in(A_Reg[0]));
  LED led_104 (.in(B_Reg[1]));
  LED led_105 (.in(B_Reg[0]));
  LED led_106 (.in(Inst_Reg[0]));
  LED led_107 (.in(Inst_Reg[1]));
  or or_14 (or_14_out, in_11, ~nSeqReset);  // Or
  LED nSBC (.in(d_ff_1_q[35]));
  LED nBITOP (.in(d_ff_1_q[36]));
  LED nFlag_Instr (.in(d_ff_1_q[33]));
  LED nShift_Right (.in(d_ff_1_q[34]));
  CounterPreset #(.maxValue(32), .Bits(5)) counterpreset_3 (
    .en(1'b1), .C(nCLOCK), .dir(1'b0), .in({{2{in_26}}, 3'b000}), .ld(1'b0), .clr(or_14_out),
    .out(counterpreset_3_out));  // open: ovf
  LED nUpdateV (.in(d_ff_1_q[31]));
  LED NoBCD (.in(d_ff_1_q[32]));
  LED led_108 (.in(counterpreset_3_out[8]));
  LED led_109 (.in(counterpreset_3_out[9]));
  EEPROMDualPort #(.AddrBits(14), .Bits(40)) R1 (
    .A({1'b0, counterpreset_3_out, Inst_Reg}), .Din({40{1'b0}}), .str(1'b0), .C(CLOCK), .ld(1'b1), .D(R1_d));
  LED nUpdateNZ (.in(d_ff_1_q[29]));
  LED nUpdateC (.in(d_ff_1_q[30]));
  LED led_110 (.in(counterpreset_3_out[10]));
  LED led_111 (.in(counterpreset_3_out[11]));
  LED led_112 (.in(counterpreset_3_out[12]));
  LED CarryZERO (.in(d_ff_1_q[27]));
  LED CarryONE (.in(d_ff_1_q[28]));
  D_FF #(.Bits(40)) d_ff_1 (.D(R1_d), .C(CLOCK), .Q({d_ff_1_q[39:18], nSeqReset, d_ff_1_q[16:0]}));  // open: nQ
  LED ALU_FLAG1 (.in(d_ff_1_q[25]));
  LED ALU_FLAG2 (.in(d_ff_1_q[26]));
  LED ALU_FLAG0 (.in(d_ff_1_q[24]));
  LED nPCSel (.in(d_ff_1_q[23]));
  LED nMem_Access (.in(d_ff_1_q[21]));
  LED nMWrite (.in(d_ff_1_q[22]));
  LED IREG_Load (.in(d_ff_1_q[20]));
  LED nPCClockHigh (.in(d_ff_1_q[19]));
  LED nPCClockLow (.in(d_ff_1_q[18]));
  LED u_nSeqReset (.in(nSeqReset));
  Decoder #(.Selector_Bits(4)) decoder_1 (
    .sel(d_ff_1_q[3:0]), .out_0(decoder_1_out_0), .out_1(decoder_1_out_1), .out_2(decoder_1_out_2),
    .out_3(decoder_1_out_3), .out_4(decoder_1_out_4), .out_5(decoder_1_out_5), .out_6(decoder_1_out_6),
    .out_7(decoder_1_out_7), .out_8(decoder_1_out_8), .out_9(decoder_1_out_9), .out_10(decoder_1_out_10),
    .out_11(decoder_1_out_11), .out_12(decoder_1_out_12), .out_13(decoder_1_out_13),
    .out_14(decoder_1_out_14), .out_15(decoder_1_out_15));
  Decoder #(.Selector_Bits(4)) decoder_2 (
    .sel(d_ff_1_q[7:4]), .out_0(decoder_2_out_0), .out_1(decoder_2_out_1), .out_2(decoder_2_out_2),
    .out_3(decoder_2_out_3), .out_4(decoder_2_out_4), .out_5(decoder_2_out_5), .out_6(decoder_2_out_6),
    .out_7(decoder_2_out_7), .out_8(decoder_2_out_8), .out_9(decoder_2_out_9), .out_10(decoder_2_out_10),
    .out_11(decoder_2_out_11), .out_12(decoder_2_out_12), .out_13(decoder_2_out_13),
    .out_14(decoder_2_out_14), .out_15(decoder_2_out_15));
  LED ALU_F3 (.in(d_ff_1_q[15]));
  LED ALU_F4 (.in(d_ff_1_q[16]));
  LED led_113 (.in(decoder_1_out_0));
  LED AREGCLK (.in(decoder_1_out_1));
  LED BREGCLK (.in(decoder_1_out_2));
  LED PCHCLK (.in(decoder_1_out_3));
  LED SPREGCLK (.in(decoder_1_out_4));
  LED EBHCLK (.in(decoder_1_out_5));
  LED PCLCLK (.in(decoder_1_out_6));
  LED ACCCLK (.in(decoder_1_out_7));
  LED EBLCLK (.in(decoder_1_out_8));
  LED led_114 (.in(decoder_1_out_9));
  LED STREGCLK (.in(decoder_1_out_10));
  LED EAHCLK (.in(decoder_1_out_11));
  LED XREGCLK (.in(decoder_1_out_12));
  LED YREGCLK (.in(decoder_1_out_13));
  LED EALCLK (.in(decoder_1_out_14));
  LED CONSTOE (.in(decoder_1_out_15));
  LED ALUOE (.in(decoder_2_out_0));
  LED AREGOE (.in(decoder_2_out_1));
  LED BREGOE (.in(decoder_2_out_2));
  LED PCHOE (.in(decoder_2_out_3));
  LED SPREGOE (.in(decoder_2_out_4));
  LED EBHOE (.in(decoder_2_out_5));
  LED PCLOE (.in(decoder_2_out_6));
  LED ACCOE (.in(decoder_2_out_7));
  LED EBLOE (.in(decoder_2_out_8));
  LED led_115 (.in(decoder_2_out_9));
  LED STREGOE (.in(decoder_2_out_10));
  LED led_116 (.in(decoder_2_out_11));
  LED XREGOE (.in(decoder_2_out_12));
  LED YREGOE (.in(decoder_2_out_13));
  LED led_117 (.in(decoder_2_out_14));
  LED CONSTOE_2 (.in(decoder_2_out_15));
  LED ALU_F1 (.in(d_ff_1_q[13]));
  LED ALU_F2 (.in(d_ff_1_q[14]));
  LED ALU_F0 (.in(d_ff_1_q[12]));
  LED Constant3 (.in(d_ff_1_q[11]));
  LED Constant1 (.in(d_ff_1_q[9]));
  LED Constant2 (.in(d_ff_1_q[10]));
  LED Constant0 (.in(d_ff_1_q[8]));
  LED W_Bus_Dest3 (.in(d_ff_1_q[7]));
  LED W_Bus_Dest1 (.in(d_ff_1_q[5]));
  LED W_Bus_Dest2 (.in(d_ff_1_q[6]));
  LED W_Bus_Dest0 (.in(d_ff_1_q[4]));
  LED W_Bus_Source3 (.in(d_ff_1_q[3]));
  LED W_Bus_Source1 (.in(d_ff_1_q[1]));
  LED W_Bus_Source2 (.in(d_ff_1_q[2]));
  LED W_Bus_Source0 (.in(d_ff_1_q[0]));

  // Other names for the same wires on the sheet: ACI = in_16; ACO = in_17; CONSI = in_18; CONSO = in_19; EBHI = in_24;
  //   EBHO = in_25; EBLI = in_22; EBLO = in_23; MasterReset = in_26; RESET = in_11; SPI = in_20; SPO = in_21;
  //   XI = in_12; XO = in_14; YI = in_13; YO = in_15

  // Notes on the sheet:
  //   clk: Hz: 8
  //   clk_2: Hz: 16
  //   clk_3: Hz: 64
  //   clk_4: Hz: 2
  //   MANUAL: default 1
  //   CLOCK
  //   contents of R4 (hex, n*v repeats v):
  //   e0,2f,74,60,3f,e0,80,64,7*0,8
  //   ALU
  //   contents of R1 (hex, n*v repeats v):
  //   4004,1408,6*0,4004,1408,4800,1200,4*0,4004,1408,4800,1020,281
  //   ,0,0,0,4004,1408,4800,1020,2c1,0,0,0,4004,1408,4800,2100,4*0,4004
  //   ,1408,a00,5*0,4004,1408,802,5*0,4004,1408,6*0,4004,1408,46*0,4004
  //   ,1408,110,5*0,4004,1408,8000,5*0,4004,1408,6*0,4004,1408,4800
  //   ,1200,4*0,4004,1408,4800,1020,281,0,0,0,4004,1408,4800,1020,2c1
  //   ,0,0,0,4004,1408,4800,2100,4*0,4004,1408,a00,5*0,4004,1408,802
  //   ,5*0,4004,1408,802,5*0,4004,1408,46*0,4004,1408,110,5*0,4004,1408
  //   ,8000,5*0,4004,1408,6*0,4004,1408,4800,1200,4*0,4004,1408,4800
  //   ,1020,281,0,0,0,4004,1408,4800,1020,2c1,0,0,0,4004,1408,4800,2100
  //   ,4*0,4004,1408,a00,5*0,4004,1408,802,5*0,4004,1408,6*0,4004,1408
  //   ,802,45*0,4004,1408,110,5*0,4004,1408,8000,5*0,4004,1408,6*0,4004
  //   ,1408,4800,1200,4*0,4004,1408,4800,1020,281,0,0,0,4004,1408,4800
  //   ,1020,2c1,0,0,0,4004,1408,4800,2100,4*0,4004,1408,a00,5*0,4004
  //   ,1408,802,5*0,4004,1408,802,5*0,4004,1408,802,45*0,4004,1408,110
  //   ,5*0,4004,1408,8000
  //   W-Bus Source
  //   W-Bus Dest
endmodule
