// Digital circuit program_memory_test.dig as structural Verilog
module program_memory_test (
  input  in_1,
  input  in_2,
  input  in_3,
  input  in_4,
  input  in_5,
  input  in_6,
  input  in_7,
  input  in_8,
  input  in_9,
  input  in_10,
  input  in_11,
  input  in_12,
  input  in_13
);

  wire [15:0] E1_d, E2_d;

  EEPROMDualPort #(.AddrBits(9), .isProgramMemory("true"), .Bits(16)) E1 (
    .A({in_9, in_8, in_7, in_6, in_5, in_1, in_2, in_3, in_4}), .Din({16{1'b0}}), .str(1'b0), .C(1'b0),
    .ld(1'b1), .D(E1_d));
  LED HT (.in(E1_d[15]));
  LED MI (.in(E1_d[14]));
  LED RI (.in(E1_d[13]));
  LED RO (.in(E1_d[12]));
  LED IO (.in(E1_d[11]));
  LED II (.in(E1_d[10]));
  LED AI (.in(E1_d[9]));
  LED AO (.in(E1_d[8]));
  LED E0 (.in(E1_d[7]));
  LED SU (.in(E1_d[6]));
  LED BI (.in(E1_d[5]));
  LED OI (.in(E1_d[4]));
  LED CE (.in(E1_d[3]));
  LED CO (.in(E1_d[2]));
  LED J (.in(E1_d[1]));
  LED FI (.in(E1_d[0]));
  EEPROMDualPort #(.AddrBits(4), .isProgramMemory("true"), .Bits(16)) E2 (
    .A({in_10, in_11, in_12, in_13}), .Din({16{1'b0}}), .str(1'b0), .C(1'b0), .ld(1'b1), .D(E2_d));
  LED led_1 (.in(E2_d[15]));
  LED led_2 (.in(E2_d[14]));
  LED led_3 (.in(E2_d[13]));
  LED led_4 (.in(E2_d[12]));
  LED led_5 (.in(E2_d[11]));
  LED led_6 (.in(E2_d[10]));
  LED led_7 (.in(E2_d[9]));
  LED led_8 (.in(E2_d[8]));
  LED led_9 (.in(E2_d[7]));
  LED led_10 (.in(E2_d[6]));
  LED led_11 (.in(E2_d[5]));
  LED led_12 (.in(E2_d[4]));
  LED led_13 (.in(E2_d[3]));
  LED led_14 (.in(E2_d[2]));
  LED led_15 (.in(E2_d[1]));
  LED led_16 (.in(E2_d[0]));

  // Notes on the sheet:
  //   contents of E1 (hex, n*v repeats v):
  //   4004,1408,6*0,4004,1408,4800,1200,4*0,4004,1408,4800,1020,281
  //   ,0,0,0,4004,1408,4800,1020,2c1,0,0,0,4004,1408,4800,2100,4*0,4004
  //   ,1408,a00,5*0,4004,1408,802,5*0,4004,1408,6*0,4004,1408,46*0,4004
  //   ,1408,110,5*0,4004,1408,8000,5*0,4004,1408,6*0,4004,1408,4800
  //   ,1200,4*0,4004,1408,4800,1020,281,0,0,0,4004,1408,4800,1020,2c1
  //   ,0,0,0,4004,1408,4800,2100,4*0,4004,1408,a00,5*0,4004,1408,802
  //   ,5*0,4004,1408,802,5*0,4004,1408,46*0,4004,1408,110,5*0,4004,1408
  //   ,8000,5*0,4004,1408,6*0,4004,1408,4800,1200,4*0,4004,1408,4800
  //   ,1020,281,0,0,0,4004,1408,4800,1020,2c1,0,0,0,4004,1408,4800,2100
  //   ,4*0,4004,1408,a00,5*0,4004,1408,802,5*0,4004,1408,6*0,4004,1408
  //   ,802,45*0,4004,1408,110,5*0,4004,1408,8000,5*0,4004,1408,6*0,4004
  //   ,1408,4800,1200,4*0,4004,1408,4800,1020,281,0,0,0,4004,1408,4800
  //   ,1020,2c1,0,0,0,4004,1408,4800,2100,4*0,4004,1408,a00,5*0,4004
  //   ,1408,802,5*0,4004,1408,802,5*0,4004,1408,802,45*0,4004,1408,110
  //   ,5*0,4004,1408,8000
  //   contents of E2 (hex, n*v repeats v):
  //   e0,2f,74,64,3f,e0,80,64,7*0,8
endmodule
