// Digital circuit relay_program_memory_test.dig as structural Verilog
module relay_program_memory_test (
  input  in_1,
  input  in_2,
  input  in_3,
  input  in_4,
  input  in_5,
  input  in_6,
  input  in_7,
  input  in_8,
  input  in_9,
  input  in_10,
  input  in_11,
  input  in_12,
  input  in_13,
  input  in_14
);

  wire CE, CO, HALT, J, LRAM, RLB, RLC, RLI, RML, ROL, RSB, RSI, SCZL, SRAM;
  wire [1:0] ALU_F;
  wire [15:0] E2_d;

  LED led_1 (.in(HALT));
  LED led_2 (.in(RML));
  LED led_3 (.in(LRAM));
  LED led_4 (.in(SRAM));
  LED led_5 (.in(RSI));
  LED led_6 (.in(RLI));
  LED led_7 (.in(RLB));
  LED led_8 (.in(RSB));
  LED led_9 (.in(ALU_F[1]));
  LED led_10 (.in(ALU_F[0]));
  LED led_11 (.in(RLC));
  LED led_12 (.in(ROL));
  LED led_13 (.in(CE));
  LED led_14 (.in(CO));
  LED led_15 (.in(J));
  LED led_16 (.in(SCZL));
  EEPROMDualPort #(.AddrBits(10), .isProgramMemory("true"), .Bits(16)) E1 (
    .A({in_14, in_9, in_8, in_7, in_6, in_5, in_1, in_2, in_3, in_4}), .Din({16{1'b0}}), .str(1'b0),
    .C(1'b0), .ld(1'b1), .D({HALT, RML, LRAM, SRAM, RSI, RLI, RLB, RSB, ALU_F, RLC, ROL, CE, CO, J, SCZL}));
  EEPROMDualPort #(.AddrBits(4), .isProgramMemory("true"), .Bits(16)) E2 (
    .A({in_10, in_11, in_12, in_13}), .Din({16{1'b0}}), .str(1'b0), .C(1'b0), .ld(1'b1), .D(E2_d));
  LED led_17 (.in(E2_d[15]));
  LED led_18 (.in(E2_d[14]));
  LED led_19 (.in(E2_d[13]));
  LED led_20 (.in(E2_d[12]));
  LED led_21 (.in(E2_d[11]));
  LED led_22 (.in(E2_d[10]));
  LED led_23 (.in(E2_d[9]));
  LED led_24 (.in(E2_d[8]));
  LED led_25 (.in(E2_d[7]));
  LED led_26 (.in(E2_d[6]));
  LED led_27 (.in(E2_d[5]));
  LED led_28 (.in(E2_d[4]));
  LED led_29 (.in(E2_d[3]));
  LED led_30 (.in(E2_d[2]));
  LED led_31 (.in(E2_d[1]));
  LED led_32 (.in(E2_d[0]));

  // Notes on the sheet:
  //   contents of E1 (hex, n*v repeats v):
  //   4004,1408,6*0,4004,1408,4800,1200,4*0,4004,1408,4800,1020,241
  //   ,11*0,4004,1408,4800,2100,4*0,4004,1408,a00,5*0,4004,1408,802
  //   ,5*0,4004,1408,6*0,4004,1408,6*0,4004,1408,22*0,4004,1408,4800
  //   ,1020,2c1,0,0,0,4004,1408,4800,1020,281,0,0,0,4004,1408,110,5*0
  //   ,4004,1408,8000,5*0,4004,1408,6*0,4004,1408,4800,1200,4*0,4004
  //   ,1408,4800,1020,241,11*0,4004,1408,4800,2100,4*0,4004,1408,a00
  //   ,5*0,4004,1408,802,5*0,4004,1408,6*0,4004,1408,802,5*0,4004,1408
  //   ,22*0,4004,1408,4800,1020,2c1,0,0,0,4004,1408,4800,1020,281,0,0,0
  //   ,4004,1408,110,5*0,4004,1408,8000,5*0,4004,1408,6*0,4004,1408
  //   ,4800,1200,4*0,4004,1408,4800,1020,241,11*0,4004,1408,4800,2100
  //   ,4*0,4004,1408,a00,5*0,4004,1408,802,5*0,4004,1408,802,5*0,4004
  //   ,1408,6*0,4004,1408,22*0,4004,1408,4800,1020,2c1,0,0,0,4004,1408
  //   ,4800,1020,281,0,0,0,4004,1408,110,5*0,4004,1408,8000,5*0,4004
  //   ,1408,6*0,4004,1408,4800,1200,4*0,4004,1408,4800,1020,241,11*0
  //   ,4004,1408,4800,2100,4*0,4004,1408,a00,5*0,4004,1408,802,5*0,4004
  //   ,1408,802,5*0,4004,1408,802,5*0,4004,1408,22*0,4004,1408,4800
  //   ,1020,2c1,0,0,0,4004,1408,4800,1020,281,0,0,0,4004,1408,110,5*0
  //   ,4004,1408,8000,5*0,4004,1408,6*0,4004,1408,4800,1200,4*0,4004
  //   ,1408,4800,1020,241,11*0,4004,1408,4800,2100,4*0,4004,1408,a00
  //   ,5*0,4004,1408,802,5*0,4004,1408,6*0,4004,1408,6*0,4004,1408,802
  //   ,21*0,4004,1408,4800,1020,2c1,0,0,0,4004,1408,4800,1020,281,0,0,0
  //   ,4004,1408,110,5*0,4004,1408,8000,5*0,4004,1408,6*0,4004,1408
  //   ,4800,1200,4*0,4004,1408,4800,1020,241,11*0,4004,1408,4800,2100
  //   ,4*0,4004,1408,a00,5*0,4004,1408,802,5*0,4004,1408,6*0,4004,1408
  //   ,802,5*0,4004,1408,802,21*0,4004,1408,4800,1020,2c1,0,0,0,4004
  //   ,1408,4800,1020,281,0,0,0,4004,1408,110,5*0,4004,1408,8000,5*0
  //   ,4004,1408,6*0,4004,1408,4800,1200,4*0,4004,1408,4800,1020,241
  //   ,11*0,4004,1408,4800,2100,4*0,4004,1408,a00,5*0,4004,1408,802
  //   ,5*0,4004,1408,802,5*0,4004,1408,6*0,4004,1408,802,21*0,4004,1408
  //   ,4800,1020,2c1,0,0,0,4004,1408,4800,1020,281,0,0,0,4004,1408,110
  //   ,5*0,4004,1408,8000,5*0,4004,1408,6*0,4004,1408,4800,1200,4*0
  //   ,4004,1408,4800,1020,241,11*0,4004,1408,4800,2100,4*0,4004,1408
  //   ,a00,5*0,4004,1408,802,5*0,4004,1408,802,5*0,4004,1408,802,5*0
  //   ,4004,1408,802,21*0,4004,1408,4800,1020,2c1,0,0,0,4004,1408,4800
  //   ,1020,281,0,0,0,4004,1408,110,5*0,4004,1408,8000
  //   contents of E2 (hex, n*v repeats v):
  //   e0,2f,74,60,f,10*0,20
endmodule
